// Logisim project CPU.circ as structural Verilog
module CPU (
  input  in_1,
  input  [4:0] in_2,
  input  [3:0] in_3,
  input  [3:0] in_4,
  input  [3:0] in_5,
  input  [3:0] in_6,
  input  [3:0] in_7,
  input  [3:0] in_8,
  input  in_9,
  input  [7:0] in_10,
  input  [7:0] in_11
);

  wire and_1_out, button_out, c1, c2, clock_1_out, condition_checker_1_out_12, condition_decoder_1_out_13,
       condition_decoder_1_out_14, D, I, inst_decoder_1_alu_read, inst_decoder_1_alu_write,
       inst_decoder_1_out_22, inst_decoder_1_out_23, inst_decoder_1_out_24, inst_decoder_1_out_25,
       inst_decoder_1_out_26, inst_decoder_1_out_27, inst_decoder_1_out_28, inst_decoder_1_out_29,
       inst_decoder_1_out_30, inst_decoder_1_out_31, N, or_2_out, or_3_out, or_6_out, or_7_out, or_11_out,
       or_14_out, output_module_1_out_9, output_module_1_out_10, output_module_1_out_11,
       output_module_1_out_12, R_out, S_out, X0, X1, XA, XB, xor_1_out, xor_2_out, xor_3_out;
  wire [2:0] condition_decoder_1_mem;
  wire [3:0] condition_checker_1_out_10, condition_checker_1_out_11, condition_decoder_1_comp,
       inst_decoder_1_dest, inst_decoder_1_isource, inst_decoder_1_out_18, inst_decoder_1_out_19,
       inst_decoder_1_out_20, inst_decoder_1_out_21, inst_decoder_1_source2, inst_reg_1_out_24,
       inst_reg_1_out_25, inst_reg_1_out_26, inst_reg_1_out_27, inst_reg_1_out_28, inst_reg_1_out_29,
       n4_buf_1_out_3, n4_buf_2_out_3, n4_buf_3_out_3, n4_buf_4_out_3, or_9_out, or_10_out,
       output_module_1_out_5, output_module_1_out_6, output_module_1_out_7, output_module_1_out_8, q1, q2;
  wire [3:3] or_15_out;
  wire [4:0] condition_decoder_1_jump_if_true, or_1_out;
  wire [7:0] alu_1_out_9, and_2_out, condition_decoder_1_constant, cpu_mem_1_out_1, cpu_mem_1_out_2,
       input_module_1_out_5, inst_decoder_1_const, n8_buf_1_out_3, n8_buf_2_out_3, n8_buf_3_out_3,
       n8_buf_4_out_3, n8_buf_5_out_3, or_5_out, or_8_out;
  wire [7:7] or_4_out;

  assign or_1_out = in_2 | condition_decoder_1_jump_if_true;  // OR_Gate or_1, 5 bits wide
  Button R (.out(R_out));
  or or_2 (or_2_out, in_1, condition_checker_1_out_12);
  Clock clock_1 (.out(clock_1_out));
  // Probe on in_10
  Output_Module output_module_1 (
    .in_2(inst_decoder_1_out_31), .in_3(cpu_mem_1_out_2), .in_4(cpu_mem_1_out_1),
    .out_5(output_module_1_out_5), .out_9(output_module_1_out_9), .out_6(output_module_1_out_6),
    .out_10(output_module_1_out_10), .out_7(output_module_1_out_7), .out_11(output_module_1_out_11),
    .out_8(output_module_1_out_8), .out_12(output_module_1_out_12), .in_1(R_out));
  Hex_Digit_Display hex_digit_display_1 (.value(output_module_1_out_6), .dp(output_module_1_out_10));
  Hex_Digit_Display hex_digit_display_2 (.value(output_module_1_out_5), .dp(output_module_1_out_9));
  Input_Module input_module_1 (
    .out_5(input_module_1_out_5), .in_1(inst_decoder_1_isource), .in_2(inst_decoder_1_out_23), .iA(in_10),
    .iB(in_11));
  Hex_Digit_Display hex_digit_display_3 (.value(output_module_1_out_8), .dp(output_module_1_out_12));
  Hex_Digit_Display hex_digit_display_4 (.value(output_module_1_out_7), .dp(output_module_1_out_11));
  Inst_Reg inst_reg_1 (
    .in_1(clock_1_out), .Prog_Count(or_1_out), .R(R_out), .in_5(in_3), .in_6(in_4), .in_7(in_5), .in_8(in_6),
    .in_9(in_7), .in_10(in_8), .in_11(button_out), .S(S_out), .in_13(in_9), .out_24(inst_reg_1_out_24),
    .out_25(inst_reg_1_out_25), .out_26(inst_reg_1_out_26), .out_27(inst_reg_1_out_27),
    .out_28(inst_reg_1_out_28), .out_29(inst_reg_1_out_29), .in_3(or_2_out));  // open: out_23, out_22, out_21, out_20, out_19, out_14, out_15, out_16, out_17, out_18
  Button button (.out(button_out));
  // Probe on in_11
  // Probe on cpu_mem_1_out_2
  Button S (.out(S_out));
  // Probe on cpu_mem_1_out_1
  and and_1 (and_1_out, inst_decoder_1_alu_read, inst_decoder_1_out_24);
  or or_3 (or_3_out, inst_decoder_1_out_26, inst_decoder_1_out_27, inst_decoder_1_out_29, inst_decoder_1_out_28);
  ALU alu_1 (
    .nA(n8_buf_1_out_3), .nB(n8_buf_2_out_3), .in_3(inst_decoder_1_out_27), .in_5(inst_decoder_1_out_29),
    .in_6(inst_decoder_1_out_28), .in_7(or_6_out), .in_8(and_1_out), .out_9(alu_1_out_9),
    .in_4(inst_decoder_1_out_26));  // open: out_10
  or or_4 (or_4_out[7], inst_decoder_1_out_27, inst_decoder_1_out_29, inst_decoder_1_out_28);
  assign or_5_out = cpu_mem_1_out_1 | and_2_out;  // OR_Gate or_5, 8 bits wide
  _8_BUF u_8_buf_1 (.in_2(or_3_out), .in_1(or_5_out), .out_3(n8_buf_1_out_3));
  or or_6 (or_6_out, inst_decoder_1_alu_write, R_out);
  assign and_2_out = {8{or_4_out[7]}} & cpu_mem_1_out_2;  // AND_Gate and_2, 8 bits wide
  _8_BUF u_8_buf_2 (.in_2(inst_decoder_1_out_26), .in_1(cpu_mem_1_out_2), .out_3(n8_buf_2_out_3));
  Inst_Decoder inst_decoder_1 (
    .Op_Code(inst_reg_1_out_24), .Op_2(inst_reg_1_out_25), .Op_3(inst_reg_1_out_26),
    .Op_4(inst_reg_1_out_27), .out_18(inst_decoder_1_out_18), .out_19(inst_decoder_1_out_19),
    .out_20(inst_decoder_1_out_20), .out_21(inst_decoder_1_out_21), .Source1(q1),
    .Source2(inst_decoder_1_source2), .iSource(inst_decoder_1_isource), .Dest(inst_decoder_1_dest),
    .ALU_Read(inst_decoder_1_alu_read), .ALU_Write(inst_decoder_1_alu_write), .Const(inst_decoder_1_const),
    .Inc(I), .Dec(D), .Neg(N), .out_22(inst_decoder_1_out_22), .out_23(inst_decoder_1_out_23),
    .out_24(inst_decoder_1_out_24), .out_25(inst_decoder_1_out_25), .out_26(inst_decoder_1_out_26),
    .out_27(inst_decoder_1_out_27), .out_28(inst_decoder_1_out_28), .out_29(inst_decoder_1_out_29),
    .out_30(inst_decoder_1_out_30), .out_31(inst_decoder_1_out_31));  // open: Read, Write, Disp
  // Probe on or_9_out
  _4_BUF u_4_buf_1 (.in_2(or_7_out), .in_1(inst_decoder_1_dest), .out_3(n4_buf_1_out_3));
  or or_7 (or_7_out, inst_decoder_1_out_24, inst_decoder_1_out_30, inst_decoder_1_out_23);
  assign or_8_out = inst_decoder_1_const | cpu_mem_1_out_2 | cpu_mem_1_out_1 | alu_1_out_9 | input_module_1_out_5;  // OR_Gate or_8, 8 bits wide
  xor xor_1 (xor_1_out, inst_decoder_1_alu_write, inst_decoder_1_out_25);
  assign or_9_out = inst_decoder_1_source2 | condition_checker_1_out_11 | q2;  // OR_Gate or_9, 4 bits wide
  _4_BUF u_4_buf_2 (.in_2(X1), .in_1(or_9_out), .out_3(n4_buf_2_out_3));
  // Probe on n4_buf_3_out_3
  Condition_Decoder condition_decoder_1 (
    .in_1(inst_decoder_1_out_18), .in_2(inst_decoder_1_out_19), .in_3(inst_decoder_1_out_20),
    .in_4(inst_decoder_1_out_21), .in_5(inst_reg_1_out_28), .in_6(inst_reg_1_out_29),
    .Comp(condition_decoder_1_comp), .Constant(condition_decoder_1_constant), .Mem(condition_decoder_1_mem),
    .Jump_if_true(condition_decoder_1_jump_if_true), .out_11(c1), .out_12(c2),
    .out_13(condition_decoder_1_out_13), .out_14(condition_decoder_1_out_14));
  _8_BUF u_8_buf_3 (.in_2(or_14_out), .in_1(cpu_mem_1_out_2), .out_3(n8_buf_3_out_3));
  assign or_10_out = q1 | condition_checker_1_out_10;  // OR_Gate or_10, 4 bits wide
  _4_BUF u_4_buf_3 (.in_2(X0), .in_1(or_10_out), .out_3(n4_buf_3_out_3));
  CPU_Mem cpu_mem_1 (
    .RES_All(R_out), .Read_1(n4_buf_3_out_3), .Write(n4_buf_1_out_3), .Out_1(cpu_mem_1_out_1),
    .in_6(n8_buf_5_out_3), .RES(n4_buf_4_out_3), .Read_2(n4_buf_2_out_3), .Out_2(cpu_mem_1_out_2));
  or or_11 (or_11_out, inst_decoder_1_out_24, inst_decoder_1_out_23, inst_decoder_1_out_30);
  Condition_Checker condition_checker_1 (
    .in_1(condition_decoder_1_comp), .in_6(condition_decoder_1_constant), .in_7(condition_decoder_1_mem),
    .out_12(condition_checker_1_out_12), .in_2(c1), .in_3(c2), .in_4(condition_decoder_1_out_13),
    .in_5(condition_decoder_1_out_14), .out_10(condition_checker_1_out_10),
    .out_11(condition_checker_1_out_11), .in_8(n8_buf_3_out_3), .in_9(n8_buf_4_out_3));
  _8_BUF u_8_buf_4 (.in_2(or_14_out), .in_1(cpu_mem_1_out_1), .out_3(n8_buf_4_out_3));
  or or_12 (XB, inst_decoder_1_out_31, inst_decoder_1_out_26, inst_decoder_1_out_24);
  or or_13 (XA, inst_decoder_1_out_24, inst_decoder_1_out_31, inst_decoder_1_out_26);
  _4_BUF u_4_buf_4 (.in_2(xor_1_out), .in_1(inst_decoder_1_dest), .out_3(n4_buf_4_out_3));
  _8_BUF u_8_buf_5 (.in_2(or_11_out), .in_1(or_8_out), .out_3(n8_buf_5_out_3));
  or or_14 (or_14_out, condition_decoder_1_out_13, condition_decoder_1_out_14, c1, c2);
  xor xor_2 (xor_2_out, XB, inst_decoder_1_alu_read);
  xor xor_3 (xor_3_out, XA, inst_decoder_1_alu_read);
  or or_15 (or_15_out[3], I, D, N);
  assign q2 = {4{or_15_out[3]}} & q1;  // AND_Gate and_3, 4 bits wide
  or or_16 (X0, xor_3_out, inst_decoder_1_out_27, or_14_out, inst_decoder_1_out_28, inst_decoder_1_out_29);
  or or_17 (X1, xor_2_out, inst_decoder_1_out_27, or_14_out, inst_decoder_1_out_28, inst_decoder_1_out_29);
endmodule

module _1_FA (
  input  in_1,
  input  in_2,
  input  in_3,
  output out_4,
  output out_5
);

  wire and_1_out, and_2_out, xor_1_out;

  xor xor_1 (xor_1_out, in_1, in_2);
  xor xor_2 (out_4, xor_1_out, in_3);
  and and_1 (and_1_out, in_3, xor_1_out);
  and and_2 (and_2_out, in_1, in_2);
  or or_1 (out_5, and_1_out, and_2_out);
endmodule

module _8_FA (
  input  in_1,
  input  in_2,
  input  in_3,
  input  in_4,
  input  in_5,
  input  in_6,
  input  in_7,
  input  in_8,
  input  in_9,
  input  in_10,
  input  in_11,
  input  in_12,
  input  in_13,
  input  in_14,
  input  in_15,
  input  in_16,
  input  in_17,
  output out_18,
  output out_19,
  output out_20,
  output out_21,
  output out_22,
  output out_23,
  output out_24,
  output out_25,
  output out_26
);

  wire n1_fa_1_out_5, n1_fa_2_out_5, n1_fa_3_out_5, n1_fa_4_out_5, n1_fa_5_out_5, n1_fa_6_out_5,
       n1_fa_7_out_5;

  _1_FA u_1_fa_1 (.in_1(in_1), .in_2(in_9), .in_3(in_17), .out_4(out_18), .out_5(n1_fa_1_out_5));
  _1_FA u_1_fa_2 (.in_1(in_2), .in_2(in_10), .in_3(n1_fa_1_out_5), .out_4(out_19), .out_5(n1_fa_2_out_5));
  _1_FA u_1_fa_3 (.in_1(in_3), .in_2(in_11), .in_3(n1_fa_2_out_5), .out_4(out_20), .out_5(n1_fa_3_out_5));
  _1_FA u_1_fa_4 (.in_1(in_4), .in_2(in_12), .in_3(n1_fa_3_out_5), .out_4(out_21), .out_5(n1_fa_4_out_5));
  _1_FA u_1_fa_5 (.in_1(in_5), .in_2(in_13), .in_3(n1_fa_4_out_5), .out_4(out_22), .out_5(n1_fa_5_out_5));
  _1_FA u_1_fa_6 (.in_1(in_6), .in_2(in_14), .in_3(n1_fa_5_out_5), .out_4(out_23), .out_5(n1_fa_6_out_5));
  _1_FA u_1_fa_7 (.in_1(in_7), .in_2(in_15), .in_3(n1_fa_6_out_5), .out_4(out_24), .out_5(n1_fa_7_out_5));
  _1_FA u_1_fa_8 (.in_1(in_8), .in_2(in_16), .in_3(n1_fa_7_out_5), .out_4(out_25), .out_5(out_26));
endmodule

module _1_HA (
  input  in_1,
  input  in_2,
  output out_3,
  output out_4
);

  xor xor_1 (out_3, in_1, in_2);
  and and_1 (out_4, in_2, in_1);
endmodule

module _8_MUX (
  input  in_1,
  input  in_2,
  input  in_3,
  input  in_4,
  input  in_5,
  input  in_6,
  input  in_7,
  input  in_8,
  input  in_9,
  input  in_10,
  input  in_11,
  input  in_12,
  input  in_13,
  input  in_14,
  input  in_15,
  input  in_16,
  input  in_17,
  output out_18,
  output out_19,
  output out_20,
  output out_21,
  output out_22,
  output out_23,
  output out_24,
  output out_25
);

  wire and_1_out, and_2_out, and_3_out, and_4_out, and_5_out, and_6_out, and_7_out, and_8_out, and_9_out,
       and_10_out, and_11_out, and_12_out, and_13_out, and_14_out, and_15_out, and_16_out, not_1_out,
       not_2_out, not_3_out, not_4_out, not_5_out, not_6_out, not_7_out, not_8_out, not_9_out;

  not not_1 (not_1_out, in_1);
  not not_2 (not_2_out, not_1_out);
  not not_3 (not_3_out, not_1_out);
  not not_4 (not_4_out, not_1_out);
  not not_5 (not_5_out, not_1_out);
  not not_6 (not_6_out, not_1_out);
  not not_7 (not_7_out, not_1_out);
  not not_8 (not_8_out, not_1_out);
  not not_9 (not_9_out, not_1_out);
  and and_1 (and_1_out, not_2_out, in_2);
  and and_2 (and_2_out, not_1_out, in_10);
  and and_3 (and_3_out, not_3_out, in_3);
  and and_4 (and_4_out, not_1_out, in_11);
  and and_5 (and_5_out, not_4_out, in_4);
  and and_6 (and_6_out, not_1_out, in_12);
  and and_7 (and_7_out, not_5_out, in_5);
  and and_8 (and_8_out, not_1_out, in_13);
  and and_9 (and_9_out, not_6_out, in_6);
  and and_10 (and_10_out, not_1_out, in_14);
  and and_11 (and_11_out, not_7_out, in_7);
  and and_12 (and_12_out, not_1_out, in_15);
  and and_13 (and_13_out, not_8_out, in_8);
  and and_14 (and_14_out, not_1_out, in_16);
  and and_15 (and_15_out, not_9_out, in_9);
  and and_16 (and_16_out, not_1_out, in_17);
  or or_1 (out_18, and_1_out, and_2_out);
  or or_2 (out_19, and_3_out, and_4_out);
  or or_3 (out_20, and_5_out, and_6_out);
  or or_4 (out_21, and_7_out, and_8_out);
  or or_5 (out_22, and_9_out, and_10_out);
  or or_6 (out_23, and_11_out, and_12_out);
  or or_7 (out_24, and_13_out, and_14_out);
  or or_8 (out_25, and_15_out, and_16_out);
endmodule

module NEG_NOT (
  input  in_1,
  input  in_2,
  input  in_3,
  input  in_4,
  input  in_5,
  input  in_6,
  input  in_7,
  input  in_8,
  input  in_9,
  input  in_10,
  output out_11,
  output out_12,
  output out_13,
  output out_14,
  output out_15,
  output out_16,
  output out_17,
  output out_18
);

  wire and_1_out, n1_ha_1_out_4, n1_ha_2_out_4, n1_ha_3_out_4, n1_ha_4_out_4, n1_ha_5_out_4, n1_ha_6_out_4,
       n1_ha_7_out_4, not_1_out, xor_1_out, xor_2_out, xor_3_out, xor_4_out, xor_5_out, xor_6_out, xor_7_out,
       xor_8_out;

  not not_1 (not_1_out, in_1);
  and and_1 (and_1_out, not_1_out, in_2);
  xor xor_1 (xor_1_out, in_2, in_3);
  xor xor_2 (xor_2_out, in_2, in_4);
  xor xor_3 (xor_3_out, in_2, in_5);
  xor xor_4 (xor_4_out, in_2, in_6);
  xor xor_5 (xor_5_out, in_2, in_7);
  xor xor_6 (xor_6_out, in_2, in_8);
  xor xor_7 (xor_7_out, in_2, in_9);
  xor xor_8 (xor_8_out, in_2, in_10);
  _1_HA u_1_ha_1 (.out_3(out_11), .out_4(n1_ha_1_out_4), .in_1(and_1_out), .in_2(xor_1_out));
  _1_HA u_1_ha_2 (.out_3(out_12), .out_4(n1_ha_2_out_4), .in_1(n1_ha_1_out_4), .in_2(xor_2_out));
  _1_HA u_1_ha_3 (.out_3(out_13), .out_4(n1_ha_3_out_4), .in_1(n1_ha_2_out_4), .in_2(xor_3_out));
  _1_HA u_1_ha_4 (.out_3(out_14), .out_4(n1_ha_4_out_4), .in_1(n1_ha_3_out_4), .in_2(xor_4_out));
  _1_HA u_1_ha_5 (.out_3(out_15), .out_4(n1_ha_5_out_4), .in_1(n1_ha_4_out_4), .in_2(xor_5_out));
  _1_HA u_1_ha_6 (.out_3(out_16), .out_4(n1_ha_6_out_4), .in_1(n1_ha_5_out_4), .in_2(xor_6_out));
  _1_HA u_1_ha_7 (.out_3(out_17), .out_4(n1_ha_7_out_4), .in_1(n1_ha_6_out_4), .in_2(xor_7_out));
  _1_HA u_1_ha_8 (.out_3(out_18), .in_1(n1_ha_7_out_4), .in_2(xor_8_out));  // open: out_4
endmodule

module RS_NOR (
  input  in_1,
  input  in_2,
  output out_3,
  output out_4
);

  nor nor_1 (out_3, in_1, out_4);
  nor nor_2 (out_4, out_3, in_2);
endmodule

module _8_RAM (
  input  in_1,
  input  in_2,
  input  in_3,
  input  in_4,
  input  in_5,
  input  in_6,
  input  in_7,
  input  in_8,
  input  in_9,
  output out_10,
  output out_11,
  output out_12,
  output out_13,
  output out_14,
  output out_15,
  output out_16,
  output out_17
);

  RS_NOR rs_nor_1 (.in_1(in_2), .in_2(in_1), .out_4(out_10));  // open: out_3
  RS_NOR rs_nor_2 (.in_1(in_3), .in_2(in_1), .out_4(out_11));  // open: out_3
  RS_NOR rs_nor_3 (.in_1(in_4), .in_2(in_1), .out_4(out_12));  // open: out_3
  RS_NOR rs_nor_4 (.in_1(in_5), .in_2(in_1), .out_4(out_13));  // open: out_3
  RS_NOR rs_nor_5 (.in_1(in_6), .in_2(in_1), .out_4(out_14));  // open: out_3
  RS_NOR rs_nor_6 (.in_1(in_7), .in_2(in_1), .out_4(out_15));  // open: out_3
  RS_NOR rs_nor_7 (.in_1(in_8), .in_2(in_1), .out_4(out_16));  // open: out_3
  RS_NOR rs_nor_8 (.in_1(in_9), .in_2(in_1), .out_4(out_17));  // open: out_3
endmodule

module _8_1_Decoder (
  input  in_1,
  input  in_2,
  input  in_3,
  input  in_4,
  input  in_5,
  input  in_6,
  input  in_7,
  input  in_8,
  output out_9,
  output out_10,
  output out_11
);

  wire not_1_out, not_2_out, not_3_out, not_4_out, not_5_out, not_6_out, not_7_out, not_8_out, not_9_out,
       not_10_out, not_11_out;

  not not_1 (not_1_out, in_1);
  not not_2 (not_2_out, out_10);
  not not_3 (not_3_out, out_11);
  and and_1 (out_9, not_2_out, not_3_out);
  not not_4 (not_4_out, in_3);
  not not_5 (not_5_out, in_4);
  not not_6 (not_6_out, in_5);
  not not_7 (not_7_out, in_2);
  and and_2 (out_10, not_1_out, not_7_out, not_4_out, not_5_out, not_6_out, not_8_out, not_10_out, not_9_out);
  not not_8 (not_8_out, in_6);
  not not_9 (not_9_out, in_8);
  not not_10 (not_10_out, in_7);
  not not_11 (not_11_out, not_9_out);
  and and_3 (out_11, not_1_out, not_7_out, not_4_out, not_5_out, not_6_out, not_8_out, not_10_out, not_11_out);
endmodule

module _8_RAM_CLK (
  input  in_1,
  input  in_2,
  input  in_3,
  input  in_4,
  input  in_5,
  input  in_6,
  input  in_7,
  input  in_8,
  input  in_9,
  input  in_10,
  input  in_11,
  output out_12,
  output out_13,
  output out_14,
  output out_15,
  output out_16,
  output out_17,
  output out_18,
  output out_19
);

  wire j_k_ff_1_q, j_k_ff_2_q, j_k_ff_3_q, j_k_ff_4_q, j_k_ff_5_q, j_k_ff_6_q, j_k_ff_7_q, j_k_ff_8_q;

  J_K_Flip_Flop j_k_ff_1 (
    .J(in_2), .clk(in_10), .K(1'b0), .Q(j_k_ff_1_q), .en(1'b1), .reset(in_1));  // open: Qn, preset
  J_K_Flip_Flop j_k_ff_2 (
    .J(in_3), .clk(in_10), .K(1'b0), .Q(j_k_ff_2_q), .en(1'b1), .reset(in_1));  // open: Qn, preset
  J_K_Flip_Flop j_k_ff_3 (
    .J(in_4), .clk(in_10), .K(1'b0), .Q(j_k_ff_3_q), .en(1'b1), .reset(in_1));  // open: Qn, preset
  J_K_Flip_Flop j_k_ff_4 (
    .J(in_5), .clk(in_10), .K(1'b0), .Q(j_k_ff_4_q), .en(1'b1), .reset(in_1));  // open: Qn, preset
  J_K_Flip_Flop j_k_ff_5 (
    .J(in_6), .clk(in_10), .K(1'b0), .Q(j_k_ff_5_q), .en(1'b1), .reset(in_1));  // open: Qn, preset
  J_K_Flip_Flop j_k_ff_6 (
    .J(in_7), .clk(in_10), .K(1'b0), .Q(j_k_ff_6_q), .en(1'b1), .reset(in_1));  // open: Qn, preset
  J_K_Flip_Flop j_k_ff_7 (
    .J(in_8), .clk(in_10), .K(1'b0), .Q(j_k_ff_7_q), .en(1'b1), .reset(in_1));  // open: Qn, preset
  J_K_Flip_Flop j_k_ff_8 (
    .J(in_9), .clk(in_10), .K(1'b0), .Q(j_k_ff_8_q), .en(1'b1), .reset(in_1));  // open: Qn, preset
  and and_1 (out_12, in_11, j_k_ff_1_q);
  and and_2 (out_13, in_11, j_k_ff_2_q);
  and and_3 (out_14, in_11, j_k_ff_3_q);
  and and_4 (out_15, in_11, j_k_ff_4_q);
  and and_5 (out_16, in_11, j_k_ff_5_q);
  and and_6 (out_17, in_11, j_k_ff_6_q);
  and and_7 (out_18, in_11, j_k_ff_7_q);
  and and_8 (out_19, in_11, j_k_ff_8_q);
endmodule

module _4_Counter (
  input  in_1,
  input  in_2,
  output out_3,
  output out_4,
  output out_5,
  output out_6
);

  wire and_1_out, and_2_out;

  J_K_Flip_Flop j_k_ff_1 (.J(in_1), .clk(in_2), .K(in_1), .Q(out_3));  // open: Qn, preset, en, reset
  J_K_Flip_Flop j_k_ff_2 (.J(out_3), .clk(in_2), .K(out_3), .Q(out_4));  // open: Qn, preset, en, reset
  and and_1 (and_1_out, out_3, out_4);
  J_K_Flip_Flop j_k_ff_3 (.J(and_1_out), .clk(in_2), .K(and_1_out), .Q(out_5));  // open: Qn, preset, en, reset
  and and_2 (and_2_out, out_4, out_3, out_5);
  J_K_Flip_Flop j_k_ff_4 (.J(and_2_out), .clk(in_2), .K(and_2_out), .Q(out_6));  // open: Qn, preset, en, reset
endmodule

module _4_Bin_Hex (
  input  in_1,
  input  in_2,
  input  in_3,
  input  in_4,
  input  in_5,
  output out_6,
  output out_7,
  output out_8,
  output out_9,
  output out_10,
  output out_11,
  output out_12,
  output out_13,
  output out_14,
  output out_15,
  output out_16,
  output out_17,
  output out_18,
  output out_19,
  output out_20,
  output out_21
);

  wire and_1_out, and_2_out, and_5_out, and_8_out, and_9_out, and_11_out, and_12_out, and_15_out, and_17_out,
       and_18_out, and_21_out, and_24_out, and_25_out, and_27_out, and_28_out, and_31_out, buffer_1_out,
       buffer_2_out, buffer_3_out, buffer_4_out, buffer_5_out, buffer_6_out, buffer_7_out, buffer_8_out,
       buffer_9_out, buffer_10_out, buffer_11_out, buffer_12_out, buffer_13_out, buffer_14_out,
       buffer_15_out, buffer_16_out, buffer_17_out, buffer_18_out, buffer_19_out, buffer_20_out,
       buffer_21_out, buffer_22_out, buffer_23_out, buffer_24_out, buffer_25_out, buffer_26_out,
       buffer_27_out, buffer_28_out, buffer_29_out, buffer_30_out, buffer_31_out, buffer_32_out,
       buffer_33_out, buffer_34_out, buffer_35_out, buffer_36_out, buffer_37_out, buffer_38_out,
       buffer_39_out, buffer_40_out, buffer_41_out, buffer_42_out, buffer_43_out, buffer_44_out,
       buffer_45_out, buffer_46_out, buffer_47_out, buffer_48_out, buffer_49_out, buffer_50_out,
       buffer_51_out, buffer_52_out, buffer_53_out, buffer_54_out, buffer_55_out, buffer_56_out,
       buffer_57_out, buffer_58_out, buffer_59_out, buffer_60_out, buffer_61_out, buffer_62_out,
       buffer_63_out, buffer_64_out, buffer_65_out, buffer_66_out, not_1_out, not_2_out, not_3_out,
       not_4_out, not_5_out, not_6_out, not_7_out, not_8_out, not_9_out, not_10_out, not_11_out, not_12_out,
       not_13_out, not_14_out, not_15_out, not_16_out, not_17_out, not_18_out, not_19_out, not_20_out,
       not_21_out, not_22_out, not_23_out, not_24_out, not_25_out, not_26_out, not_27_out, not_28_out,
       not_29_out, not_30_out, not_31_out, not_32_out;

  buf buffer_1 (buffer_1_out, in_1);
  buf buffer_2 (buffer_2_out, buffer_1_out);
  buf buffer_3 (buffer_3_out, not_2_out);
  not not_1 (not_1_out, in_5);
  not not_2 (not_2_out, in_2);
  not not_3 (not_3_out, in_4);
  not not_4 (not_4_out, in_4);
  not not_5 (not_5_out, in_3);
  not not_6 (not_6_out, in_3);
  buf buffer_4 (buffer_4_out, not_5_out);
  buf buffer_5 (buffer_5_out, in_2);
  buf buffer_6 (buffer_6_out, not_6_out);
  buf buffer_7 (buffer_7_out, not_4_out);
  buf buffer_8 (buffer_8_out, not_1_out);
  buf buffer_9 (buffer_9_out, not_3_out);
  and and_1 (and_1_out, buffer_5_out, buffer_6_out, buffer_7_out, buffer_15_out);
  and and_2 (and_2_out, buffer_3_out, buffer_4_out, buffer_9_out, buffer_8_out);
  and and_3 (out_7, buffer_2_out, and_1_out);
  and and_4 (out_6, buffer_2_out, and_2_out);
  not not_7 (not_7_out, in_5);
  not not_8 (not_8_out, in_4);
  not not_9 (not_9_out, in_2);
  not not_10 (not_10_out, in_5);
  buf buffer_10 (buffer_10_out, not_8_out);
  buf buffer_11 (buffer_11_out, in_2);
  buf buffer_12 (buffer_12_out, in_3);
  buf buffer_13 (buffer_13_out, not_9_out);
  buf buffer_14 (buffer_14_out, not_10_out);
  buf buffer_15 (buffer_15_out, not_7_out);
  buf buffer_16 (buffer_16_out, in_3);
  and and_5 (and_5_out, buffer_13_out, buffer_12_out, buffer_10_out, buffer_14_out);
  and and_6 (out_9, buffer_2_out, and_9_out);
  and and_7 (out_8, buffer_2_out, and_5_out);
  not not_11 (not_11_out, in_4);
  not not_12 (not_12_out, in_3);
  not not_13 (not_13_out, in_2);
  not not_14 (not_14_out, in_5);
  not not_15 (not_15_out, in_5);
  buf buffer_17 (buffer_17_out, not_11_out);
  buf buffer_18 (buffer_18_out, not_14_out);
  buf buffer_19 (buffer_19_out, not_13_out);
  buf buffer_20 (buffer_20_out, not_12_out);
  buf buffer_21 (buffer_21_out, in_4);
  buf buffer_22 (buffer_22_out, not_15_out);
  and and_8 (and_8_out, buffer_19_out, buffer_20_out, buffer_21_out, buffer_18_out);
  and and_9 (and_9_out, buffer_11_out, buffer_16_out, buffer_17_out, buffer_22_out);
  and and_10 (out_10, buffer_2_out, and_8_out);
  not not_16 (not_16_out, in_5);
  not not_17 (not_17_out, in_3);
  not not_18 (not_18_out, in_2);
  buf buffer_23 (buffer_23_out, in_2);
  buf buffer_24 (buffer_24_out, not_18_out);
  buf buffer_25 (buffer_25_out, in_3);
  buf buffer_26 (buffer_26_out, in_4);
  buf buffer_27 (buffer_27_out, not_16_out);
  buf buffer_28 (buffer_28_out, not_17_out);
  and and_11 (and_11_out, buffer_23_out, buffer_28_out, buffer_26_out, buffer_27_out);
  and and_12 (and_12_out, buffer_24_out, buffer_25_out, buffer_32_out, buffer_33_out);
  and and_13 (out_12, buffer_2_out, and_12_out);
  and and_14 (out_11, buffer_2_out, and_11_out);
  not not_19 (not_19_out, in_5);
  not not_20 (not_20_out, in_5);
  buf buffer_29 (buffer_29_out, in_2);
  buf buffer_30 (buffer_30_out, not_19_out);
  buf buffer_31 (buffer_31_out, in_3);
  buf buffer_32 (buffer_32_out, in_4);
  buf buffer_33 (buffer_33_out, not_20_out);
  buf buffer_34 (buffer_34_out, in_4);
  buf buffer_35 (buffer_35_out, not_22_out);
  and and_15 (and_15_out, buffer_29_out, buffer_31_out, buffer_34_out, buffer_30_out);
  and and_16 (out_13, buffer_2_out, and_15_out);
  not not_21 (not_21_out, in_3);
  not not_22 (not_22_out, in_2);
  not not_23 (not_23_out, in_3);
  not not_24 (not_24_out, in_4);
  not not_25 (not_25_out, in_4);
  buf buffer_36 (buffer_36_out, not_24_out);
  buf buffer_37 (buffer_37_out, not_23_out);
  buf buffer_38 (buffer_38_out, not_21_out);
  buf buffer_39 (buffer_39_out, in_2);
  buf buffer_40 (buffer_40_out, in_5);
  buf buffer_41 (buffer_41_out, not_25_out);
  and and_17 (and_17_out, buffer_39_out, buffer_37_out, buffer_36_out, buffer_45_out);
  and and_18 (and_18_out, buffer_35_out, buffer_38_out, buffer_41_out, buffer_40_out);
  and and_19 (out_14, buffer_2_out, and_18_out);
  and and_20 (out_15, buffer_2_out, and_17_out);
  not not_26 (not_26_out, in_2);
  not not_27 (not_27_out, in_4);
  buf buffer_42 (buffer_42_out, in_2);
  buf buffer_43 (buffer_43_out, not_27_out);
  buf buffer_44 (buffer_44_out, in_3);
  buf buffer_45 (buffer_45_out, in_5);
  buf buffer_46 (buffer_46_out, in_3);
  buf buffer_47 (buffer_47_out, not_26_out);
  buf buffer_48 (buffer_48_out, in_5);
  and and_21 (and_21_out, buffer_47_out, buffer_44_out, buffer_43_out, buffer_48_out);
  and and_22 (out_17, buffer_2_out, and_25_out);
  and and_23 (out_16, buffer_2_out, and_21_out);
  not not_28 (not_28_out, in_2);
  not not_29 (not_29_out, in_4);
  not not_30 (not_30_out, in_3);
  buf buffer_49 (buffer_49_out, not_29_out);
  buf buffer_50 (buffer_50_out, not_30_out);
  buf buffer_51 (buffer_51_out, in_5);
  buf buffer_52 (buffer_52_out, in_5);
  buf buffer_53 (buffer_53_out, not_28_out);
  buf buffer_54 (buffer_54_out, in_4);
  and and_24 (and_24_out, buffer_53_out, buffer_50_out, buffer_54_out, buffer_51_out);
  and and_25 (and_25_out, buffer_42_out, buffer_46_out, buffer_49_out, buffer_52_out);
  and and_26 (out_18, buffer_2_out, and_24_out);
  not not_31 (not_31_out, in_2);
  not not_32 (not_32_out, in_3);
  buf buffer_55 (buffer_55_out, in_5);
  buf buffer_56 (buffer_56_out, in_4);
  buf buffer_57 (buffer_57_out, not_31_out);
  buf buffer_58 (buffer_58_out, in_2);
  buf buffer_59 (buffer_59_out, in_3);
  buf buffer_60 (buffer_60_out, not_32_out);
  and and_27 (and_27_out, buffer_58_out, buffer_60_out, buffer_56_out, buffer_55_out);
  and and_28 (and_28_out, buffer_57_out, buffer_59_out, buffer_66_out, buffer_62_out);
  and and_29 (out_19, buffer_2_out, and_27_out);
  and and_30 (out_20, buffer_2_out, and_28_out);
  buf buffer_61 (buffer_61_out, in_3);
  buf buffer_62 (buffer_62_out, in_5);
  buf buffer_63 (buffer_63_out, in_2);
  buf buffer_64 (buffer_64_out, in_4);
  buf buffer_65 (buffer_65_out, in_5);
  buf buffer_66 (buffer_66_out, in_4);
  and and_31 (and_31_out, buffer_63_out, buffer_61_out, buffer_64_out, buffer_65_out);
  and and_32 (out_21, buffer_2_out, and_31_out);
endmodule

module _8_DEC (
  input  in_1,
  input  [7:0] in_2,
  output [7:0] out_3,
  output out_4
);

  wire and_1_out, and_2_out, and_3_out, and_4_out, and_5_out, and_6_out, and_7_out, not_1_out, not_2_out,
       not_3_out, not_4_out, not_5_out, not_6_out, not_7_out, not_8_out;

  not not_1 (not_1_out, in_2[0]);
  and and_1 (and_1_out, not_1_out, in_1);
  not not_2 (not_2_out, in_2[1]);
  and and_2 (and_2_out, not_2_out, and_1_out);
  not not_3 (not_3_out, in_2[2]);
  and and_3 (and_3_out, not_3_out, and_2_out);
  not not_4 (not_4_out, in_2[3]);
  and and_4 (and_4_out, not_4_out, and_3_out);
  not not_5 (not_5_out, in_2[4]);
  and and_5 (and_5_out, not_5_out, and_4_out);
  not not_6 (not_6_out, in_2[5]);
  and and_6 (and_6_out, not_6_out, and_5_out);
  not not_7 (not_7_out, in_2[6]);
  and and_7 (and_7_out, not_7_out, and_6_out);
  not not_8 (not_8_out, in_2[7]);
  and and_8 (out_4, not_8_out, and_7_out);
  xor xor_1 (out_3[0], in_2[0], in_1);
  xor xor_2 (out_3[1], in_2[1], and_1_out);
  xor xor_3 (out_3[2], in_2[2], and_2_out);
  xor xor_4 (out_3[3], in_2[3], and_3_out);
  xor xor_5 (out_3[4], in_2[4], and_4_out);
  xor xor_6 (out_3[5], in_2[5], and_5_out);
  xor xor_7 (out_3[6], in_2[6], and_6_out);
  xor xor_8 (out_3[7], in_2[7], and_7_out);
endmodule

module _4_INC (
  input  in_1,
  input  in_2,
  input  in_3,
  input  in_4,
  input  in_5,
  input  in_6,
  input  in_7,
  input  in_8,
  input  in_9,
  output out_10,
  output out_11,
  output out_12,
  output out_13,
  output out_14,
  output out_15,
  output out_16,
  output out_17,
  output out_18
);

  wire n1_ha_1_out_4, n1_ha_2_out_4, n1_ha_3_out_4, n1_ha_4_out_4, n1_ha_5_out_4, n1_ha_6_out_4,
       n1_ha_7_out_4;

  _1_HA u_1_ha_1 (.out_3(out_10), .out_4(n1_ha_1_out_4), .in_1(in_1), .in_2(in_2));
  _1_HA u_1_ha_2 (.out_3(out_11), .out_4(n1_ha_2_out_4), .in_1(n1_ha_1_out_4), .in_2(in_3));
  _1_HA u_1_ha_3 (.out_3(out_12), .out_4(n1_ha_3_out_4), .in_1(n1_ha_2_out_4), .in_2(in_4));
  _1_HA u_1_ha_4 (.out_3(out_13), .out_4(n1_ha_4_out_4), .in_1(n1_ha_3_out_4), .in_2(in_5));
  _1_HA u_1_ha_5 (.out_3(out_14), .out_4(n1_ha_5_out_4), .in_1(n1_ha_4_out_4), .in_2(in_6));
  _1_HA u_1_ha_6 (.out_3(out_15), .out_4(n1_ha_6_out_4), .in_1(n1_ha_5_out_4), .in_2(in_7));
  _1_HA u_1_ha_7 (.out_3(out_16), .out_4(n1_ha_7_out_4), .in_1(n1_ha_6_out_4), .in_2(in_8));
  _1_HA u_1_ha_8 (.out_3(out_17), .out_4(out_18), .in_1(n1_ha_7_out_4), .in_2(in_9));
endmodule

module _4_REG (
  input  in_1,
  input  in_2,
  input  in_3,
  input  in_4,
  input  in_5,
  input  in_6,
  input  in_7,
  output out_8,
  output out_9,
  output out_10,
  output out_11
);

  J_K_Flip_Flop j_k_ff_1 (.J(in_1), .clk(in_6), .K(1'b0), .Q(out_8), .en(in_5), .reset(in_7));  // open: Qn, preset
  J_K_Flip_Flop j_k_ff_2 (.J(in_2), .clk(in_6), .K(1'b0), .Q(out_9), .en(in_5), .reset(in_7));  // open: Qn, preset
  J_K_Flip_Flop j_k_ff_3 (.J(in_3), .clk(in_6), .K(1'b0), .Q(out_10), .en(in_5), .reset(in_7));  // open: Qn, preset
  J_K_Flip_Flop j_k_ff_4 (.J(in_4), .clk(in_6), .K(1'b0), .Q(out_11), .en(in_5), .reset(in_7));  // open: Qn, preset
endmodule

module _4_MUX (
  input  in_1,
  input  in_2,
  input  in_3,
  input  in_4,
  input  in_5,
  input  in_6,
  input  in_7,
  input  in_8,
  input  in_9,
  output out_10,
  output out_11,
  output out_12,
  output out_13
);

  wire and_1_out, and_2_out, and_3_out, and_4_out, and_5_out, and_6_out, and_7_out, and_8_out, not_1_out,
       not_2_out, not_3_out, not_4_out, not_5_out;

  not not_1 (not_1_out, in_1);
  not not_2 (not_2_out, not_1_out);
  not not_3 (not_3_out, not_1_out);
  not not_4 (not_4_out, not_1_out);
  not not_5 (not_5_out, not_1_out);
  and and_1 (and_1_out, not_2_out, in_2);
  and and_2 (and_2_out, not_1_out, in_6);
  and and_3 (and_3_out, not_3_out, in_3);
  and and_4 (and_4_out, not_1_out, in_7);
  and and_5 (and_5_out, not_4_out, in_4);
  and and_6 (and_6_out, not_1_out, in_8);
  and and_7 (and_7_out, not_5_out, in_5);
  and and_8 (and_8_out, not_1_out, in_9);
  or or_1 (out_10, and_1_out, and_2_out);
  or or_2 (out_11, and_3_out, and_4_out);
  or or_3 (out_12, and_5_out, and_6_out);
  or or_4 (out_13, and_7_out, and_8_out);
endmodule

module _4_BUF (
  input  [3:0] in_1,
  input  in_2,
  output [3:0] out_3
);

  and and_1 (out_3[2], in_2, in_1[2]);
  and and_2 (out_3[3], in_2, in_1[3]);
  and and_3 (out_3[0], in_1[0], in_2);
  and and_4 (out_3[1], in_1[1], in_2);
endmodule

module _5_Counter (
  input  in_1,
  input  in_2,
  input  in_3,
  input  in_4,
  input  in_5,
  input  in_6,
  input  in_7,
  input  in_8,
  output out_9,
  output out_10,
  output out_11,
  output out_12,
  output out_13
);

  wire and_1_out, and_2_out, and_3_out, n1_shortdelay_1_out_2, n1_shortdelay_2_out_2, n1_shortdelay_3_out_2,
       n1_shortdelay_4_out_2, n1_shortdelay_5_out_2, or_1_out, or_2_out;

  or or_1 (or_1_out, in_3, or_2_out);
  _1_ShortDelay u_1_shortdelay_1 (.in_1(in_4), .out_2(n1_shortdelay_1_out_2));
  J_K_Flip_Flop j_k_ff_1 (
    .J(in_1), .clk(in_2), .K(in_1), .Q(out_9), .preset(n1_shortdelay_1_out_2), .en(in_1), .reset(or_1_out));  // open: Qn
  J_K_Flip_Flop j_k_ff_2 (
    .J(out_9), .clk(in_2), .K(out_9), .Q(out_10), .preset(n1_shortdelay_2_out_2), .en(in_1), .reset(or_1_out));  // open: Qn
  _1_ShortDelay u_1_shortdelay_2 (.in_1(in_5), .out_2(n1_shortdelay_2_out_2));
  and and_1 (and_1_out, out_9, out_10);
  J_K_Flip_Flop j_k_ff_3 (
    .J(and_1_out), .clk(in_2), .K(and_1_out), .Q(out_11), .preset(n1_shortdelay_3_out_2), .en(in_1),
    .reset(or_1_out));  // open: Qn
  _1_ShortDelay u_1_shortdelay_3 (.in_1(in_6), .out_2(n1_shortdelay_3_out_2));
  and and_2 (and_2_out, out_10, out_9, out_11);
  J_K_Flip_Flop j_k_ff_4 (
    .J(and_2_out), .clk(in_2), .K(and_2_out), .Q(out_12), .preset(n1_shortdelay_4_out_2), .en(in_1),
    .reset(or_1_out));  // open: Qn
  _1_ShortDelay u_1_shortdelay_4 (.in_1(in_7), .out_2(n1_shortdelay_4_out_2));
  and and_3 (and_3_out, out_12, out_11, out_10, out_9);
  J_K_Flip_Flop j_k_ff_5 (
    .J(and_3_out), .clk(in_2), .K(and_3_out), .Q(out_13), .preset(n1_shortdelay_5_out_2), .en(in_1),
    .reset(or_1_out));  // open: Qn
  _1_ShortDelay u_1_shortdelay_5 (.in_1(in_8), .out_2(n1_shortdelay_5_out_2));
  or or_2 (or_2_out, in_8, in_7, in_6, in_5, in_4);
endmodule

module Inst_Reg (
  input  in_1,
  input  [4:0] Prog_Count,
  input  in_3,
  input  R,
  input  [3:0] in_5,
  input  [3:0] in_6,
  input  [3:0] in_7,
  input  [3:0] in_8,
  input  [3:0] in_9,
  input  [3:0] in_10,
  input  in_11,
  input  S,
  input  in_13,
  output out_14,
  output out_15,
  output out_16,
  output out_17,
  output out_18,
  output out_19,
  output out_20,
  output out_21,
  output out_22,
  output out_23,
  output [3:0] out_24,
  output [3:0] out_25,
  output [3:0] out_26,
  output [3:0] out_27,
  output [3:0] out_28,
  output [3:0] out_29
);

  wire and_1_out, and_2_out, buffer_1_out, n1_delay_1_out_2, n1_shortdelay_1_out_2, not_1_out, or_1_out,
       s_r_ff_1_qn;
  wire [4:0] n5_buf_1_out_3;
  wire [23:0] n5_bin_dec2_1_out_8, n5_bin_dec2_2_out_7, n24_buf_1_out_3;

  buf buffer_1 (buffer_1_out, in_1);
  and and_1 (and_1_out, in_1, s_r_ff_1_qn, in_13);
  not not_1 (not_1_out, n1_delay_1_out_2);
  S_R_Flip_Flop s_r_ff_1 (
    .S(1'b0), .clk(buffer_1_out), .R(in_1), .Qn(s_r_ff_1_qn), .preset(or_1_out), .en(1'b1));  // open: Q, reset
  _1_ShortDelay u_1_shortdelay_1 (.in_1(and_1_out), .out_2(n1_shortdelay_1_out_2));
  and and_2 (and_2_out, in_1, not_1_out, in_13);
  _1_Delay u_1_delay_1 (.in_1(in_1), .out_2(n1_delay_1_out_2));
  _1_ShortDelay u_1_shortdelay_2 ();  // open: in_1, out_2
  or or_1 (or_1_out, Prog_Count[0], Prog_Count[1], Prog_Count[2], Prog_Count[3], Prog_Count[4]);
  _5_Counter u_5_counter_1 (
    .in_1(in_13), .in_2(and_2_out), .out_9(out_19), .out_10(out_20), .out_11(out_21), .out_12(out_22),
    .out_13(out_23), .in_3(R), .in_4(n5_buf_1_out_3[0]), .in_5(n5_buf_1_out_3[1]), .in_6(n5_buf_1_out_3[2]),
    .in_7(n5_buf_1_out_3[3]), .in_8(n5_buf_1_out_3[4]));
  _5_BUF u_5_buf_1 (.in_2(in_3), .in_1(Prog_Count), .out_3(n5_buf_1_out_3));
  _5_Bin_Dec2 u_5_bin_dec2_1 (
    .in_2(out_19), .in_3(out_20), .in_4(out_21), .in_5(out_22), .in_6(out_23),
    .out_8(n5_bin_dec2_1_out_8[0]), .out_9(n5_bin_dec2_1_out_8[1]), .out_10(n5_bin_dec2_1_out_8[2]),
    .out_11(n5_bin_dec2_1_out_8[3]), .out_12(n5_bin_dec2_1_out_8[4]), .out_13(n5_bin_dec2_1_out_8[5]),
    .out_14(n5_bin_dec2_1_out_8[6]), .out_15(n5_bin_dec2_1_out_8[7]), .out_16(n5_bin_dec2_1_out_8[8]),
    .out_17(n5_bin_dec2_1_out_8[9]), .out_18(n5_bin_dec2_1_out_8[10]), .out_19(n5_bin_dec2_1_out_8[11]),
    .out_20(n5_bin_dec2_1_out_8[12]), .out_21(n5_bin_dec2_1_out_8[13]), .out_22(n5_bin_dec2_1_out_8[14]),
    .out_23(n5_bin_dec2_1_out_8[15]), .out_24(n5_bin_dec2_1_out_8[16]), .out_25(n5_bin_dec2_1_out_8[17]),
    .out_26(n5_bin_dec2_1_out_8[18]), .out_27(n5_bin_dec2_1_out_8[19]), .out_28(n5_bin_dec2_1_out_8[20]),
    .out_29(n5_bin_dec2_1_out_8[21]), .out_30(n5_bin_dec2_1_out_8[22]), .out_31(n5_bin_dec2_1_out_8[23]),
    .in_1(n1_shortdelay_1_out_2));  // open: out_7, out_32, out_33, out_34, out_35, out_36, out_37, out_38
  _5_Counter u_5_counter_2 (
    .in_1(1'b1), .in_2(in_11), .out_9(out_18), .out_10(out_17), .out_11(out_16), .out_12(out_15),
    .out_13(out_14), .in_3(R));  // open: in_4, in_5, in_6, in_7, in_8
  _5_Bin_Dec2 u_5_bin_dec2_2 (
    .in_2(out_18), .in_3(out_17), .in_4(out_16), .in_5(out_15), .in_6(out_14),
    .out_7(n5_bin_dec2_2_out_7[0]), .out_8(n5_bin_dec2_2_out_7[1]), .out_9(n5_bin_dec2_2_out_7[2]),
    .out_10(n5_bin_dec2_2_out_7[3]), .out_11(n5_bin_dec2_2_out_7[4]), .out_12(n5_bin_dec2_2_out_7[5]),
    .out_13(n5_bin_dec2_2_out_7[6]), .out_14(n5_bin_dec2_2_out_7[7]), .out_15(n5_bin_dec2_2_out_7[8]),
    .out_16(n5_bin_dec2_2_out_7[9]), .out_17(n5_bin_dec2_2_out_7[10]), .out_18(n5_bin_dec2_2_out_7[11]),
    .out_19(n5_bin_dec2_2_out_7[12]), .out_20(n5_bin_dec2_2_out_7[13]), .out_21(n5_bin_dec2_2_out_7[14]),
    .out_22(n5_bin_dec2_2_out_7[15]), .out_23(n5_bin_dec2_2_out_7[16]), .out_24(n5_bin_dec2_2_out_7[17]),
    .out_25(n5_bin_dec2_2_out_7[18]), .out_26(n5_bin_dec2_2_out_7[19]), .out_27(n5_bin_dec2_2_out_7[20]),
    .out_28(n5_bin_dec2_2_out_7[21]), .out_29(n5_bin_dec2_2_out_7[22]), .out_30(n5_bin_dec2_2_out_7[23]),
    .in_1(1'b1));  // open: out_31, out_32, out_33, out_34, out_35, out_36, out_37, out_38
  _24_BUF u_24_buf_1 (.in_1(n5_bin_dec2_2_out_7), .in_2(S), .out_3(n24_buf_1_out_3));
  Prog_Mem prog_mem_1 (
    .Memory_Location(n24_buf_1_out_3), .Program_Counter(n5_bin_dec2_1_out_8),
    .out_7({out_29, out_28, out_27, out_26, out_25, out_24}), .in_3({in_10, in_9}), .in_4({in_8, in_7}),
    .in_5({in_6, in_5}), .in_6(R));
endmodule

module _5_Bin_Dec (
  input  in_1,
  input  in_2,
  input  in_3,
  input  in_4,
  input  in_5,
  input  in_6,
  output out_7,
  output out_8,
  output out_9,
  output out_10,
  output out_11,
  output out_12,
  output out_13,
  output out_14,
  output out_15,
  output out_16,
  output out_17,
  output out_18,
  output out_19,
  output out_20,
  output out_21,
  output out_22,
  output out_23,
  output out_24,
  output out_25,
  output out_26,
  output out_27,
  output out_28,
  output out_29,
  output out_30,
  output out_31,
  output out_32,
  output out_33,
  output out_34,
  output out_35,
  output out_36,
  output out_37,
  output out_38
);

  wire and_2_out, and_3_out, and_6_out, and_7_out, and_12_out, and_13_out, and_14_out, and_15_out,
       and_18_out, and_19_out, and_22_out, and_23_out, and_28_out, and_29_out, and_30_out, and_31_out,
       and_34_out, and_35_out, and_38_out, and_39_out, and_44_out, and_45_out, and_46_out, and_47_out,
       and_50_out, and_51_out, and_54_out, and_55_out, and_60_out, and_61_out, and_62_out, and_63_out,
       buffer_1_out, buffer_2_out, buffer_3_out, buffer_4_out, buffer_5_out, buffer_6_out, buffer_7_out,
       buffer_8_out, buffer_9_out, buffer_10_out, buffer_11_out, buffer_12_out, buffer_13_out, buffer_14_out,
       buffer_15_out, buffer_16_out, buffer_17_out, buffer_18_out, buffer_19_out, buffer_20_out,
       buffer_21_out, buffer_22_out, buffer_23_out, buffer_24_out, buffer_25_out, buffer_26_out,
       buffer_27_out, buffer_28_out, buffer_29_out, buffer_30_out, buffer_31_out, buffer_32_out, not_1_out,
       not_2_out, not_3_out, not_4_out, not_5_out, not_6_out, not_7_out, not_8_out, not_9_out, not_10_out,
       not_11_out, not_12_out, not_13_out, not_14_out, not_15_out, not_16_out, not_17_out, not_18_out,
       not_19_out, not_20_out, not_21_out, not_22_out, not_23_out, not_24_out, not_25_out, not_26_out,
       not_27_out, not_28_out, not_29_out, not_30_out, not_31_out, not_32_out, not_33_out, not_34_out,
       not_35_out, not_36_out, not_37_out, not_38_out, not_39_out, not_40_out, not_41_out, not_42_out,
       not_43_out, not_44_out, not_45_out, not_46_out, not_47_out, not_48_out, not_49_out, not_50_out,
       not_51_out, not_52_out, not_53_out, not_54_out, not_55_out, not_56_out, not_57_out, not_58_out,
       not_59_out, not_60_out, not_61_out, not_62_out, not_63_out, not_64_out, not_65_out, not_66_out,
       not_67_out, not_68_out, not_69_out, not_70_out, not_71_out, not_72_out, not_73_out, not_74_out,
       not_75_out, not_76_out, not_77_out, not_78_out, not_79_out, not_80_out;

  and and_1 (out_7, in_1, buffer_1_out);
  buf buffer_1 (buffer_1_out, and_2_out);
  and and_2 (and_2_out, in_2, not_3_out, not_4_out, not_2_out, not_1_out);
  not not_1 (not_1_out, in_6);
  not not_2 (not_2_out, in_5);
  not not_3 (not_3_out, in_3);
  not not_4 (not_4_out, in_4);
  not not_5 (not_5_out, in_6);
  not not_6 (not_6_out, in_3);
  not not_7 (not_7_out, in_4);
  not not_8 (not_8_out, in_2);
  not not_9 (not_9_out, in_5);
  and and_3 (and_3_out, not_8_out, not_6_out, not_7_out, not_9_out, not_5_out);
  buf buffer_2 (buffer_2_out, and_3_out);
  and and_4 (out_23, in_1, buffer_2_out);
  and and_5 (out_8, in_1, buffer_3_out);
  buf buffer_3 (buffer_3_out, and_6_out);
  and and_6 (and_6_out, in_2, in_3, not_12_out, not_10_out, not_11_out);
  not not_10 (not_10_out, in_5);
  not not_11 (not_11_out, in_6);
  not not_12 (not_12_out, in_4);
  not not_13 (not_13_out, in_2);
  not not_14 (not_14_out, in_5);
  not not_15 (not_15_out, in_4);
  not not_16 (not_16_out, in_3);
  not not_17 (not_17_out, in_2);
  not not_18 (not_18_out, in_6);
  and and_7 (and_7_out, not_13_out, in_3, not_15_out, not_14_out, not_18_out);
  buf buffer_4 (buffer_4_out, and_7_out);
  and and_8 (out_25, in_1, buffer_7_out);
  and and_9 (out_24, in_1, buffer_4_out);
  and and_10 (out_9, in_1, buffer_5_out);
  and and_11 (out_10, in_1, buffer_6_out);
  buf buffer_5 (buffer_5_out, and_13_out);
  buf buffer_6 (buffer_6_out, and_12_out);
  and and_12 (and_12_out, in_2, in_3, in_4, not_28_out, not_26_out);
  and and_13 (and_13_out, in_2, not_20_out, in_4, not_19_out, not_21_out);
  not not_19 (not_19_out, in_5);
  not not_20 (not_20_out, in_3);
  not not_21 (not_21_out, in_6);
  not not_22 (not_22_out, in_6);
  not not_23 (not_23_out, in_5);
  not not_24 (not_24_out, in_2);
  not not_25 (not_25_out, in_5);
  and and_14 (and_14_out, not_24_out, in_3, in_4, not_25_out, not_33_out);
  and and_15 (and_15_out, not_17_out, not_16_out, in_4, not_23_out, not_22_out);
  buf buffer_7 (buffer_7_out, and_15_out);
  buf buffer_8 (buffer_8_out, and_14_out);
  and and_16 (out_26, in_1, buffer_8_out);
  and and_17 (out_11, in_1, buffer_9_out);
  buf buffer_9 (buffer_9_out, and_18_out);
  and and_18 (and_18_out, in_2, not_27_out, not_30_out, in_5, not_29_out);
  not not_26 (not_26_out, in_6);
  not not_27 (not_27_out, in_3);
  not not_28 (not_28_out, in_5);
  not not_29 (not_29_out, in_6);
  not not_30 (not_30_out, in_4);
  not not_31 (not_31_out, in_4);
  not not_32 (not_32_out, in_3);
  not not_33 (not_33_out, in_6);
  not not_34 (not_34_out, in_6);
  not not_35 (not_35_out, in_2);
  and and_19 (and_19_out, not_35_out, not_32_out, not_31_out, in_5, not_34_out);
  buf buffer_10 (buffer_10_out, and_19_out);
  and and_20 (out_27, in_1, buffer_10_out);
  and and_21 (out_12, in_1, buffer_11_out);
  buf buffer_11 (buffer_11_out, and_22_out);
  and and_22 (and_22_out, in_2, in_3, not_37_out, in_5, not_36_out);
  not not_36 (not_36_out, in_6);
  not not_37 (not_37_out, in_4);
  not not_38 (not_38_out, in_2);
  not not_39 (not_39_out, in_2);
  not not_40 (not_40_out, in_4);
  not not_41 (not_41_out, in_6);
  not not_42 (not_42_out, in_3);
  and and_23 (and_23_out, not_39_out, in_3, not_40_out, in_5, not_41_out);
  buf buffer_12 (buffer_12_out, and_23_out);
  and and_24 (out_29, in_1, buffer_16_out);
  and and_25 (out_28, in_1, buffer_12_out);
  and and_26 (out_14, in_1, buffer_13_out);
  and and_27 (out_13, in_1, buffer_14_out);
  buf buffer_13 (buffer_13_out, and_29_out);
  buf buffer_14 (buffer_14_out, and_28_out);
  and and_28 (and_28_out, in_2, not_44_out, in_4, in_5, not_43_out);
  and and_29 (and_29_out, in_2, in_3, in_4, in_5, not_48_out);
  not not_43 (not_43_out, in_6);
  not not_44 (not_44_out, in_3);
  not not_45 (not_45_out, in_6);
  not not_46 (not_46_out, in_2);
  and and_30 (and_30_out, not_46_out, in_3, in_4, in_5, not_54_out);
  and and_31 (and_31_out, not_38_out, not_42_out, in_4, in_5, not_45_out);
  buf buffer_15 (buffer_15_out, and_30_out);
  buf buffer_16 (buffer_16_out, and_31_out);
  and and_32 (out_30, in_1, buffer_15_out);
  and and_33 (out_15, in_1, buffer_17_out);
  buf buffer_17 (buffer_17_out, and_34_out);
  and and_34 (and_34_out, in_2, not_47_out, not_50_out, not_49_out, in_6);
  not not_47 (not_47_out, in_3);
  not not_48 (not_48_out, in_6);
  not not_49 (not_49_out, in_5);
  not not_50 (not_50_out, in_4);
  not not_51 (not_51_out, in_4);
  not not_52 (not_52_out, in_3);
  not not_53 (not_53_out, in_5);
  not not_54 (not_54_out, in_6);
  not not_55 (not_55_out, in_2);
  and and_35 (and_35_out, not_55_out, not_52_out, not_51_out, not_53_out, in_6);
  buf buffer_18 (buffer_18_out, and_35_out);
  and and_36 (out_31, in_1, buffer_18_out);
  and and_37 (out_16, in_1, buffer_19_out);
  buf buffer_19 (buffer_19_out, and_38_out);
  and and_38 (and_38_out, in_2, in_3, not_56_out, not_57_out, in_6);
  not not_56 (not_56_out, in_4);
  not not_57 (not_57_out, in_5);
  not not_58 (not_58_out, in_5);
  not not_59 (not_59_out, in_3);
  not not_60 (not_60_out, in_2);
  not not_61 (not_61_out, in_4);
  not not_62 (not_62_out, in_2);
  and and_39 (and_39_out, not_60_out, in_3, not_61_out, not_58_out, in_6);
  buf buffer_20 (buffer_20_out, and_39_out);
  and and_40 (out_32, in_1, buffer_20_out);
  and and_41 (out_33, in_1, buffer_23_out);
  and and_42 (out_17, in_1, buffer_21_out);
  and and_43 (out_18, in_1, buffer_22_out);
  buf buffer_21 (buffer_21_out, and_45_out);
  buf buffer_22 (buffer_22_out, and_44_out);
  and and_44 (and_44_out, in_2, in_3, in_4, not_68_out, in_6);
  and and_45 (and_45_out, in_2, not_64_out, in_4, not_63_out, in_6);
  not not_63 (not_63_out, in_5);
  not not_64 (not_64_out, in_3);
  not not_65 (not_65_out, in_5);
  not not_66 (not_66_out, in_5);
  not not_67 (not_67_out, in_2);
  and and_46 (and_46_out, not_67_out, in_3, in_4, not_65_out, in_6);
  and and_47 (and_47_out, not_62_out, not_59_out, in_4, not_66_out, in_6);
  buf buffer_23 (buffer_23_out, and_47_out);
  buf buffer_24 (buffer_24_out, and_46_out);
  and and_48 (out_34, in_1, buffer_24_out);
  and and_49 (out_19, in_1, buffer_25_out);
  buf buffer_25 (buffer_25_out, and_50_out);
  and and_50 (and_50_out, in_2, not_70_out, not_69_out, in_5, in_6);
  not not_68 (not_68_out, in_5);
  not not_69 (not_69_out, in_4);
  not not_70 (not_70_out, in_3);
  not not_71 (not_71_out, in_3);
  not not_72 (not_72_out, in_2);
  not not_73 (not_73_out, in_4);
  and and_51 (and_51_out, not_72_out, not_71_out, not_73_out, in_5, in_6);
  buf buffer_26 (buffer_26_out, and_51_out);
  and and_52 (out_35, in_1, buffer_26_out);
  and and_53 (out_20, in_1, buffer_27_out);
  buf buffer_27 (buffer_27_out, and_54_out);
  and and_54 (and_54_out, in_2, in_3, not_74_out, in_5, in_6);
  not not_74 (not_74_out, in_4);
  not not_75 (not_75_out, in_4);
  not not_76 (not_76_out, in_3);
  not not_77 (not_77_out, in_2);
  not not_78 (not_78_out, in_2);
  and and_55 (and_55_out, not_78_out, in_3, not_75_out, in_5, in_6);
  buf buffer_28 (buffer_28_out, and_55_out);
  and and_56 (out_37, in_1, buffer_31_out);
  and and_57 (out_36, in_1, buffer_28_out);
  and and_58 (out_21, in_1, buffer_30_out);
  and and_59 (out_22, in_1, buffer_29_out);
  buf buffer_29 (buffer_29_out, and_60_out);
  buf buffer_30 (buffer_30_out, and_61_out);
  and and_60 (and_60_out, in_2, in_3, in_4, in_5, in_6);
  and and_61 (and_61_out, in_2, not_79_out, in_4, in_5, in_6);
  not not_79 (not_79_out, in_3);
  not not_80 (not_80_out, in_2);
  and and_62 (and_62_out, not_80_out, in_3, in_4, in_5, in_6);
  and and_63 (and_63_out, not_77_out, not_76_out, in_4, in_5, in_6);
  buf buffer_31 (buffer_31_out, and_63_out);
  buf buffer_32 (buffer_32_out, and_62_out);
  and and_64 (out_38, in_1, buffer_32_out);
endmodule

module _5_Bin_Dec2 (
  input  in_1,
  input  in_2,
  input  in_3,
  input  in_4,
  input  in_5,
  input  in_6,
  output out_7,
  output out_8,
  output out_9,
  output out_10,
  output out_11,
  output out_12,
  output out_13,
  output out_14,
  output out_15,
  output out_16,
  output out_17,
  output out_18,
  output out_19,
  output out_20,
  output out_21,
  output out_22,
  output out_23,
  output out_24,
  output out_25,
  output out_26,
  output out_27,
  output out_28,
  output out_29,
  output out_30,
  output out_31,
  output out_32,
  output out_33,
  output out_34,
  output out_35,
  output out_36,
  output out_37,
  output out_38
);

  _5_Bin_Dec u_5_bin_dec_1 (
    .in_2(in_2), .in_3(in_3), .in_4(in_4), .in_5(in_5), .in_6(in_6), .out_7(out_8), .out_8(out_10),
    .out_9(out_12), .out_10(out_14), .out_11(out_16), .out_12(out_18), .out_13(out_20), .out_14(out_22),
    .out_15(out_24), .out_16(out_26), .out_17(out_28), .out_18(out_30), .out_19(out_32), .out_20(out_34),
    .out_21(out_36), .out_22(out_38), .out_23(out_7), .out_24(out_9), .out_25(out_11), .out_26(out_13),
    .out_27(out_15), .out_28(out_17), .out_29(out_19), .out_30(out_21), .out_31(out_23), .out_32(out_25),
    .out_33(out_27), .out_34(out_29), .out_35(out_31), .out_36(out_33), .out_37(out_35), .out_38(out_37),
    .in_1(in_1));
endmodule

module Prog_Mem (
  input  [23:0] Memory_Location,
  input  [23:0] Program_Counter,
  input  [7:0] in_3,
  input  [7:0] in_4,
  input  [7:0] in_5,
  input  in_6,
  output [23:0] out_7
);

  wire n1_delay_1_out_2, n1_delay_2_out_2, n1_delay_3_out_2, n1_delay_4_out_2, n1_delay_5_out_2,
       n1_delay_6_out_2, n1_delay_7_out_2, n1_delay_8_out_2, n1_delay_9_out_2, n1_delay_10_out_2,
       n1_delay_11_out_2, n1_delay_12_out_2, n1_delay_13_out_2, n1_delay_14_out_2, n1_delay_15_out_2,
       n1_delay_16_out_2, n1_delay_17_out_2, n1_delay_18_out_2, n1_delay_19_out_2, n1_delay_20_out_2,
       n1_delay_21_out_2, n1_delay_22_out_2, n1_delay_23_out_2, n1_delay_24_out_2;
  wire [23:0] _0, _1_t, _2_t, _3_t, _4, _5, _6, _7, _8, _9, _10, _11, _12, _13, _14, _15, _16, _17, _18, _19,
       _20, _21, _22, _23;

  _1_Delay u_1_delay_1 (.in_1(Memory_Location[3]), .out_2(n1_delay_1_out_2));
  _1_Delay u_1_delay_2 (.in_1(Memory_Location[4]), .out_2(n1_delay_2_out_2));
  _1_Delay u_1_delay_3 (.in_1(Memory_Location[5]), .out_2(n1_delay_3_out_2));
  _1_Delay u_1_delay_4 (.in_1(Memory_Location[6]), .out_2(n1_delay_4_out_2));
  _1_Delay u_1_delay_5 (.in_1(Memory_Location[7]), .out_2(n1_delay_5_out_2));
  _1_Delay u_1_delay_6 (.in_1(Memory_Location[0]), .out_2(n1_delay_6_out_2));
  Prog_Mem_3B_Cell prog_mem_3b_cell_1 (
    .in_2(in_3), .out_7(_0[23:16]), .out_8(_0[15:8]), .out_9(_0[7:0]), .in_3(in_4), .in_4(in_5),
    .in_5(n1_delay_6_out_2), .in_6(Program_Counter[0]), .in_1(in_6));
  _1_Delay u_1_delay_7 (.in_1(Memory_Location[1]), .out_2(n1_delay_7_out_2));
  Prog_Mem_3B_Cell prog_mem_3b_cell_2 (
    .in_2(in_3), .out_7(_1_t[23:16]), .out_8(_1_t[15:8]), .out_9(_1_t[7:0]), .in_3(in_4), .in_4(in_5),
    .in_5(n1_delay_7_out_2), .in_6(Program_Counter[1]), .in_1(in_6));
  _1_Delay u_1_delay_8 (.in_1(Memory_Location[2]), .out_2(n1_delay_8_out_2));
  Prog_Mem_3B_Cell prog_mem_3b_cell_3 (
    .in_2(in_3), .out_7(_2_t[23:16]), .out_8(_2_t[15:8]), .out_9(_2_t[7:0]), .in_3(in_4), .in_4(in_5),
    .in_5(n1_delay_8_out_2), .in_6(Program_Counter[2]), .in_1(in_6));
  Prog_Mem_3B_Cell prog_mem_3b_cell_4 (
    .in_2(in_3), .out_7(_3_t[23:16]), .out_8(_3_t[15:8]), .out_9(_3_t[7:0]), .in_3(in_4), .in_4(in_5),
    .in_5(n1_delay_1_out_2), .in_6(Program_Counter[3]), .in_1(in_6));
  Prog_Mem_3B_Cell prog_mem_3b_cell_5 (
    .in_2(in_3), .out_7(_4[23:16]), .out_8(_4[15:8]), .out_9(_4[7:0]), .in_3(in_4), .in_4(in_5),
    .in_5(n1_delay_2_out_2), .in_6(Program_Counter[4]), .in_1(in_6));
  Prog_Mem_3B_Cell prog_mem_3b_cell_6 (
    .in_2(in_3), .out_7(_5[23:16]), .out_8(_5[15:8]), .out_9(_5[7:0]), .in_3(in_4), .in_4(in_5),
    .in_5(n1_delay_3_out_2), .in_6(Program_Counter[5]), .in_1(in_6));
  Prog_Mem_3B_Cell prog_mem_3b_cell_7 (
    .in_2(in_3), .out_7(_6[23:16]), .out_8(_6[15:8]), .out_9(_6[7:0]), .in_3(in_4), .in_4(in_5),
    .in_5(n1_delay_4_out_2), .in_6(Program_Counter[6]), .in_1(in_6));
  Prog_Mem_3B_Cell prog_mem_3b_cell_8 (
    .in_2(in_3), .out_7(_7[23:16]), .out_8(_7[15:8]), .out_9(_7[7:0]), .in_3(in_4), .in_4(in_5),
    .in_5(n1_delay_5_out_2), .in_6(Program_Counter[7]), .in_1(in_6));
  _1_Delay u_1_delay_9 (.in_1(Memory_Location[11]), .out_2(n1_delay_9_out_2));
  _1_Delay u_1_delay_10 (.in_1(Memory_Location[12]), .out_2(n1_delay_10_out_2));
  _1_Delay u_1_delay_11 (.in_1(Memory_Location[13]), .out_2(n1_delay_11_out_2));
  _1_Delay u_1_delay_12 (.in_1(Memory_Location[14]), .out_2(n1_delay_12_out_2));
  _1_Delay u_1_delay_13 (.in_1(Memory_Location[15]), .out_2(n1_delay_13_out_2));
  _1_Delay u_1_delay_14 (.in_1(Memory_Location[8]), .out_2(n1_delay_14_out_2));
  Prog_Mem_3B_Cell prog_mem_3b_cell_9 (
    .in_2(in_3), .out_7(_8[23:16]), .out_8(_8[15:8]), .out_9(_8[7:0]), .in_3(in_4), .in_4(in_5),
    .in_5(n1_delay_14_out_2), .in_6(Program_Counter[8]), .in_1(in_6));
  _1_Delay u_1_delay_15 (.in_1(Memory_Location[9]), .out_2(n1_delay_15_out_2));
  Prog_Mem_3B_Cell prog_mem_3b_cell_10 (
    .in_2(in_3), .out_7(_9[23:16]), .out_8(_9[15:8]), .out_9(_9[7:0]), .in_3(in_4), .in_4(in_5),
    .in_5(n1_delay_15_out_2), .in_6(Program_Counter[9]), .in_1(in_6));
  _1_Delay u_1_delay_16 (.in_1(Memory_Location[10]), .out_2(n1_delay_16_out_2));
  Prog_Mem_3B_Cell prog_mem_3b_cell_11 (
    .in_2(in_3), .out_7(_10[23:16]), .out_8(_10[15:8]), .out_9(_10[7:0]), .in_3(in_4), .in_4(in_5),
    .in_5(n1_delay_16_out_2), .in_6(Program_Counter[10]), .in_1(in_6));
  Prog_Mem_3B_Cell prog_mem_3b_cell_12 (
    .in_2(in_3), .out_7(_11[23:16]), .out_8(_11[15:8]), .out_9(_11[7:0]), .in_3(in_4), .in_4(in_5),
    .in_5(n1_delay_9_out_2), .in_6(Program_Counter[11]), .in_1(in_6));
  Prog_Mem_3B_Cell prog_mem_3b_cell_13 (
    .in_2(in_3), .out_7(_12[23:16]), .out_8(_12[15:8]), .out_9(_12[7:0]), .in_3(in_4), .in_4(in_5),
    .in_5(n1_delay_10_out_2), .in_6(Program_Counter[12]), .in_1(in_6));
  Prog_Mem_3B_Cell prog_mem_3b_cell_14 (
    .in_2(in_3), .out_7(_13[23:16]), .out_8(_13[15:8]), .out_9(_13[7:0]), .in_3(in_4), .in_4(in_5),
    .in_5(n1_delay_11_out_2), .in_6(Program_Counter[13]), .in_1(in_6));
  Prog_Mem_3B_Cell prog_mem_3b_cell_15 (
    .in_2(in_3), .out_7(_14[23:16]), .out_8(_14[15:8]), .out_9(_14[7:0]), .in_3(in_4), .in_4(in_5),
    .in_5(n1_delay_12_out_2), .in_6(Program_Counter[14]), .in_1(in_6));
  Prog_Mem_3B_Cell prog_mem_3b_cell_16 (
    .in_2(in_3), .out_7(_15[23:16]), .out_8(_15[15:8]), .out_9(_15[7:0]), .in_3(in_4), .in_4(in_5),
    .in_5(n1_delay_13_out_2), .in_6(Program_Counter[15]), .in_1(in_6));
  _1_Delay u_1_delay_17 (.in_1(Memory_Location[16]), .out_2(n1_delay_17_out_2));
  _1_Delay u_1_delay_18 (.in_1(Memory_Location[17]), .out_2(n1_delay_18_out_2));
  _1_Delay u_1_delay_19 (.in_1(Memory_Location[18]), .out_2(n1_delay_19_out_2));
  _1_Delay u_1_delay_20 (.in_1(Memory_Location[19]), .out_2(n1_delay_20_out_2));
  _1_Delay u_1_delay_21 (.in_1(Memory_Location[20]), .out_2(n1_delay_21_out_2));
  _1_Delay u_1_delay_22 (.in_1(Memory_Location[21]), .out_2(n1_delay_22_out_2));
  _1_Delay u_1_delay_23 (.in_1(Memory_Location[22]), .out_2(n1_delay_23_out_2));
  _1_Delay u_1_delay_24 (.in_1(Memory_Location[23]), .out_2(n1_delay_24_out_2));
  Prog_Mem_3B_Cell prog_mem_3b_cell_17 (
    .in_2(in_3), .out_7(_16[23:16]), .out_8(_16[15:8]), .out_9(_16[7:0]), .in_3(in_4), .in_4(in_5),
    .in_5(n1_delay_17_out_2), .in_6(Program_Counter[16]), .in_1(in_6));
  Prog_Mem_3B_Cell prog_mem_3b_cell_18 (
    .in_2(in_3), .out_7(_17[23:16]), .out_8(_17[15:8]), .out_9(_17[7:0]), .in_3(in_4), .in_4(in_5),
    .in_5(n1_delay_18_out_2), .in_6(Program_Counter[17]), .in_1(in_6));
  Prog_Mem_3B_Cell prog_mem_3b_cell_19 (
    .in_2(in_3), .out_7(_18[23:16]), .out_8(_18[15:8]), .out_9(_18[7:0]), .in_3(in_4), .in_4(in_5),
    .in_5(n1_delay_19_out_2), .in_6(Program_Counter[18]), .in_1(in_6));
  Prog_Mem_3B_Cell prog_mem_3b_cell_20 (
    .in_2(in_3), .out_7(_19[23:16]), .out_8(_19[15:8]), .out_9(_19[7:0]), .in_3(in_4), .in_4(in_5),
    .in_5(n1_delay_20_out_2), .in_6(Program_Counter[19]), .in_1(in_6));
  Prog_Mem_3B_Cell prog_mem_3b_cell_21 (
    .in_2(in_3), .out_7(_20[23:16]), .out_8(_20[15:8]), .out_9(_20[7:0]), .in_3(in_4), .in_4(in_5),
    .in_5(n1_delay_21_out_2), .in_6(Program_Counter[20]), .in_1(in_6));
  Prog_Mem_3B_Cell prog_mem_3b_cell_22 (
    .in_2(in_3), .out_7(_21[23:16]), .out_8(_21[15:8]), .out_9(_21[7:0]), .in_3(in_4), .in_4(in_5),
    .in_5(n1_delay_22_out_2), .in_6(Program_Counter[21]), .in_1(in_6));
  Prog_Mem_3B_Cell prog_mem_3b_cell_23 (
    .in_2(in_3), .out_7(_22[23:16]), .out_8(_22[15:8]), .out_9(_22[7:0]), .in_3(in_4), .in_4(in_5),
    .in_5(n1_delay_23_out_2), .in_6(Program_Counter[22]), .in_1(in_6));
  Prog_Mem_3B_Cell prog_mem_3b_cell_24 (
    .in_2(in_3), .out_7(_23[23:16]), .out_8(_23[15:8]), .out_9(_23[7:0]), .in_3(in_4), .in_4(in_5),
    .in_5(n1_delay_24_out_2), .in_6(Program_Counter[23]), .in_1(in_6));
  assign out_7 = _0 | _1_t | _2_t | _3_t | _4 | _5 | _6 | _7 | _8 | _9 | _10 | _11 | _12 | _13 | _14 | _15 | _16 | _17 | _18 | _19 | _20 | _21 | _22 | _23;  // OR_Gate or_1, 24 bits wide

  // Other names for the same wires on the sheet: _1[7:0] = in_3; _2[7:0] = in_4; _3[7:0] = in_5; R = in_6
endmodule

module Prog_Mem_3B_Cell (
  input  in_1,
  input  [7:0] in_2,
  input  [7:0] in_3,
  input  [7:0] in_4,
  input  in_5,
  input  in_6,
  output [7:0] out_7,
  output [7:0] out_8,
  output [7:0] out_9
);

  _8_RAM_CLK u_8_ram_clk_1 (
    .out_12(out_7[0]), .out_13(out_7[1]), .out_14(out_7[2]), .out_15(out_7[3]), .out_16(out_7[4]),
    .out_17(out_7[5]), .out_18(out_7[6]), .out_19(out_7[7]), .in_11(in_6), .in_2(in_2[0]), .in_3(in_2[1]),
    .in_4(in_2[2]), .in_5(in_2[3]), .in_6(in_2[4]), .in_7(in_2[5]), .in_8(in_2[6]), .in_9(in_2[7]),
    .in_10(in_5), .in_1(in_1));
  _8_RAM_CLK u_8_ram_clk_2 (
    .out_12(out_8[0]), .out_13(out_8[1]), .out_14(out_8[2]), .out_15(out_8[3]), .out_16(out_8[4]),
    .out_17(out_8[5]), .out_18(out_8[6]), .out_19(out_8[7]), .in_11(in_6), .in_2(in_3[0]), .in_3(in_3[1]),
    .in_4(in_3[2]), .in_5(in_3[3]), .in_6(in_3[4]), .in_7(in_3[5]), .in_8(in_3[6]), .in_9(in_3[7]),
    .in_10(in_5), .in_1(in_1));
  _8_RAM_CLK u_8_ram_clk_3 (
    .out_12(out_9[0]), .out_13(out_9[1]), .out_14(out_9[2]), .out_15(out_9[3]), .out_16(out_9[4]),
    .out_17(out_9[5]), .out_18(out_9[6]), .out_19(out_9[7]), .in_11(in_6), .in_2(in_4[0]), .in_3(in_4[1]),
    .in_4(in_4[2]), .in_5(in_4[3]), .in_6(in_4[4]), .in_7(in_4[5]), .in_8(in_4[6]), .in_9(in_4[7]),
    .in_10(in_5), .in_1(in_1));
endmodule

module _24_BUF (
  input  [23:0] in_1,
  input  in_2,
  output [23:0] out_3
);

  and and_1 (out_3[0], in_1[0], in_2);
  and and_2 (out_3[1], in_1[1], in_2);
  and and_3 (out_3[2], in_1[2], in_2);
  and and_4 (out_3[3], in_1[3], in_2);
  and and_5 (out_3[4], in_1[4], in_2);
  and and_6 (out_3[5], in_1[5], in_2);
  and and_7 (out_3[6], in_1[6], in_2);
  and and_8 (out_3[7], in_1[7], in_2);
  and and_9 (out_3[8], in_1[8], in_2);
  and and_10 (out_3[9], in_1[9], in_2);
  and and_11 (out_3[10], in_1[10], in_2);
  and and_12 (out_3[11], in_1[11], in_2);
  and and_13 (out_3[12], in_1[12], in_2);
  and and_14 (out_3[13], in_1[13], in_2);
  and and_15 (out_3[14], in_1[14], in_2);
  and and_16 (out_3[15], in_1[15], in_2);
  and and_17 (out_3[16], in_1[16], in_2);
  and and_18 (out_3[17], in_1[17], in_2);
  and and_19 (out_3[18], in_1[18], in_2);
  and and_20 (out_3[19], in_1[19], in_2);
  and and_21 (out_3[20], in_1[20], in_2);
  and and_22 (out_3[21], in_1[21], in_2);
  and and_23 (out_3[22], in_1[22], in_2);
  and and_24 (out_3[23], in_1[23], in_2);
endmodule

module Inst_Decoder (
  input  [3:0] Op_Code,
  input  [3:0] Op_2,
  input  [3:0] Op_3,
  input  [3:0] Op_4,
  output Read,
  output Write,
  output [3:0] Source1,
  output [3:0] Source2,
  output [3:0] iSource,
  output [3:0] Dest,
  output ALU_Read,
  output ALU_Write,
  output [7:0] Const,
  output Inc,
  output Dec,
  output Neg,
  output Disp,
  output [3:0] out_18,
  output [3:0] out_19,
  output [3:0] out_20,
  output [3:0] out_21,
  output out_22,
  output out_23,
  output out_24,
  output out_25,
  output out_26,
  output out_27,
  output out_28,
  output out_29,
  output out_30,
  output out_31
);

  wire and_1_out, and_2_out, and_4_out, and_7_out, and_13_out, and_18_out, and_22_out, n1_delay_1_out_2,
       not_1_out, not_2_out, not_3_out, not_4_out, not_5_out, not_6_out, not_7_out, not_8_out, not_9_out,
       not_10_out, not_11_out, not_12_out, not_13_out, not_14_out, not_15_out, not_16_out, not_17_out,
       not_18_out, not_19_out, not_20_out, not_21_out, not_22_out, not_23_out, not_24_out, not_25_out,
       xor_1_out;
  wire [3:0] enabler_1_out_3, enabler_2_out_3, enabler_3_out_3, enabler_4_out_3, enabler_5_out_3,
       enabler_6_out_3, enabler_7_out_3, enabler_8_out_3, enabler_9_out_3, enabler_10_out_3,
       enabler_13_out_3, enabler_14_out_3, enabler_15_out_3, n4_splitter_1_out_2, n4_splitter_1_out_3;

  ExactlyOne xor_1 (
    .out(xor_1_out), .in0(and_2_out), .in1(and_4_out), .in2(and_7_out), .in3(and_13_out), .in4(and_18_out),
    .in5(Inc), .in6(Dec), .in7(Neg), .in8(and_22_out), .in9(Disp));
  or or_1 (Read, and_7_out, and_18_out, Inc, Dec, Neg, Disp);
  not not_1 (not_1_out, Op_Code[3]);
  not not_2 (not_2_out, Op_Code[0]);
  not not_3 (not_3_out, Op_Code[2]);
  not not_4 (not_4_out, Op_Code[3]);
  not not_5 (not_5_out, Op_Code[1]);
  and and_1 (and_1_out, not_4_out, not_3_out, not_5_out, not_2_out);
  and and_2 (and_2_out, Op_2[0], and_1_out);
  _1_Delay u_1_delay_1 (.in_1(xor_1_out), .out_2(n1_delay_1_out_2));
  and and_3 (out_22, n1_delay_1_out_2, and_1_out);
  not not_6 (not_6_out, Op_Code[1]);
  not not_7 (not_7_out, Op_Code[2]);
  and and_4 (and_4_out, not_1_out, not_7_out, not_6_out, Op_Code[0]);
  Enabler enabler_1 (.Op_3(Op_2), .in_1(and_4_out), .out_3(enabler_1_out_3));
  Enabler enabler_2 (.Op_3(Op_3), .in_1(and_4_out), .out_3(enabler_2_out_3));
  and and_5 (out_24, n1_delay_1_out_2, and_7_out);
  and and_6 (out_23, n1_delay_1_out_2, and_4_out);
  or or_2 (Write, and_4_out, and_7_out, and_13_out, and_22_out);
  not not_8 (not_8_out, Op_Code[2]);
  not not_9 (not_9_out, Op_Code[3]);
  and and_7 (and_7_out, not_9_out, not_8_out, Op_Code[1], not_10_out);
  and and_8 (out_26, n1_delay_1_out_2, and_18_out);
  and and_9 (out_25, n1_delay_1_out_2, and_13_out);
  _4_Splitter u_4_splitter_1 (.out_2(n4_splitter_1_out_2), .out_3(n4_splitter_1_out_3), .in_1(enabler_3_out_3));
  not not_10 (not_10_out, Op_Code[0]);
  Enabler enabler_3 (.Op_3(Op_2), .in_1(and_7_out), .out_3(enabler_3_out_3));
  Enabler enabler_4 (.Op_3(Op_3), .in_1(and_7_out), .out_3(enabler_4_out_3));
  and and_10 (ALU_Read, and_7_out, Op_4[0]);
  and and_11 (out_28, n1_delay_1_out_2, Dec);
  and and_12 (out_27, n1_delay_1_out_2, Inc);
  assign Source1 = n4_splitter_1_out_3 | enabler_6_out_3 | enabler_8_out_3 | enabler_9_out_3 | enabler_10_out_3 | enabler_14_out_3;  // OR_Gate or_3, 4 bits wide
  not not_11 (not_11_out, Op_Code[2]);
  not not_12 (not_12_out, Op_Code[3]);
  and and_13 (and_13_out, not_12_out, not_11_out, Op_Code[1], Op_Code[0]);
  and and_14 (out_29, n1_delay_1_out_2, Neg);
  and and_15 (out_30, n1_delay_1_out_2, and_22_out);
  Enabler enabler_5 (.Op_3(Op_2), .in_1(and_13_out), .out_3(enabler_5_out_3));
  and and_16 (ALU_Write, and_13_out, Op_4[0]);
  and and_17 (out_31, n1_delay_1_out_2, Disp);
  assign Source2 = enabler_7_out_3 | enabler_15_out_3 | n4_splitter_1_out_2;  // OR_Gate or_4, 4 bits wide
  not not_13 (not_13_out, Op_Code[1]);
  not not_14 (not_14_out, Op_Code[0]);
  not not_15 (not_15_out, Op_Code[3]);
  and and_18 (and_18_out, not_15_out, Op_Code[2], not_13_out, not_14_out);
  assign iSource = enabler_1_out_3;  // OR_Gate or_5, 4 bits wide OR_Gate
  Enabler enabler_6 (.Op_3(Op_2), .in_1(and_18_out), .out_3(enabler_6_out_3));
  Enabler enabler_7 (.Op_3(Op_3), .in_1(and_18_out), .out_3(enabler_7_out_3));
  not not_16 (not_16_out, Op_Code[3]);
  not not_17 (not_17_out, Op_Code[1]);
  and and_19 (Inc, not_16_out, Op_Code[2], not_17_out, Op_Code[0]);
  assign Dest = enabler_2_out_3 | enabler_4_out_3 | enabler_5_out_3 | enabler_13_out_3;  // OR_Gate or_6, 4 bits wide
  not not_18 (not_18_out, Op_Code[3]);
  Enabler enabler_8 (.Op_3(Op_2), .in_1(Inc), .out_3(enabler_8_out_3));
  not not_19 (not_19_out, Op_Code[0]);
  and and_20 (Dec, not_18_out, Op_Code[2], Op_Code[1], not_19_out);
  Enabler enabler_9 (.Op_3(Op_2), .in_1(Dec), .out_3(enabler_9_out_3));
  not not_20 (not_20_out, Op_Code[3]);
  and and_21 (Neg, not_20_out, Op_Code[2], Op_Code[1], Op_Code[0]);
  Enabler enabler_10 (.Op_3(Op_2), .in_1(Neg), .out_3(enabler_10_out_3));
  not not_21 (not_21_out, Op_Code[0]);
  not not_22 (not_22_out, Op_Code[2]);
  not not_23 (not_23_out, Op_Code[1]);
  and and_22 (and_22_out, Op_Code[3], not_22_out, not_23_out, not_21_out);
  Enabler enabler_11 (.Op_3(Op_2), .in_1(and_22_out), .out_3(Const[7:4]));
  Enabler enabler_12 (.Op_3(Op_3), .in_1(and_22_out), .out_3(Const[3:0]));
  Enabler enabler_13 (.Op_3(Op_4), .in_1(and_22_out), .out_3(enabler_13_out_3));
  not not_24 (not_24_out, Op_Code[2]);
  not not_25 (not_25_out, Op_Code[1]);
  and and_23 (Disp, Op_Code[3], not_24_out, not_25_out, Op_Code[0]);
  Enabler enabler_14 (.Op_3(Op_2), .in_1(Disp), .out_3(enabler_14_out_3));
  Enabler enabler_15 (.Op_3(Op_3), .in_1(Disp), .out_3(enabler_15_out_3));

  assign out_18 = Op_Code;
  assign out_19 = Op_2;
  assign out_20 = Op_3;
  assign out_21 = Op_4;
endmodule

module Enabler (
  input  in_1,
  input  [3:0] Op_3,
  output [3:0] out_3
);

  wire or_1_out;
  wire [3:3] and_1_out;

  or or_1 (or_1_out, Op_3[3], Op_3[2], Op_3[1], Op_3[0]);
  and and_1 (and_1_out[3], in_1, or_1_out);
  assign out_3 = {and_1_out[3], {3{in_1}}} & Op_3;  // AND_Gate and_2, 4 bits wide
endmodule

module Condition_Decoder (
  input  [3:0] in_1,
  input  [3:0] in_2,
  input  [3:0] in_3,
  input  [3:0] in_4,
  input  [3:0] in_5,
  input  [3:0] in_6,
  output [3:0] Comp,
  output [7:0] Constant,
  output [2:0] Mem,
  output [4:0] Jump_if_true,
  output out_11,
  output out_12,
  output out_13,
  output out_14
);

  wire and_1_out, and_2_out, and_3_out, and_5_out, and_7_out, and_9_out, n1_shortdelay_1_out_2, not_1_out,
       not_2_out, not_3_out, not_4_out, not_5_out, not_6_out, not_7_out, or_1_out, or_2_out, or_3_out,
       or_4_out;

  _4_BUF u_4_buf_1 (.in_2(or_4_out), .in_1(in_2), .out_3(Comp));
  not not_1 (not_1_out, in_1[2]);
  _8_BUF u_8_buf_1 (.in_2(or_4_out), .in_1({in_3, in_4}), .out_3(Constant));
  not not_2 (not_2_out, in_1[0]);
  not not_3 (not_3_out, in_1[2]);
  and and_1 (and_1_out, in_1[3], not_3_out, in_1[1], in_1[0]);
  and and_2 (and_2_out, in_1[3], not_1_out, in_1[1], not_2_out);
  not not_4 (not_4_out, in_1[1]);
  not not_5 (not_5_out, in_1[0]);
  and and_3 (and_3_out, in_1[3], in_1[2], not_4_out, not_5_out);
  or or_1 (or_1_out, and_2_out, and_5_out, and_7_out);
  and and_4 (out_11, or_1_out, n1_shortdelay_1_out_2);
  _3_BUF u_3_buf_1 (.in_2(or_4_out), .in_1(in_5[3:1]), .out_3(Mem));
  not not_6 (not_6_out, in_1[1]);
  and and_5 (and_5_out, in_1[3], in_1[2], not_6_out, in_1[0]);
  or or_2 (or_2_out, and_1_out, and_5_out);
  and and_6 (out_12, or_2_out, n1_shortdelay_1_out_2);
  not not_7 (not_7_out, in_1[0]);
  and and_7 (and_7_out, in_1[3], in_1[2], in_1[1], not_7_out);
  or or_3 (or_3_out, and_3_out, and_7_out);
  and and_8 (out_13, or_3_out, n1_shortdelay_1_out_2);
  _5_BUF u_5_buf_1 (.in_2(or_4_out), .in_1({in_5[0], in_6}), .out_3(Jump_if_true));
  and and_9 (and_9_out, in_1[3], in_1[2], in_1[1], in_1[0]);
  or or_4 (or_4_out, and_2_out, and_1_out, and_3_out, and_5_out, and_7_out, and_9_out);
  and and_10 (out_14, and_9_out, n1_shortdelay_1_out_2);
  _1_ShortDelay u_1_shortdelay_1 (.in_1(or_4_out), .out_2(n1_shortdelay_1_out_2));
endmodule

module _8_Comparator (
  input  [7:0] in_1,
  input  [7:0] in_2,
  output out_3,
  output out_4,
  output out_5
);

  wire comp2_1_out_6, comp2_1_out_7;

  Comp2 comp2_1 (
    .in_1(in_1[3:0]), .in_2(in_2[3:0]), .in_3(1'b0), .in_4(1'b1), .in_5(1'b1), .out_6(comp2_1_out_6),
    .out_7(comp2_1_out_7));  // open: out_8
  Comp2 comp2_2 (
    .in_1(in_1[7:4]), .in_2(in_2[7:4]), .in_3(comp2_1_out_6), .in_4(comp2_1_out_7), .in_5(1'b1),
    .out_6(out_3), .out_7(out_4), .out_8(out_5));
endmodule

module ALU (
  input  [7:0] nA,
  input  [7:0] nB,
  input  in_3,
  input  in_4,
  input  in_5,
  input  in_6,
  input  in_7,
  input  in_8,
  output [7:0] out_9,
  output out_10
);

  wire and_1_out, n1_delay_1_out_2, n1_delay_2_out_2, n1_delay_3_out_2, n1_delay_4_out_2, n1_delay_5_out_2,
       n1_delay_6_out_2, n1_delay_7_out_2, n1_delay_8_out_2, n1_delay_9_out_2, n1_delay_10_out_2,
       n1_delay_11_out_2, n1_delay_12_out_2, or_1_out, or_2_out, or_4_out;
  wire [7:0] n8_buf_1_out_3, n8_buf_2_out_3, n8_buf_3_out_3, n8_buf_4_out_3, n8_buf_5_out_3, n8_dec_1_out_3,
       n8_fa_1_out_18, n8_inc_1_out_3, neg_1_out_3, or_3_out;

  or or_1 (or_1_out, nA[0], nA[1], nA[2], nA[3], nA[4], nA[5], nA[6], nA[7]);
  or or_2 (or_2_out, or_1_out, in_3);
  // Probe on nA
  _8_BUF u_8_buf_1 (.in_2(in_4), .in_1(nA), .out_3(n8_buf_1_out_3));
  _8_BUF u_8_buf_2 (.in_2(in_4), .in_1(nB), .out_3(n8_buf_2_out_3));
  _1_Delay u_1_delay_1 (.in_1(in_3), .out_2(n1_delay_1_out_2));
  _8_FA u_8_fa_1 (
    .in_1(n8_buf_1_out_3[0]), .in_2(n8_buf_1_out_3[1]), .in_3(n8_buf_1_out_3[2]), .in_4(n8_buf_1_out_3[3]),
    .in_5(n8_buf_1_out_3[4]), .in_6(n8_buf_1_out_3[5]), .in_7(n8_buf_1_out_3[6]), .in_8(n8_buf_1_out_3[7]),
    .in_9(n8_buf_2_out_3[0]), .in_10(n8_buf_2_out_3[1]), .in_11(n8_buf_2_out_3[2]),
    .in_12(n8_buf_2_out_3[3]), .in_13(n8_buf_2_out_3[4]), .in_14(n8_buf_2_out_3[5]),
    .in_15(n8_buf_2_out_3[6]), .in_16(n8_buf_2_out_3[7]), .out_18(n8_fa_1_out_18[0]),
    .out_19(n8_fa_1_out_18[1]), .out_20(n8_fa_1_out_18[2]), .out_21(n8_fa_1_out_18[3]),
    .out_22(n8_fa_1_out_18[4]), .out_23(n8_fa_1_out_18[5]), .out_24(n8_fa_1_out_18[6]),
    .out_25(n8_fa_1_out_18[7]), .in_17(1'b0), .out_26(out_10));
  _8_BUF u_8_buf_3 (.in_2(n1_delay_1_out_2), .in_1(nA), .out_3(n8_buf_3_out_3));
  _1_Delay u_1_delay_2 (.in_1(or_2_out), .out_2(n1_delay_2_out_2));
  _1_Delay u_1_delay_3 (.in_1(in_5), .out_2(n1_delay_3_out_2));
  NEG neg_1 (.in_2(nA), .out_3(neg_1_out_3), .in_1(n1_delay_3_out_2));
  _8_INC u_8_inc_1 (.in_2(n8_buf_3_out_3), .out_3(n8_inc_1_out_3), .in_1(n1_delay_1_out_2));  // open: out_4
  _1_Delay u_1_delay_4 (.in_1(in_6), .out_2(n1_delay_4_out_2));
  _8_BUF u_8_buf_4 (.in_2(n1_delay_3_out_2), .in_1(neg_1_out_3), .out_3(n8_buf_4_out_3));
  _1_Delay u_1_delay_5 (.in_1(n1_delay_4_out_2), .out_2(n1_delay_5_out_2));
  _1_Delay u_1_delay_6 (.in_1(n1_delay_5_out_2), .out_2(n1_delay_6_out_2));
  _1_Delay u_1_delay_7 (.in_1(n1_delay_1_out_2), .out_2(n1_delay_7_out_2));
  _1_Delay u_1_delay_8 (.in_1(n1_delay_7_out_2), .out_2(n1_delay_8_out_2));
  // Probe on n8_dec_1_out_3
  // Probe on n8_inc_1_out_3
  _8_BUF u_8_buf_5 (.in_2(n1_delay_4_out_2), .in_1(nA), .out_3(n8_buf_5_out_3));
  _1_Delay u_1_delay_9 (.in_1(n1_delay_3_out_2), .out_2(n1_delay_9_out_2));
  _1_Delay u_1_delay_10 (.in_1(n1_delay_9_out_2), .out_2(n1_delay_10_out_2));
  _1_Delay u_1_delay_11 (.in_1(in_4), .out_2(n1_delay_11_out_2));
  _1_Delay u_1_delay_12 (.in_1(n1_delay_11_out_2), .out_2(n1_delay_12_out_2));
  // Probe on n8_fa_1_out_18
  // Probe on n8_buf_4_out_3
  assign or_3_out = n8_fa_1_out_18 | n8_dec_1_out_3 | n8_buf_4_out_3 | n8_inc_1_out_3;  // OR_Gate or_3, 8 bits wide
  or or_4 (or_4_out, n1_delay_6_out_2, n1_delay_10_out_2, n1_delay_8_out_2, n1_delay_12_out_2);
  _8_DEC u_8_dec_1 (.in_1(n1_delay_4_out_2), .in_2(n8_buf_5_out_3), .out_3(n8_dec_1_out_3));  // open: out_4
  _8_RAM_CLK u_8_ram_clk_1 (
    .out_12(out_9[0]), .out_13(out_9[1]), .out_14(out_9[2]), .out_15(out_9[3]), .out_16(out_9[4]),
    .out_17(out_9[5]), .out_18(out_9[6]), .out_19(out_9[7]), .in_11(in_8), .in_2(or_3_out[0]),
    .in_3(or_3_out[1]), .in_4(or_3_out[2]), .in_5(or_3_out[3]), .in_6(or_3_out[4]), .in_7(or_3_out[5]),
    .in_8(or_3_out[6]), .in_9(or_3_out[7]), .in_10(and_1_out), .in_1(in_7));
  and and_1 (and_1_out, or_4_out, n1_delay_2_out_2);
  // Probe on or_3_out
  // Probe on out_9
endmodule

module NEG (
  input  in_1,
  input  [7:0] in_2,
  output [7:0] out_3
);

  wire n1_ha_1_out_4, n1_ha_2_out_4, n1_ha_3_out_4, n1_ha_4_out_4, n1_ha_5_out_4, n1_ha_6_out_4,
       n1_ha_7_out_4, xor_1_out, xor_2_out, xor_3_out, xor_4_out, xor_5_out, xor_6_out, xor_7_out, xor_8_out;

  xor xor_1 (xor_1_out, in_2[0], in_1);
  xor xor_2 (xor_2_out, in_2[1], in_1);
  xor xor_3 (xor_3_out, in_2[2], in_1);
  xor xor_4 (xor_4_out, in_2[3], in_1);
  xor xor_5 (xor_5_out, in_2[4], in_1);
  xor xor_6 (xor_6_out, in_2[5], in_1);
  xor xor_7 (xor_7_out, in_2[6], in_1);
  xor xor_8 (xor_8_out, in_2[7], in_1);
  _1_HA u_1_ha_1 (.out_3(out_3[0]), .out_4(n1_ha_1_out_4), .in_1(1'b1), .in_2(xor_1_out));
  _1_HA u_1_ha_2 (.out_3(out_3[1]), .out_4(n1_ha_2_out_4), .in_1(n1_ha_1_out_4), .in_2(xor_2_out));
  _1_HA u_1_ha_3 (.out_3(out_3[2]), .out_4(n1_ha_3_out_4), .in_1(n1_ha_2_out_4), .in_2(xor_3_out));
  _1_HA u_1_ha_4 (.out_3(out_3[3]), .out_4(n1_ha_4_out_4), .in_1(n1_ha_3_out_4), .in_2(xor_4_out));
  _1_HA u_1_ha_5 (.out_3(out_3[4]), .out_4(n1_ha_5_out_4), .in_1(n1_ha_4_out_4), .in_2(xor_5_out));
  _1_HA u_1_ha_6 (.out_3(out_3[5]), .out_4(n1_ha_6_out_4), .in_1(n1_ha_5_out_4), .in_2(xor_6_out));
  _1_HA u_1_ha_7 (.out_3(out_3[6]), .out_4(n1_ha_7_out_4), .in_1(n1_ha_6_out_4), .in_2(xor_7_out));
  _1_HA u_1_ha_8 (.out_3(out_3[7]), .in_1(n1_ha_7_out_4), .in_2(xor_8_out));  // open: out_4
endmodule

module _8_BUF (
  input  [7:0] in_1,
  input  in_2,
  output [7:0] out_3
);

  and and_1 (out_3[7], in_1[7], in_2);
  and and_2 (out_3[6], in_1[6], in_2);
  and and_3 (out_3[4], in_1[4], in_2);
  and and_4 (out_3[5], in_1[5], in_2);
  and and_5 (out_3[2], in_1[2], in_2);
  and and_6 (out_3[1], in_1[1], in_2);
  and and_7 (out_3[3], in_1[3], in_2);
  and and_8 (out_3[0], in_1[0], in_2);
endmodule

module _5_BUF (
  input  [4:0] in_1,
  input  in_2,
  output [4:0] out_3
);

  and and_1 (out_3[4], in_1[4], in_2);
  and and_2 (out_3[3], in_1[3], in_2);
  and and_3 (out_3[2], in_1[2], in_2);
  and and_4 (out_3[1], in_1[1], in_2);
  and and_5 (out_3[0], in_1[0], in_2);
endmodule

module _1_Delay (
  input  in_1,
  output out_2
);

  wire buffer_1_out, buffer_2_out, buffer_3_out, buffer_4_out, buffer_5_out, buffer_6_out, buffer_7_out,
       buffer_8_out, buffer_9_out, buffer_10_out, buffer_11_out, buffer_12_out, buffer_13_out, buffer_14_out,
       buffer_15_out, buffer_16_out, buffer_17_out, buffer_18_out, buffer_19_out, buffer_20_out,
       buffer_21_out, buffer_22_out, buffer_23_out, buffer_24_out, buffer_25_out, buffer_26_out,
       buffer_27_out, buffer_28_out, buffer_29_out, buffer_30_out, buffer_31_out, buffer_32_out,
       buffer_33_out, buffer_34_out, buffer_35_out, buffer_36_out, buffer_37_out, buffer_38_out,
       buffer_39_out, buffer_40_out, buffer_41_out, buffer_42_out, buffer_43_out, buffer_44_out,
       buffer_45_out, buffer_46_out, buffer_47_out, buffer_48_out, buffer_49_out, buffer_50_out,
       buffer_51_out, buffer_52_out, buffer_53_out, buffer_54_out, buffer_55_out, buffer_56_out,
       buffer_57_out, buffer_58_out, buffer_59_out, buffer_60_out, buffer_61_out, buffer_62_out,
       buffer_63_out, buffer_64_out, buffer_65_out, buffer_66_out, buffer_67_out, buffer_68_out,
       buffer_69_out, buffer_70_out, buffer_71_out, buffer_72_out, buffer_73_out, buffer_74_out,
       buffer_75_out, buffer_76_out, buffer_77_out, buffer_78_out, buffer_79_out, buffer_80_out,
       buffer_81_out, buffer_82_out, buffer_83_out, buffer_84_out, buffer_85_out, buffer_86_out,
       buffer_87_out, buffer_88_out, buffer_89_out, buffer_90_out, buffer_91_out, buffer_92_out,
       buffer_93_out, buffer_94_out, buffer_95_out, buffer_96_out, buffer_97_out, buffer_98_out,
       buffer_99_out, buffer_100_out, buffer_101_out, buffer_102_out, buffer_103_out, buffer_104_out,
       buffer_105_out, buffer_106_out, buffer_107_out, buffer_108_out, buffer_109_out, buffer_110_out,
       buffer_111_out, buffer_112_out, buffer_113_out, buffer_114_out, buffer_115_out, buffer_116_out,
       buffer_117_out, buffer_118_out, buffer_119_out, buffer_120_out, buffer_121_out, buffer_122_out,
       buffer_123_out, buffer_124_out, buffer_125_out, buffer_126_out, buffer_127_out, buffer_128_out,
       buffer_129_out, buffer_130_out, buffer_131_out, buffer_132_out, buffer_133_out, buffer_134_out,
       buffer_135_out, buffer_136_out, buffer_137_out, buffer_138_out, buffer_139_out, buffer_140_out,
       buffer_141_out, buffer_142_out, buffer_143_out, buffer_144_out, buffer_145_out, buffer_146_out,
       buffer_147_out, buffer_148_out, buffer_149_out, buffer_150_out, buffer_151_out, buffer_152_out,
       buffer_153_out, buffer_154_out, buffer_155_out, buffer_156_out, buffer_157_out, buffer_158_out,
       buffer_159_out, buffer_160_out, buffer_161_out, buffer_162_out, buffer_163_out, buffer_164_out,
       buffer_165_out, buffer_166_out, buffer_167_out, buffer_168_out, buffer_169_out, buffer_170_out,
       buffer_171_out, buffer_172_out, buffer_173_out, buffer_175_out, buffer_176_out;

  buf buffer_1 (buffer_1_out, in_1);
  buf buffer_2 (buffer_2_out, buffer_23_out);
  buf buffer_3 (buffer_3_out, buffer_2_out);
  buf buffer_4 (buffer_4_out, buffer_3_out);
  buf buffer_5 (buffer_5_out, buffer_6_out);
  buf buffer_6 (buffer_6_out, buffer_32_out);
  buf buffer_7 (buffer_7_out, buffer_5_out);
  buf buffer_8 (buffer_8_out, buffer_9_out);
  buf buffer_9 (buffer_9_out, buffer_40_out);
  buf buffer_10 (buffer_10_out, buffer_8_out);
  buf buffer_11 (buffer_11_out, buffer_12_out);
  buf buffer_12 (buffer_12_out, buffer_47_out);
  buf buffer_13 (buffer_13_out, buffer_11_out);
  buf buffer_14 (buffer_14_out, buffer_56_out);
  buf buffer_15 (buffer_15_out, buffer_14_out);
  buf buffer_16 (buffer_16_out, buffer_15_out);
  buf buffer_17 (buffer_17_out, buffer_18_out);
  buf buffer_18 (buffer_18_out, buffer_19_out);
  buf buffer_19 (buffer_19_out, buffer_1_out);
  buf buffer_20 (buffer_20_out, buffer_17_out);
  buf buffer_21 (buffer_21_out, buffer_22_out);
  buf buffer_22 (buffer_22_out, buffer_67_out);
  buf buffer_23 (buffer_23_out, buffer_24_out);
  buf buffer_24 (buffer_24_out, buffer_21_out);
  buf buffer_25 (buffer_25_out, buffer_27_out);
  buf buffer_26 (buffer_26_out, buffer_25_out);
  buf buffer_27 (buffer_27_out, buffer_28_out);
  buf buffer_28 (buffer_28_out, buffer_4_out);
  buf buffer_29 (buffer_29_out, buffer_31_out);
  buf buffer_30 (buffer_30_out, buffer_76_out);
  buf buffer_31 (buffer_31_out, buffer_30_out);
  buf buffer_32 (buffer_32_out, buffer_29_out);
  buf buffer_33 (buffer_33_out, buffer_34_out);
  buf buffer_34 (buffer_34_out, buffer_35_out);
  buf buffer_35 (buffer_35_out, buffer_36_out);
  buf buffer_36 (buffer_36_out, buffer_7_out);
  buf buffer_37 (buffer_37_out, buffer_82_out);
  buf buffer_38 (buffer_38_out, buffer_37_out);
  buf buffer_39 (buffer_39_out, buffer_38_out);
  buf buffer_40 (buffer_40_out, buffer_39_out);
  buf buffer_41 (buffer_41_out, buffer_44_out);
  buf buffer_42 (buffer_42_out, buffer_10_out);
  buf buffer_43 (buffer_43_out, buffer_41_out);
  buf buffer_44 (buffer_44_out, buffer_42_out);
  buf buffer_45 (buffer_45_out, buffer_89_out);
  buf buffer_46 (buffer_46_out, buffer_45_out);
  buf buffer_47 (buffer_47_out, buffer_48_out);
  buf buffer_48 (buffer_48_out, buffer_46_out);
  buf buffer_49 (buffer_49_out, buffer_13_out);
  buf buffer_50 (buffer_50_out, buffer_51_out);
  buf buffer_51 (buffer_51_out, buffer_49_out);
  buf buffer_52 (buffer_52_out, buffer_50_out);
  buf buffer_53 (buffer_53_out, buffer_55_out);
  buf buffer_54 (buffer_54_out, buffer_53_out);
  buf buffer_55 (buffer_55_out, buffer_100_out);
  buf buffer_56 (buffer_56_out, buffer_54_out);
  buf buffer_57 (buffer_57_out, buffer_58_out);
  buf buffer_58 (buffer_58_out, buffer_16_out);
  buf buffer_59 (buffer_59_out, buffer_60_out);
  buf buffer_60 (buffer_60_out, buffer_57_out);
  buf buffer_61 (buffer_61_out, buffer_64_out);
  buf buffer_62 (buffer_62_out, buffer_61_out);
  buf buffer_63 (buffer_63_out, buffer_20_out);
  buf buffer_64 (buffer_64_out, buffer_63_out);
  buf buffer_65 (buffer_65_out, buffer_68_out);
  buf buffer_66 (buffer_66_out, buffer_111_out);
  buf buffer_67 (buffer_67_out, buffer_65_out);
  buf buffer_68 (buffer_68_out, buffer_66_out);
  buf buffer_69 (buffer_69_out, buffer_26_out);
  buf buffer_70 (buffer_70_out, buffer_69_out);
  buf buffer_71 (buffer_71_out, buffer_70_out);
  buf buffer_72 (buffer_72_out, buffer_71_out);
  buf buffer_73 (buffer_73_out, buffer_74_out);
  buf buffer_74 (buffer_74_out, buffer_75_out);
  buf buffer_75 (buffer_75_out, buffer_118_out);
  buf buffer_76 (buffer_76_out, buffer_73_out);
  buf buffer_77 (buffer_77_out, buffer_80_out);
  buf buffer_78 (buffer_78_out, buffer_77_out);
  buf buffer_79 (buffer_79_out, buffer_78_out);
  buf buffer_80 (buffer_80_out, buffer_33_out);
  buf buffer_81 (buffer_81_out, buffer_83_out);
  buf buffer_82 (buffer_82_out, buffer_84_out);
  buf buffer_83 (buffer_83_out, buffer_128_out);
  buf buffer_84 (buffer_84_out, buffer_81_out);
  buf buffer_85 (buffer_85_out, buffer_88_out);
  buf buffer_86 (buffer_86_out, buffer_85_out);
  buf buffer_87 (buffer_87_out, buffer_86_out);
  buf buffer_88 (buffer_88_out, buffer_43_out);
  buf buffer_89 (buffer_89_out, buffer_91_out);
  buf buffer_90 (buffer_90_out, buffer_133_out);
  buf buffer_91 (buffer_91_out, buffer_92_out);
  buf buffer_92 (buffer_92_out, buffer_90_out);
  buf buffer_93 (buffer_93_out, buffer_95_out);
  buf buffer_94 (buffer_94_out, buffer_52_out);
  buf buffer_95 (buffer_95_out, buffer_96_out);
  buf buffer_96 (buffer_96_out, buffer_94_out);
  buf buffer_97 (buffer_97_out, buffer_144_out);
  buf buffer_98 (buffer_98_out, buffer_99_out);
  buf buffer_99 (buffer_99_out, buffer_97_out);
  buf buffer_100 (buffer_100_out, buffer_98_out);
  buf buffer_101 (buffer_101_out, buffer_103_out);
  buf buffer_102 (buffer_102_out, buffer_59_out);
  buf buffer_103 (buffer_103_out, buffer_104_out);
  buf buffer_104 (buffer_104_out, buffer_102_out);
  buf buffer_105 (buffer_105_out, buffer_108_out);
  buf buffer_106 (buffer_106_out, buffer_105_out);
  buf buffer_107 (buffer_107_out, buffer_106_out);
  buf buffer_108 (buffer_108_out, buffer_62_out);
  buf buffer_109 (buffer_109_out, buffer_152_out);
  buf buffer_110 (buffer_110_out, buffer_112_out);
  buf buffer_111 (buffer_111_out, buffer_110_out);
  buf buffer_112 (buffer_112_out, buffer_109_out);
  buf buffer_113 (buffer_113_out, buffer_72_out);
  buf buffer_114 (buffer_114_out, buffer_115_out);
  buf buffer_115 (buffer_115_out, buffer_113_out);
  buf buffer_116 (buffer_116_out, buffer_114_out);
  buf buffer_117 (buffer_117_out, buffer_120_out);
  buf buffer_118 (buffer_118_out, buffer_117_out);
  buf buffer_119 (buffer_119_out, buffer_158_out);
  buf buffer_120 (buffer_120_out, buffer_119_out);
  buf buffer_121 (buffer_121_out, buffer_124_out);
  buf buffer_122 (buffer_122_out, buffer_123_out);
  buf buffer_123 (buffer_123_out, buffer_121_out);
  buf buffer_124 (buffer_124_out, buffer_79_out);
  buf buffer_125 (buffer_125_out, buffer_126_out);
  buf buffer_126 (buffer_126_out, buffer_163_out);
  buf buffer_127 (buffer_127_out, buffer_125_out);
  buf buffer_128 (buffer_128_out, buffer_127_out);
  buf buffer_129 (buffer_129_out, buffer_130_out);
  buf buffer_130 (buffer_130_out, buffer_87_out);
  buf buffer_131 (buffer_131_out, buffer_132_out);
  buf buffer_132 (buffer_132_out, buffer_129_out);
  buf buffer_133 (buffer_133_out, buffer_136_out);
  buf buffer_134 (buffer_134_out, buffer_135_out);
  buf buffer_135 (buffer_135_out, buffer_167_out);
  buf buffer_136 (buffer_136_out, buffer_134_out);
  buf buffer_137 (buffer_137_out, buffer_93_out);
  buf buffer_138 (buffer_138_out, buffer_140_out);
  buf buffer_139 (buffer_139_out, buffer_137_out);
  buf buffer_140 (buffer_140_out, buffer_139_out);
  buf buffer_141 (buffer_141_out, buffer_143_out);
  buf buffer_142 (buffer_142_out, buffer_172_out);
  buf buffer_143 (buffer_143_out, buffer_142_out);
  buf buffer_144 (buffer_144_out, buffer_141_out);
  buf buffer_145 (buffer_145_out, buffer_146_out);
  buf buffer_146 (buffer_146_out, buffer_148_out);
  buf buffer_147 (buffer_147_out, buffer_145_out);
  buf buffer_148 (buffer_148_out, buffer_101_out);
  buf buffer_149 (buffer_149_out, buffer_107_out);
  buf buffer_150 (buffer_150_out, buffer_151_out);
  buf buffer_151 (buffer_151_out, buffer_149_out);
  buf buffer_152 (buffer_152_out, buffer_153_out);
  buf buffer_153 (buffer_153_out, buffer_150_out);
  buf buffer_154 (buffer_154_out, buffer_155_out);
  buf buffer_155 (buffer_155_out, buffer_116_out);
  buf buffer_156 (buffer_156_out, buffer_154_out);
  buf buffer_157 (buffer_157_out, buffer_156_out);
  buf buffer_158 (buffer_158_out, buffer_157_out);
  buf buffer_159 (buffer_159_out, buffer_160_out);
  buf buffer_160 (buffer_160_out, buffer_161_out);
  buf buffer_161 (buffer_161_out, buffer_122_out);
  buf buffer_162 (buffer_162_out, buffer_159_out);
  buf buffer_163 (buffer_163_out, buffer_162_out);
  buf buffer_164 (buffer_164_out, buffer_131_out);
  buf buffer_165 (buffer_165_out, buffer_164_out);
  buf buffer_166 (buffer_166_out, buffer_165_out);
  buf buffer_167 (buffer_167_out, buffer_168_out);
  buf buffer_168 (buffer_168_out, buffer_166_out);
  buf buffer_169 (buffer_169_out, buffer_138_out);
  buf buffer_170 (buffer_170_out, buffer_169_out);
  buf buffer_171 (buffer_171_out, buffer_170_out);
  buf buffer_172 (buffer_172_out, buffer_173_out);
  buf buffer_173 (buffer_173_out, buffer_171_out);
  buf buffer_174 (out_2, buffer_175_out);
  buf buffer_175 (buffer_175_out, buffer_176_out);
  buf buffer_176 (buffer_176_out, buffer_147_out);
endmodule

module _8_INC (
  input  in_1,
  input  [7:0] in_2,
  output [7:0] out_3,
  output out_4
);

  wire n1_ha_1_out_4, n1_ha_2_out_4, n1_ha_3_out_4, n1_ha_4_out_4, n1_ha_5_out_4, n1_ha_6_out_4,
       n1_ha_7_out_4;

  _1_HA u_1_ha_1 (.out_3(out_3[0]), .out_4(n1_ha_1_out_4), .in_1(in_1), .in_2(in_2[0]));
  _1_HA u_1_ha_2 (.out_3(out_3[1]), .out_4(n1_ha_2_out_4), .in_1(n1_ha_1_out_4), .in_2(in_2[1]));
  _1_HA u_1_ha_3 (.out_3(out_3[2]), .out_4(n1_ha_3_out_4), .in_1(n1_ha_2_out_4), .in_2(in_2[2]));
  _1_HA u_1_ha_4 (.out_3(out_3[3]), .out_4(n1_ha_4_out_4), .in_1(n1_ha_3_out_4), .in_2(in_2[3]));
  _1_HA u_1_ha_5 (.out_3(out_3[4]), .out_4(n1_ha_5_out_4), .in_1(n1_ha_4_out_4), .in_2(in_2[4]));
  _1_HA u_1_ha_6 (.out_3(out_3[5]), .out_4(n1_ha_6_out_4), .in_1(n1_ha_5_out_4), .in_2(in_2[5]));
  _1_HA u_1_ha_7 (.out_3(out_3[6]), .out_4(n1_ha_7_out_4), .in_1(n1_ha_6_out_4), .in_2(in_2[6]));
  _1_HA u_1_ha_8 (.out_3(out_3[7]), .out_4(out_4), .in_1(n1_ha_7_out_4), .in_2(in_2[7]));
endmodule

module _4__2_Deco (
  input  in_1,
  input  in_2,
  input  in_3,
  input  in_4,
  input  in_5,
  output out_6,
  output out_7,
  output out_8
);

  wire and_1_out, and_3_out, and_6_out, not_1_out, not_2_out, not_3_out, not_4_out, not_5_out, not_6_out,
       not_7_out, not_8_out, not_9_out, not_10_out;

  not not_1 (not_1_out, in_3);
  not not_2 (not_2_out, in_2);
  not not_3 (not_3_out, in_4);
  and and_1 (and_1_out, not_2_out, not_1_out, not_3_out, not_8_out);
  and and_2 (out_6, in_1, and_1_out);
  not not_4 (not_4_out, in_4);
  not not_5 (not_5_out, in_3);
  not not_6 (not_6_out, in_5);
  not not_7 (not_7_out, in_2);
  not not_8 (not_8_out, in_5);
  and and_3 (and_3_out, in_2, not_5_out, not_4_out, not_6_out);
  and and_4 (out_8, in_1, and_6_out);
  and and_5 (out_7, in_1, and_3_out);
  not not_9 (not_9_out, in_4);
  not not_10 (not_10_out, in_5);
  and and_6 (and_6_out, not_7_out, in_3, not_9_out, not_10_out);
endmodule
module CPU_Mem (
  input  [3:0] RES,
  input  [3:0] Read_1,
  input  [3:0] Read_2,
  input  RES_All,
  input  [3:0] Write,
  input  [7:0] in_6,
  output [7:0] Out_1,
  output [7:0] Out_2
);

  wire n1_shortdelay_1_out_2, n1_shortdelay_2_out_2, n1_shortdelay_3_out_2, n1_shortdelay_4_out_2,
       n1_shortdelay_5_out_2, n1_shortdelay_6_out_2, or_1_out, or_3_out, or_6_out, or_7_out, or_8_out;
  wire [7:0] n4_bin_hex_3_out_6, n4_bin_hex_4_out_14, n8_ram_clk_1_out_12, n8_ram_clk_2_out_12,
       n8_ram_clk_3_out_12, n8_ram_clk_4_out_12, n8_ram_clk_5_out_12, n8_ram_clk_6_out_12,
       n8_ram_clk_7_out_12, n8_ram_clk_8_out_12, n8_ram_clk_9_out_12, n8_ram_clk_10_out_12,
       n8_ram_clk_11_out_12, n8_ram_clk_12_out_12, n8_ram_clk_13_out_12, n8_ram_clk_14_out_12,
       n8_ram_clk_15_out_12, or_4_out, or_5_out;
  wire [15:0] n4_bin_hex_1_out_6, n4_bin_hex_2_out_6, or_2_out;

  or or_1 (or_1_out, RES[0], RES[1], RES[2], RES[3]);
  assign or_2_out = n4_bin_hex_1_out_6 | {16{RES_All}};  // OR_Gate or_2, 16 bits wide
  _1_ShortDelay u_1_shortdelay_1 (.in_1(or_1_out), .out_2(n1_shortdelay_1_out_2));
  _4_Bin_Hex u_4_bin_hex_1 (
    .in_2(RES[0]), .in_3(RES[1]), .in_4(RES[2]), .in_5(RES[3]), .out_6(n4_bin_hex_1_out_6[0]),
    .out_7(n4_bin_hex_1_out_6[1]), .out_8(n4_bin_hex_1_out_6[2]), .out_9(n4_bin_hex_1_out_6[3]),
    .out_10(n4_bin_hex_1_out_6[4]), .out_11(n4_bin_hex_1_out_6[5]), .out_12(n4_bin_hex_1_out_6[6]),
    .out_13(n4_bin_hex_1_out_6[7]), .out_14(n4_bin_hex_1_out_6[8]), .out_15(n4_bin_hex_1_out_6[9]),
    .out_16(n4_bin_hex_1_out_6[10]), .out_17(n4_bin_hex_1_out_6[11]), .out_18(n4_bin_hex_1_out_6[12]),
    .out_19(n4_bin_hex_1_out_6[13]), .out_20(n4_bin_hex_1_out_6[14]), .out_21(n4_bin_hex_1_out_6[15]),
    .in_1(n1_shortdelay_1_out_2));
  _8_RAM_CLK u_8_ram_clk_1 (
    .out_12(n8_ram_clk_1_out_12[0]), .out_13(n8_ram_clk_1_out_12[1]), .out_14(n8_ram_clk_1_out_12[2]),
    .out_15(n8_ram_clk_1_out_12[3]), .out_16(n8_ram_clk_1_out_12[4]), .out_17(n8_ram_clk_1_out_12[5]),
    .out_18(n8_ram_clk_1_out_12[6]), .out_19(n8_ram_clk_1_out_12[7]), .in_11(n4_bin_hex_3_out_6[4]),
    .in_2(in_6[0]), .in_3(in_6[1]), .in_4(in_6[2]), .in_5(in_6[3]), .in_6(in_6[4]), .in_7(in_6[5]),
    .in_8(in_6[6]), .in_9(in_6[7]), .in_10(n4_bin_hex_2_out_6[4]), .in_1(or_2_out[4]));
  _8_RAM_CLK u_8_ram_clk_2 (
    .out_12(n8_ram_clk_2_out_12[0]), .out_13(n8_ram_clk_2_out_12[1]), .out_14(n8_ram_clk_2_out_12[2]),
    .out_15(n8_ram_clk_2_out_12[3]), .out_16(n8_ram_clk_2_out_12[4]), .out_17(n8_ram_clk_2_out_12[5]),
    .out_18(n8_ram_clk_2_out_12[6]), .out_19(n8_ram_clk_2_out_12[7]), .in_11(n4_bin_hex_4_out_14[0]),
    .in_2(in_6[0]), .in_3(in_6[1]), .in_4(in_6[2]), .in_5(in_6[3]), .in_6(in_6[4]), .in_7(in_6[5]),
    .in_8(in_6[6]), .in_9(in_6[7]), .in_10(n4_bin_hex_2_out_6[8]), .in_1(or_2_out[8]));
  _8_RAM_CLK u_8_ram_clk_3 (
    .out_12(n8_ram_clk_3_out_12[0]), .out_13(n8_ram_clk_3_out_12[1]), .out_14(n8_ram_clk_3_out_12[2]),
    .out_15(n8_ram_clk_3_out_12[3]), .out_16(n8_ram_clk_3_out_12[4]), .out_17(n8_ram_clk_3_out_12[5]),
    .out_18(n8_ram_clk_3_out_12[6]), .out_19(n8_ram_clk_3_out_12[7]), .in_11(n4_bin_hex_4_out_14[4]),
    .in_2(in_6[0]), .in_3(in_6[1]), .in_4(in_6[2]), .in_5(in_6[3]), .in_6(in_6[4]), .in_7(in_6[5]),
    .in_8(in_6[6]), .in_9(in_6[7]), .in_10(n4_bin_hex_2_out_6[12]), .in_1(or_2_out[12]));
  _8_RAM_CLK u_8_ram_clk_4 (
    .out_12(n8_ram_clk_4_out_12[0]), .out_13(n8_ram_clk_4_out_12[1]), .out_14(n8_ram_clk_4_out_12[2]),
    .out_15(n8_ram_clk_4_out_12[3]), .out_16(n8_ram_clk_4_out_12[4]), .out_17(n8_ram_clk_4_out_12[5]),
    .out_18(n8_ram_clk_4_out_12[6]), .out_19(n8_ram_clk_4_out_12[7]), .in_11(n4_bin_hex_3_out_6[1]),
    .in_2(in_6[0]), .in_3(in_6[1]), .in_4(in_6[2]), .in_5(in_6[3]), .in_6(in_6[4]), .in_7(in_6[5]),
    .in_8(in_6[6]), .in_9(in_6[7]), .in_10(n4_bin_hex_2_out_6[1]), .in_1(or_2_out[1]));
  _8_RAM_CLK u_8_ram_clk_5 (
    .out_12(n8_ram_clk_5_out_12[0]), .out_13(n8_ram_clk_5_out_12[1]), .out_14(n8_ram_clk_5_out_12[2]),
    .out_15(n8_ram_clk_5_out_12[3]), .out_16(n8_ram_clk_5_out_12[4]), .out_17(n8_ram_clk_5_out_12[5]),
    .out_18(n8_ram_clk_5_out_12[6]), .out_19(n8_ram_clk_5_out_12[7]), .in_11(n4_bin_hex_3_out_6[5]),
    .in_2(in_6[0]), .in_3(in_6[1]), .in_4(in_6[2]), .in_5(in_6[3]), .in_6(in_6[4]), .in_7(in_6[5]),
    .in_8(in_6[6]), .in_9(in_6[7]), .in_10(n4_bin_hex_2_out_6[5]), .in_1(or_2_out[5]));
  _8_RAM_CLK u_8_ram_clk_6 (
    .out_12(n8_ram_clk_6_out_12[0]), .out_13(n8_ram_clk_6_out_12[1]), .out_14(n8_ram_clk_6_out_12[2]),
    .out_15(n8_ram_clk_6_out_12[3]), .out_16(n8_ram_clk_6_out_12[4]), .out_17(n8_ram_clk_6_out_12[5]),
    .out_18(n8_ram_clk_6_out_12[6]), .out_19(n8_ram_clk_6_out_12[7]), .in_11(n4_bin_hex_4_out_14[1]),
    .in_2(in_6[0]), .in_3(in_6[1]), .in_4(in_6[2]), .in_5(in_6[3]), .in_6(in_6[4]), .in_7(in_6[5]),
    .in_8(in_6[6]), .in_9(in_6[7]), .in_10(n4_bin_hex_2_out_6[9]), .in_1(or_2_out[9]));
  _8_RAM_CLK u_8_ram_clk_7 (
    .out_12(n8_ram_clk_7_out_12[0]), .out_13(n8_ram_clk_7_out_12[1]), .out_14(n8_ram_clk_7_out_12[2]),
    .out_15(n8_ram_clk_7_out_12[3]), .out_16(n8_ram_clk_7_out_12[4]), .out_17(n8_ram_clk_7_out_12[5]),
    .out_18(n8_ram_clk_7_out_12[6]), .out_19(n8_ram_clk_7_out_12[7]), .in_11(n4_bin_hex_4_out_14[5]),
    .in_2(in_6[0]), .in_3(in_6[1]), .in_4(in_6[2]), .in_5(in_6[3]), .in_6(in_6[4]), .in_7(in_6[5]),
    .in_8(in_6[6]), .in_9(in_6[7]), .in_10(n4_bin_hex_2_out_6[13]), .in_1(or_2_out[13]));
  _8_RAM_CLK u_8_ram_clk_8 (
    .out_12(n8_ram_clk_8_out_12[0]), .out_13(n8_ram_clk_8_out_12[1]), .out_14(n8_ram_clk_8_out_12[2]),
    .out_15(n8_ram_clk_8_out_12[3]), .out_16(n8_ram_clk_8_out_12[4]), .out_17(n8_ram_clk_8_out_12[5]),
    .out_18(n8_ram_clk_8_out_12[6]), .out_19(n8_ram_clk_8_out_12[7]), .in_11(n4_bin_hex_3_out_6[2]),
    .in_2(in_6[0]), .in_3(in_6[1]), .in_4(in_6[2]), .in_5(in_6[3]), .in_6(in_6[4]), .in_7(in_6[5]),
    .in_8(in_6[6]), .in_9(in_6[7]), .in_10(n4_bin_hex_2_out_6[2]), .in_1(or_2_out[2]));
  _8_RAM_CLK u_8_ram_clk_9 (
    .out_12(n8_ram_clk_9_out_12[0]), .out_13(n8_ram_clk_9_out_12[1]), .out_14(n8_ram_clk_9_out_12[2]),
    .out_15(n8_ram_clk_9_out_12[3]), .out_16(n8_ram_clk_9_out_12[4]), .out_17(n8_ram_clk_9_out_12[5]),
    .out_18(n8_ram_clk_9_out_12[6]), .out_19(n8_ram_clk_9_out_12[7]), .in_11(n4_bin_hex_3_out_6[6]),
    .in_2(in_6[0]), .in_3(in_6[1]), .in_4(in_6[2]), .in_5(in_6[3]), .in_6(in_6[4]), .in_7(in_6[5]),
    .in_8(in_6[6]), .in_9(in_6[7]), .in_10(n4_bin_hex_2_out_6[6]), .in_1(or_2_out[6]));
  _8_RAM_CLK u_8_ram_clk_10 (
    .out_12(n8_ram_clk_10_out_12[0]), .out_13(n8_ram_clk_10_out_12[1]), .out_14(n8_ram_clk_10_out_12[2]),
    .out_15(n8_ram_clk_10_out_12[3]), .out_16(n8_ram_clk_10_out_12[4]), .out_17(n8_ram_clk_10_out_12[5]),
    .out_18(n8_ram_clk_10_out_12[6]), .out_19(n8_ram_clk_10_out_12[7]), .in_11(n4_bin_hex_4_out_14[2]),
    .in_2(in_6[0]), .in_3(in_6[1]), .in_4(in_6[2]), .in_5(in_6[3]), .in_6(in_6[4]), .in_7(in_6[5]),
    .in_8(in_6[6]), .in_9(in_6[7]), .in_10(n4_bin_hex_2_out_6[10]), .in_1(or_2_out[10]));
  _8_RAM_CLK u_8_ram_clk_11 (
    .out_12(n8_ram_clk_11_out_12[0]), .out_13(n8_ram_clk_11_out_12[1]), .out_14(n8_ram_clk_11_out_12[2]),
    .out_15(n8_ram_clk_11_out_12[3]), .out_16(n8_ram_clk_11_out_12[4]), .out_17(n8_ram_clk_11_out_12[5]),
    .out_18(n8_ram_clk_11_out_12[6]), .out_19(n8_ram_clk_11_out_12[7]), .in_11(n4_bin_hex_4_out_14[6]),
    .in_2(in_6[0]), .in_3(in_6[1]), .in_4(in_6[2]), .in_5(in_6[3]), .in_6(in_6[4]), .in_7(in_6[5]),
    .in_8(in_6[6]), .in_9(in_6[7]), .in_10(n4_bin_hex_2_out_6[14]), .in_1(or_2_out[14]));
  _8_RAM_CLK u_8_ram_clk_12 (
    .out_12(n8_ram_clk_12_out_12[0]), .out_13(n8_ram_clk_12_out_12[1]), .out_14(n8_ram_clk_12_out_12[2]),
    .out_15(n8_ram_clk_12_out_12[3]), .out_16(n8_ram_clk_12_out_12[4]), .out_17(n8_ram_clk_12_out_12[5]),
    .out_18(n8_ram_clk_12_out_12[6]), .out_19(n8_ram_clk_12_out_12[7]), .in_11(n4_bin_hex_3_out_6[3]),
    .in_2(in_6[0]), .in_3(in_6[1]), .in_4(in_6[2]), .in_5(in_6[3]), .in_6(in_6[4]), .in_7(in_6[5]),
    .in_8(in_6[6]), .in_9(in_6[7]), .in_10(n4_bin_hex_2_out_6[3]), .in_1(or_2_out[3]));
  _8_RAM_CLK u_8_ram_clk_13 (
    .out_12(n8_ram_clk_13_out_12[0]), .out_13(n8_ram_clk_13_out_12[1]), .out_14(n8_ram_clk_13_out_12[2]),
    .out_15(n8_ram_clk_13_out_12[3]), .out_16(n8_ram_clk_13_out_12[4]), .out_17(n8_ram_clk_13_out_12[5]),
    .out_18(n8_ram_clk_13_out_12[6]), .out_19(n8_ram_clk_13_out_12[7]), .in_11(n4_bin_hex_3_out_6[7]),
    .in_2(in_6[0]), .in_3(in_6[1]), .in_4(in_6[2]), .in_5(in_6[3]), .in_6(in_6[4]), .in_7(in_6[5]),
    .in_8(in_6[6]), .in_9(in_6[7]), .in_10(n4_bin_hex_2_out_6[7]), .in_1(or_2_out[7]));
  _8_RAM_CLK u_8_ram_clk_14 (
    .out_12(n8_ram_clk_14_out_12[0]), .out_13(n8_ram_clk_14_out_12[1]), .out_14(n8_ram_clk_14_out_12[2]),
    .out_15(n8_ram_clk_14_out_12[3]), .out_16(n8_ram_clk_14_out_12[4]), .out_17(n8_ram_clk_14_out_12[5]),
    .out_18(n8_ram_clk_14_out_12[6]), .out_19(n8_ram_clk_14_out_12[7]), .in_11(n4_bin_hex_4_out_14[3]),
    .in_2(in_6[0]), .in_3(in_6[1]), .in_4(in_6[2]), .in_5(in_6[3]), .in_6(in_6[4]), .in_7(in_6[5]),
    .in_8(in_6[6]), .in_9(in_6[7]), .in_10(n4_bin_hex_2_out_6[11]), .in_1(or_2_out[11]));
  _8_RAM_CLK u_8_ram_clk_15 (
    .out_12(n8_ram_clk_15_out_12[0]), .out_13(n8_ram_clk_15_out_12[1]), .out_14(n8_ram_clk_15_out_12[2]),
    .out_15(n8_ram_clk_15_out_12[3]), .out_16(n8_ram_clk_15_out_12[4]), .out_17(n8_ram_clk_15_out_12[5]),
    .out_18(n8_ram_clk_15_out_12[6]), .out_19(n8_ram_clk_15_out_12[7]), .in_11(n4_bin_hex_4_out_14[7]),
    .in_2(in_6[0]), .in_3(in_6[1]), .in_4(in_6[2]), .in_5(in_6[3]), .in_6(in_6[4]), .in_7(in_6[5]),
    .in_8(in_6[6]), .in_9(in_6[7]), .in_10(n4_bin_hex_2_out_6[15]), .in_1(or_2_out[15]));
  // Probe on n8_ram_clk_15_out_12
  _4_Bin_Hex u_4_bin_hex_2 (
    .in_2(Write[0]), .in_3(Write[1]), .in_4(Write[2]), .in_5(Write[3]), .out_6(n4_bin_hex_2_out_6[0]),
    .out_7(n4_bin_hex_2_out_6[1]), .out_8(n4_bin_hex_2_out_6[2]), .out_9(n4_bin_hex_2_out_6[3]),
    .out_10(n4_bin_hex_2_out_6[4]), .out_11(n4_bin_hex_2_out_6[5]), .out_12(n4_bin_hex_2_out_6[6]),
    .out_13(n4_bin_hex_2_out_6[7]), .out_14(n4_bin_hex_2_out_6[8]), .out_15(n4_bin_hex_2_out_6[9]),
    .out_16(n4_bin_hex_2_out_6[10]), .out_17(n4_bin_hex_2_out_6[11]), .out_18(n4_bin_hex_2_out_6[12]),
    .out_19(n4_bin_hex_2_out_6[13]), .out_20(n4_bin_hex_2_out_6[14]), .out_21(n4_bin_hex_2_out_6[15]),
    .in_1(n1_shortdelay_2_out_2));
  _4_Bin_Hex u_4_bin_hex_3 (
    .in_2(Read_1[0]), .in_3(Read_1[1]), .in_4(Read_1[2]), .in_5(Read_1[3]), .out_6(n4_bin_hex_3_out_6[0]),
    .out_7(n4_bin_hex_3_out_6[1]), .out_8(n4_bin_hex_3_out_6[2]), .out_9(n4_bin_hex_3_out_6[3]),
    .out_10(n4_bin_hex_3_out_6[4]), .out_11(n4_bin_hex_3_out_6[5]), .out_12(n4_bin_hex_3_out_6[6]),
    .out_13(n4_bin_hex_3_out_6[7]), .in_1(n1_shortdelay_4_out_2));  // open: out_14, out_15, out_16, out_17, out_18, out_19, out_20, out_21
  _4_Bin_Hex u_4_bin_hex_4 (
    .in_2(Read_2[0]), .in_3(Read_2[1]), .in_4(Read_2[2]), .in_5(Read_2[3]), .out_14(n4_bin_hex_4_out_14[0]),
    .out_15(n4_bin_hex_4_out_14[1]), .out_16(n4_bin_hex_4_out_14[2]), .out_17(n4_bin_hex_4_out_14[3]),
    .out_18(n4_bin_hex_4_out_14[4]), .out_19(n4_bin_hex_4_out_14[5]), .out_20(n4_bin_hex_4_out_14[6]),
    .out_21(n4_bin_hex_4_out_14[7]), .in_1(n1_shortdelay_5_out_2));  // open: out_6, out_7, out_8, out_9, out_10, out_11, out_12, out_13
  _1_ShortDelay u_1_shortdelay_2 (.in_1(or_3_out), .out_2(n1_shortdelay_2_out_2));
  or or_3 (or_3_out, Write[3], Write[2], Write[0], Write[1]);
  assign or_4_out = n8_ram_clk_2_out_12 | n8_ram_clk_6_out_12 | n8_ram_clk_10_out_12 | n8_ram_clk_14_out_12 | n8_ram_clk_15_out_12 | n8_ram_clk_11_out_12 | n8_ram_clk_7_out_12 | n8_ram_clk_3_out_12;  // OR_Gate or_4, 8 bits wide
  _1_ShortDelay u_1_shortdelay_3 (.in_1(or_7_out), .out_2(n1_shortdelay_3_out_2));
  assign or_5_out = {8{1'b0}} | n8_ram_clk_1_out_12 | n8_ram_clk_4_out_12 | n8_ram_clk_5_out_12 | n8_ram_clk_8_out_12 | n8_ram_clk_9_out_12 | n8_ram_clk_12_out_12 | n8_ram_clk_13_out_12;  // OR_Gate or_5, 8 bits wide
  _8_BUF u_8_buf_1 (.in_2(n1_shortdelay_3_out_2), .in_1(or_4_out), .out_3(Out_2));
  _1_ShortDelay u_1_shortdelay_4 (.in_1(or_6_out), .out_2(n1_shortdelay_4_out_2));
  or or_6 (or_6_out, Read_1[3], Read_1[2], Read_1[1], Read_1[0]);
  or or_7 (or_7_out, Read_1[3], Read_1[2], Read_1[1], Read_1[0], Read_2[3], Read_2[2], Read_2[1], Read_2[0]);
  _1_ShortDelay u_1_shortdelay_5 (.in_1(or_8_out), .out_2(n1_shortdelay_5_out_2));
  or or_8 (or_8_out, Read_2[3], Read_2[2], Read_2[1], Read_2[0]);
  // Probe on or_5_out
  _1_ShortDelay u_1_shortdelay_6 (.in_1(or_7_out), .out_2(n1_shortdelay_6_out_2));
  // Probe on Out_2
  // Probe on Out_1
  _8_BUF u_8_buf_2 (.in_2(n1_shortdelay_6_out_2), .in_1(or_5_out), .out_3(Out_1));
  // Probe on Out_2
endmodule

module Input_Module (
  input  [3:0] in_1,
  input  in_2,
  input  [7:0] iA,
  input  [7:0] iB,
  output [7:0] out_5
);

  wire n4_2_deco_1_out_7, n4_2_deco_1_out_8;
  wire [7:0] n8_buf_1_out_3, n8_buf_2_out_3;

  _8_BUF u_8_buf_1 (.in_2(n4_2_deco_1_out_7), .in_1(iA), .out_3(n8_buf_1_out_3));
  _8_BUF u_8_buf_2 (.in_2(n4_2_deco_1_out_8), .in_1(iB), .out_3(n8_buf_2_out_3));
  _4__2_Deco u_4_2_deco_1 (
    .in_2(in_1[0]), .in_3(in_1[1]), .in_4(in_1[2]), .in_5(in_1[3]), .in_1(in_2), .out_7(n4_2_deco_1_out_7),
    .out_8(n4_2_deco_1_out_8));  // open: out_6
  assign out_5 = n8_buf_2_out_3 | n8_buf_1_out_3;  // OR_Gate or_1, 8 bits wide
endmodule

module Condition_Checker (
  input  [3:0] in_1,
  input  in_2,
  input  in_3,
  input  in_4,
  input  in_5,
  input  [7:0] in_6,
  input  [2:0] in_7,
  input  [7:0] in_8,
  input  [7:0] in_9,
  output [3:0] out_10,
  output [3:0] out_11,
  output out_12
);

  wire and_1_out, and_2_out, and_3_out, and_4_out, n1_delay_1_out_2, n1_delay_2_out_2, n1_delay_3_out_2,
       n1_delay_4_out_2, n8_comparator_1_out_3, n8_comparator_1_out_4, n8_comparator_1_out_5, not_1_out;
  wire [7:0] or_1_out;

  assign or_1_out = in_6 | in_9;  // OR_Gate or_1, 8 bits wide
  _1_Delay u_1_delay_1 (.in_1(in_2), .out_2(n1_delay_1_out_2));
  _1_Delay u_1_delay_2 (.in_1(in_5), .out_2(n1_delay_2_out_2));
  _1_Delay u_1_delay_3 (.in_1(in_4), .out_2(n1_delay_3_out_2));
  _1_Delay u_1_delay_4 (.in_1(in_3), .out_2(n1_delay_4_out_2));
  _8_Comparator u_8_comparator_1 (
    .in_1(in_8), .in_2(or_1_out), .out_3(n8_comparator_1_out_3), .out_4(n8_comparator_1_out_4),
    .out_5(n8_comparator_1_out_5));
  not not_1 (not_1_out, n8_comparator_1_out_4);
  and and_1 (and_1_out, n1_delay_4_out_2, n8_comparator_1_out_3);
  and and_2 (and_2_out, n1_delay_1_out_2, n8_comparator_1_out_4);
  and and_3 (and_3_out, not_1_out, n1_delay_2_out_2);
  and and_4 (and_4_out, n8_comparator_1_out_5, n1_delay_3_out_2);
  or or_2 (out_12, and_4_out, and_3_out, and_2_out, and_1_out);

  assign out_10 = {1'b0, in_7};
  assign out_11 = in_1;
endmodule

module Comp2 (
  input  [3:0] in_1,
  input  [3:0] in_2,
  input  in_3,
  input  in_4,
  input  in_5,
  output out_6,
  output out_7,
  output out_8
);

  wire nand_1_out, nand_2_out, nand_3_out, nand_4_out, nand_5_out, nand_6_out, nand_7_out, nand_8_out,
       nand_9_out, nand_10_out, nand_11_out, nand_12_out, not_1_out, not_2_out, not_3_out, not_4_out,
       not_5_out, not_6_out, not_7_out, not_8_out, not_9_out, not_10_out, not_11_out, not_12_out, not_13_out,
       not_14_out, not_15_out, not_16_out, not_17_out, not_18_out, not_19_out, or_1_out, or_2_out, or_3_out,
       or_4_out;

  not not_1 (not_1_out, in_2[3]);
  not not_2 (not_2_out, not_1_out);
  not not_3 (not_3_out, in_1[3]);
  not not_4 (not_4_out, not_3_out);
  not not_5 (not_5_out, not_6_out);
  not not_6 (not_6_out, in_2[2]);
  not not_7 (not_7_out, not_8_out);
  not not_8 (not_8_out, in_1[2]);
  not not_9 (not_9_out, in_2[1]);
  not not_10 (not_10_out, not_9_out);
  not not_11 (not_11_out, in_1[1]);
  not not_12 (not_12_out, not_11_out);
  not not_13 (not_13_out, not_14_out);
  not not_14 (not_14_out, in_2[0]);
  not not_15 (not_15_out, in_1[0]);
  not not_16 (not_16_out, not_15_out);
  not not_17 (not_17_out, in_3);
  not not_18 (not_18_out, in_4);
  not not_19 (not_19_out, in_5);
  nand nand_1 (nand_1_out, not_2_out, not_3_out);
  nand nand_2 (nand_2_out, not_1_out, not_4_out);
  nand nand_3 (nand_3_out, not_5_out, not_8_out);
  nand nand_4 (nand_4_out, not_6_out, not_7_out);
  nand nand_5 (nand_5_out, not_10_out, not_11_out);
  nand nand_6 (nand_6_out, not_9_out, not_12_out);
  nand nand_7 (nand_7_out, not_13_out, not_15_out);
  nand nand_8 (nand_8_out, not_14_out, not_16_out);
  nand nand_9 (nand_9_out, nand_1_out, nand_2_out);
  nand nand_10 (nand_10_out, nand_3_out, nand_4_out);
  nand nand_11 (nand_11_out, nand_5_out, nand_6_out);
  nand nand_12 (nand_12_out, nand_7_out, nand_8_out);
  or or_1 (or_1_out, nand_9_out, nand_3_out);
  or or_2 (or_2_out, nand_9_out, nand_10_out, nand_5_out);
  or or_3 (or_3_out, nand_9_out, nand_10_out, nand_11_out, nand_7_out);
  or or_4 (or_4_out, nand_9_out, nand_10_out, nand_11_out, nand_12_out, not_17_out);
  nor nor_1 (out_7, nand_9_out, nand_10_out, nand_11_out, nand_12_out, not_18_out);
  nand nand_13 (out_6, nand_1_out, or_1_out, or_2_out, or_3_out, or_4_out);
  nor nor_2 (out_8, out_6, out_7, not_19_out);
endmodule

module Output_Module (
  input  in_1,
  input  in_2,
  input  [7:0] in_3,
  input  [7:0] in_4,
  output [3:0] out_5,
  output [3:0] out_6,
  output [3:0] out_7,
  output [3:0] out_8,
  output out_9,
  output out_10,
  output out_11,
  output out_12
);

  wire [7:0] n8_buf_1_out_3, n8_buf_2_out_3;

  _8_MemLatch u_8_memlatch_1 (.in_1(in_1), .out_3({out_5, out_6}), .in_2(n8_buf_1_out_3));
  _8_BUF u_8_buf_1 (.in_2(in_2), .in_1(in_4), .out_3(n8_buf_1_out_3));
  _8_MemLatch u_8_memlatch_2 (.in_1(in_1), .out_3({out_7, out_8}), .in_2(n8_buf_2_out_3));
  _8_BUF u_8_buf_2 (.in_2(in_2), .in_1(in_3), .out_3(n8_buf_2_out_3));

  assign out_9 = 1'b0;
  assign out_10 = 1'b0;
  assign out_11 = 1'b0;
  assign out_12 = 1'b0;
endmodule

module _4_Splitter (
  input  [3:0] in_1,
  output [3:0] out_2,
  output [3:0] out_3
);

  wire not_2_out;

  not not_1 (out_2[3], not_2_out);
  and and_1 (out_3[2], in_1[2], not_2_out);
  not not_2 (not_2_out, in_1[3]);
  and and_2 (out_2[2], in_1[2], in_1[3]);
  and and_3 (out_3[1], in_1[1], not_2_out);
  and and_4 (out_3[0], in_1[0], not_2_out);
  and and_5 (out_2[0], in_1[0], in_1[3]);
  and and_6 (out_2[1], in_1[1], in_1[3]);

  assign out_3[3] = 1'b0;
endmodule

module _8_MemLatch (
  input  in_1,
  input  [7:0] in_2,
  output [7:0] out_3
);

  RS_NOR rs_nor_1 (.in_1(in_2[7]), .in_2(in_1), .out_4(out_3[7]));  // open: out_3
  RS_NOR rs_nor_2 (.in_1(in_2[6]), .in_2(in_1), .out_4(out_3[6]));  // open: out_3
  RS_NOR rs_nor_3 (.in_1(in_2[5]), .in_2(in_1), .out_4(out_3[5]));  // open: out_3
  RS_NOR rs_nor_4 (.in_1(in_2[4]), .in_2(in_1), .out_4(out_3[4]));  // open: out_3
  RS_NOR rs_nor_5 (.in_1(in_2[3]), .in_2(in_1), .out_4(out_3[3]));  // open: out_3
  RS_NOR rs_nor_6 (.in_1(in_2[2]), .in_2(in_1), .out_4(out_3[2]));  // open: out_3
  RS_NOR rs_nor_7 (.in_1(in_2[1]), .in_2(in_1), .out_4(out_3[1]));  // open: out_3
  RS_NOR rs_nor_8 (.in_1(in_2[0]), .in_2(in_1), .out_4(out_3[0]));  // open: out_3
endmodule

module _1_ShortDelay (
  input  in_1,
  output out_2
);

  wire buffer_1_out, buffer_2_out, buffer_3_out, buffer_4_out, buffer_5_out, buffer_6_out, buffer_7_out,
       buffer_8_out, buffer_9_out, buffer_10_out, buffer_11_out, buffer_12_out, buffer_13_out, buffer_14_out,
       buffer_15_out, buffer_16_out, buffer_17_out, buffer_18_out, buffer_19_out, buffer_20_out,
       buffer_21_out, buffer_22_out, buffer_23_out, buffer_24_out, buffer_25_out, buffer_26_out,
       buffer_27_out, buffer_28_out, buffer_29_out, buffer_30_out, buffer_31_out;

  buf buffer_1 (buffer_1_out, in_1);
  buf buffer_2 (buffer_2_out, buffer_28_out);
  buf buffer_3 (buffer_3_out, buffer_4_out);
  buf buffer_4 (buffer_4_out, buffer_1_out);
  buf buffer_5 (buffer_5_out, buffer_6_out);
  buf buffer_6 (buffer_6_out, buffer_3_out);
  buf buffer_7 (buffer_7_out, buffer_9_out);
  buf buffer_8 (buffer_8_out, buffer_2_out);
  buf buffer_9 (buffer_9_out, buffer_10_out);
  buf buffer_10 (buffer_10_out, buffer_8_out);
  buf buffer_11 (buffer_11_out, buffer_13_out);
  buf buffer_12 (buffer_12_out, buffer_14_out);
  buf buffer_13 (buffer_13_out, buffer_12_out);
  buf buffer_14 (buffer_14_out, buffer_5_out);
  buf buffer_15 (buffer_15_out, buffer_7_out);
  buf buffer_16 (buffer_16_out, buffer_18_out);
  buf buffer_17 (buffer_17_out, buffer_15_out);
  buf buffer_18 (buffer_18_out, buffer_17_out);
  buf buffer_19 (buffer_19_out, buffer_11_out);
  buf buffer_20 (buffer_20_out, buffer_19_out);
  buf buffer_21 (buffer_21_out, buffer_20_out);
  buf buffer_22 (buffer_22_out, buffer_21_out);
  buf buffer_23 (buffer_23_out, buffer_16_out);
  buf buffer_24 (buffer_24_out, buffer_26_out);
  buf buffer_25 (buffer_25_out, buffer_23_out);
  buf buffer_26 (buffer_26_out, buffer_25_out);
  buf buffer_27 (buffer_27_out, buffer_29_out);
  buf buffer_28 (buffer_28_out, buffer_27_out);
  buf buffer_29 (buffer_29_out, buffer_22_out);
  buf buffer_30 (buffer_30_out, buffer_24_out);
  buf buffer_31 (buffer_31_out, buffer_30_out);
  buf buffer_32 (out_2, buffer_31_out);
endmodule

module _3_BUF (
  input  [2:0] in_1,
  input  in_2,
  output [2:0] out_3
);

  and and_1 (out_3[2], in_1[2], in_2);
  and and_2 (out_3[0], in_1[0], in_2);
  and and_3 (out_3[1], in_1[1], in_2);
endmodule

module _5_DEC (
  input  in_1,
  input  [4:0] in_2,
  output [4:0] out_3,
  output out_4
);

  wire and_1_out, and_2_out, and_3_out, and_4_out, and_6_out, buffer_1_out, buffer_2_out, buffer_3_out,
       buffer_4_out, buffer_5_out, buffer_7_out, buffer_8_out, buffer_11_out, buffer_12_out, buffer_15_out,
       n1_shortdelay_1_out_2, nand_1_out, nor_1_out, not_1_out, not_2_out, not_3_out, not_4_out, not_5_out,
       xor_1_out, xor_2_out, xor_3_out, xor_4_out, xor_5_out;
  wire [4:0] buffer_6_out;

  nor nor_1 (nor_1_out, in_2[4], in_2[3], in_2[2], in_2[1], in_2[0]);
  not not_1 (not_1_out, in_2[0]);
  and and_1 (and_1_out, not_1_out, in_1);
  not not_2 (not_2_out, in_2[1]);
  and and_2 (and_2_out, not_2_out, and_1_out);
  not not_3 (not_3_out, in_2[2]);
  and and_3 (and_3_out, not_3_out, and_2_out);
  not not_4 (not_4_out, in_2[3]);
  and and_4 (and_4_out, not_4_out, and_3_out);
  not not_5 (not_5_out, in_2[4]);
  and and_5 (out_4, not_5_out, and_4_out);
  xor xor_1 (xor_1_out, in_2[0], in_1);
  buf buffer_1 (buffer_1_out, xor_1_out);
  buf buffer_2 (buffer_2_out, xor_2_out);
  xor xor_2 (xor_2_out, in_2[1], and_1_out);
  buf buffer_3 (buffer_3_out, xor_3_out);
  xor xor_3 (xor_3_out, in_2[2], and_2_out);
  buf buffer_4 (buffer_4_out, xor_4_out);
  xor xor_4 (xor_4_out, in_2[3], and_3_out);
  xor xor_5 (xor_5_out, in_2[4], and_4_out);
  buf buffer_5 (buffer_5_out, xor_5_out);
  nand nand_1 (nand_1_out, nor_1_out, in_1);
  buf buffer_6 (buffer_6_out[0], buffer_7_out);
  buf buffer_7 (buffer_7_out, buffer_1_out);
  buf buffer_8 (buffer_8_out, buffer_2_out);
  buf buffer_9 (buffer_6_out[1], buffer_8_out);
  buf buffer_10 (buffer_6_out[2], buffer_11_out);
  buf buffer_11 (buffer_11_out, buffer_3_out);
  buf buffer_12 (buffer_12_out, buffer_4_out);
  buf buffer_13 (buffer_6_out[3], buffer_12_out);
  buf buffer_14 (buffer_6_out[4], buffer_15_out);
  buf buffer_15 (buffer_15_out, buffer_5_out);
  _1_ShortDelay u_1_shortdelay_1 (.in_1(nand_1_out), .out_2(n1_shortdelay_1_out_2));
  and and_6 (and_6_out, n1_shortdelay_1_out_2, ~nor_1_out, in_1);  // AND_Gate
  _5_BUF u_5_buf_1 (.in_2(and_6_out), .in_1(buffer_6_out), .out_3(out_3));
endmodule
