// Logisim project NewCPU.circ as structural Verilog
module CPU (
  input  RESET,
  input  POWER,
  input  in_3,
  input  in_4,
  input  [3:0] in_5,
  input  [3:0] in_6,
  input  [3:0] in_7,
  input  [3:0] in_8,
  input  Clear,
  input  Write,
  input  [15:0] iA,
  input  [15:0] iB,
  input  [15:0] iC,
  input  [15:0] iD,
  output [5:0] Instruction_Loc,
  output [5:0] Program_Loc,
  output [3:0] out_17,
  output [3:0] out_18,
  output [3:0] Current_Program,
  output [3:0] out_20
);

  wire and_1_out, and_2_out, and_3_out, and_4_out, and_5_out, and_6_out, and_7_out, and_8_out, and_9_out,
       and_10_out, and_11_out, and_12_out, and_13_out, and_14_out, and_15_out, and_16_out, clock_1_out,
       condition_checker_1_out_10, condition_decoder_1_out_3, condition_decoder_1_out_4,
       condition_decoder_1_out_5, condition_decoder_1_out_6, condition_decoder_1_out_7,
       condition_decoder_1_out_8, condition_decoder_1_out_9, d_ff_1_q, demultiplexer_1_out0,
       demultiplexer_1_out1, demultiplexer_2_out0, demultiplexer_2_out1, demultiplexer_3_out0,
       demultiplexer_3_out1, demultiplexer_4_out0, demultiplexer_4_out1, instruction_decoder_1_a_b_reg,
       instruction_decoder_1_alu, instruction_decoder_1_alu_2, instruction_decoder_1_cnd,
       instruction_decoder_1_copy, instruction_decoder_1_creg, instruction_decoder_1_end,
       instruction_decoder_1_get, instruction_decoder_1_get_set, instruction_decoder_1_jump,
       instruction_decoder_1_res, instruction_decoder_1_sft, instruction_decoder_1_shft,
       instruction_decoder_1_shft_dir, instruction_decoder_1_shft_rot, instruction_decoder_1_sreg,
       instruction_decoder_1_stor, instruction_register_1_out_14, nor_1_out, or_1_out, or_2_out, or_3_out,
       or_4_out, or_5_out, or_6_out, or_8_out, or_9_out, or_10_out, or_11_out, xor_1_out;
  wire [1:0] instruction_decoder_1_ix;
  wire [3:0] instruction_decoder_1_nalu, instruction_decoder_1_rd, instruction_decoder_1_rs,
       instruction_decoder_1_shft_2, instruction_decoder_1_wr, instruction_register_1_out_18,
       instruction_register_1_out_19, instruction_register_1_out_20, instruction_register_1_out_21;
  wire [5:0] instruction_decoder_1_jump_2;
  wire [7:0] instruction_decoder_1_mem_dest, instruction_decoder_1_mem_src;
  wire [15:0] alu_1_out_5, bit_shifter_1_out_7, cpu_memory_1_out_9, multiplexer_1_out, n2b_alu_reg_1_out_5,
       n2b_alu_reg_2_out_5, n2b_alu_reg_3_out_5, n2b_alu_reg_4_out_5, n2b_alu_reg_5_out_5,
       n16_buffer_1_out_3, n16_buffer_2_out_3, n16_buffer_3_out_3, n16_buffer_4_out_3, or_7_out;

  Clock clock_1 (.out(clock_1_out));
  D_Flip_Flop d_ff_1 (.Q(d_ff_1_q), .preset(condition_checker_1_out_10), .reset(or_1_out));  // open: clk, D, Qn, en
  or or_1 (or_1_out, instruction_register_1_out_14, RESET, and_9_out);
  Instruction_Register instruction_register_1 (
    .in_9(in_5), .in_10(in_6), .in_11(in_7), .in_12(in_8), .in_4(in_3), .in_5(in_4), .in_3(clock_1_out),
    .Pwr(xor_1_out), .Cl(Clear), .Wr(Write), .out_18(instruction_register_1_out_18),
    .out_19(instruction_register_1_out_19), .out_20(instruction_register_1_out_20),
    .out_21(instruction_register_1_out_21), .Res(RESET), .in_1(instruction_decoder_1_jump_2),
    .in_2(and_1_out), .out_17(Program_Loc), .out_16(Instruction_Loc),
    .out_15({out_17, out_18, Current_Program, out_20}), .out_14(instruction_register_1_out_14));
  xor xor_1 (xor_1_out, instruction_decoder_1_end, POWER);
  and and_1 (and_1_out, d_ff_1_q, instruction_decoder_1_jump);
  Multiplexer #(.select(2), .width(16), .enable("false")) multiplexer_1 (
    .in0(iA), .in1(iB), .in2(iC), .in3(iD), .out(multiplexer_1_out), .sel(instruction_decoder_1_ix));
  _16_Buffer u_16_buffer_1 (.in_1(multiplexer_1_out), .in_2(instruction_decoder_1_stor), .out_3(n16_buffer_1_out_3));
  Instruction_Decoder instruction_decoder_1 (
    .in_1(instruction_register_1_out_18), .in_2(instruction_register_1_out_19),
    .in_3(instruction_register_1_out_20), .in_4(instruction_register_1_out_21),
    .STOR(instruction_decoder_1_stor), .COPY(instruction_decoder_1_copy), .RES(instruction_decoder_1_res),
    .ALU(instruction_decoder_1_alu), .SHFT(instruction_decoder_1_shft),
    .GET_SET(instruction_decoder_1_get_set), .END(instruction_decoder_1_end), .iX(instruction_decoder_1_ix),
    .Wr(instruction_decoder_1_wr), .Rs(instruction_decoder_1_rs), .Rd(instruction_decoder_1_rd),
    .ALU_2(instruction_decoder_1_alu_2), .SFT(instruction_decoder_1_sft), .CND(instruction_decoder_1_cnd),
    .nALU(instruction_decoder_1_nalu), .Shft_2(instruction_decoder_1_shft_2),
    .Shft_Dir(instruction_decoder_1_shft_dir), .Mem_Src(instruction_decoder_1_mem_src),
    .Mem_Dest(instruction_decoder_1_mem_dest), .Jump_2(instruction_decoder_1_jump_2),
    .JUMP(instruction_decoder_1_jump), .Shft_Rot(instruction_decoder_1_shft_rot),
    .SREG(instruction_decoder_1_sreg), .A_B_Reg(instruction_decoder_1_a_b_reg),
    .CREG(instruction_decoder_1_creg), .GET(instruction_decoder_1_get));  // open: GET_2
  and and_2 (and_2_out, instruction_decoder_1_sft, instruction_decoder_1_sreg);
  Condition_Decoder condition_decoder_1 (
    .in_1(instruction_register_1_out_18), .out_3(condition_decoder_1_out_3),
    .out_4(condition_decoder_1_out_4), .out_5(condition_decoder_1_out_5), .out_6(condition_decoder_1_out_6),
    .out_7(condition_decoder_1_out_7), .out_8(condition_decoder_1_out_8),
    .in_2(instruction_register_1_out_19), .out_9(condition_decoder_1_out_9));
  _2B_ALU_Reg u_2b_alu_reg_1 (
    .in_1(n16_buffer_4_out_3), .in_3(instruction_decoder_1_shft), .in_4(or_2_out),
    .out_5(n2b_alu_reg_1_out_5), .in_2(and_2_out));
  or or_2 (or_2_out, RESET, and_3_out);
  and and_3 (and_3_out, instruction_decoder_1_creg, instruction_decoder_1_sft);
  Condition_Checker condition_checker_1 (
    .out_10(condition_checker_1_out_10), .in_1(n2b_alu_reg_2_out_5), .in_4(condition_decoder_1_out_3),
    .in_5(condition_decoder_1_out_4), .in_6(condition_decoder_1_out_5), .in_7(condition_decoder_1_out_6),
    .in_8(condition_decoder_1_out_7), .in_9(condition_decoder_1_out_8), .in_2(n2b_alu_reg_3_out_5),
    .in_3(condition_decoder_1_out_9));
  and and_4 (and_4_out, instruction_decoder_1_sft, instruction_decoder_1_copy);
  and and_5 (and_5_out, instruction_decoder_1_alu_2, instruction_decoder_1_copy);
  _2B_ALU_Reg u_2b_alu_reg_2 (
    .in_1(n16_buffer_4_out_3), .in_3(condition_decoder_1_out_9), .in_4(or_5_out),
    .out_5(n2b_alu_reg_2_out_5), .in_2(and_11_out));
  and and_6 (and_6_out, instruction_decoder_1_res, instruction_decoder_1_alu_2);
  and and_7 (and_7_out, instruction_decoder_1_alu_2, demultiplexer_3_out0);
  or or_3 (or_3_out, RESET, and_6_out);
  Bit_Shifter bit_shifter_1 (
    .in_1(n2b_alu_reg_1_out_5), .in_2(instruction_decoder_1_shft_dir), .in_4(instruction_decoder_1_shft_2),
    .out_7(bit_shifter_1_out_7), .in_5(and_4_out), .in_6(and_8_out), .in_3(instruction_decoder_1_shft_rot));
  _2B_ALU_Reg u_2b_alu_reg_3 (
    .in_1(n16_buffer_4_out_3), .in_3(condition_decoder_1_out_9), .in_4(or_6_out),
    .out_5(n2b_alu_reg_3_out_5), .in_2(and_12_out));
  and and_8 (and_8_out, instruction_decoder_1_res, instruction_decoder_1_sft);
  and and_9 (and_9_out, instruction_decoder_1_res, instruction_decoder_1_cnd);
  _2B_ALU_Reg u_2b_alu_reg_4 (
    .in_1(n16_buffer_4_out_3), .in_3(instruction_decoder_1_alu), .in_4(or_4_out),
    .out_5(n2b_alu_reg_4_out_5), .in_2(and_10_out));
  and and_10 (and_10_out, instruction_decoder_1_alu_2, demultiplexer_4_out0);
  or or_4 (or_4_out, and_7_out, RESET);
  ALU alu_1 (
    .in_1(instruction_decoder_1_nalu), .in_2(n2b_alu_reg_4_out_5), .out_5(alu_1_out_5), .in_4(or_3_out),
    .in_3(n2b_alu_reg_5_out_5));  // open: out_6, out_7
  or or_5 (or_5_out, RESET, demultiplexer_2_out0);
  or or_6 (or_6_out, RESET, demultiplexer_2_out1);
  and and_11 (and_11_out, instruction_decoder_1_cnd, demultiplexer_1_out0);
  and and_12 (and_12_out, demultiplexer_1_out1, instruction_decoder_1_cnd);
  and and_13 (and_13_out, instruction_decoder_1_copy, nor_1_out);
  nor nor_1 (nor_1_out, instruction_decoder_1_cnd, instruction_decoder_1_sft, instruction_decoder_1_alu_2);
  and and_14 (and_14_out, instruction_decoder_1_alu_2, demultiplexer_4_out1);
  Demultiplexer #(.enable("false")) demultiplexer_1 (
    .out0(demultiplexer_1_out0), .out1(demultiplexer_1_out1), .in(instruction_decoder_1_sreg),
    .sel(instruction_decoder_1_a_b_reg));
  and and_15 (and_15_out, nor_1_out, instruction_decoder_1_res);
  assign or_7_out = n16_buffer_2_out_3 | bit_shifter_1_out_7 | n16_buffer_1_out_3 | n16_buffer_4_out_3;  // OR_Gate or_7, 16 bits wide
  _2B_ALU_Reg u_2b_alu_reg_5 (
    .in_1(n16_buffer_4_out_3), .in_3(instruction_decoder_1_alu), .in_4(or_8_out),
    .out_5(n2b_alu_reg_5_out_5), .in_2(and_14_out));
  or or_8 (or_8_out, and_16_out, RESET);
  _16_Buffer u_16_buffer_2 (.in_1(alu_1_out_5), .in_2(and_5_out), .out_3(n16_buffer_2_out_3));
  Demultiplexer #(.enable("false")) demultiplexer_2 (
    .out0(demultiplexer_2_out0), .out1(demultiplexer_2_out1), .in(instruction_decoder_1_creg),
    .sel(instruction_decoder_1_a_b_reg));
  _16_Buffer u_16_buffer_3 (.in_1(or_7_out), .in_2(or_9_out), .out_3(n16_buffer_3_out_3));
  or or_9 (or_9_out, instruction_decoder_1_get, instruction_decoder_1_stor, instruction_decoder_1_copy);
  Demultiplexer #(.enable("false")) demultiplexer_3 (
    .out0(demultiplexer_3_out0), .out1(demultiplexer_3_out1), .in(instruction_decoder_1_creg),
    .sel(instruction_decoder_1_a_b_reg));
  Demultiplexer #(.enable("false")) demultiplexer_4 (
    .out0(demultiplexer_4_out0), .out1(demultiplexer_4_out1), .in(instruction_decoder_1_sreg),
    .sel(instruction_decoder_1_a_b_reg));
  and and_16 (and_16_out, demultiplexer_3_out1, instruction_decoder_1_alu_2);
  or or_10 (or_10_out, instruction_decoder_1_copy, instruction_decoder_1_stor, instruction_decoder_1_get);
  CPU_Memory cpu_memory_1 (
    .in_3(and_15_out), .in_4(or_10_out), .in_5(instruction_decoder_1_wr), .in_7(n16_buffer_3_out_3),
    .in_2(or_11_out), .in_1(instruction_decoder_1_rd), .out_9(cpu_memory_1_out_9),
    .in_6(instruction_decoder_1_rs), .in_8(RESET));
  or or_11 (or_11_out, instruction_decoder_1_sreg, and_13_out);
  _16_Buffer u_16_buffer_4 (.in_1(cpu_memory_1_out_9), .in_2(or_11_out), .out_3(n16_buffer_4_out_3));
endmodule

module ALU (
  input  [3:0] in_1,
  input  [15:0] in_2,
  input  [15:0] in_3,
  input  in_4,
  output [15:0] out_5,
  output out_6,
  output out_7
);

  wire n1_delay_1_out_2, n1_shortdelay_1_out_2, n4_bin_hex_1_out_6, n4_bin_hex_1_out_7, n4_bin_hex_1_out_8,
       n4_bin_hex_1_out_9, n4_bin_hex_1_out_10, n4_bin_hex_1_out_11, n4_bin_hex_1_out_12,
       n4_bin_hex_1_out_13, n4_bin_hex_1_out_14, n4_bin_hex_1_out_15, n4_bin_hex_1_out_16,
       n4_bin_hex_1_out_17, n4_bin_hex_1_out_18, n4_bin_hex_1_out_19, n4_bin_hex_1_out_20,
       n4_bin_hex_1_out_21, n4_detector_1_out_2;
  wire [15:0] n16_2cmp_1_out_3, n16_and_1_out_4, n16_bcnt_1_out_3, n16_cla_adder_1_out_4, n16_dec_1_out_3,
       n16_inc_1_out_3, n16_nand_1_out_4, n16_nor_1_out_4, n16_not_1_out_3, n16_or_1_out_4, n16_rand_1_out_2,
       n16_sqrt_1_out_3, n16_squr_1_out_3, n16_sub_1_out_4, n16_xnor_1_out_4, n16_xor_1_out_4, or_1_out;

  _4_Detector u_4_detector_1 (.in_1(in_1), .out_2(n4_detector_1_out_2));
  _4_Bin_Hex u_4_bin_hex_1 (
    .in_2(in_1[0]), .in_3(in_1[1]), .in_4(in_1[2]), .in_5(in_1[3]), .out_6(n4_bin_hex_1_out_6),
    .out_7(n4_bin_hex_1_out_7), .out_8(n4_bin_hex_1_out_8), .out_9(n4_bin_hex_1_out_9),
    .out_10(n4_bin_hex_1_out_10), .out_11(n4_bin_hex_1_out_11), .out_12(n4_bin_hex_1_out_12),
    .out_13(n4_bin_hex_1_out_13), .out_14(n4_bin_hex_1_out_14), .out_15(n4_bin_hex_1_out_15),
    .out_16(n4_bin_hex_1_out_16), .out_17(n4_bin_hex_1_out_17), .out_18(n4_bin_hex_1_out_18),
    .out_19(n4_bin_hex_1_out_19), .out_20(n4_bin_hex_1_out_20), .out_21(n4_bin_hex_1_out_21),
    .in_1(n4_detector_1_out_2));
  // Probe on in_2
  // Probe on in_3
  _16_DEC u_16_dec_1 (.in_1(in_2), .in_2(n4_bin_hex_1_out_8), .out_3(n16_dec_1_out_3));
  _16_INC u_16_inc_1 (.in_1(in_2), .in_2(n4_bin_hex_1_out_7), .out_3(n16_inc_1_out_3));
  _16_CLA_Adder u_16_cla_adder_1 (
    .in_1(in_2), .Input_A(in_3), .out_4(n16_cla_adder_1_out_4), .out_5(out_6), .in_3(n4_bin_hex_1_out_6));
  _16_SUB u_16_sub_1 (.in_1(in_2), .in_2(in_3), .in_3(n4_bin_hex_1_out_18), .out_4(n16_sub_1_out_4), .out_5(out_7));
  _16_OR u_16_or_1 (.in_1(in_2), .in_2(in_3), .in_3(n4_bin_hex_1_out_10), .out_4(n16_or_1_out_4));
  _16_AND u_16_and_1 (.in_1(in_2), .in_2(in_3), .in_3(n4_bin_hex_1_out_11), .out_4(n16_and_1_out_4));
  _16_XOR u_16_xor_1 (.in_1(in_2), .in_2(in_3), .in_3(n4_bin_hex_1_out_12), .out_4(n16_xor_1_out_4));
  _16_NOR u_16_nor_1 (.in_1(in_2), .in_2(in_3), .in_3(n4_bin_hex_1_out_13), .out_4(n16_nor_1_out_4));
  _16_NAND u_16_nand_1 (.in_1(in_2), .in_2(in_3), .in_3(n4_bin_hex_1_out_14), .out_4(n16_nand_1_out_4));
  _16_XNOR u_16_xnor_1 (.in_1(in_2), .in_2(in_3), .in_3(n4_bin_hex_1_out_15), .out_4(n16_xnor_1_out_4));
  _16_SQRT u_16_sqrt_1 (.in_1(in_2), .in_2(n4_bin_hex_1_out_20), .out_3(n16_sqrt_1_out_3));
  _16_SQUR u_16_squr_1 (.in_1(in_2), .out_3(n16_squr_1_out_3), .in_2(n4_bin_hex_1_out_19));
  _16_BCNT u_16_bcnt_1 (.in_1(in_2), .out_3(n16_bcnt_1_out_3), .in_2(n4_bin_hex_1_out_17));
  _16_2CMP u_16_2cmp_1 (.in_1(in_2), .in_2(n4_bin_hex_1_out_16), .out_3(n16_2cmp_1_out_3));
  _16_NOT u_16_not_1 (.in_1(in_2), .out_3(n16_not_1_out_3), .in_2(n4_bin_hex_1_out_9));
  _16_Rand u_16_rand_1 (.in_1(n4_bin_hex_1_out_21), .out_2(n16_rand_1_out_2));
  _1_ShortDelay u_1_shortdelay_1 (.in_1(n4_detector_1_out_2), .out_2(n1_shortdelay_1_out_2));
  _1_Delay u_1_delay_1 (.in_1(n1_shortdelay_1_out_2), .out_2(n1_delay_1_out_2));
  // Probe on or_1_out
  assign or_1_out = n16_sqrt_1_out_3 | n16_squr_1_out_3 | n16_bcnt_1_out_3 | n16_2cmp_1_out_3 | n16_dec_1_out_3 | n16_inc_1_out_3 | n16_not_1_out_3 | n16_cla_adder_1_out_4 | n16_sub_1_out_4 | n16_rand_1_out_2 | n16_or_1_out_4 | n16_and_1_out_4 | n16_xor_1_out_4 | n16_nor_1_out_4 | n16_nand_1_out_4 | n16_xnor_1_out_4;  // OR_Gate or_1, 16 bits wide
  // Probe on or_1_out
  // Probe on out_5
  ALU_Accumulator alu_accumulator_1 (.in_1(or_1_out), .in_2(n1_delay_1_out_2), .in_3(in_4), .out_4(out_5));
endmodule

module CPU_Memory (
  input  [3:0] in_1,
  input  in_2,
  input  in_3,
  input  in_4,
  input  [3:0] in_5,
  input  [3:0] in_6,
  input  [15:0] in_7,
  input  in_8,
  output [15:0] out_9
);

  wire n1_4t_delay_1_out_2, n1_4t_delay_2_out_2, n1_4t_delay_3_out_2, n1_4t_delay_4_out_2,
       n1_4t_delay_5_out_2, n1_4t_delay_6_out_2, n1_4t_delay_7_out_2, n1_4t_delay_8_out_2,
       n2b_register_2_out_6, n2b_register_3_out_6, n2b_register_4_out_6, n2b_register_5_out_6,
       n2b_register_6_out_6, n2b_register_7_out_6, n2b_register_8_out_6, n2b_register_9_out_6,
       n2b_register_10_out_6, n2b_register_11_out_6, n2b_register_12_out_6, n2b_register_13_out_6,
       n2b_register_14_out_6, n2b_register_15_out_6, n2b_register_16_out_6, n4_bin_hex_1_out_6,
       n4_bin_hex_1_out_7, n4_bin_hex_1_out_8, n4_bin_hex_1_out_9, n4_bin_hex_1_out_10, n4_bin_hex_1_out_11,
       n4_bin_hex_1_out_12, n4_bin_hex_1_out_13, n4_bin_hex_1_out_14, n4_bin_hex_1_out_15,
       n4_bin_hex_1_out_16, n4_bin_hex_1_out_17, n4_bin_hex_1_out_18, n4_bin_hex_1_out_19,
       n4_bin_hex_1_out_20, n4_bin_hex_1_out_21, n4_bin_hex_2_out_6, n4_bin_hex_2_out_7, n4_bin_hex_2_out_8,
       n4_bin_hex_2_out_9, n4_bin_hex_2_out_10, n4_bin_hex_2_out_11, n4_bin_hex_2_out_12,
       n4_bin_hex_2_out_13, n4_bin_hex_2_out_14, n4_bin_hex_2_out_15, n4_bin_hex_2_out_16,
       n4_bin_hex_2_out_17, n4_bin_hex_2_out_18, n4_bin_hex_2_out_19, n4_bin_hex_2_out_20,
       n4_bin_hex_2_out_21, n4_bin_hex_3_out_6, n4_bin_hex_3_out_7, n4_bin_hex_3_out_8, n4_bin_hex_3_out_9,
       n4_bin_hex_3_out_10, n4_bin_hex_3_out_11, n4_bin_hex_3_out_12, n4_bin_hex_3_out_13,
       n4_bin_hex_3_out_14, n4_bin_hex_3_out_15, n4_bin_hex_3_out_16, n4_bin_hex_3_out_17,
       n4_bin_hex_3_out_18, n4_bin_hex_3_out_19, n4_bin_hex_3_out_20, n4_bin_hex_3_out_21;
  wire [15:0] n2b_register_1_out_7, n2b_register_2_out_7, n2b_register_3_out_7, n2b_register_4_out_7,
       n2b_register_5_out_7, n2b_register_6_out_7, n2b_register_7_out_7, n2b_register_8_out_7,
       n2b_register_9_out_7, n2b_register_10_out_7, n2b_register_11_out_7, n2b_register_12_out_7,
       n2b_register_13_out_7, n2b_register_14_out_7, n2b_register_15_out_7, n2b_register_16_out_7;

  _1_4T_Delay u_1_4t_delay_1 (.in_1(in_4), .out_2(n1_4t_delay_1_out_2));
  _1_4T_Delay u_1_4t_delay_2 (.in_1(n1_4t_delay_1_out_2), .out_2(n1_4t_delay_2_out_2));
  _1_4T_Delay u_1_4t_delay_3 (.in_1(n1_4t_delay_2_out_2), .out_2(n1_4t_delay_3_out_2));
  _1_4T_Delay u_1_4t_delay_4 (.in_1(n1_4t_delay_5_out_2), .out_2(n1_4t_delay_4_out_2));
  _1_4T_Delay u_1_4t_delay_5 (.in_1(n1_4t_delay_3_out_2), .out_2(n1_4t_delay_5_out_2));
  _1_4T_Delay u_1_4t_delay_6 (.in_1(n1_4t_delay_4_out_2), .out_2(n1_4t_delay_6_out_2));
  _1_4T_Delay u_1_4t_delay_7 (.in_1(n1_4t_delay_6_out_2), .out_2(n1_4t_delay_7_out_2));
  _1_4T_Delay u_1_4t_delay_8 (.in_1(n1_4t_delay_7_out_2), .out_2(n1_4t_delay_8_out_2));
  _4_Bin_Hex u_4_bin_hex_1 (
    .in_2(in_5[0]), .in_3(in_5[1]), .in_4(in_5[2]), .in_5(in_5[3]), .out_6(n4_bin_hex_1_out_6),
    .out_7(n4_bin_hex_1_out_7), .out_8(n4_bin_hex_1_out_8), .out_9(n4_bin_hex_1_out_9),
    .out_10(n4_bin_hex_1_out_10), .out_11(n4_bin_hex_1_out_11), .out_12(n4_bin_hex_1_out_12),
    .out_13(n4_bin_hex_1_out_13), .out_14(n4_bin_hex_1_out_14), .out_15(n4_bin_hex_1_out_15),
    .out_16(n4_bin_hex_1_out_16), .out_17(n4_bin_hex_1_out_17), .out_18(n4_bin_hex_1_out_18),
    .out_19(n4_bin_hex_1_out_19), .out_20(n4_bin_hex_1_out_20), .out_21(n4_bin_hex_1_out_21),
    .in_1(n1_4t_delay_8_out_2));
  _2B_Register u_2b_register_1 (
    .in_1(in_7), .in_2(n4_bin_hex_1_out_6), .out_7(n2b_register_1_out_7), .in_3(n4_bin_hex_3_out_6),
    .in_4(n4_bin_hex_2_out_6), .in_5(n2b_register_2_out_6));  // open: out_6
  _2B_Register u_2b_register_2 (
    .in_1(in_7), .in_2(n4_bin_hex_1_out_7), .out_7(n2b_register_2_out_7), .in_3(n4_bin_hex_3_out_7),
    .in_4(n4_bin_hex_2_out_7), .in_5(n2b_register_3_out_6), .out_6(n2b_register_2_out_6));
  _2B_Register u_2b_register_3 (
    .in_1(in_7), .in_2(n4_bin_hex_1_out_8), .out_7(n2b_register_3_out_7), .in_3(n4_bin_hex_3_out_8),
    .in_4(n4_bin_hex_2_out_8), .in_5(n2b_register_4_out_6), .out_6(n2b_register_3_out_6));
  _2B_Register u_2b_register_4 (
    .in_1(in_7), .in_2(n4_bin_hex_1_out_9), .out_7(n2b_register_4_out_7), .in_3(n4_bin_hex_3_out_9),
    .in_4(n4_bin_hex_2_out_9), .in_5(n2b_register_5_out_6), .out_6(n2b_register_4_out_6));
  _2B_Register u_2b_register_5 (
    .in_1(in_7), .in_2(n4_bin_hex_1_out_10), .out_7(n2b_register_5_out_7), .in_3(n4_bin_hex_3_out_10),
    .in_4(n4_bin_hex_2_out_10), .in_5(n2b_register_6_out_6), .out_6(n2b_register_5_out_6));
  _2B_Register u_2b_register_6 (
    .in_1(in_7), .in_2(n4_bin_hex_1_out_11), .out_7(n2b_register_6_out_7), .in_3(n4_bin_hex_3_out_11),
    .in_4(n4_bin_hex_2_out_11), .in_5(n2b_register_7_out_6), .out_6(n2b_register_6_out_6));
  _2B_Register u_2b_register_7 (
    .in_1(in_7), .in_2(n4_bin_hex_1_out_12), .out_7(n2b_register_7_out_7), .in_3(n4_bin_hex_3_out_12),
    .in_4(n4_bin_hex_2_out_12), .in_5(n2b_register_8_out_6), .out_6(n2b_register_7_out_6));
  _2B_Register u_2b_register_8 (
    .in_1(in_7), .in_2(n4_bin_hex_1_out_13), .out_7(n2b_register_8_out_7), .in_3(n4_bin_hex_3_out_13),
    .in_4(n4_bin_hex_2_out_13), .in_5(n2b_register_9_out_6), .out_6(n2b_register_8_out_6));
  _2B_Register u_2b_register_9 (
    .in_1(in_7), .in_2(n4_bin_hex_1_out_14), .out_7(n2b_register_9_out_7), .in_3(n4_bin_hex_3_out_14),
    .in_4(n4_bin_hex_2_out_14), .in_5(n2b_register_10_out_6), .out_6(n2b_register_9_out_6));
  _2B_Register u_2b_register_10 (
    .in_1(in_7), .in_2(n4_bin_hex_1_out_15), .out_7(n2b_register_10_out_7), .in_3(n4_bin_hex_3_out_15),
    .in_4(n4_bin_hex_2_out_15), .in_5(n2b_register_11_out_6), .out_6(n2b_register_10_out_6));
  _2B_Register u_2b_register_11 (
    .in_1(in_7), .in_2(n4_bin_hex_1_out_16), .out_7(n2b_register_11_out_7), .in_3(n4_bin_hex_3_out_16),
    .in_4(n4_bin_hex_2_out_16), .in_5(n2b_register_12_out_6), .out_6(n2b_register_11_out_6));
  _2B_Register u_2b_register_12 (
    .in_1(in_7), .in_2(n4_bin_hex_1_out_17), .out_7(n2b_register_12_out_7), .in_3(n4_bin_hex_3_out_17),
    .in_4(n4_bin_hex_2_out_17), .in_5(n2b_register_13_out_6), .out_6(n2b_register_12_out_6));
  _2B_Register u_2b_register_13 (
    .in_1(in_7), .in_2(n4_bin_hex_1_out_18), .out_7(n2b_register_13_out_7), .in_3(n4_bin_hex_3_out_18),
    .in_4(n4_bin_hex_2_out_18), .in_5(n2b_register_14_out_6), .out_6(n2b_register_13_out_6));
  _2B_Register u_2b_register_14 (
    .in_1(in_7), .in_2(n4_bin_hex_1_out_19), .out_7(n2b_register_14_out_7), .in_3(n4_bin_hex_3_out_19),
    .in_4(n4_bin_hex_2_out_19), .in_5(n2b_register_15_out_6), .out_6(n2b_register_14_out_6));
  _2B_Register u_2b_register_15 (
    .in_1(in_7), .in_2(n4_bin_hex_1_out_20), .out_7(n2b_register_15_out_7), .in_3(n4_bin_hex_3_out_20),
    .in_4(n4_bin_hex_2_out_20), .in_5(n2b_register_16_out_6), .out_6(n2b_register_15_out_6));
  _2B_Register u_2b_register_16 (
    .in_1(in_7), .in_2(n4_bin_hex_1_out_21), .out_7(n2b_register_16_out_7), .in_3(n4_bin_hex_3_out_21),
    .in_4(n4_bin_hex_2_out_21), .in_5(in_8), .out_6(n2b_register_16_out_6));
  _4_Bin_Hex u_4_bin_hex_2 (
    .in_2(in_1[0]), .in_3(in_1[1]), .in_4(in_1[2]), .in_5(in_1[3]), .out_6(n4_bin_hex_2_out_6),
    .out_7(n4_bin_hex_2_out_7), .out_8(n4_bin_hex_2_out_8), .out_9(n4_bin_hex_2_out_9),
    .out_10(n4_bin_hex_2_out_10), .out_11(n4_bin_hex_2_out_11), .out_12(n4_bin_hex_2_out_12),
    .out_13(n4_bin_hex_2_out_13), .out_14(n4_bin_hex_2_out_14), .out_15(n4_bin_hex_2_out_15),
    .out_16(n4_bin_hex_2_out_16), .out_17(n4_bin_hex_2_out_17), .out_18(n4_bin_hex_2_out_18),
    .out_19(n4_bin_hex_2_out_19), .out_20(n4_bin_hex_2_out_20), .out_21(n4_bin_hex_2_out_21), .in_1(in_2));
  _4_Bin_Hex u_4_bin_hex_3 (
    .in_2(in_6[0]), .in_3(in_6[1]), .in_4(in_6[2]), .in_5(in_6[3]), .out_6(n4_bin_hex_3_out_6),
    .out_7(n4_bin_hex_3_out_7), .out_8(n4_bin_hex_3_out_8), .out_9(n4_bin_hex_3_out_9),
    .out_10(n4_bin_hex_3_out_10), .out_11(n4_bin_hex_3_out_11), .out_12(n4_bin_hex_3_out_12),
    .out_13(n4_bin_hex_3_out_13), .out_14(n4_bin_hex_3_out_14), .out_15(n4_bin_hex_3_out_15),
    .out_16(n4_bin_hex_3_out_16), .out_17(n4_bin_hex_3_out_17), .out_18(n4_bin_hex_3_out_18),
    .out_19(n4_bin_hex_3_out_19), .out_20(n4_bin_hex_3_out_20), .out_21(n4_bin_hex_3_out_21), .in_1(in_3));
  assign out_9 = n2b_register_1_out_7 | n2b_register_2_out_7 | n2b_register_3_out_7 | n2b_register_4_out_7 | n2b_register_5_out_7 | n2b_register_6_out_7 | n2b_register_7_out_7 | n2b_register_8_out_7 | n2b_register_9_out_7 | n2b_register_10_out_7 | n2b_register_11_out_7 | n2b_register_12_out_7 | n2b_register_13_out_7 | n2b_register_14_out_7 | n2b_register_15_out_7 | n2b_register_16_out_7;  // OR_Gate or_1, 16 bits wide
endmodule

module Bit_Shifter (
  input  [15:0] in_1,
  input  in_2,
  input  in_3,
  input  [3:0] in_4,
  input  in_5,
  input  in_6,
  output [15:0] out_7
);

  wire multiplexer_1_out, multiplexer_2_out, multiplexer_3_out, multiplexer_4_out, multiplexer_5_out,
       multiplexer_6_out, multiplexer_7_out, multiplexer_8_out, multiplexer_9_out, multiplexer_10_out,
       multiplexer_11_out, multiplexer_12_out, multiplexer_13_out, multiplexer_14_out, multiplexer_15_out,
       multiplexer_16_out, multiplexer_17_out, multiplexer_18_out, multiplexer_19_out, multiplexer_20_out,
       multiplexer_21_out, multiplexer_22_out, multiplexer_23_out, multiplexer_24_out, multiplexer_25_out,
       multiplexer_26_out, multiplexer_27_out, multiplexer_28_out, multiplexer_29_out, multiplexer_30_out,
       multiplexer_31_out, multiplexer_32_out, multiplexer_33_out, multiplexer_34_out, multiplexer_35_out,
       multiplexer_36_out, multiplexer_37_out, multiplexer_38_out, multiplexer_39_out, multiplexer_40_out,
       multiplexer_41_out, multiplexer_42_out, multiplexer_43_out, multiplexer_44_out, multiplexer_45_out,
       multiplexer_46_out, multiplexer_47_out, multiplexer_48_out, multiplexer_49_out, multiplexer_50_out,
       multiplexer_51_out, multiplexer_52_out, multiplexer_53_out, multiplexer_54_out, multiplexer_55_out,
       multiplexer_56_out, multiplexer_57_out, multiplexer_58_out, multiplexer_59_out, multiplexer_60_out,
       multiplexer_61_out, multiplexer_62_out, multiplexer_63_out, multiplexer_64_out, multiplexer_65_out,
       multiplexer_66_out, multiplexer_67_out, multiplexer_68_out, multiplexer_69_out, multiplexer_70_out,
       multiplexer_71_out, multiplexer_72_out, multiplexer_73_out, multiplexer_74_out, multiplexer_75_out,
       multiplexer_76_out, multiplexer_77_out, multiplexer_78_out, multiplexer_79_out, multiplexer_80_out,
       multiplexer_81_out, multiplexer_82_out, multiplexer_83_out, multiplexer_84_out, multiplexer_85_out,
       multiplexer_86_out, multiplexer_87_out, multiplexer_88_out, multiplexer_89_out, multiplexer_90_out,
       multiplexer_91_out, multiplexer_92_out, multiplexer_93_out, multiplexer_94_out, multiplexer_95_out,
       multiplexer_96_out, n1_shortdelay_1_out_2, n5t_edge_trigger_1_out_2, not_1_out, not_2_out, not_3_out,
       not_4_out, or_1_out;
  wire [15:0] demultiplexer_1_out0, demultiplexer_1_out1, multiplexer_112_out, multiplexer_128_out,
       multiplexer_129_out;

  or or_1 (or_1_out, in_1[15], in_1[14], in_1[13], in_1[12], in_1[11], in_1[10], in_1[9], in_1[8], in_1[6], in_1[5], in_1[4], in_1[3], in_1[2], in_1[1], in_1[0], in_1[7]);
  _5T_Edge_Trigger u_5t_edge_trigger_1 (.in_1(or_1_out), .out_2(n5t_edge_trigger_1_out_2));
  Demultiplexer #(.width(16), .enable("false")) demultiplexer_1 (
    .out0(demultiplexer_1_out0), .out1(demultiplexer_1_out1), .in(in_1), .sel(in_2));
  Multiplexer #(.enable("false")) multiplexer_1 (
    .in0(demultiplexer_1_out0[15]), .in1(demultiplexer_1_out0[14]), .out(multiplexer_1_out), .sel(in_4[0]));
  Multiplexer #(.enable("false")) multiplexer_2 (
    .in0(demultiplexer_1_out0[14]), .in1(demultiplexer_1_out0[13]), .out(multiplexer_2_out), .sel(in_4[0]));
  Multiplexer #(.enable("false")) multiplexer_3 (
    .in0(demultiplexer_1_out0[13]), .in1(demultiplexer_1_out0[12]), .out(multiplexer_3_out), .sel(in_4[0]));
  Multiplexer #(.enable("false")) multiplexer_4 (
    .in0(demultiplexer_1_out0[12]), .in1(demultiplexer_1_out0[11]), .out(multiplexer_4_out), .sel(in_4[0]));
  Multiplexer #(.enable("false")) multiplexer_5 (
    .in0(demultiplexer_1_out0[11]), .in1(demultiplexer_1_out0[10]), .out(multiplexer_5_out), .sel(in_4[0]));
  Multiplexer #(.enable("false")) multiplexer_6 (
    .in0(demultiplexer_1_out0[10]), .in1(demultiplexer_1_out0[9]), .out(multiplexer_6_out), .sel(in_4[0]));
  Multiplexer #(.enable("false")) multiplexer_7 (
    .in0(demultiplexer_1_out0[9]), .in1(demultiplexer_1_out0[8]), .out(multiplexer_7_out), .sel(in_4[0]));
  Multiplexer #(.enable("false")) multiplexer_8 (
    .in0(demultiplexer_1_out0[8]), .in1(demultiplexer_1_out0[7]), .out(multiplexer_8_out), .sel(in_4[0]));
  Multiplexer #(.enable("false")) multiplexer_9 (
    .in0(demultiplexer_1_out0[7]), .in1(demultiplexer_1_out0[6]), .out(multiplexer_9_out), .sel(in_4[0]));
  Multiplexer #(.enable("false")) multiplexer_10 (
    .in0(demultiplexer_1_out0[6]), .in1(demultiplexer_1_out0[5]), .out(multiplexer_10_out), .sel(in_4[0]));
  Multiplexer #(.enable("false")) multiplexer_11 (
    .in0(demultiplexer_1_out0[5]), .in1(demultiplexer_1_out0[4]), .out(multiplexer_11_out), .sel(in_4[0]));
  Multiplexer #(.enable("false")) multiplexer_12 (
    .in0(demultiplexer_1_out0[4]), .in1(demultiplexer_1_out0[3]), .out(multiplexer_12_out), .sel(in_4[0]));
  Multiplexer #(.enable("false")) multiplexer_13 (
    .in0(demultiplexer_1_out0[3]), .in1(demultiplexer_1_out0[2]), .out(multiplexer_13_out), .sel(in_4[0]));
  Multiplexer #(.enable("false")) multiplexer_14 (
    .in0(demultiplexer_1_out0[2]), .in1(demultiplexer_1_out0[1]), .out(multiplexer_14_out), .sel(in_4[0]));
  Multiplexer #(.enable("false")) multiplexer_15 (
    .in0(demultiplexer_1_out0[1]), .in1(demultiplexer_1_out0[0]), .out(multiplexer_15_out), .sel(in_4[0]));
  Multiplexer #(.enable("false")) multiplexer_16 (
    .in0(demultiplexer_1_out0[0]), .in1(1'b0), .out(multiplexer_16_out), .sel(in_4[0]));
  not not_1 (not_1_out, in_4[0]);
  Multiplexer #(.enable("false")) multiplexer_17 (
    .in0(1'b0), .in1(demultiplexer_1_out1[15]), .out(multiplexer_17_out), .sel(not_1_out));
  Multiplexer #(.enable("false")) multiplexer_18 (
    .in0(demultiplexer_1_out1[15]), .in1(demultiplexer_1_out1[14]), .out(multiplexer_18_out), .sel(not_1_out));
  Multiplexer #(.enable("false")) multiplexer_19 (
    .in0(demultiplexer_1_out1[14]), .in1(demultiplexer_1_out1[13]), .out(multiplexer_19_out), .sel(not_1_out));
  Multiplexer #(.enable("false")) multiplexer_20 (
    .in0(demultiplexer_1_out1[13]), .in1(demultiplexer_1_out1[12]), .out(multiplexer_20_out), .sel(not_1_out));
  Multiplexer #(.enable("false")) multiplexer_21 (
    .in0(demultiplexer_1_out1[12]), .in1(demultiplexer_1_out1[11]), .out(multiplexer_21_out), .sel(not_1_out));
  Multiplexer #(.enable("false")) multiplexer_22 (
    .in0(demultiplexer_1_out1[11]), .in1(demultiplexer_1_out1[10]), .out(multiplexer_22_out), .sel(not_1_out));
  Multiplexer #(.enable("false")) multiplexer_23 (
    .in0(demultiplexer_1_out1[10]), .in1(demultiplexer_1_out1[9]), .out(multiplexer_23_out), .sel(not_1_out));
  Multiplexer #(.enable("false")) multiplexer_24 (
    .in0(demultiplexer_1_out1[9]), .in1(demultiplexer_1_out1[8]), .out(multiplexer_24_out), .sel(not_1_out));
  Multiplexer #(.enable("false")) multiplexer_25 (
    .in0(demultiplexer_1_out1[8]), .in1(demultiplexer_1_out1[7]), .out(multiplexer_25_out), .sel(not_1_out));
  Multiplexer #(.enable("false")) multiplexer_26 (
    .in0(demultiplexer_1_out1[7]), .in1(demultiplexer_1_out1[6]), .out(multiplexer_26_out), .sel(not_1_out));
  Multiplexer #(.enable("false")) multiplexer_27 (
    .in0(demultiplexer_1_out1[6]), .in1(demultiplexer_1_out1[5]), .out(multiplexer_27_out), .sel(not_1_out));
  Multiplexer #(.enable("false")) multiplexer_28 (
    .in0(demultiplexer_1_out1[5]), .in1(demultiplexer_1_out1[4]), .out(multiplexer_28_out), .sel(not_1_out));
  Multiplexer #(.enable("false")) multiplexer_29 (
    .in0(demultiplexer_1_out1[4]), .in1(demultiplexer_1_out1[3]), .out(multiplexer_29_out), .sel(not_1_out));
  Multiplexer #(.enable("false")) multiplexer_30 (
    .in0(demultiplexer_1_out1[3]), .in1(demultiplexer_1_out1[2]), .out(multiplexer_30_out), .sel(not_1_out));
  Multiplexer #(.enable("false")) multiplexer_31 (
    .in0(demultiplexer_1_out1[2]), .in1(demultiplexer_1_out1[1]), .out(multiplexer_31_out), .sel(not_1_out));
  Multiplexer #(.enable("false")) multiplexer_32 (
    .in0(demultiplexer_1_out1[1]), .in1(demultiplexer_1_out1[0]), .out(multiplexer_32_out), .sel(not_1_out));
  Multiplexer #(.enable("false")) multiplexer_33 (
    .in0(multiplexer_1_out), .in1(multiplexer_3_out), .out(multiplexer_33_out), .sel(in_4[1]));
  Multiplexer #(.enable("false")) multiplexer_34 (
    .in0(multiplexer_2_out), .in1(multiplexer_4_out), .out(multiplexer_34_out), .sel(in_4[1]));
  Multiplexer #(.enable("false")) multiplexer_35 (
    .in0(multiplexer_3_out), .in1(multiplexer_5_out), .out(multiplexer_35_out), .sel(in_4[1]));
  Multiplexer #(.enable("false")) multiplexer_36 (
    .in0(multiplexer_4_out), .in1(multiplexer_6_out), .out(multiplexer_36_out), .sel(in_4[1]));
  Multiplexer #(.enable("false")) multiplexer_37 (
    .in0(multiplexer_5_out), .in1(multiplexer_7_out), .out(multiplexer_37_out), .sel(in_4[1]));
  Multiplexer #(.enable("false")) multiplexer_38 (
    .in0(multiplexer_6_out), .in1(multiplexer_8_out), .out(multiplexer_38_out), .sel(in_4[1]));
  Multiplexer #(.enable("false")) multiplexer_39 (
    .in0(multiplexer_7_out), .in1(multiplexer_9_out), .out(multiplexer_39_out), .sel(in_4[1]));
  Multiplexer #(.enable("false")) multiplexer_40 (
    .in0(multiplexer_8_out), .in1(multiplexer_10_out), .out(multiplexer_40_out), .sel(in_4[1]));
  Multiplexer #(.enable("false")) multiplexer_41 (
    .in0(multiplexer_9_out), .in1(multiplexer_11_out), .out(multiplexer_41_out), .sel(in_4[1]));
  Multiplexer #(.enable("false")) multiplexer_42 (
    .in0(multiplexer_10_out), .in1(multiplexer_12_out), .out(multiplexer_42_out), .sel(in_4[1]));
  Multiplexer #(.enable("false")) multiplexer_43 (
    .in0(multiplexer_11_out), .in1(multiplexer_13_out), .out(multiplexer_43_out), .sel(in_4[1]));
  Multiplexer #(.enable("false")) multiplexer_44 (
    .in0(multiplexer_12_out), .in1(multiplexer_14_out), .out(multiplexer_44_out), .sel(in_4[1]));
  Multiplexer #(.enable("false")) multiplexer_45 (
    .in0(multiplexer_13_out), .in1(multiplexer_15_out), .out(multiplexer_45_out), .sel(in_4[1]));
  Multiplexer #(.enable("false")) multiplexer_46 (
    .in0(multiplexer_14_out), .in1(multiplexer_16_out), .out(multiplexer_46_out), .sel(in_4[1]));
  Multiplexer #(.enable("false")) multiplexer_47 (
    .in0(multiplexer_15_out), .in1(1'b0), .out(multiplexer_47_out), .sel(in_4[1]));
  Multiplexer #(.enable("false")) multiplexer_48 (
    .in0(multiplexer_16_out), .in1(1'b0), .out(multiplexer_48_out), .sel(in_4[1]));
  not not_2 (not_2_out, in_4[1]);
  Multiplexer #(.enable("false")) multiplexer_49 (
    .in0(1'b0), .in1(multiplexer_17_out), .out(multiplexer_49_out), .sel(not_2_out));
  Multiplexer #(.enable("false")) multiplexer_50 (
    .in0(1'b0), .in1(multiplexer_18_out), .out(multiplexer_50_out), .sel(not_2_out));
  Multiplexer #(.enable("false")) multiplexer_51 (
    .in0(multiplexer_17_out), .in1(multiplexer_19_out), .out(multiplexer_51_out), .sel(not_2_out));
  Multiplexer #(.enable("false")) multiplexer_52 (
    .in0(multiplexer_18_out), .in1(multiplexer_20_out), .out(multiplexer_52_out), .sel(not_2_out));
  Multiplexer #(.enable("false")) multiplexer_53 (
    .in0(multiplexer_19_out), .in1(multiplexer_21_out), .out(multiplexer_53_out), .sel(not_2_out));
  Multiplexer #(.enable("false")) multiplexer_54 (
    .in0(multiplexer_20_out), .in1(multiplexer_22_out), .out(multiplexer_54_out), .sel(not_2_out));
  Multiplexer #(.enable("false")) multiplexer_55 (
    .in0(multiplexer_21_out), .in1(multiplexer_23_out), .out(multiplexer_55_out), .sel(not_2_out));
  Multiplexer #(.enable("false")) multiplexer_56 (
    .in0(multiplexer_22_out), .in1(multiplexer_24_out), .out(multiplexer_56_out), .sel(not_2_out));
  Multiplexer #(.enable("false")) multiplexer_57 (
    .in0(multiplexer_23_out), .in1(multiplexer_25_out), .out(multiplexer_57_out), .sel(not_2_out));
  Multiplexer #(.enable("false")) multiplexer_58 (
    .in0(multiplexer_24_out), .in1(multiplexer_26_out), .out(multiplexer_58_out), .sel(not_2_out));
  Multiplexer #(.enable("false")) multiplexer_59 (
    .in0(multiplexer_25_out), .in1(multiplexer_27_out), .out(multiplexer_59_out), .sel(not_2_out));
  Multiplexer #(.enable("false")) multiplexer_60 (
    .in0(multiplexer_26_out), .in1(multiplexer_28_out), .out(multiplexer_60_out), .sel(not_2_out));
  Multiplexer #(.enable("false")) multiplexer_61 (
    .in0(multiplexer_27_out), .in1(multiplexer_29_out), .out(multiplexer_61_out), .sel(not_2_out));
  Multiplexer #(.enable("false")) multiplexer_62 (
    .in0(multiplexer_28_out), .in1(multiplexer_30_out), .out(multiplexer_62_out), .sel(not_2_out));
  Multiplexer #(.enable("false")) multiplexer_63 (
    .in0(multiplexer_29_out), .in1(multiplexer_31_out), .out(multiplexer_63_out), .sel(not_2_out));
  Multiplexer #(.enable("false")) multiplexer_64 (
    .in0(multiplexer_30_out), .in1(multiplexer_32_out), .out(multiplexer_64_out), .sel(not_2_out));
  Multiplexer #(.enable("false")) multiplexer_65 (
    .in0(multiplexer_33_out), .in1(multiplexer_37_out), .out(multiplexer_65_out), .sel(in_4[2]));
  Multiplexer #(.enable("false")) multiplexer_66 (
    .in0(multiplexer_34_out), .in1(multiplexer_38_out), .out(multiplexer_66_out), .sel(in_4[2]));
  Multiplexer #(.enable("false")) multiplexer_67 (
    .in0(multiplexer_35_out), .in1(multiplexer_39_out), .out(multiplexer_67_out), .sel(in_4[2]));
  Multiplexer #(.enable("false")) multiplexer_68 (
    .in0(multiplexer_36_out), .in1(multiplexer_40_out), .out(multiplexer_68_out), .sel(in_4[2]));
  Multiplexer #(.enable("false")) multiplexer_69 (
    .in0(multiplexer_37_out), .in1(multiplexer_41_out), .out(multiplexer_69_out), .sel(in_4[2]));
  Multiplexer #(.enable("false")) multiplexer_70 (
    .in0(multiplexer_38_out), .in1(multiplexer_42_out), .out(multiplexer_70_out), .sel(in_4[2]));
  Multiplexer #(.enable("false")) multiplexer_71 (
    .in0(multiplexer_39_out), .in1(multiplexer_43_out), .out(multiplexer_71_out), .sel(in_4[2]));
  Multiplexer #(.enable("false")) multiplexer_72 (
    .in0(multiplexer_40_out), .in1(multiplexer_44_out), .out(multiplexer_72_out), .sel(in_4[2]));
  Multiplexer #(.enable("false")) multiplexer_73 (
    .in0(multiplexer_41_out), .in1(multiplexer_45_out), .out(multiplexer_73_out), .sel(in_4[2]));
  Multiplexer #(.enable("false")) multiplexer_74 (
    .in0(multiplexer_42_out), .in1(multiplexer_46_out), .out(multiplexer_74_out), .sel(in_4[2]));
  Multiplexer #(.enable("false")) multiplexer_75 (
    .in0(multiplexer_43_out), .in1(multiplexer_47_out), .out(multiplexer_75_out), .sel(in_4[2]));
  Multiplexer #(.enable("false")) multiplexer_76 (
    .in0(multiplexer_44_out), .in1(multiplexer_48_out), .out(multiplexer_76_out), .sel(in_4[2]));
  Multiplexer #(.enable("false")) multiplexer_77 (
    .in0(multiplexer_45_out), .in1(1'b0), .out(multiplexer_77_out), .sel(in_4[2]));
  Multiplexer #(.enable("false")) multiplexer_78 (
    .in0(multiplexer_46_out), .in1(1'b0), .out(multiplexer_78_out), .sel(in_4[2]));
  Multiplexer #(.enable("false")) multiplexer_79 (
    .in0(multiplexer_47_out), .in1(1'b0), .out(multiplexer_79_out), .sel(in_4[2]));
  Multiplexer #(.enable("false")) multiplexer_80 (
    .in0(multiplexer_48_out), .in1(1'b0), .out(multiplexer_80_out), .sel(in_4[2]));
  not not_3 (not_3_out, in_4[2]);
  Multiplexer #(.enable("false")) multiplexer_81 (
    .in0(1'b0), .in1(multiplexer_49_out), .out(multiplexer_81_out), .sel(not_3_out));
  Multiplexer #(.enable("false")) multiplexer_82 (
    .in0(1'b0), .in1(multiplexer_50_out), .out(multiplexer_82_out), .sel(not_3_out));
  Multiplexer #(.enable("false")) multiplexer_83 (
    .in0(1'b0), .in1(multiplexer_51_out), .out(multiplexer_83_out), .sel(not_3_out));
  Multiplexer #(.enable("false")) multiplexer_84 (
    .in0(1'b0), .in1(multiplexer_52_out), .out(multiplexer_84_out), .sel(not_3_out));
  Multiplexer #(.enable("false")) multiplexer_85 (
    .in0(multiplexer_49_out), .in1(multiplexer_53_out), .out(multiplexer_85_out), .sel(not_3_out));
  Multiplexer #(.enable("false")) multiplexer_86 (
    .in0(multiplexer_50_out), .in1(multiplexer_54_out), .out(multiplexer_86_out), .sel(not_3_out));
  Multiplexer #(.enable("false")) multiplexer_87 (
    .in0(multiplexer_51_out), .in1(multiplexer_55_out), .out(multiplexer_87_out), .sel(not_3_out));
  Multiplexer #(.enable("false")) multiplexer_88 (
    .in0(multiplexer_52_out), .in1(multiplexer_56_out), .out(multiplexer_88_out), .sel(not_3_out));
  Multiplexer #(.enable("false")) multiplexer_89 (
    .in0(multiplexer_53_out), .in1(multiplexer_57_out), .out(multiplexer_89_out), .sel(not_3_out));
  Multiplexer #(.enable("false")) multiplexer_90 (
    .in0(multiplexer_54_out), .in1(multiplexer_58_out), .out(multiplexer_90_out), .sel(not_3_out));
  Multiplexer #(.enable("false")) multiplexer_91 (
    .in0(multiplexer_55_out), .in1(multiplexer_59_out), .out(multiplexer_91_out), .sel(not_3_out));
  Multiplexer #(.enable("false")) multiplexer_92 (
    .in0(multiplexer_56_out), .in1(multiplexer_60_out), .out(multiplexer_92_out), .sel(not_3_out));
  Multiplexer #(.enable("false")) multiplexer_93 (
    .in0(multiplexer_57_out), .in1(multiplexer_61_out), .out(multiplexer_93_out), .sel(not_3_out));
  Multiplexer #(.enable("false")) multiplexer_94 (
    .in0(multiplexer_58_out), .in1(multiplexer_62_out), .out(multiplexer_94_out), .sel(not_3_out));
  Multiplexer #(.enable("false")) multiplexer_95 (
    .in0(multiplexer_59_out), .in1(multiplexer_63_out), .out(multiplexer_95_out), .sel(not_3_out));
  Multiplexer #(.enable("false")) multiplexer_96 (
    .in0(multiplexer_60_out), .in1(multiplexer_64_out), .out(multiplexer_96_out), .sel(not_3_out));
  Multiplexer #(.enable("false")) multiplexer_97 (
    .in0(multiplexer_65_out), .in1(multiplexer_73_out), .out(multiplexer_112_out[15]), .sel(in_4[3]));
  Multiplexer #(.enable("false")) multiplexer_98 (
    .in0(multiplexer_66_out), .in1(multiplexer_74_out), .out(multiplexer_112_out[14]), .sel(in_4[3]));
  Multiplexer #(.enable("false")) multiplexer_99 (
    .in0(multiplexer_67_out), .in1(multiplexer_75_out), .out(multiplexer_112_out[13]), .sel(in_4[3]));
  Multiplexer #(.enable("false")) multiplexer_100 (
    .in0(multiplexer_68_out), .in1(multiplexer_76_out), .out(multiplexer_112_out[12]), .sel(in_4[3]));
  Multiplexer #(.enable("false")) multiplexer_101 (
    .in0(multiplexer_69_out), .in1(multiplexer_77_out), .out(multiplexer_112_out[11]), .sel(in_4[3]));
  Multiplexer #(.enable("false")) multiplexer_102 (
    .in0(multiplexer_70_out), .in1(multiplexer_78_out), .out(multiplexer_112_out[10]), .sel(in_4[3]));
  Multiplexer #(.enable("false")) multiplexer_103 (
    .in0(multiplexer_71_out), .in1(multiplexer_79_out), .out(multiplexer_112_out[9]), .sel(in_4[3]));
  Multiplexer #(.enable("false")) multiplexer_104 (
    .in0(multiplexer_72_out), .in1(multiplexer_80_out), .out(multiplexer_112_out[8]), .sel(in_4[3]));
  Multiplexer #(.enable("false")) multiplexer_105 (
    .in0(multiplexer_73_out), .in1(1'b0), .out(multiplexer_112_out[7]), .sel(in_4[3]));
  Multiplexer #(.enable("false")) multiplexer_106 (
    .in0(multiplexer_74_out), .in1(1'b0), .out(multiplexer_112_out[6]), .sel(in_4[3]));
  Multiplexer #(.enable("false")) multiplexer_107 (
    .in0(multiplexer_75_out), .in1(1'b0), .out(multiplexer_112_out[5]), .sel(in_4[3]));
  Multiplexer #(.enable("false")) multiplexer_108 (
    .in0(multiplexer_76_out), .in1(1'b0), .out(multiplexer_112_out[4]), .sel(in_4[3]));
  Multiplexer #(.enable("false")) multiplexer_109 (
    .in0(multiplexer_77_out), .in1(1'b0), .out(multiplexer_112_out[3]), .sel(in_4[3]));
  Multiplexer #(.enable("false")) multiplexer_110 (
    .in0(multiplexer_78_out), .in1(1'b0), .out(multiplexer_112_out[2]), .sel(in_4[3]));
  Multiplexer #(.enable("false")) multiplexer_111 (
    .in0(multiplexer_79_out), .in1(1'b0), .out(multiplexer_112_out[1]), .sel(in_4[3]));
  Multiplexer #(.enable("false")) multiplexer_112 (
    .in0(multiplexer_80_out), .in1(1'b0), .out(multiplexer_112_out[0]), .sel(in_4[3]));
  not not_4 (not_4_out, in_4[3]);
  Multiplexer #(.enable("false")) multiplexer_113 (
    .in0(1'b0), .in1(multiplexer_81_out), .out(multiplexer_128_out[15]), .sel(not_4_out));
  Multiplexer #(.enable("false")) multiplexer_114 (
    .in0(1'b0), .in1(multiplexer_82_out), .out(multiplexer_128_out[14]), .sel(not_4_out));
  Multiplexer #(.enable("false")) multiplexer_115 (
    .in0(1'b0), .in1(multiplexer_83_out), .out(multiplexer_128_out[13]), .sel(not_4_out));
  Multiplexer #(.enable("false")) multiplexer_116 (
    .in0(1'b0), .in1(multiplexer_84_out), .out(multiplexer_128_out[12]), .sel(not_4_out));
  Multiplexer #(.enable("false")) multiplexer_117 (
    .in0(1'b0), .in1(multiplexer_85_out), .out(multiplexer_128_out[11]), .sel(not_4_out));
  Multiplexer #(.enable("false")) multiplexer_118 (
    .in0(1'b0), .in1(multiplexer_86_out), .out(multiplexer_128_out[10]), .sel(not_4_out));
  Multiplexer #(.enable("false")) multiplexer_119 (
    .in0(1'b0), .in1(multiplexer_87_out), .out(multiplexer_128_out[9]), .sel(not_4_out));
  Multiplexer #(.enable("false")) multiplexer_120 (
    .in0(1'b0), .in1(multiplexer_88_out), .out(multiplexer_128_out[8]), .sel(not_4_out));
  Multiplexer #(.enable("false")) multiplexer_121 (
    .in0(multiplexer_81_out), .in1(multiplexer_89_out), .out(multiplexer_128_out[7]), .sel(not_4_out));
  Multiplexer #(.enable("false")) multiplexer_122 (
    .in0(multiplexer_82_out), .in1(multiplexer_90_out), .out(multiplexer_128_out[6]), .sel(not_4_out));
  Multiplexer #(.enable("false")) multiplexer_123 (
    .in0(multiplexer_83_out), .in1(multiplexer_91_out), .out(multiplexer_128_out[5]), .sel(not_4_out));
  Multiplexer #(.enable("false")) multiplexer_124 (
    .in0(multiplexer_84_out), .in1(multiplexer_92_out), .out(multiplexer_128_out[4]), .sel(not_4_out));
  Multiplexer #(.enable("false")) multiplexer_125 (
    .in0(multiplexer_85_out), .in1(multiplexer_93_out), .out(multiplexer_128_out[3]), .sel(not_4_out));
  Multiplexer #(.enable("false")) multiplexer_126 (
    .in0(multiplexer_86_out), .in1(multiplexer_94_out), .out(multiplexer_128_out[2]), .sel(not_4_out));
  Multiplexer #(.enable("false")) multiplexer_127 (
    .in0(multiplexer_87_out), .in1(multiplexer_95_out), .out(multiplexer_128_out[1]), .sel(not_4_out));
  Multiplexer #(.enable("false")) multiplexer_128 (
    .in0(multiplexer_88_out), .in1(multiplexer_96_out), .out(multiplexer_128_out[0]), .sel(not_4_out));
  Multiplexer #(.width(16), .enable("false")) multiplexer_129 (
    .in0(multiplexer_112_out), .in1(multiplexer_128_out), .out(multiplexer_129_out), .sel(in_2));
  _2B_Register u_2b_register_1 (
    .in_1(multiplexer_129_out), .in_2(n1_shortdelay_1_out_2), .out_7(out_7), .in_3(in_6), .in_4(in_5),
    .in_5(1'b0));  // open: out_6
  _1_ShortDelay u_1_shortdelay_1 (.in_1(n5t_edge_trigger_1_out_2), .out_2(n1_shortdelay_1_out_2));
endmodule

module Instruction_Register (
  input  [5:0] in_1,
  input  in_2,
  input  in_3,
  input  in_4,
  input  in_5,
  input  Wr,
  input  Cl,
  input  Res,
  input  [3:0] in_9,
  input  [3:0] in_10,
  input  [3:0] in_11,
  input  [3:0] in_12,
  input  Pwr,
  output out_14,
  output [15:0] out_15,
  output [5:0] out_16,
  output [5:0] out_17,
  output [3:0] out_18,
  output [3:0] out_19,
  output [3:0] out_20,
  output [3:0] out_21
);

  wire and_2_out, and_3_out, d_ff_1_q, falling_trigger_1_out_2, multiplexer_2_out, n1_4t_delay_1_out_2,
       n1_4t_delay_2_out_2, n1_4t_delay_3_out_2, n1_4t_delay_4_out_2, n1_4t_delay_5_out_2, not_1_out,
       not_2_out, not_3_out, not_4_out, or_1_out, or_2_out;
  wire [5:0] multiplexer_1_out, n6_buf_1_out_3, n6_buf_2_out_3;
  wire [15:0] demultiplexer_1_out0, program_memory_1_out_10;

  not not_1 (not_1_out, in_3);
  and and_1 (out_14, d_ff_1_q, not_1_out);
  D_Flip_Flop d_ff_1 (.Q(d_ff_1_q), .preset(in_2), .reset(out_14));  // open: clk, D, Qn, en
  and and_2 (and_2_out, in_3, Pwr);
  _6_Up_Down_Counter u_6_up_down_counter_1 (.out_4(out_16), .in_1(in_4), .in_2(in_5), .in_3(or_1_out));
  or or_1 (or_1_out, Res, Pwr);
  Falling_Trigger falling_trigger_1 (.in_1(and_2_out), .out_2(falling_trigger_1_out_2));
  not not_2 (not_2_out, and_2_out);
  and and_3 (and_3_out, in_2, falling_trigger_1_out_2);
  Program_Counter program_counter_1 (
    .in_1(not_2_out), .in_2(n6_buf_1_out_3), .in_3(or_2_out), .in_4(Pwr), .out_5(out_17));
  _6_BUF u_6_buf_1 (.in_2(in_2), .in_1(in_1), .out_3(n6_buf_1_out_3));
  or or_2 (or_2_out, and_3_out, Res);
  _6_BUF u_6_buf_2 (.in_2(and_2_out), .in_1(out_17), .out_3(n6_buf_2_out_3));
  _1_4T_Delay u_1_4t_delay_1 (.in_1(n1_4t_delay_2_out_2), .out_2(n1_4t_delay_1_out_2));
  _1_4T_Delay u_1_4t_delay_2 (.in_1(n1_4t_delay_3_out_2), .out_2(n1_4t_delay_2_out_2));
  _1_4T_Delay u_1_4t_delay_3 (.in_1(and_2_out), .out_2(n1_4t_delay_3_out_2));
  Multiplexer #(.width(6), .enable("false")) multiplexer_1 (
    .in0(out_16), .in1(n6_buf_2_out_3), .out(multiplexer_1_out), .sel(Pwr));
  _1_4T_Delay u_1_4t_delay_4 (.in_1(n1_4t_delay_5_out_2), .out_2(n1_4t_delay_4_out_2));
  _1_4T_Delay u_1_4t_delay_5 (.in_1(n1_4t_delay_1_out_2), .out_2(n1_4t_delay_5_out_2));
  Program_Memory program_memory_1 (
    .Rs(Cl), .Wr(Wr), .Rd(multiplexer_2_out), .in_4(multiplexer_1_out), .in_5(in_9),
    .out_10(program_memory_1_out_10), .in_7(in_11), .in_8(in_12), .in_6(in_10), .in_9(Res));
  not not_3 (not_3_out, Pwr);
  Demultiplexer #(.width(16), .enable("false")) demultiplexer_1 (
    .out0(demultiplexer_1_out0), .out1(out_15), .in(program_memory_1_out_10), .sel(not_3_out));
  Multiplexer #(.enable("false")) multiplexer_2 (.in0(and_2_out), .in1(1'b1), .out(multiplexer_2_out), .sel(not_3_out));
  not not_4 (not_4_out, and_2_out);
  _4_REG u_4_reg_1 (.in_3(demultiplexer_1_out0[15:12]), .out_4(out_18), .in_1(n1_4t_delay_4_out_2), .in_2(not_4_out));
  _4_REG u_4_reg_2 (.in_3(demultiplexer_1_out0[11:8]), .out_4(out_19), .in_1(n1_4t_delay_4_out_2), .in_2(not_4_out));
  _4_REG u_4_reg_3 (.in_3(demultiplexer_1_out0[7:4]), .out_4(out_20), .in_1(n1_4t_delay_4_out_2), .in_2(not_4_out));
  _4_REG u_4_reg_4 (.in_3(demultiplexer_1_out0[3:0]), .out_4(out_21), .in_1(n1_4t_delay_4_out_2), .in_2(not_4_out));
endmodule

module Instruction_Decoder (
  input  [3:0] in_1,
  input  [3:0] in_2,
  input  [3:0] in_3,
  input  [3:0] in_4,
  output STOR,
  output COPY,
  output RES,
  output ALU,
  output SHFT,
  output GET,
  output GET_SET,
  output GET_2,
  output JUMP,
  output SREG,
  output CREG,
  output END,
  output [1:0] iX,
  output [3:0] Wr,
  output [3:0] Rs,
  output [3:0] Rd,
  output ALU_2,
  output SFT,
  output CND,
  output [3:0] nALU,
  output [3:0] Shft_2,
  output Shft_Dir,
  output Shft_Rot,
  output [7:0] Mem_Src,
  output [7:0] Mem_Dest,
  output [5:0] Jump_2,
  output A_B_Reg
);

  wire and_1_out, and_2_out, and_5_out, and_7_out, and_10_out, and_14_out, and_17_out, and_19_out,
       and_23_out, and_25_out, and_27_out, and_30_out, demultiplexer_1_out1, demultiplexer_1_out2,
       demultiplexer_2_out1, demultiplexer_2_out2, demultiplexer_2_out3, demultiplexer_3_out0,
       demultiplexer_3_out1, demultiplexer_3_out2, n1_4t_delay_1_out_2, n1_4t_delay_2_out_2,
       n1_4t_delay_3_out_2, n1_4t_delay_4_out_2, n4_detector_1_out_2, not_1_out, not_2_out, not_3_out,
       not_4_out, not_5_out, not_6_out, not_7_out, not_8_out, not_9_out, not_10_out, not_11_out, not_12_out,
       not_13_out, not_14_out, not_15_out, not_16_out, not_17_out, not_18_out, not_19_out, not_20_out,
       not_21_out, not_22_out, not_23_out, not_24_out, not_25_out, or_2_out, or_4_out, or_5_out, or_6_out,
       or_7_out, or_8_out, or_9_out, or_10_out, or_12_out, xor_1_out, xor_2_out;
  wire [1:0] n4_buf_1_out_3, n4_buf_1_out_3_2, n4_buf_23_out_3, n4_buf_23_out_3_2, n4_buf_24_out_3,
       n4_buf_24_out_3_2, or_11_out;
  wire [3:0] n4_buf_2_out_3, n4_buf_4_out_3, n4_buf_6_out_3, n4_buf_7_out_3, n4_buf_9_out_3, n4_buf_10_out_3,
       n4_buf_11_out_3, n4_buf_14_out_3, n4_buf_15_out_3, n4_buf_18_out_3, n4_buf_21_out_3, n4_buf_22_out_3,
       n4_detector_2_out_2, or_1_out, or_3_out;
  wire [5:0] n6_buf_1_out_3;
  wire [7:0] n4_buf_17_out_3, n4_buf_20_out_3;

  _4_Detector u_4_detector_1 (.in_1(n4_detector_2_out_2), .out_2(n4_detector_1_out_2));
  _4_Detector u_4_detector_2 (.in_1(in_1), .out_2(n4_detector_2_out_2[0]));
  _4_Detector u_4_detector_3 (.in_1(in_2), .out_2(n4_detector_2_out_2[1]));
  _1_4T_Delay u_1_4t_delay_1 (.in_1(n1_4t_delay_2_out_2), .out_2(n1_4t_delay_1_out_2));
  _1_4T_Delay u_1_4t_delay_2 (.in_1(n4_detector_1_out_2), .out_2(n1_4t_delay_2_out_2));
  _4_Detector u_4_detector_4 (.in_1(in_3), .out_2(n4_detector_2_out_2[2]));
  _4_Detector u_4_detector_5 (.in_1(in_4), .out_2(n4_detector_2_out_2[3]));
  _1_4T_Delay u_1_4t_delay_3 (.in_1(n1_4t_delay_1_out_2), .out_2(n1_4t_delay_3_out_2));
  _1_4T_Delay u_1_4t_delay_4 (.in_1(n1_4t_delay_3_out_2), .out_2(n1_4t_delay_4_out_2));
  not not_1 (not_1_out, in_1[3]);
  not not_2 (not_2_out, in_1[0]);
  not not_3 (not_3_out, in_1[2]);
  not not_4 (not_4_out, in_1[1]);
  and and_1 (and_1_out, not_1_out, not_3_out, not_2_out, not_4_out);
  and and_2 (and_2_out, in_2[0], and_1_out);
  and and_3 (END, n1_4t_delay_4_out_2, and_2_out);
  and and_4 (STOR, n1_4t_delay_4_out_2, and_5_out);
  not not_5 (not_5_out, in_1[1]);
  not not_6 (not_6_out, in_1[2]);
  not not_7 (not_7_out, in_1[3]);
  and and_5 (and_5_out, not_7_out, not_6_out, in_1[0], not_5_out);
  _4_BUF u_4_buf_1 (.in_2(and_5_out), .in_1(in_3), .out_3({n4_buf_1_out_3, n4_buf_1_out_3_2}));
  _2_BUF u_2_buf_1 (.in_2(n1_4t_delay_4_out_2), .in_1(n4_buf_1_out_3), .out_3(iX));
  _4_BUF u_4_buf_2 (.in_2(and_5_out), .in_1(in_2), .out_3(n4_buf_2_out_3));
  assign or_1_out = n4_buf_2_out_3 | n4_buf_7_out_3 | n4_buf_18_out_3;  // OR_Gate or_1, 4 bits wide
  _4_BUF u_4_buf_3 (.in_2(n1_4t_delay_4_out_2), .in_1(or_1_out), .out_3(Wr));
  and and_6 (COPY, n1_4t_delay_4_out_2, and_7_out);
  _4_BUF u_4_buf_4 (.in_2(and_7_out), .in_1(in_4), .out_3(n4_buf_4_out_3));
  or or_2 (or_2_out, n4_buf_4_out_3[3], n4_buf_4_out_3[2]);
  _4_BUF u_4_buf_5 (.in_2(n1_4t_delay_4_out_2), .in_1(n4_buf_10_out_3), .out_3(Rs));
  not not_8 (not_8_out, in_1[3]);
  not not_9 (not_9_out, in_1[2]);
  not not_10 (not_10_out, in_1[0]);
  and and_7 (and_7_out, not_8_out, not_9_out, not_10_out, in_1[1]);
  _4_BUF u_4_buf_6 (.in_2(xor_1_out), .in_1(in_2), .out_3(n4_buf_6_out_3));
  xor xor_1 (xor_1_out, and_7_out, or_2_out);
  _4_BUF u_4_buf_7 (.in_2(and_7_out), .in_1(in_3), .out_3(n4_buf_7_out_3));
  Demultiplexer #(.select(2), .enable("false")) demultiplexer_1 (
    .out1(demultiplexer_1_out1), .out2(demultiplexer_1_out2), .in(or_2_out), .sel(n4_buf_4_out_3[3:2]));  // open: out0, out3
  assign or_3_out = n4_buf_6_out_3 | n4_buf_22_out_3 | n4_buf_21_out_3;  // OR_Gate or_3, 4 bits wide
  _4_BUF u_4_buf_8 (.in_2(n1_4t_delay_4_out_2), .in_1(or_3_out), .out_3(Rd));
  and and_8 (RES, n1_4t_delay_4_out_2, and_10_out);
  xor xor_2 (xor_2_out, and_10_out, or_4_out);
  _4_BUF u_4_buf_9 (.in_2(and_10_out), .in_1(in_3), .out_3(n4_buf_9_out_3));
  or or_4 (or_4_out, n4_buf_9_out_3[3], n4_buf_9_out_3[2]);
  or or_5 (or_5_out, demultiplexer_2_out1, demultiplexer_1_out1);
  or or_6 (or_6_out, demultiplexer_3_out0, or_5_out);
  and and_9 (ALU_2, n1_4t_delay_4_out_2, or_6_out);
  not not_11 (not_11_out, in_1[3]);
  not not_12 (not_12_out, in_1[2]);
  and and_10 (and_10_out, not_11_out, not_12_out, in_1[0], in_1[1]);
  _4_BUF u_4_buf_10 (.in_2(xor_2_out), .in_1(in_2), .out_3(n4_buf_10_out_3));
  Demultiplexer #(.select(2), .enable("false")) demultiplexer_2 (
    .out1(demultiplexer_2_out1), .out2(demultiplexer_2_out2), .out3(demultiplexer_2_out3), .in(or_4_out),
    .sel(n4_buf_9_out_3[3:2]));  // open: out0
  or or_7 (or_7_out, demultiplexer_2_out2, demultiplexer_1_out2);
  or or_8 (or_8_out, demultiplexer_3_out2, demultiplexer_2_out3);
  or or_9 (or_9_out, demultiplexer_3_out1, or_7_out);
  and and_11 (CND, n1_4t_delay_4_out_2, or_8_out);
  and and_12 (SFT, n1_4t_delay_4_out_2, or_9_out);
  and and_13 (ALU, n1_4t_delay_4_out_2, and_14_out);
  not not_13 (not_13_out, in_1[3]);
  _4_BUF u_4_buf_11 (.in_2(and_14_out), .in_1(in_2), .out_3(n4_buf_11_out_3));
  _4_BUF u_4_buf_12 (.in_2(n1_4t_delay_4_out_2), .in_1(n4_buf_11_out_3), .out_3(nALU));
  not not_14 (not_14_out, in_1[1]);
  not not_15 (not_15_out, in_1[0]);
  and and_14 (and_14_out, not_13_out, in_1[2], not_15_out, not_14_out);
  _4_BUF u_4_buf_13 (.in_2(n1_4t_delay_4_out_2), .in_1(n4_buf_14_out_3), .out_3(Shft_2));
  and and_15 (SHFT, n1_4t_delay_4_out_2, and_17_out);
  not not_16 (not_16_out, in_1[3]);
  _4_BUF u_4_buf_14 (.in_2(and_17_out), .in_1(in_2), .out_3(n4_buf_14_out_3));
  and and_16 (Shft_Dir, n1_4t_delay_4_out_2, n4_buf_15_out_3[3]);
  not not_17 (not_17_out, in_1[1]);
  and and_17 (and_17_out, not_16_out, in_1[2], in_1[0], not_17_out);
  _4_BUF u_4_buf_15 (.in_2(and_17_out), .in_1(in_3), .out_3(n4_buf_15_out_3));
  and and_18 (Shft_Rot, n1_4t_delay_4_out_2, n4_buf_15_out_3[2]);
  not not_18 (not_18_out, in_1[3]);
  and and_19 (and_19_out, not_18_out, in_1[2], not_19_out, in_1[1]);
  _8_BUF u_8_buf_1 (.in_2(n1_4t_delay_4_out_2), .in_1(n4_buf_17_out_3), .out_3(Mem_Src));
  and and_20 (GET, n1_4t_delay_4_out_2, and_19_out);
  and and_21 (GET_SET, n1_4t_delay_4_out_2, or_10_out);
  not not_19 (not_19_out, in_1[0]);
  or or_10 (or_10_out, and_19_out, and_23_out);
  _4_BUF u_4_buf_16 (.in_2(and_19_out), .in_1(in_2), .out_3(n4_buf_17_out_3[7:4]));
  _4_BUF u_4_buf_17 (.in_2(and_19_out), .in_1(in_3), .out_3(n4_buf_17_out_3[3:0]));
  _4_BUF u_4_buf_18 (.in_2(and_19_out), .in_1(in_4), .out_3(n4_buf_18_out_3));
  _8_BUF u_8_buf_2 (.in_2(n1_4t_delay_4_out_2), .in_1(n4_buf_20_out_3), .out_3(Mem_Dest));
  and and_22 (GET_2, and_23_out, n1_4t_delay_4_out_2);
  not not_20 (not_20_out, in_1[3]);
  and and_23 (and_23_out, not_20_out, in_1[2], in_1[0], in_1[1]);
  and and_24 (JUMP, n1_4t_delay_4_out_2, and_25_out);
  _4_BUF u_4_buf_19 (.in_2(and_23_out), .in_1(in_2), .out_3(n4_buf_20_out_3[7:4]));
  _4_BUF u_4_buf_20 (.in_2(and_23_out), .in_1(in_3), .out_3(n4_buf_20_out_3[3:0]));
  _4_BUF u_4_buf_21 (.in_2(and_23_out), .in_1(in_4), .out_3(n4_buf_21_out_3));
  not not_21 (not_21_out, in_1[2]);
  not not_22 (not_22_out, in_1[1]);
  and and_25 (and_25_out, in_1[3], not_21_out, in_1[0], not_22_out);
  _6_BUF u_6_buf_1 (.in_2(and_25_out), .in_1({in_2[1:0], in_3}), .out_3(n6_buf_1_out_3));
  Demultiplexer #(.select(2), .enable("false")) demultiplexer_3 (
    .out0(demultiplexer_3_out0), .out1(demultiplexer_3_out1), .out2(demultiplexer_3_out2), .in(and_27_out),
    .sel(or_11_out));  // open: out3
  assign or_11_out = n4_buf_23_out_3_2 | n4_buf_24_out_3_2;  // OR_Gate or_11, 2 bits wide
  _6_BUF u_6_buf_2 (.in_2(n1_4t_delay_4_out_2), .in_1(n6_buf_1_out_3), .out_3(Jump_2));
  and and_26 (SREG, n1_4t_delay_4_out_2, and_27_out);
  not not_23 (not_23_out, in_1[0]);
  not not_24 (not_24_out, in_1[2]);
  and and_27 (and_27_out, in_1[3], not_24_out, not_23_out, in_1[1]);
  or or_12 (or_12_out, n4_buf_23_out_3[0], n4_buf_24_out_3[0]);
  and and_28 (A_B_Reg, n1_4t_delay_4_out_2, or_12_out);
  _4_BUF u_4_buf_22 (.in_2(and_27_out), .in_1(in_2), .out_3(n4_buf_22_out_3));
  _4_BUF u_4_buf_23 (
    .in_2(and_27_out), .in_1(in_3), .out_3({n4_buf_23_out_3_2[0], n4_buf_23_out_3_2[1], n4_buf_23_out_3}));
  and and_29 (CREG, n1_4t_delay_4_out_2, and_30_out);
  not not_25 (not_25_out, in_1[2]);
  and and_30 (and_30_out, in_1[3], not_25_out, in_1[0], in_1[1]);
  _4_BUF u_4_buf_24 (
    .in_2(and_30_out), .in_1(in_2), .out_3({n4_buf_24_out_3_2[0], n4_buf_24_out_3_2[1], n4_buf_24_out_3}));
endmodule

module Condition_Decoder (
  input  [3:0] in_1,
  input  [3:0] in_2,
  output out_3,
  output out_4,
  output out_5,
  output out_6,
  output out_7,
  output out_8,
  output out_9
);

  wire not_1_out, not_2_out, not_3_out;

  not not_1 (not_1_out, in_1[1]);
  not not_2 (not_2_out, in_1[2]);
  not not_3 (not_3_out, in_1[0]);
  and and_1 (out_9, not_2_out, in_1[3], not_1_out, not_3_out);
  Demultiplexer #(.select(3), .enable("false")) demultiplexer_1 (
    .out0(out_3), .out1(out_4), .out2(out_5), .out3(out_6), .out4(out_7), .out5(out_8), .in(out_9),
    .sel(in_2[3:1]));  // open: out6, out7
endmodule

module Condition_Checker (
  input  [15:0] in_1,
  input  [15:0] in_2,
  input  in_3,
  input  in_4,
  input  in_5,
  input  in_6,
  input  in_7,
  input  in_8,
  input  in_9,
  output out_10
);

  wire and_2_out, and_3_out, and_4_out, and_5_out, and_6_out, and_7_out, and_8_out, and_9_out, and_10_out,
       and_11_out, and_12_out, and_13_out, n1_4t_delay_1_out_2, n1_4t_delay_2_out_2, n1_4t_delay_3_out_2,
       n1_4t_delay_4_out_2, n1_4t_delay_5_out_2, n1_4t_delay_6_out_2, n1_4t_delay_7_out_2,
       n1_4t_delay_8_out_2, n16_comparator_1_out_3, n16_comparator_1_out_4, n16_comparator_1_out_5, or_1_out,
       or_2_out, or_3_out, or_4_out;

  and and_1 (out_10, or_1_out, n1_4t_delay_8_out_2);
  or or_1 (or_1_out, and_6_out, and_4_out, and_3_out, and_5_out, and_2_out, and_7_out);
  and and_2 (and_2_out, or_2_out, and_10_out);
  and and_3 (and_3_out, n16_comparator_1_out_4, and_8_out);
  and and_4 (and_4_out, and_9_out, n16_comparator_1_out_3);
  or or_2 (or_2_out, n16_comparator_1_out_3, n16_comparator_1_out_5);
  and and_5 (and_5_out, n16_comparator_1_out_5, and_11_out);
  and and_6 (and_6_out, and_12_out, or_4_out);
  and and_7 (and_7_out, and_13_out, or_3_out);
  or or_3 (or_3_out, n16_comparator_1_out_5, n16_comparator_1_out_4);
  and and_8 (and_8_out, in_4, in_3);
  and and_9 (and_9_out, in_6, in_3);
  and and_10 (and_10_out, in_5, in_3);
  or or_4 (or_4_out, n16_comparator_1_out_3, n16_comparator_1_out_4);
  and and_11 (and_11_out, in_7, in_3);
  and and_12 (and_12_out, in_8, in_3);
  and and_13 (and_13_out, in_9, in_3);
  _16_Comparator u_16_comparator_1 (
    .in_1(in_1), .in_2(in_2), .out_3(n16_comparator_1_out_3), .out_4(n16_comparator_1_out_4),
    .out_5(n16_comparator_1_out_5));
  _1_4T_Delay u_1_4t_delay_1 (.in_1(in_3), .out_2(n1_4t_delay_1_out_2));
  _1_4T_Delay u_1_4t_delay_2 (.in_1(n1_4t_delay_1_out_2), .out_2(n1_4t_delay_2_out_2));
  _1_4T_Delay u_1_4t_delay_3 (.in_1(n1_4t_delay_2_out_2), .out_2(n1_4t_delay_3_out_2));
  _1_4T_Delay u_1_4t_delay_4 (.in_1(n1_4t_delay_5_out_2), .out_2(n1_4t_delay_4_out_2));
  _1_4T_Delay u_1_4t_delay_5 (.in_1(n1_4t_delay_3_out_2), .out_2(n1_4t_delay_5_out_2));
  _1_4T_Delay u_1_4t_delay_6 (.in_1(n1_4t_delay_7_out_2), .out_2(n1_4t_delay_6_out_2));
  _1_4T_Delay u_1_4t_delay_7 (.in_1(n1_4t_delay_4_out_2), .out_2(n1_4t_delay_7_out_2));
  _1_4T_Delay u_1_4t_delay_8 (.in_1(n1_4t_delay_6_out_2), .out_2(n1_4t_delay_8_out_2));
endmodule

module Reset_Decoder (
  input  [3:0] in_1,
  input  in_2
);
endmodule

module _16_Comparator (
  input  [15:0] in_1,
  input  [15:0] in_2,
  output out_3,
  output out_4,
  output out_5
);

  wire comp2_1_out_6, comp2_1_out_7, comp2_2_out_6, comp2_2_out_7, comp2_3_out_6, comp2_3_out_7;

  Comp2 comp2_1 (
    .in_1(in_1[3:0]), .in_2(in_2[3:0]), .in_3(1'b0), .in_4(1'b1), .in_5(1'b1), .out_6(comp2_1_out_6),
    .out_7(comp2_1_out_7));  // open: out_8
  Comp2 comp2_2 (
    .in_1(in_1[7:4]), .in_2(in_2[7:4]), .in_3(comp2_1_out_6), .in_4(comp2_1_out_7), .in_5(1'b1),
    .out_6(comp2_2_out_6), .out_7(comp2_2_out_7));  // open: out_8
  Comp2 comp2_3 (
    .in_1(in_1[11:8]), .in_2(in_2[11:8]), .in_3(comp2_2_out_6), .in_4(comp2_2_out_7), .in_5(1'b1),
    .out_6(comp2_3_out_6), .out_7(comp2_3_out_7));  // open: out_8
  Comp2 comp2_4 (
    .in_1(in_1[15:12]), .in_2(in_2[15:12]), .in_3(comp2_3_out_6), .in_4(comp2_3_out_7), .in_5(1'b1),
    .out_6(out_3), .out_7(out_4), .out_8(out_5));
endmodule

module Program_Memory (
  input  Rs,
  input  Wr,
  input  Rd,
  input  [5:0] in_4,
  input  [3:0] in_5,
  input  [3:0] in_6,
  input  [3:0] in_7,
  input  [3:0] in_8,
  input  in_9,
  output [15:0] out_10
);

  wire demultiplexer_1_out0, demultiplexer_1_out1, demultiplexer_1_out2, demultiplexer_1_out3,
       demultiplexer_2_out0, demultiplexer_2_out1, demultiplexer_2_out2, demultiplexer_2_out3,
       demultiplexer_3_out0, demultiplexer_3_out1, demultiplexer_3_out2, demultiplexer_3_out3,
       n2b_register_2_out_6, n2b_register_3_out_6, n2b_register_4_out_6, n2b_register_5_out_6,
       n2b_register_6_out_6, n2b_register_7_out_6, n2b_register_8_out_6, n2b_register_9_out_6,
       n2b_register_10_out_6, n2b_register_11_out_6, n2b_register_12_out_6, n2b_register_13_out_6,
       n2b_register_14_out_6, n2b_register_15_out_6, n2b_register_16_out_6, n2b_register_18_out_6,
       n2b_register_19_out_6, n2b_register_20_out_6, n2b_register_21_out_6, n2b_register_22_out_6,
       n2b_register_23_out_6, n2b_register_24_out_6, n2b_register_25_out_6, n2b_register_26_out_6,
       n2b_register_27_out_6, n2b_register_28_out_6, n2b_register_29_out_6, n2b_register_30_out_6,
       n2b_register_31_out_6, n2b_register_32_out_6, n2b_register_34_out_6, n2b_register_35_out_6,
       n2b_register_36_out_6, n2b_register_37_out_6, n2b_register_38_out_6, n2b_register_39_out_6,
       n2b_register_40_out_6, n2b_register_41_out_6, n2b_register_42_out_6, n2b_register_43_out_6,
       n2b_register_44_out_6, n2b_register_45_out_6, n2b_register_46_out_6, n2b_register_47_out_6,
       n2b_register_48_out_6, n2b_register_50_out_6, n2b_register_51_out_6, n2b_register_52_out_6,
       n2b_register_53_out_6, n2b_register_54_out_6, n2b_register_55_out_6, n2b_register_56_out_6,
       n2b_register_57_out_6, n2b_register_58_out_6, n2b_register_59_out_6, n2b_register_60_out_6,
       n2b_register_61_out_6, n2b_register_62_out_6, n2b_register_63_out_6, n2b_register_64_out_6,
       n4_bin_hex_1_out_6, n4_bin_hex_1_out_7, n4_bin_hex_1_out_8, n4_bin_hex_1_out_9, n4_bin_hex_1_out_10,
       n4_bin_hex_1_out_11, n4_bin_hex_1_out_12, n4_bin_hex_1_out_13, n4_bin_hex_1_out_14,
       n4_bin_hex_1_out_15, n4_bin_hex_1_out_16, n4_bin_hex_1_out_17, n4_bin_hex_1_out_18,
       n4_bin_hex_1_out_19, n4_bin_hex_1_out_20, n4_bin_hex_1_out_21, n4_bin_hex_2_out_6, n4_bin_hex_2_out_7,
       n4_bin_hex_2_out_8, n4_bin_hex_2_out_9, n4_bin_hex_2_out_10, n4_bin_hex_2_out_11, n4_bin_hex_2_out_12,
       n4_bin_hex_2_out_13, n4_bin_hex_2_out_14, n4_bin_hex_2_out_15, n4_bin_hex_2_out_16,
       n4_bin_hex_2_out_17, n4_bin_hex_2_out_18, n4_bin_hex_2_out_19, n4_bin_hex_2_out_20,
       n4_bin_hex_2_out_21, n4_bin_hex_3_out_6, n4_bin_hex_3_out_7, n4_bin_hex_3_out_8, n4_bin_hex_3_out_9,
       n4_bin_hex_3_out_10, n4_bin_hex_3_out_11, n4_bin_hex_3_out_12, n4_bin_hex_3_out_13,
       n4_bin_hex_3_out_14, n4_bin_hex_3_out_15, n4_bin_hex_3_out_16, n4_bin_hex_3_out_17,
       n4_bin_hex_3_out_18, n4_bin_hex_3_out_19, n4_bin_hex_3_out_20, n4_bin_hex_3_out_21,
       n4_bin_hex_4_out_6, n4_bin_hex_4_out_7, n4_bin_hex_4_out_8, n4_bin_hex_4_out_9, n4_bin_hex_4_out_10,
       n4_bin_hex_4_out_11, n4_bin_hex_4_out_12, n4_bin_hex_4_out_13, n4_bin_hex_4_out_14,
       n4_bin_hex_4_out_15, n4_bin_hex_4_out_16, n4_bin_hex_4_out_17, n4_bin_hex_4_out_18,
       n4_bin_hex_4_out_19, n4_bin_hex_4_out_20, n4_bin_hex_4_out_21, n4_bin_hex_5_out_6, n4_bin_hex_5_out_7,
       n4_bin_hex_5_out_8, n4_bin_hex_5_out_9, n4_bin_hex_5_out_10, n4_bin_hex_5_out_11, n4_bin_hex_5_out_12,
       n4_bin_hex_5_out_13, n4_bin_hex_5_out_14, n4_bin_hex_5_out_15, n4_bin_hex_5_out_16,
       n4_bin_hex_5_out_17, n4_bin_hex_5_out_18, n4_bin_hex_5_out_19, n4_bin_hex_5_out_20,
       n4_bin_hex_5_out_21, n4_bin_hex_6_out_6, n4_bin_hex_6_out_7, n4_bin_hex_6_out_8, n4_bin_hex_6_out_9,
       n4_bin_hex_6_out_10, n4_bin_hex_6_out_11, n4_bin_hex_6_out_12, n4_bin_hex_6_out_13,
       n4_bin_hex_6_out_14, n4_bin_hex_6_out_15, n4_bin_hex_6_out_16, n4_bin_hex_6_out_17,
       n4_bin_hex_6_out_18, n4_bin_hex_6_out_19, n4_bin_hex_6_out_20, n4_bin_hex_6_out_21,
       n4_bin_hex_7_out_6, n4_bin_hex_7_out_7, n4_bin_hex_7_out_8, n4_bin_hex_7_out_9, n4_bin_hex_7_out_10,
       n4_bin_hex_7_out_11, n4_bin_hex_7_out_12, n4_bin_hex_7_out_13, n4_bin_hex_7_out_14,
       n4_bin_hex_7_out_15, n4_bin_hex_7_out_16, n4_bin_hex_7_out_17, n4_bin_hex_7_out_18,
       n4_bin_hex_7_out_19, n4_bin_hex_7_out_20, n4_bin_hex_7_out_21, n4_bin_hex_8_out_6, n4_bin_hex_8_out_7,
       n4_bin_hex_8_out_8, n4_bin_hex_8_out_9, n4_bin_hex_8_out_10, n4_bin_hex_8_out_11, n4_bin_hex_8_out_12,
       n4_bin_hex_8_out_13, n4_bin_hex_8_out_14, n4_bin_hex_8_out_15, n4_bin_hex_8_out_16,
       n4_bin_hex_8_out_17, n4_bin_hex_8_out_18, n4_bin_hex_8_out_19, n4_bin_hex_8_out_20,
       n4_bin_hex_8_out_21, n4_bin_hex_9_out_6, n4_bin_hex_9_out_7, n4_bin_hex_9_out_8, n4_bin_hex_9_out_9,
       n4_bin_hex_9_out_10, n4_bin_hex_9_out_11, n4_bin_hex_9_out_12, n4_bin_hex_9_out_13,
       n4_bin_hex_9_out_14, n4_bin_hex_9_out_15, n4_bin_hex_9_out_16, n4_bin_hex_9_out_17,
       n4_bin_hex_9_out_18, n4_bin_hex_9_out_19, n4_bin_hex_9_out_20, n4_bin_hex_9_out_21,
       n4_bin_hex_10_out_6, n4_bin_hex_10_out_7, n4_bin_hex_10_out_8, n4_bin_hex_10_out_9,
       n4_bin_hex_10_out_10, n4_bin_hex_10_out_11, n4_bin_hex_10_out_12, n4_bin_hex_10_out_13,
       n4_bin_hex_10_out_14, n4_bin_hex_10_out_15, n4_bin_hex_10_out_16, n4_bin_hex_10_out_17,
       n4_bin_hex_10_out_18, n4_bin_hex_10_out_19, n4_bin_hex_10_out_20, n4_bin_hex_10_out_21,
       n4_bin_hex_11_out_6, n4_bin_hex_11_out_7, n4_bin_hex_11_out_8, n4_bin_hex_11_out_9,
       n4_bin_hex_11_out_10, n4_bin_hex_11_out_11, n4_bin_hex_11_out_12, n4_bin_hex_11_out_13,
       n4_bin_hex_11_out_14, n4_bin_hex_11_out_15, n4_bin_hex_11_out_16, n4_bin_hex_11_out_17,
       n4_bin_hex_11_out_18, n4_bin_hex_11_out_19, n4_bin_hex_11_out_20, n4_bin_hex_11_out_21,
       n4_bin_hex_12_out_6, n4_bin_hex_12_out_7, n4_bin_hex_12_out_8, n4_bin_hex_12_out_9,
       n4_bin_hex_12_out_10, n4_bin_hex_12_out_11, n4_bin_hex_12_out_12, n4_bin_hex_12_out_13,
       n4_bin_hex_12_out_14, n4_bin_hex_12_out_15, n4_bin_hex_12_out_16, n4_bin_hex_12_out_17,
       n4_bin_hex_12_out_18, n4_bin_hex_12_out_19, n4_bin_hex_12_out_20, n4_bin_hex_12_out_21;
  wire [3:0] demultiplexer_4_out0, demultiplexer_4_out1, demultiplexer_4_out2, demultiplexer_4_out3;
  wire [15:0] n2b_register_1_out_7, n2b_register_2_out_7, n2b_register_3_out_7, n2b_register_4_out_7,
       n2b_register_5_out_7, n2b_register_6_out_7, n2b_register_7_out_7, n2b_register_8_out_7,
       n2b_register_9_out_7, n2b_register_10_out_7, n2b_register_11_out_7, n2b_register_12_out_7,
       n2b_register_13_out_7, n2b_register_14_out_7, n2b_register_15_out_7, n2b_register_16_out_7,
       n2b_register_17_out_7, n2b_register_18_out_7, n2b_register_19_out_7, n2b_register_20_out_7,
       n2b_register_21_out_7, n2b_register_22_out_7, n2b_register_23_out_7, n2b_register_24_out_7,
       n2b_register_25_out_7, n2b_register_26_out_7, n2b_register_27_out_7, n2b_register_28_out_7,
       n2b_register_29_out_7, n2b_register_30_out_7, n2b_register_31_out_7, n2b_register_32_out_7,
       n2b_register_33_out_7, n2b_register_34_out_7, n2b_register_35_out_7, n2b_register_36_out_7,
       n2b_register_37_out_7, n2b_register_38_out_7, n2b_register_39_out_7, n2b_register_40_out_7,
       n2b_register_41_out_7, n2b_register_42_out_7, n2b_register_43_out_7, n2b_register_44_out_7,
       n2b_register_46_out_7, n2b_register_47_out_7, n2b_register_48_out_7, n2b_register_49_out_7,
       n2b_register_50_out_7, n2b_register_51_out_7, n2b_register_52_out_7, n2b_register_53_out_7,
       n2b_register_54_out_7, n2b_register_55_out_7, n2b_register_56_out_7, n2b_register_57_out_7,
       n2b_register_58_out_7, n2b_register_59_out_7, n2b_register_60_out_7, n2b_register_61_out_7,
       n2b_register_62_out_7, n2b_register_63_out_7, n2b_register_64_out_7, or_1_out, or_2_out, or_3_out,
       or_4_out;

  Demultiplexer #(.select(2)) demultiplexer_1 (
    .out0(demultiplexer_1_out0), .out1(demultiplexer_1_out1), .out2(demultiplexer_1_out2),
    .out3(demultiplexer_1_out3), .in(Rs), .sel(in_4[5:4]), .en(1'b1));
  Demultiplexer #(.select(2)) demultiplexer_2 (
    .out0(demultiplexer_2_out0), .out1(demultiplexer_2_out1), .out2(demultiplexer_2_out2),
    .out3(demultiplexer_2_out3), .in(Wr), .sel(in_4[5:4]), .en(1'b1));
  Demultiplexer #(.select(2)) demultiplexer_3 (
    .out0(demultiplexer_3_out0), .out1(demultiplexer_3_out1), .out2(demultiplexer_3_out2),
    .out3(demultiplexer_3_out3), .in(Rd), .sel(in_4[5:4]), .en(1'b1));
  Demultiplexer #(.select(2), .width(4), .disabled(0)) demultiplexer_4 (
    .out0(demultiplexer_4_out0), .out1(demultiplexer_4_out1), .out2(demultiplexer_4_out2),
    .out3(demultiplexer_4_out3), .in(in_4[3:0]), .sel(in_4[5:4]), .en(1'b1));
  _4_Bin_Hex u_4_bin_hex_1 (
    .in_2(demultiplexer_4_out0[0]), .in_3(demultiplexer_4_out0[1]), .in_4(demultiplexer_4_out0[2]),
    .in_5(demultiplexer_4_out0[3]), .out_6(n4_bin_hex_1_out_6), .out_7(n4_bin_hex_1_out_7),
    .out_8(n4_bin_hex_1_out_8), .out_9(n4_bin_hex_1_out_9), .out_10(n4_bin_hex_1_out_10),
    .out_11(n4_bin_hex_1_out_11), .out_12(n4_bin_hex_1_out_12), .out_13(n4_bin_hex_1_out_13),
    .out_14(n4_bin_hex_1_out_14), .out_15(n4_bin_hex_1_out_15), .out_16(n4_bin_hex_1_out_16),
    .out_17(n4_bin_hex_1_out_17), .out_18(n4_bin_hex_1_out_18), .out_19(n4_bin_hex_1_out_19),
    .out_20(n4_bin_hex_1_out_20), .out_21(n4_bin_hex_1_out_21), .in_1(demultiplexer_2_out0));
  _4_Bin_Hex u_4_bin_hex_2 (
    .in_2(demultiplexer_4_out0[0]), .in_3(demultiplexer_4_out0[1]), .in_4(demultiplexer_4_out0[2]),
    .in_5(demultiplexer_4_out0[3]), .out_6(n4_bin_hex_2_out_6), .out_7(n4_bin_hex_2_out_7),
    .out_8(n4_bin_hex_2_out_8), .out_9(n4_bin_hex_2_out_9), .out_10(n4_bin_hex_2_out_10),
    .out_11(n4_bin_hex_2_out_11), .out_12(n4_bin_hex_2_out_12), .out_13(n4_bin_hex_2_out_13),
    .out_14(n4_bin_hex_2_out_14), .out_15(n4_bin_hex_2_out_15), .out_16(n4_bin_hex_2_out_16),
    .out_17(n4_bin_hex_2_out_17), .out_18(n4_bin_hex_2_out_18), .out_19(n4_bin_hex_2_out_19),
    .out_20(n4_bin_hex_2_out_20), .out_21(n4_bin_hex_2_out_21), .in_1(demultiplexer_1_out0));
  _2B_Register u_2b_register_1 (
    .in_1({in_5, in_6, in_7, in_8}), .in_2(n4_bin_hex_1_out_6), .out_7(n2b_register_1_out_7),
    .in_3(n4_bin_hex_2_out_6), .in_4(n4_bin_hex_3_out_6), .in_5(n2b_register_2_out_6));  // open: out_6
  _2B_Register u_2b_register_2 (
    .in_1({in_5, in_6, in_7, in_8}), .in_2(n4_bin_hex_1_out_7), .out_7(n2b_register_2_out_7),
    .in_3(n4_bin_hex_2_out_7), .in_4(n4_bin_hex_3_out_7), .in_5(n2b_register_3_out_6),
    .out_6(n2b_register_2_out_6));
  _2B_Register u_2b_register_3 (
    .in_1({in_5, in_6, in_7, in_8}), .in_2(n4_bin_hex_1_out_8), .out_7(n2b_register_3_out_7),
    .in_3(n4_bin_hex_2_out_8), .in_4(n4_bin_hex_3_out_8), .in_5(n2b_register_4_out_6),
    .out_6(n2b_register_3_out_6));
  _2B_Register u_2b_register_4 (
    .in_1({in_5, in_6, in_7, in_8}), .in_2(n4_bin_hex_1_out_9), .out_7(n2b_register_4_out_7),
    .in_3(n4_bin_hex_2_out_9), .in_4(n4_bin_hex_3_out_9), .in_5(n2b_register_5_out_6),
    .out_6(n2b_register_4_out_6));
  _2B_Register u_2b_register_5 (
    .in_1({in_5, in_6, in_7, in_8}), .in_2(n4_bin_hex_1_out_10), .out_7(n2b_register_5_out_7),
    .in_3(n4_bin_hex_2_out_10), .in_4(n4_bin_hex_3_out_10), .in_5(n2b_register_6_out_6),
    .out_6(n2b_register_5_out_6));
  _2B_Register u_2b_register_6 (
    .in_1({in_5, in_6, in_7, in_8}), .in_2(n4_bin_hex_1_out_11), .out_7(n2b_register_6_out_7),
    .in_3(n4_bin_hex_2_out_11), .in_4(n4_bin_hex_3_out_11), .in_5(n2b_register_7_out_6),
    .out_6(n2b_register_6_out_6));
  _2B_Register u_2b_register_7 (
    .in_1({in_5, in_6, in_7, in_8}), .in_2(n4_bin_hex_1_out_12), .out_7(n2b_register_7_out_7),
    .in_3(n4_bin_hex_2_out_12), .in_4(n4_bin_hex_3_out_12), .in_5(n2b_register_8_out_6),
    .out_6(n2b_register_7_out_6));
  _2B_Register u_2b_register_8 (
    .in_1({in_5, in_6, in_7, in_8}), .in_2(n4_bin_hex_1_out_13), .out_7(n2b_register_8_out_7),
    .in_3(n4_bin_hex_2_out_13), .in_4(n4_bin_hex_3_out_13), .in_5(n2b_register_9_out_6),
    .out_6(n2b_register_8_out_6));
  _2B_Register u_2b_register_9 (
    .in_1({in_5, in_6, in_7, in_8}), .in_2(n4_bin_hex_1_out_14), .out_7(n2b_register_9_out_7),
    .in_3(n4_bin_hex_2_out_14), .in_4(n4_bin_hex_3_out_14), .in_5(n2b_register_10_out_6),
    .out_6(n2b_register_9_out_6));
  _2B_Register u_2b_register_10 (
    .in_1({in_5, in_6, in_7, in_8}), .in_2(n4_bin_hex_1_out_15), .out_7(n2b_register_10_out_7),
    .in_3(n4_bin_hex_2_out_15), .in_4(n4_bin_hex_3_out_15), .in_5(n2b_register_11_out_6),
    .out_6(n2b_register_10_out_6));
  _2B_Register u_2b_register_11 (
    .in_1({in_5, in_6, in_7, in_8}), .in_2(n4_bin_hex_1_out_16), .out_7(n2b_register_11_out_7),
    .in_3(n4_bin_hex_2_out_16), .in_4(n4_bin_hex_3_out_16), .in_5(n2b_register_12_out_6),
    .out_6(n2b_register_11_out_6));
  _2B_Register u_2b_register_12 (
    .in_1({in_5, in_6, in_7, in_8}), .in_2(n4_bin_hex_1_out_17), .out_7(n2b_register_12_out_7),
    .in_3(n4_bin_hex_2_out_17), .in_4(n4_bin_hex_3_out_17), .in_5(n2b_register_13_out_6),
    .out_6(n2b_register_12_out_6));
  _2B_Register u_2b_register_13 (
    .in_1({in_5, in_6, in_7, in_8}), .in_2(n4_bin_hex_1_out_18), .out_7(n2b_register_13_out_7),
    .in_3(n4_bin_hex_2_out_18), .in_4(n4_bin_hex_3_out_18), .in_5(n2b_register_14_out_6),
    .out_6(n2b_register_13_out_6));
  _2B_Register u_2b_register_14 (
    .in_1({in_5, in_6, in_7, in_8}), .in_2(n4_bin_hex_1_out_19), .out_7(n2b_register_14_out_7),
    .in_3(n4_bin_hex_2_out_19), .in_4(n4_bin_hex_3_out_19), .in_5(n2b_register_15_out_6),
    .out_6(n2b_register_14_out_6));
  _2B_Register u_2b_register_15 (
    .in_1({in_5, in_6, in_7, in_8}), .in_2(n4_bin_hex_1_out_20), .out_7(n2b_register_15_out_7),
    .in_3(n4_bin_hex_2_out_20), .in_4(n4_bin_hex_3_out_20), .in_5(n2b_register_16_out_6),
    .out_6(n2b_register_15_out_6));
  _2B_Register u_2b_register_16 (
    .in_1({in_5, in_6, in_7, in_8}), .in_2(n4_bin_hex_1_out_21), .out_7(n2b_register_16_out_7),
    .in_3(n4_bin_hex_2_out_21), .in_4(n4_bin_hex_3_out_21), .in_5(in_9), .out_6(n2b_register_16_out_6));
  _4_Bin_Hex u_4_bin_hex_3 (
    .in_2(demultiplexer_4_out0[0]), .in_3(demultiplexer_4_out0[1]), .in_4(demultiplexer_4_out0[2]),
    .in_5(demultiplexer_4_out0[3]), .out_6(n4_bin_hex_3_out_6), .out_7(n4_bin_hex_3_out_7),
    .out_8(n4_bin_hex_3_out_8), .out_9(n4_bin_hex_3_out_9), .out_10(n4_bin_hex_3_out_10),
    .out_11(n4_bin_hex_3_out_11), .out_12(n4_bin_hex_3_out_12), .out_13(n4_bin_hex_3_out_13),
    .out_14(n4_bin_hex_3_out_14), .out_15(n4_bin_hex_3_out_15), .out_16(n4_bin_hex_3_out_16),
    .out_17(n4_bin_hex_3_out_17), .out_18(n4_bin_hex_3_out_18), .out_19(n4_bin_hex_3_out_19),
    .out_20(n4_bin_hex_3_out_20), .out_21(n4_bin_hex_3_out_21), .in_1(demultiplexer_3_out0));
  assign or_1_out = n2b_register_1_out_7 | n2b_register_2_out_7 | n2b_register_3_out_7 | n2b_register_4_out_7 | n2b_register_5_out_7 | n2b_register_6_out_7 | n2b_register_7_out_7 | n2b_register_8_out_7 | n2b_register_9_out_7 | n2b_register_10_out_7 | n2b_register_11_out_7 | n2b_register_13_out_7 | n2b_register_14_out_7 | n2b_register_15_out_7 | n2b_register_16_out_7 | n2b_register_12_out_7;  // OR_Gate or_1, 16 bits wide
  _4_Bin_Hex u_4_bin_hex_4 (
    .in_2(demultiplexer_4_out1[0]), .in_3(demultiplexer_4_out1[1]), .in_4(demultiplexer_4_out1[2]),
    .in_5(demultiplexer_4_out1[3]), .out_6(n4_bin_hex_4_out_6), .out_7(n4_bin_hex_4_out_7),
    .out_8(n4_bin_hex_4_out_8), .out_9(n4_bin_hex_4_out_9), .out_10(n4_bin_hex_4_out_10),
    .out_11(n4_bin_hex_4_out_11), .out_12(n4_bin_hex_4_out_12), .out_13(n4_bin_hex_4_out_13),
    .out_14(n4_bin_hex_4_out_14), .out_15(n4_bin_hex_4_out_15), .out_16(n4_bin_hex_4_out_16),
    .out_17(n4_bin_hex_4_out_17), .out_18(n4_bin_hex_4_out_18), .out_19(n4_bin_hex_4_out_19),
    .out_20(n4_bin_hex_4_out_20), .out_21(n4_bin_hex_4_out_21), .in_1(demultiplexer_2_out1));
  _4_Bin_Hex u_4_bin_hex_5 (
    .in_2(demultiplexer_4_out1[0]), .in_3(demultiplexer_4_out1[1]), .in_4(demultiplexer_4_out1[2]),
    .in_5(demultiplexer_4_out1[3]), .out_6(n4_bin_hex_5_out_6), .out_7(n4_bin_hex_5_out_7),
    .out_8(n4_bin_hex_5_out_8), .out_9(n4_bin_hex_5_out_9), .out_10(n4_bin_hex_5_out_10),
    .out_11(n4_bin_hex_5_out_11), .out_12(n4_bin_hex_5_out_12), .out_13(n4_bin_hex_5_out_13),
    .out_14(n4_bin_hex_5_out_14), .out_15(n4_bin_hex_5_out_15), .out_16(n4_bin_hex_5_out_16),
    .out_17(n4_bin_hex_5_out_17), .out_18(n4_bin_hex_5_out_18), .out_19(n4_bin_hex_5_out_19),
    .out_20(n4_bin_hex_5_out_20), .out_21(n4_bin_hex_5_out_21), .in_1(demultiplexer_1_out1));
  _2B_Register u_2b_register_17 (
    .in_1({in_5, in_6, in_7, in_8}), .in_2(n4_bin_hex_4_out_6), .out_7(n2b_register_17_out_7),
    .in_3(n4_bin_hex_5_out_6), .in_4(n4_bin_hex_6_out_6), .in_5(n2b_register_18_out_6));  // open: out_6
  _2B_Register u_2b_register_18 (
    .in_1({in_5, in_6, in_7, in_8}), .in_2(n4_bin_hex_4_out_7), .out_7(n2b_register_18_out_7),
    .in_3(n4_bin_hex_5_out_7), .in_4(n4_bin_hex_6_out_7), .in_5(n2b_register_19_out_6),
    .out_6(n2b_register_18_out_6));
  _2B_Register u_2b_register_19 (
    .in_1({in_5, in_6, in_7, in_8}), .in_2(n4_bin_hex_4_out_8), .out_7(n2b_register_19_out_7),
    .in_3(n4_bin_hex_5_out_8), .in_4(n4_bin_hex_6_out_8), .in_5(n2b_register_20_out_6),
    .out_6(n2b_register_19_out_6));
  _2B_Register u_2b_register_20 (
    .in_1({in_5, in_6, in_7, in_8}), .in_2(n4_bin_hex_4_out_9), .out_7(n2b_register_20_out_7),
    .in_3(n4_bin_hex_5_out_9), .in_4(n4_bin_hex_6_out_9), .in_5(n2b_register_21_out_6),
    .out_6(n2b_register_20_out_6));
  _2B_Register u_2b_register_21 (
    .in_1({in_5, in_6, in_7, in_8}), .in_2(n4_bin_hex_4_out_10), .out_7(n2b_register_21_out_7),
    .in_3(n4_bin_hex_5_out_10), .in_4(n4_bin_hex_6_out_10), .in_5(n2b_register_22_out_6),
    .out_6(n2b_register_21_out_6));
  _2B_Register u_2b_register_22 (
    .in_1({in_5, in_6, in_7, in_8}), .in_2(n4_bin_hex_4_out_11), .out_7(n2b_register_22_out_7),
    .in_3(n4_bin_hex_5_out_11), .in_4(n4_bin_hex_6_out_11), .in_5(n2b_register_23_out_6),
    .out_6(n2b_register_22_out_6));
  _2B_Register u_2b_register_23 (
    .in_1({in_5, in_6, in_7, in_8}), .in_2(n4_bin_hex_4_out_12), .out_7(n2b_register_23_out_7),
    .in_3(n4_bin_hex_5_out_12), .in_4(n4_bin_hex_6_out_12), .in_5(n2b_register_24_out_6),
    .out_6(n2b_register_23_out_6));
  _2B_Register u_2b_register_24 (
    .in_1({in_5, in_6, in_7, in_8}), .in_2(n4_bin_hex_4_out_13), .out_7(n2b_register_24_out_7),
    .in_3(n4_bin_hex_5_out_13), .in_4(n4_bin_hex_6_out_13), .in_5(n2b_register_25_out_6),
    .out_6(n2b_register_24_out_6));
  _2B_Register u_2b_register_25 (
    .in_1({in_5, in_6, in_7, in_8}), .in_2(n4_bin_hex_4_out_14), .out_7(n2b_register_25_out_7),
    .in_3(n4_bin_hex_5_out_14), .in_4(n4_bin_hex_6_out_14), .in_5(n2b_register_26_out_6),
    .out_6(n2b_register_25_out_6));
  _2B_Register u_2b_register_26 (
    .in_1({in_5, in_6, in_7, in_8}), .in_2(n4_bin_hex_4_out_15), .out_7(n2b_register_26_out_7),
    .in_3(n4_bin_hex_5_out_15), .in_4(n4_bin_hex_6_out_15), .in_5(n2b_register_27_out_6),
    .out_6(n2b_register_26_out_6));
  _2B_Register u_2b_register_27 (
    .in_1({in_5, in_6, in_7, in_8}), .in_2(n4_bin_hex_4_out_16), .out_7(n2b_register_27_out_7),
    .in_3(n4_bin_hex_5_out_16), .in_4(n4_bin_hex_6_out_16), .in_5(n2b_register_28_out_6),
    .out_6(n2b_register_27_out_6));
  _2B_Register u_2b_register_28 (
    .in_1({in_5, in_6, in_7, in_8}), .in_2(n4_bin_hex_4_out_17), .out_7(n2b_register_28_out_7),
    .in_3(n4_bin_hex_5_out_17), .in_4(n4_bin_hex_6_out_17), .in_5(n2b_register_29_out_6),
    .out_6(n2b_register_28_out_6));
  _2B_Register u_2b_register_29 (
    .in_1({in_5, in_6, in_7, in_8}), .in_2(n4_bin_hex_4_out_18), .out_7(n2b_register_29_out_7),
    .in_3(n4_bin_hex_5_out_18), .in_4(n4_bin_hex_6_out_18), .in_5(n2b_register_30_out_6),
    .out_6(n2b_register_29_out_6));
  _2B_Register u_2b_register_30 (
    .in_1({in_5, in_6, in_7, in_8}), .in_2(n4_bin_hex_4_out_19), .out_7(n2b_register_30_out_7),
    .in_3(n4_bin_hex_5_out_19), .in_4(n4_bin_hex_6_out_19), .in_5(n2b_register_31_out_6),
    .out_6(n2b_register_30_out_6));
  _2B_Register u_2b_register_31 (
    .in_1({in_5, in_6, in_7, in_8}), .in_2(n4_bin_hex_4_out_20), .out_7(n2b_register_31_out_7),
    .in_3(n4_bin_hex_5_out_20), .in_4(n4_bin_hex_6_out_20), .in_5(n2b_register_32_out_6),
    .out_6(n2b_register_31_out_6));
  _2B_Register u_2b_register_32 (
    .in_1({in_5, in_6, in_7, in_8}), .in_2(n4_bin_hex_4_out_21), .out_7(n2b_register_32_out_7),
    .in_3(n4_bin_hex_5_out_21), .in_4(n4_bin_hex_6_out_21), .in_5(in_9), .out_6(n2b_register_32_out_6));
  _4_Bin_Hex u_4_bin_hex_6 (
    .in_2(demultiplexer_4_out1[0]), .in_3(demultiplexer_4_out1[1]), .in_4(demultiplexer_4_out1[2]),
    .in_5(demultiplexer_4_out1[3]), .out_6(n4_bin_hex_6_out_6), .out_7(n4_bin_hex_6_out_7),
    .out_8(n4_bin_hex_6_out_8), .out_9(n4_bin_hex_6_out_9), .out_10(n4_bin_hex_6_out_10),
    .out_11(n4_bin_hex_6_out_11), .out_12(n4_bin_hex_6_out_12), .out_13(n4_bin_hex_6_out_13),
    .out_14(n4_bin_hex_6_out_14), .out_15(n4_bin_hex_6_out_15), .out_16(n4_bin_hex_6_out_16),
    .out_17(n4_bin_hex_6_out_17), .out_18(n4_bin_hex_6_out_18), .out_19(n4_bin_hex_6_out_19),
    .out_20(n4_bin_hex_6_out_20), .out_21(n4_bin_hex_6_out_21), .in_1(demultiplexer_3_out1));
  assign or_2_out = n2b_register_17_out_7 | n2b_register_18_out_7 | n2b_register_19_out_7 | n2b_register_20_out_7 | n2b_register_21_out_7 | n2b_register_22_out_7 | n2b_register_23_out_7 | n2b_register_24_out_7 | n2b_register_25_out_7 | n2b_register_26_out_7 | n2b_register_27_out_7 | n2b_register_29_out_7 | n2b_register_30_out_7 | n2b_register_31_out_7 | n2b_register_32_out_7 | n2b_register_28_out_7;  // OR_Gate or_2, 16 bits wide
  _4_Bin_Hex u_4_bin_hex_7 (
    .in_2(demultiplexer_4_out2[0]), .in_3(demultiplexer_4_out2[1]), .in_4(demultiplexer_4_out2[2]),
    .in_5(demultiplexer_4_out2[3]), .out_6(n4_bin_hex_7_out_6), .out_7(n4_bin_hex_7_out_7),
    .out_8(n4_bin_hex_7_out_8), .out_9(n4_bin_hex_7_out_9), .out_10(n4_bin_hex_7_out_10),
    .out_11(n4_bin_hex_7_out_11), .out_12(n4_bin_hex_7_out_12), .out_13(n4_bin_hex_7_out_13),
    .out_14(n4_bin_hex_7_out_14), .out_15(n4_bin_hex_7_out_15), .out_16(n4_bin_hex_7_out_16),
    .out_17(n4_bin_hex_7_out_17), .out_18(n4_bin_hex_7_out_18), .out_19(n4_bin_hex_7_out_19),
    .out_20(n4_bin_hex_7_out_20), .out_21(n4_bin_hex_7_out_21), .in_1(demultiplexer_2_out2));
  _4_Bin_Hex u_4_bin_hex_8 (
    .in_2(demultiplexer_4_out2[0]), .in_3(demultiplexer_4_out2[1]), .in_4(demultiplexer_4_out2[2]),
    .in_5(demultiplexer_4_out2[3]), .out_6(n4_bin_hex_8_out_6), .out_7(n4_bin_hex_8_out_7),
    .out_8(n4_bin_hex_8_out_8), .out_9(n4_bin_hex_8_out_9), .out_10(n4_bin_hex_8_out_10),
    .out_11(n4_bin_hex_8_out_11), .out_12(n4_bin_hex_8_out_12), .out_13(n4_bin_hex_8_out_13),
    .out_14(n4_bin_hex_8_out_14), .out_15(n4_bin_hex_8_out_15), .out_16(n4_bin_hex_8_out_16),
    .out_17(n4_bin_hex_8_out_17), .out_18(n4_bin_hex_8_out_18), .out_19(n4_bin_hex_8_out_19),
    .out_20(n4_bin_hex_8_out_20), .out_21(n4_bin_hex_8_out_21), .in_1(demultiplexer_1_out2));
  _2B_Register u_2b_register_33 (
    .in_1({in_5, in_6, in_7, in_8}), .in_2(n4_bin_hex_7_out_6), .out_7(n2b_register_33_out_7),
    .in_3(n4_bin_hex_8_out_6), .in_4(n4_bin_hex_9_out_6), .in_5(n2b_register_34_out_6));  // open: out_6
  _2B_Register u_2b_register_34 (
    .in_1({in_5, in_6, in_7, in_8}), .in_2(n4_bin_hex_7_out_7), .out_7(n2b_register_34_out_7),
    .in_3(n4_bin_hex_8_out_7), .in_4(n4_bin_hex_9_out_7), .in_5(n2b_register_35_out_6),
    .out_6(n2b_register_34_out_6));
  _2B_Register u_2b_register_35 (
    .in_1({in_5, in_6, in_7, in_8}), .in_2(n4_bin_hex_7_out_8), .out_7(n2b_register_35_out_7),
    .in_3(n4_bin_hex_8_out_8), .in_4(n4_bin_hex_9_out_8), .in_5(n2b_register_36_out_6),
    .out_6(n2b_register_35_out_6));
  _2B_Register u_2b_register_36 (
    .in_1({in_5, in_6, in_7, in_8}), .in_2(n4_bin_hex_7_out_9), .out_7(n2b_register_36_out_7),
    .in_3(n4_bin_hex_8_out_9), .in_4(n4_bin_hex_9_out_9), .in_5(n2b_register_37_out_6),
    .out_6(n2b_register_36_out_6));
  _2B_Register u_2b_register_37 (
    .in_1({in_5, in_6, in_7, in_8}), .in_2(n4_bin_hex_7_out_10), .out_7(n2b_register_37_out_7),
    .in_3(n4_bin_hex_8_out_10), .in_4(n4_bin_hex_9_out_10), .in_5(n2b_register_38_out_6),
    .out_6(n2b_register_37_out_6));
  _2B_Register u_2b_register_38 (
    .in_1({in_5, in_6, in_7, in_8}), .in_2(n4_bin_hex_7_out_11), .out_7(n2b_register_38_out_7),
    .in_3(n4_bin_hex_8_out_11), .in_4(n4_bin_hex_9_out_11), .in_5(n2b_register_39_out_6),
    .out_6(n2b_register_38_out_6));
  _2B_Register u_2b_register_39 (
    .in_1({in_5, in_6, in_7, in_8}), .in_2(n4_bin_hex_7_out_12), .out_7(n2b_register_39_out_7),
    .in_3(n4_bin_hex_8_out_12), .in_4(n4_bin_hex_9_out_12), .in_5(n2b_register_40_out_6),
    .out_6(n2b_register_39_out_6));
  _2B_Register u_2b_register_40 (
    .in_1({in_5, in_6, in_7, in_8}), .in_2(n4_bin_hex_7_out_13), .out_7(n2b_register_40_out_7),
    .in_3(n4_bin_hex_8_out_13), .in_4(n4_bin_hex_9_out_13), .in_5(n2b_register_41_out_6),
    .out_6(n2b_register_40_out_6));
  _2B_Register u_2b_register_41 (
    .in_1({in_5, in_6, in_7, in_8}), .in_2(n4_bin_hex_7_out_14), .out_7(n2b_register_41_out_7),
    .in_3(n4_bin_hex_8_out_14), .in_4(n4_bin_hex_9_out_14), .in_5(n2b_register_42_out_6),
    .out_6(n2b_register_41_out_6));
  _2B_Register u_2b_register_42 (
    .in_1({in_5, in_6, in_7, in_8}), .in_2(n4_bin_hex_7_out_15), .out_7(n2b_register_42_out_7),
    .in_3(n4_bin_hex_8_out_15), .in_4(n4_bin_hex_9_out_15), .in_5(n2b_register_43_out_6),
    .out_6(n2b_register_42_out_6));
  _2B_Register u_2b_register_43 (
    .in_1({in_5, in_6, in_7, in_8}), .in_2(n4_bin_hex_7_out_16), .out_7(n2b_register_43_out_7),
    .in_3(n4_bin_hex_8_out_16), .in_4(n4_bin_hex_9_out_16), .in_5(n2b_register_44_out_6),
    .out_6(n2b_register_43_out_6));
  _2B_Register u_2b_register_44 (
    .in_1({in_5, in_6, in_7, in_8}), .in_2(n4_bin_hex_7_out_17), .out_7(n2b_register_44_out_7),
    .in_3(n4_bin_hex_8_out_17), .in_4(n4_bin_hex_9_out_17), .in_5(n2b_register_45_out_6),
    .out_6(n2b_register_44_out_6));
  _2B_Register u_2b_register_45 (
    .in_1({in_5, in_6, in_7, in_8}), .in_2(n4_bin_hex_7_out_18), .out_7(n2b_register_42_out_7),
    .in_3(n4_bin_hex_8_out_18), .in_4(n4_bin_hex_9_out_18), .in_5(n2b_register_46_out_6),
    .out_6(n2b_register_45_out_6));
  _2B_Register u_2b_register_46 (
    .in_1({in_5, in_6, in_7, in_8}), .in_2(n4_bin_hex_7_out_19), .out_7(n2b_register_46_out_7),
    .in_3(n4_bin_hex_8_out_19), .in_4(n4_bin_hex_9_out_19), .in_5(n2b_register_47_out_6),
    .out_6(n2b_register_46_out_6));
  _2B_Register u_2b_register_47 (
    .in_1({in_5, in_6, in_7, in_8}), .in_2(n4_bin_hex_7_out_20), .out_7(n2b_register_47_out_7),
    .in_3(n4_bin_hex_8_out_20), .in_4(n4_bin_hex_9_out_20), .in_5(n2b_register_48_out_6),
    .out_6(n2b_register_47_out_6));
  _2B_Register u_2b_register_48 (
    .in_1({in_5, in_6, in_7, in_8}), .in_2(n4_bin_hex_7_out_21), .out_7(n2b_register_48_out_7),
    .in_3(n4_bin_hex_8_out_21), .in_4(n4_bin_hex_9_out_21), .in_5(in_9), .out_6(n2b_register_48_out_6));
  _4_Bin_Hex u_4_bin_hex_9 (
    .in_2(demultiplexer_4_out2[0]), .in_3(demultiplexer_4_out2[1]), .in_4(demultiplexer_4_out2[2]),
    .in_5(demultiplexer_4_out2[3]), .out_6(n4_bin_hex_9_out_6), .out_7(n4_bin_hex_9_out_7),
    .out_8(n4_bin_hex_9_out_8), .out_9(n4_bin_hex_9_out_9), .out_10(n4_bin_hex_9_out_10),
    .out_11(n4_bin_hex_9_out_11), .out_12(n4_bin_hex_9_out_12), .out_13(n4_bin_hex_9_out_13),
    .out_14(n4_bin_hex_9_out_14), .out_15(n4_bin_hex_9_out_15), .out_16(n4_bin_hex_9_out_16),
    .out_17(n4_bin_hex_9_out_17), .out_18(n4_bin_hex_9_out_18), .out_19(n4_bin_hex_9_out_19),
    .out_20(n4_bin_hex_9_out_20), .out_21(n4_bin_hex_9_out_21), .in_1(demultiplexer_3_out2));
  assign or_3_out = n2b_register_33_out_7 | n2b_register_34_out_7 | n2b_register_35_out_7 | n2b_register_36_out_7 | n2b_register_37_out_7 | n2b_register_38_out_7 | n2b_register_39_out_7 | n2b_register_40_out_7 | n2b_register_41_out_7 | n2b_register_42_out_7 | n2b_register_43_out_7 | n2b_register_42_out_7 | n2b_register_46_out_7 | n2b_register_47_out_7 | n2b_register_48_out_7 | n2b_register_44_out_7;  // OR_Gate or_3, 16 bits wide
  _4_Bin_Hex u_4_bin_hex_10 (
    .in_2(demultiplexer_4_out3[0]), .in_3(demultiplexer_4_out3[1]), .in_4(demultiplexer_4_out3[2]),
    .in_5(demultiplexer_4_out3[3]), .out_6(n4_bin_hex_10_out_6), .out_7(n4_bin_hex_10_out_7),
    .out_8(n4_bin_hex_10_out_8), .out_9(n4_bin_hex_10_out_9), .out_10(n4_bin_hex_10_out_10),
    .out_11(n4_bin_hex_10_out_11), .out_12(n4_bin_hex_10_out_12), .out_13(n4_bin_hex_10_out_13),
    .out_14(n4_bin_hex_10_out_14), .out_15(n4_bin_hex_10_out_15), .out_16(n4_bin_hex_10_out_16),
    .out_17(n4_bin_hex_10_out_17), .out_18(n4_bin_hex_10_out_18), .out_19(n4_bin_hex_10_out_19),
    .out_20(n4_bin_hex_10_out_20), .out_21(n4_bin_hex_10_out_21), .in_1(demultiplexer_2_out3));
  _4_Bin_Hex u_4_bin_hex_11 (
    .in_2(demultiplexer_4_out3[0]), .in_3(demultiplexer_4_out3[1]), .in_4(demultiplexer_4_out3[2]),
    .in_5(demultiplexer_4_out3[3]), .out_6(n4_bin_hex_11_out_6), .out_7(n4_bin_hex_11_out_7),
    .out_8(n4_bin_hex_11_out_8), .out_9(n4_bin_hex_11_out_9), .out_10(n4_bin_hex_11_out_10),
    .out_11(n4_bin_hex_11_out_11), .out_12(n4_bin_hex_11_out_12), .out_13(n4_bin_hex_11_out_13),
    .out_14(n4_bin_hex_11_out_14), .out_15(n4_bin_hex_11_out_15), .out_16(n4_bin_hex_11_out_16),
    .out_17(n4_bin_hex_11_out_17), .out_18(n4_bin_hex_11_out_18), .out_19(n4_bin_hex_11_out_19),
    .out_20(n4_bin_hex_11_out_20), .out_21(n4_bin_hex_11_out_21), .in_1(demultiplexer_1_out3));
  _2B_Register u_2b_register_49 (
    .in_1({in_5, in_6, in_7, in_8}), .in_2(n4_bin_hex_10_out_6), .out_7(n2b_register_49_out_7),
    .in_3(n4_bin_hex_11_out_6), .in_4(n4_bin_hex_12_out_6), .in_5(n2b_register_50_out_6));  // open: out_6
  _2B_Register u_2b_register_50 (
    .in_1({in_5, in_6, in_7, in_8}), .in_2(n4_bin_hex_10_out_7), .out_7(n2b_register_50_out_7),
    .in_3(n4_bin_hex_11_out_7), .in_4(n4_bin_hex_12_out_7), .in_5(n2b_register_51_out_6),
    .out_6(n2b_register_50_out_6));
  _2B_Register u_2b_register_51 (
    .in_1({in_5, in_6, in_7, in_8}), .in_2(n4_bin_hex_10_out_8), .out_7(n2b_register_51_out_7),
    .in_3(n4_bin_hex_11_out_8), .in_4(n4_bin_hex_12_out_8), .in_5(n2b_register_52_out_6),
    .out_6(n2b_register_51_out_6));
  _2B_Register u_2b_register_52 (
    .in_1({in_5, in_6, in_7, in_8}), .in_2(n4_bin_hex_10_out_9), .out_7(n2b_register_52_out_7),
    .in_3(n4_bin_hex_11_out_9), .in_4(n4_bin_hex_12_out_9), .in_5(n2b_register_53_out_6),
    .out_6(n2b_register_52_out_6));
  _2B_Register u_2b_register_53 (
    .in_1({in_5, in_6, in_7, in_8}), .in_2(n4_bin_hex_10_out_10), .out_7(n2b_register_53_out_7),
    .in_3(n4_bin_hex_11_out_10), .in_4(n4_bin_hex_12_out_10), .in_5(n2b_register_54_out_6),
    .out_6(n2b_register_53_out_6));
  _2B_Register u_2b_register_54 (
    .in_1({in_5, in_6, in_7, in_8}), .in_2(n4_bin_hex_10_out_11), .out_7(n2b_register_54_out_7),
    .in_3(n4_bin_hex_11_out_11), .in_4(n4_bin_hex_12_out_11), .in_5(n2b_register_55_out_6),
    .out_6(n2b_register_54_out_6));
  _2B_Register u_2b_register_55 (
    .in_1({in_5, in_6, in_7, in_8}), .in_2(n4_bin_hex_10_out_12), .out_7(n2b_register_55_out_7),
    .in_3(n4_bin_hex_11_out_12), .in_4(n4_bin_hex_12_out_12), .in_5(n2b_register_56_out_6),
    .out_6(n2b_register_55_out_6));
  _2B_Register u_2b_register_56 (
    .in_1({in_5, in_6, in_7, in_8}), .in_2(n4_bin_hex_10_out_13), .out_7(n2b_register_56_out_7),
    .in_3(n4_bin_hex_11_out_13), .in_4(n4_bin_hex_12_out_13), .in_5(n2b_register_57_out_6),
    .out_6(n2b_register_56_out_6));
  _2B_Register u_2b_register_57 (
    .in_1({in_5, in_6, in_7, in_8}), .in_2(n4_bin_hex_10_out_14), .out_7(n2b_register_57_out_7),
    .in_3(n4_bin_hex_11_out_14), .in_4(n4_bin_hex_12_out_14), .in_5(n2b_register_58_out_6),
    .out_6(n2b_register_57_out_6));
  _2B_Register u_2b_register_58 (
    .in_1({in_5, in_6, in_7, in_8}), .in_2(n4_bin_hex_10_out_15), .out_7(n2b_register_58_out_7),
    .in_3(n4_bin_hex_11_out_15), .in_4(n4_bin_hex_12_out_15), .in_5(n2b_register_59_out_6),
    .out_6(n2b_register_58_out_6));
  _2B_Register u_2b_register_59 (
    .in_1({in_5, in_6, in_7, in_8}), .in_2(n4_bin_hex_10_out_16), .out_7(n2b_register_59_out_7),
    .in_3(n4_bin_hex_11_out_16), .in_4(n4_bin_hex_12_out_16), .in_5(n2b_register_60_out_6),
    .out_6(n2b_register_59_out_6));
  _2B_Register u_2b_register_60 (
    .in_1({in_5, in_6, in_7, in_8}), .in_2(n4_bin_hex_10_out_17), .out_7(n2b_register_60_out_7),
    .in_3(n4_bin_hex_11_out_17), .in_4(n4_bin_hex_12_out_17), .in_5(n2b_register_61_out_6),
    .out_6(n2b_register_60_out_6));
  _2B_Register u_2b_register_61 (
    .in_1({in_5, in_6, in_7, in_8}), .in_2(n4_bin_hex_10_out_18), .out_7(n2b_register_61_out_7),
    .in_3(n4_bin_hex_11_out_18), .in_4(n4_bin_hex_12_out_18), .in_5(n2b_register_62_out_6),
    .out_6(n2b_register_61_out_6));
  _2B_Register u_2b_register_62 (
    .in_1({in_5, in_6, in_7, in_8}), .in_2(n4_bin_hex_10_out_19), .out_7(n2b_register_62_out_7),
    .in_3(n4_bin_hex_11_out_19), .in_4(n4_bin_hex_12_out_19), .in_5(n2b_register_63_out_6),
    .out_6(n2b_register_62_out_6));
  _2B_Register u_2b_register_63 (
    .in_1({in_5, in_6, in_7, in_8}), .in_2(n4_bin_hex_10_out_20), .out_7(n2b_register_63_out_7),
    .in_3(n4_bin_hex_11_out_20), .in_4(n4_bin_hex_12_out_20), .in_5(n2b_register_64_out_6),
    .out_6(n2b_register_63_out_6));
  _2B_Register u_2b_register_64 (
    .in_1({in_5, in_6, in_7, in_8}), .in_2(n4_bin_hex_10_out_21), .out_7(n2b_register_64_out_7),
    .in_3(n4_bin_hex_11_out_21), .in_4(n4_bin_hex_12_out_21), .in_5(in_9), .out_6(n2b_register_64_out_6));
  _4_Bin_Hex u_4_bin_hex_12 (
    .in_2(demultiplexer_4_out3[0]), .in_3(demultiplexer_4_out3[1]), .in_4(demultiplexer_4_out3[2]),
    .in_5(demultiplexer_4_out3[3]), .out_6(n4_bin_hex_12_out_6), .out_7(n4_bin_hex_12_out_7),
    .out_8(n4_bin_hex_12_out_8), .out_9(n4_bin_hex_12_out_9), .out_10(n4_bin_hex_12_out_10),
    .out_11(n4_bin_hex_12_out_11), .out_12(n4_bin_hex_12_out_12), .out_13(n4_bin_hex_12_out_13),
    .out_14(n4_bin_hex_12_out_14), .out_15(n4_bin_hex_12_out_15), .out_16(n4_bin_hex_12_out_16),
    .out_17(n4_bin_hex_12_out_17), .out_18(n4_bin_hex_12_out_18), .out_19(n4_bin_hex_12_out_19),
    .out_20(n4_bin_hex_12_out_20), .out_21(n4_bin_hex_12_out_21), .in_1(demultiplexer_3_out3));
  assign or_4_out = n2b_register_49_out_7 | n2b_register_50_out_7 | n2b_register_51_out_7 | n2b_register_52_out_7 | n2b_register_53_out_7 | n2b_register_54_out_7 | n2b_register_55_out_7 | n2b_register_56_out_7 | n2b_register_57_out_7 | n2b_register_58_out_7 | n2b_register_59_out_7 | n2b_register_61_out_7 | n2b_register_62_out_7 | n2b_register_63_out_7 | n2b_register_64_out_7 | n2b_register_60_out_7;  // OR_Gate or_4, 16 bits wide
  assign out_10 = or_1_out | or_2_out | or_3_out | or_4_out;  // OR_Gate or_5, 16 bits wide
endmodule

module Program_Counter (
  input  in_1,
  input  [5:0] in_2,
  input  in_3,
  input  in_4,
  output [5:0] out_5
);

  wire and_1_out, and_2_out, and_3_out, and_4_out;

  J_K_Flip_Flop j_k_ff_1 (
    .J(in_4), .clk(in_1), .K(in_4), .Q(out_5[0]), .preset(in_2[0]), .reset(in_3));  // open: Qn, en
  J_K_Flip_Flop j_k_ff_2 (
    .J(out_5[0]), .clk(in_1), .K(out_5[0]), .Q(out_5[1]), .preset(in_2[1]), .reset(in_3));  // open: Qn, en
  and and_1 (and_1_out, out_5[0], out_5[1]);
  J_K_Flip_Flop j_k_ff_3 (
    .J(and_1_out), .clk(in_1), .K(and_1_out), .Q(out_5[2]), .preset(in_2[2]), .reset(in_3));  // open: Qn, en
  and and_2 (and_2_out, out_5[0], out_5[1], out_5[2]);
  J_K_Flip_Flop j_k_ff_4 (
    .J(and_2_out), .clk(in_1), .K(and_2_out), .Q(out_5[3]), .preset(in_2[3]), .reset(in_3));  // open: Qn, en
  and and_3 (and_3_out, out_5[0], out_5[1], out_5[2], out_5[3]);
  J_K_Flip_Flop j_k_ff_5 (
    .J(and_3_out), .clk(in_1), .K(and_3_out), .Q(out_5[4]), .preset(in_2[4]), .reset(in_3));  // open: Qn, en
  and and_4 (and_4_out, out_5[0], out_5[1], out_5[2], out_5[3], out_5[4]);
  J_K_Flip_Flop j_k_ff_6 (
    .J(and_4_out), .clk(in_1), .K(and_4_out), .Q(out_5[5]), .preset(in_2[5]), .reset(in_3));  // open: Qn, en
endmodule
module ALU_Accumulator (
  input  [15:0] in_1,
  input  in_2,
  input  in_3,
  output [15:0] out_4
);

  wire n5t_edge_trigger_1_out_2;
  wire [15:0] n16_buffer_1_out_3;

  _16_Buffer u_16_buffer_1 (.in_1(in_1), .in_2(n5t_edge_trigger_1_out_2), .out_3(n16_buffer_1_out_3));
  _5T_Edge_Trigger u_5t_edge_trigger_1 (.in_1(in_2), .out_2(n5t_edge_trigger_1_out_2));
  RS_NOR rs_nor_1 (.in_1(n16_buffer_1_out_3[0]), .in_2(in_3), .out_3(out_4[0]));
  RS_NOR rs_nor_2 (.in_1(n16_buffer_1_out_3[1]), .in_2(in_3), .out_3(out_4[1]));
  RS_NOR rs_nor_3 (.in_1(n16_buffer_1_out_3[2]), .in_2(in_3), .out_3(out_4[2]));
  RS_NOR rs_nor_4 (.in_1(n16_buffer_1_out_3[3]), .in_2(in_3), .out_3(out_4[3]));
  RS_NOR rs_nor_5 (.in_1(n16_buffer_1_out_3[4]), .in_2(in_3), .out_3(out_4[4]));
  RS_NOR rs_nor_6 (.in_1(n16_buffer_1_out_3[5]), .in_2(in_3), .out_3(out_4[5]));
  RS_NOR rs_nor_7 (.in_1(n16_buffer_1_out_3[6]), .in_2(in_3), .out_3(out_4[6]));
  RS_NOR rs_nor_8 (.in_1(n16_buffer_1_out_3[7]), .in_2(in_3), .out_3(out_4[7]));
  RS_NOR rs_nor_9 (.in_1(n16_buffer_1_out_3[8]), .in_2(in_3), .out_3(out_4[8]));
  RS_NOR rs_nor_10 (.in_1(n16_buffer_1_out_3[9]), .in_2(in_3), .out_3(out_4[9]));
  RS_NOR rs_nor_11 (.in_1(n16_buffer_1_out_3[10]), .in_2(in_3), .out_3(out_4[10]));
  RS_NOR rs_nor_12 (.in_1(n16_buffer_1_out_3[11]), .in_2(in_3), .out_3(out_4[11]));
  RS_NOR rs_nor_13 (.in_1(n16_buffer_1_out_3[12]), .in_2(in_3), .out_3(out_4[12]));
  RS_NOR rs_nor_14 (.in_1(n16_buffer_1_out_3[13]), .in_2(in_3), .out_3(out_4[13]));
  RS_NOR rs_nor_15 (.in_1(n16_buffer_1_out_3[14]), .in_2(in_3), .out_3(out_4[14]));
  RS_NOR rs_nor_16 (.in_1(n16_buffer_1_out_3[15]), .in_2(in_3), .out_3(out_4[15]));
endmodule

module _16_CLA_Adder (
  input  [15:0] in_1,
  input  [15:0] Input_A,
  input  in_3,
  output [15:0] out_4,
  output out_5
);

  wire and_1_out, carry_lookahead_adder_1_out_5, carry_lookahead_adder_1_out_6,
       carry_lookahead_adder_2_out_5, carry_lookahead_adder_2_out_6, carry_lookahead_adder_3_out_5,
       carry_lookahead_adder_3_out_6, carry_lookahead_adder_4_out_5, carry_lookahead_adder_4_out_6,
       carry_lookahead_adder_5_out_5, carry_lookahead_adder_5_out_6, carry_lookahead_adder_6_out_5,
       carry_lookahead_adder_6_out_6, carry_lookahead_adder_7_out_5, carry_lookahead_adder_7_out_6,
       carry_lookahead_adder_8_out_5, carry_lookahead_adder_8_out_6, carry_lookahead_adder_9_out_5,
       carry_lookahead_adder_9_out_6, carry_lookahead_adder_10_out_5, carry_lookahead_adder_10_out_6,
       carry_lookahead_adder_11_out_5, carry_lookahead_adder_11_out_6, carry_lookahead_adder_12_out_5,
       carry_lookahead_adder_12_out_6, carry_lookahead_adder_13_out_5, carry_lookahead_adder_13_out_6,
       carry_lookahead_adder_14_out_5, carry_lookahead_adder_14_out_6, carry_lookahead_adder_15_out_5,
       carry_lookahead_adder_15_out_6, carry_lookahead_adder_16_out_5, carry_lookahead_adder_16_out_6,
       lookahead_unit_1_out_6, lookahead_unit_1_out_7, lookahead_unit_1_out_8, lookahead_unit_1_out_9,
       lookahead_unit_2_out_6, lookahead_unit_2_out_7, lookahead_unit_2_out_8, lookahead_unit_2_out_9,
       lookahead_unit_3_out_6, lookahead_unit_3_out_7, lookahead_unit_3_out_8, lookahead_unit_3_out_9,
       lookahead_unit_4_out_6, lookahead_unit_4_out_7, lookahead_unit_4_out_8, lookahead_unit_4_out_9,
       lookahead_unit_5_out_6, lookahead_unit_5_out_7, lookahead_unit_5_out_8, lookahead_unit_5_out_9,
       lookahead_unit_6_out_6, lookahead_unit_6_out_7, lookahead_unit_6_out_8, lookahead_unit_6_out_9,
       lookahead_unit_7_out_6, lookahead_unit_7_out_7, lookahead_unit_7_out_8, lookahead_unit_7_out_9,
       lookahead_unit_8_out_6, lookahead_unit_8_out_7, lookahead_unit_8_out_8, lookahead_unit_8_out_9,
       lookahead_unit_9_out_6, lookahead_unit_9_out_7, lookahead_unit_9_out_8, lookahead_unit_9_out_9,
       lookahead_unit_10_out_6, lookahead_unit_10_out_7, lookahead_unit_10_out_8, lookahead_unit_10_out_9,
       lookahead_unit_11_out_6, lookahead_unit_11_out_7, lookahead_unit_11_out_8, lookahead_unit_11_out_9,
       lookahead_unit_12_out_6, lookahead_unit_12_out_7, lookahead_unit_12_out_8, lookahead_unit_12_out_9,
       lookahead_unit_13_out_6, lookahead_unit_13_out_7, lookahead_unit_13_out_8, lookahead_unit_13_out_9,
       lookahead_unit_14_out_6, lookahead_unit_14_out_7, lookahead_unit_14_out_8, lookahead_unit_14_out_9,
       lookahead_unit_15_out_6, lookahead_unit_15_out_7, lookahead_unit_15_out_8, lookahead_unit_15_out_9;
  wire [15:0] n16_buffer_1_out_3, n16_buffer_2_out_3;

  _16_Buffer u_16_buffer_1 (.in_1(in_1), .in_2(in_3), .out_3(n16_buffer_1_out_3));
  Carry_Lookahead_Adder carry_lookahead_adder_1 (
    .in_1(lookahead_unit_1_out_6), .in_2(n16_buffer_1_out_3[15]), .in_3(n16_buffer_2_out_3[15]),
    .out_4(out_4[15]), .out_5(carry_lookahead_adder_1_out_5), .out_6(carry_lookahead_adder_1_out_6));
  or or_1 (out_5, lookahead_unit_4_out_9, and_1_out);
  Carry_Lookahead_Adder carry_lookahead_adder_2 (
    .in_1(lookahead_unit_1_out_7), .in_2(n16_buffer_1_out_3[14]), .in_3(n16_buffer_2_out_3[14]),
    .out_4(out_4[14]), .out_5(carry_lookahead_adder_2_out_5), .out_6(carry_lookahead_adder_2_out_6));
  Lookahead_Unit lookahead_unit_1 (
    .in_1(carry_lookahead_adder_2_out_6), .in_2(carry_lookahead_adder_2_out_5),
    .in_3(lookahead_unit_2_out_6), .in_4(carry_lookahead_adder_1_out_6),
    .in_5(carry_lookahead_adder_1_out_5), .out_6(lookahead_unit_1_out_6), .out_7(lookahead_unit_1_out_7),
    .out_8(lookahead_unit_1_out_8), .out_9(lookahead_unit_1_out_9));
  Lookahead_Unit lookahead_unit_2 (
    .in_1(lookahead_unit_5_out_8), .in_2(lookahead_unit_5_out_9), .in_3(lookahead_unit_3_out_6),
    .in_4(lookahead_unit_1_out_8), .in_5(lookahead_unit_1_out_9), .out_6(lookahead_unit_2_out_6),
    .out_7(lookahead_unit_2_out_7), .out_8(lookahead_unit_2_out_8), .out_9(lookahead_unit_2_out_9));
  Lookahead_Unit lookahead_unit_3 (
    .in_1(lookahead_unit_7_out_8), .in_2(lookahead_unit_7_out_9), .in_3(lookahead_unit_4_out_6),
    .in_4(lookahead_unit_2_out_8), .in_5(lookahead_unit_2_out_9), .out_6(lookahead_unit_3_out_6),
    .out_7(lookahead_unit_3_out_7), .out_8(lookahead_unit_3_out_8), .out_9(lookahead_unit_3_out_9));
  Lookahead_Unit lookahead_unit_4 (
    .in_1(lookahead_unit_11_out_8), .in_2(lookahead_unit_11_out_9), .in_3(1'b0),
    .in_4(lookahead_unit_3_out_8), .in_5(lookahead_unit_3_out_9), .out_6(lookahead_unit_4_out_6),
    .out_7(lookahead_unit_4_out_7), .out_8(lookahead_unit_4_out_8), .out_9(lookahead_unit_4_out_9));
  and and_1 (and_1_out, lookahead_unit_4_out_8, 1'b0);
  Carry_Lookahead_Adder carry_lookahead_adder_3 (
    .in_1(lookahead_unit_5_out_6), .in_2(n16_buffer_1_out_3[13]), .in_3(n16_buffer_2_out_3[13]),
    .out_4(out_4[13]), .out_5(carry_lookahead_adder_3_out_5), .out_6(carry_lookahead_adder_3_out_6));
  Lookahead_Unit lookahead_unit_5 (
    .in_1(carry_lookahead_adder_4_out_6), .in_2(carry_lookahead_adder_4_out_5),
    .in_3(lookahead_unit_2_out_7), .in_4(carry_lookahead_adder_3_out_6),
    .in_5(carry_lookahead_adder_3_out_5), .out_6(lookahead_unit_5_out_6), .out_7(lookahead_unit_5_out_7),
    .out_8(lookahead_unit_5_out_8), .out_9(lookahead_unit_5_out_9));
  Carry_Lookahead_Adder carry_lookahead_adder_4 (
    .in_1(lookahead_unit_5_out_7), .in_2(n16_buffer_1_out_3[12]), .in_3(n16_buffer_2_out_3[12]),
    .out_4(out_4[12]), .out_5(carry_lookahead_adder_4_out_5), .out_6(carry_lookahead_adder_4_out_6));
  Carry_Lookahead_Adder carry_lookahead_adder_5 (
    .in_1(lookahead_unit_6_out_6), .in_2(n16_buffer_1_out_3[11]), .in_3(n16_buffer_2_out_3[11]),
    .out_4(out_4[11]), .out_5(carry_lookahead_adder_5_out_5), .out_6(carry_lookahead_adder_5_out_6));
  Lookahead_Unit lookahead_unit_6 (
    .in_1(carry_lookahead_adder_6_out_6), .in_2(carry_lookahead_adder_6_out_5),
    .in_3(lookahead_unit_7_out_6), .in_4(carry_lookahead_adder_5_out_6),
    .in_5(carry_lookahead_adder_5_out_5), .out_6(lookahead_unit_6_out_6), .out_7(lookahead_unit_6_out_7),
    .out_8(lookahead_unit_6_out_8), .out_9(lookahead_unit_6_out_9));
  Lookahead_Unit lookahead_unit_7 (
    .in_1(lookahead_unit_8_out_8), .in_2(lookahead_unit_8_out_9), .in_3(lookahead_unit_3_out_7),
    .in_4(lookahead_unit_6_out_8), .in_5(lookahead_unit_6_out_9), .out_6(lookahead_unit_7_out_6),
    .out_7(lookahead_unit_7_out_7), .out_8(lookahead_unit_7_out_8), .out_9(lookahead_unit_7_out_9));
  Carry_Lookahead_Adder carry_lookahead_adder_6 (
    .in_1(lookahead_unit_6_out_7), .in_2(n16_buffer_1_out_3[10]), .in_3(n16_buffer_2_out_3[10]),
    .out_4(out_4[10]), .out_5(carry_lookahead_adder_6_out_5), .out_6(carry_lookahead_adder_6_out_6));
  Carry_Lookahead_Adder carry_lookahead_adder_7 (
    .in_1(lookahead_unit_8_out_6), .in_2(n16_buffer_1_out_3[9]), .in_3(n16_buffer_2_out_3[9]),
    .out_4(out_4[9]), .out_5(carry_lookahead_adder_7_out_5), .out_6(carry_lookahead_adder_7_out_6));
  Lookahead_Unit lookahead_unit_8 (
    .in_1(carry_lookahead_adder_8_out_6), .in_2(carry_lookahead_adder_8_out_5),
    .in_3(lookahead_unit_7_out_7), .in_4(carry_lookahead_adder_7_out_6),
    .in_5(carry_lookahead_adder_7_out_5), .out_6(lookahead_unit_8_out_6), .out_7(lookahead_unit_8_out_7),
    .out_8(lookahead_unit_8_out_8), .out_9(lookahead_unit_8_out_9));
  Carry_Lookahead_Adder carry_lookahead_adder_8 (
    .in_1(lookahead_unit_8_out_7), .in_2(n16_buffer_1_out_3[8]), .in_3(n16_buffer_2_out_3[8]),
    .out_4(out_4[8]), .out_5(carry_lookahead_adder_8_out_5), .out_6(carry_lookahead_adder_8_out_6));
  Carry_Lookahead_Adder carry_lookahead_adder_9 (
    .in_1(lookahead_unit_9_out_6), .in_2(n16_buffer_1_out_3[7]), .in_3(n16_buffer_2_out_3[7]),
    .out_4(out_4[7]), .out_5(carry_lookahead_adder_9_out_5), .out_6(carry_lookahead_adder_9_out_6));
  Carry_Lookahead_Adder carry_lookahead_adder_10 (
    .in_1(lookahead_unit_9_out_7), .in_2(n16_buffer_1_out_3[6]), .in_3(n16_buffer_2_out_3[6]),
    .out_4(out_4[6]), .out_5(carry_lookahead_adder_10_out_5), .out_6(carry_lookahead_adder_10_out_6));
  Lookahead_Unit lookahead_unit_9 (
    .in_1(carry_lookahead_adder_10_out_6), .in_2(carry_lookahead_adder_10_out_5),
    .in_3(lookahead_unit_10_out_6), .in_4(carry_lookahead_adder_9_out_6),
    .in_5(carry_lookahead_adder_9_out_5), .out_6(lookahead_unit_9_out_6), .out_7(lookahead_unit_9_out_7),
    .out_8(lookahead_unit_9_out_8), .out_9(lookahead_unit_9_out_9));
  Lookahead_Unit lookahead_unit_10 (
    .in_1(lookahead_unit_12_out_8), .in_2(lookahead_unit_12_out_9), .in_3(lookahead_unit_11_out_6),
    .in_4(lookahead_unit_9_out_8), .in_5(lookahead_unit_9_out_9), .out_6(lookahead_unit_10_out_6),
    .out_7(lookahead_unit_10_out_7), .out_8(lookahead_unit_10_out_8), .out_9(lookahead_unit_10_out_9));
  Lookahead_Unit lookahead_unit_11 (
    .in_1(lookahead_unit_14_out_8), .in_2(lookahead_unit_14_out_9), .in_3(lookahead_unit_4_out_7),
    .in_4(lookahead_unit_10_out_8), .in_5(lookahead_unit_10_out_9), .out_6(lookahead_unit_11_out_6),
    .out_7(lookahead_unit_11_out_7), .out_8(lookahead_unit_11_out_8), .out_9(lookahead_unit_11_out_9));
  Carry_Lookahead_Adder carry_lookahead_adder_11 (
    .in_1(lookahead_unit_12_out_6), .in_2(n16_buffer_1_out_3[5]), .in_3(n16_buffer_2_out_3[5]),
    .out_4(out_4[5]), .out_5(carry_lookahead_adder_11_out_5), .out_6(carry_lookahead_adder_11_out_6));
  Lookahead_Unit lookahead_unit_12 (
    .in_1(carry_lookahead_adder_12_out_6), .in_2(carry_lookahead_adder_12_out_5),
    .in_3(lookahead_unit_10_out_7), .in_4(carry_lookahead_adder_11_out_6),
    .in_5(carry_lookahead_adder_11_out_5), .out_6(lookahead_unit_12_out_6), .out_7(lookahead_unit_12_out_7),
    .out_8(lookahead_unit_12_out_8), .out_9(lookahead_unit_12_out_9));
  Carry_Lookahead_Adder carry_lookahead_adder_12 (
    .in_1(lookahead_unit_12_out_7), .in_2(n16_buffer_1_out_3[4]), .in_3(n16_buffer_2_out_3[4]),
    .out_4(out_4[4]), .out_5(carry_lookahead_adder_12_out_5), .out_6(carry_lookahead_adder_12_out_6));
  Carry_Lookahead_Adder carry_lookahead_adder_13 (
    .in_1(lookahead_unit_13_out_6), .in_2(n16_buffer_1_out_3[3]), .in_3(n16_buffer_2_out_3[3]),
    .out_4(out_4[3]), .out_5(carry_lookahead_adder_13_out_5), .out_6(carry_lookahead_adder_13_out_6));
  Lookahead_Unit lookahead_unit_13 (
    .in_1(carry_lookahead_adder_14_out_6), .in_2(carry_lookahead_adder_14_out_5),
    .in_3(lookahead_unit_14_out_6), .in_4(carry_lookahead_adder_13_out_6),
    .in_5(carry_lookahead_adder_13_out_5), .out_6(lookahead_unit_13_out_6), .out_7(lookahead_unit_13_out_7),
    .out_8(lookahead_unit_13_out_8), .out_9(lookahead_unit_13_out_9));
  Lookahead_Unit lookahead_unit_14 (
    .in_1(lookahead_unit_15_out_8), .in_2(lookahead_unit_15_out_9), .in_3(lookahead_unit_11_out_7),
    .in_4(lookahead_unit_13_out_8), .in_5(lookahead_unit_13_out_9), .out_6(lookahead_unit_14_out_6),
    .out_7(lookahead_unit_14_out_7), .out_8(lookahead_unit_14_out_8), .out_9(lookahead_unit_14_out_9));
  Carry_Lookahead_Adder carry_lookahead_adder_14 (
    .in_1(lookahead_unit_13_out_7), .in_2(n16_buffer_1_out_3[2]), .in_3(n16_buffer_2_out_3[2]),
    .out_4(out_4[2]), .out_5(carry_lookahead_adder_14_out_5), .out_6(carry_lookahead_adder_14_out_6));
  Carry_Lookahead_Adder carry_lookahead_adder_15 (
    .in_1(lookahead_unit_15_out_6), .in_2(n16_buffer_1_out_3[1]), .in_3(n16_buffer_2_out_3[1]),
    .out_4(out_4[1]), .out_5(carry_lookahead_adder_15_out_5), .out_6(carry_lookahead_adder_15_out_6));
  Lookahead_Unit lookahead_unit_15 (
    .in_1(carry_lookahead_adder_16_out_6), .in_2(carry_lookahead_adder_16_out_5),
    .in_3(lookahead_unit_14_out_7), .in_4(carry_lookahead_adder_15_out_6),
    .in_5(carry_lookahead_adder_15_out_5), .out_6(lookahead_unit_15_out_6), .out_7(lookahead_unit_15_out_7),
    .out_8(lookahead_unit_15_out_8), .out_9(lookahead_unit_15_out_9));
  Carry_Lookahead_Adder carry_lookahead_adder_16 (
    .in_1(lookahead_unit_15_out_7), .in_2(n16_buffer_1_out_3[0]), .in_3(n16_buffer_2_out_3[0]),
    .out_4(out_4[0]), .out_5(carry_lookahead_adder_16_out_5), .out_6(carry_lookahead_adder_16_out_6));
  _16_Buffer u_16_buffer_2 (.in_1(Input_A), .in_2(in_3), .out_3(n16_buffer_2_out_3));
endmodule

module _16_NOT (
  input  [15:0] in_1,
  input  in_2,
  output [15:0] out_3
);

  wire [15:0] xor_1_out;

  xor xor_1 (xor_1_out[0], in_1[0], in_2);
  xor xor_2 (xor_1_out[1], in_1[1], in_2);
  xor xor_3 (xor_1_out[2], in_1[2], in_2);
  xor xor_4 (xor_1_out[3], in_1[3], in_2);
  xor xor_5 (xor_1_out[4], in_1[4], in_2);
  xor xor_6 (xor_1_out[5], in_1[5], in_2);
  xor xor_7 (xor_1_out[6], in_1[6], in_2);
  xor xor_8 (xor_1_out[7], in_1[7], in_2);
  xor xor_9 (xor_1_out[8], in_1[8], in_2);
  xor xor_10 (xor_1_out[9], in_1[9], in_2);
  xor xor_11 (xor_1_out[10], in_1[10], in_2);
  xor xor_12 (xor_1_out[11], in_1[11], in_2);
  xor xor_13 (xor_1_out[12], in_1[12], in_2);
  xor xor_14 (xor_1_out[13], in_1[13], in_2);
  xor xor_15 (xor_1_out[14], in_1[14], in_2);
  xor xor_16 (xor_1_out[15], in_1[15], in_2);
  _16_Buffer u_16_buffer_1 (.in_1(xor_1_out), .in_2(in_2), .out_3(out_3));
endmodule

module _16_INC (
  input  [15:0] in_1,
  input  in_2,
  output [15:0] out_3
);

  wire half_adder_1_out_4, half_adder_2_out_4, half_adder_3_out_4, half_adder_4_out_4, half_adder_5_out_4,
       half_adder_6_out_4, half_adder_7_out_4, half_adder_8_out_4, half_adder_9_out_4, half_adder_10_out_4,
       half_adder_11_out_4, half_adder_12_out_4, half_adder_13_out_4, half_adder_14_out_4,
       half_adder_15_out_4;
  wire [15:0] n16_buffer_1_out_3;

  _16_Buffer u_16_buffer_1 (.in_1(in_1), .in_2(in_2), .out_3(n16_buffer_1_out_3));
  Half_Adder half_adder_1 (.in_1(in_2), .in_2(n16_buffer_1_out_3[0]), .out_3(out_3[0]), .out_4(half_adder_1_out_4));
  Half_Adder half_adder_2 (
    .in_1(half_adder_1_out_4), .in_2(n16_buffer_1_out_3[1]), .out_3(out_3[1]), .out_4(half_adder_2_out_4));
  Half_Adder half_adder_3 (
    .in_1(half_adder_2_out_4), .in_2(n16_buffer_1_out_3[2]), .out_3(out_3[2]), .out_4(half_adder_3_out_4));
  Half_Adder half_adder_4 (
    .in_1(half_adder_3_out_4), .in_2(n16_buffer_1_out_3[3]), .out_3(out_3[3]), .out_4(half_adder_4_out_4));
  Half_Adder half_adder_5 (
    .in_1(half_adder_4_out_4), .in_2(n16_buffer_1_out_3[4]), .out_3(out_3[4]), .out_4(half_adder_5_out_4));
  Half_Adder half_adder_6 (
    .in_1(half_adder_5_out_4), .in_2(n16_buffer_1_out_3[5]), .out_3(out_3[5]), .out_4(half_adder_6_out_4));
  Half_Adder half_adder_7 (
    .in_1(half_adder_6_out_4), .in_2(n16_buffer_1_out_3[6]), .out_3(out_3[6]), .out_4(half_adder_7_out_4));
  Half_Adder half_adder_8 (
    .in_1(half_adder_7_out_4), .in_2(n16_buffer_1_out_3[7]), .out_3(out_3[7]), .out_4(half_adder_8_out_4));
  Half_Adder half_adder_9 (
    .in_1(half_adder_8_out_4), .in_2(n16_buffer_1_out_3[8]), .out_3(out_3[8]), .out_4(half_adder_9_out_4));
  Half_Adder half_adder_10 (
    .in_1(half_adder_9_out_4), .in_2(n16_buffer_1_out_3[9]), .out_3(out_3[9]), .out_4(half_adder_10_out_4));
  Half_Adder half_adder_11 (
    .in_1(half_adder_10_out_4), .in_2(n16_buffer_1_out_3[10]), .out_3(out_3[10]), .out_4(half_adder_11_out_4));
  Half_Adder half_adder_12 (
    .in_1(half_adder_11_out_4), .in_2(n16_buffer_1_out_3[11]), .out_3(out_3[11]), .out_4(half_adder_12_out_4));
  Half_Adder half_adder_13 (
    .in_1(half_adder_12_out_4), .in_2(n16_buffer_1_out_3[12]), .out_3(out_3[12]), .out_4(half_adder_13_out_4));
  Half_Adder half_adder_14 (
    .in_1(half_adder_13_out_4), .in_2(n16_buffer_1_out_3[13]), .out_3(out_3[13]), .out_4(half_adder_14_out_4));
  Half_Adder half_adder_15 (
    .in_1(half_adder_14_out_4), .in_2(n16_buffer_1_out_3[14]), .out_3(out_3[14]), .out_4(half_adder_15_out_4));
  Half_Adder half_adder_16 (
    .in_1(half_adder_15_out_4), .in_2(n16_buffer_1_out_3[15]), .out_3(out_3[15]));  // open: out_4
endmodule

module _16_DEC (
  input  [15:0] in_1,
  input  in_2,
  output [15:0] out_3
);

  wire and_1_out, and_2_out, and_3_out, and_4_out, and_5_out, and_6_out, and_7_out, and_8_out, and_9_out,
       and_10_out, and_11_out, and_12_out, and_13_out, and_14_out, and_15_out, not_1_out, not_2_out,
       not_3_out, not_4_out, not_5_out, not_6_out, not_7_out, not_8_out, not_9_out, not_10_out, not_11_out,
       not_12_out, not_13_out, not_14_out, not_15_out;
  wire [15:0] n16_buffer_1_out_3;

  _16_Buffer u_16_buffer_1 (.in_1(in_1), .in_2(in_2), .out_3(n16_buffer_1_out_3));
  not not_1 (not_1_out, n16_buffer_1_out_3[0]);
  and and_1 (and_1_out, not_1_out, in_2);
  not not_2 (not_2_out, n16_buffer_1_out_3[1]);
  and and_2 (and_2_out, not_2_out, and_1_out);
  not not_3 (not_3_out, n16_buffer_1_out_3[2]);
  and and_3 (and_3_out, not_3_out, and_2_out);
  not not_4 (not_4_out, n16_buffer_1_out_3[3]);
  and and_4 (and_4_out, not_4_out, and_3_out);
  not not_5 (not_5_out, n16_buffer_1_out_3[4]);
  and and_5 (and_5_out, not_5_out, and_4_out);
  not not_6 (not_6_out, n16_buffer_1_out_3[5]);
  and and_6 (and_6_out, not_6_out, and_5_out);
  not not_7 (not_7_out, n16_buffer_1_out_3[6]);
  and and_7 (and_7_out, not_7_out, and_6_out);
  not not_8 (not_8_out, n16_buffer_1_out_3[7]);
  and and_8 (and_8_out, not_8_out, and_7_out);
  not not_9 (not_9_out, n16_buffer_1_out_3[8]);
  and and_9 (and_9_out, not_9_out, and_8_out);
  not not_10 (not_10_out, n16_buffer_1_out_3[9]);
  and and_10 (and_10_out, not_10_out, and_9_out);
  not not_11 (not_11_out, n16_buffer_1_out_3[10]);
  and and_11 (and_11_out, not_11_out, and_10_out);
  not not_12 (not_12_out, n16_buffer_1_out_3[11]);
  and and_12 (and_12_out, not_12_out, and_11_out);
  not not_13 (not_13_out, n16_buffer_1_out_3[12]);
  and and_13 (and_13_out, not_13_out, and_12_out);
  not not_14 (not_14_out, n16_buffer_1_out_3[13]);
  and and_14 (and_14_out, not_14_out, and_13_out);
  not not_15 (not_15_out, n16_buffer_1_out_3[14]);
  and and_15 (and_15_out, not_15_out, and_14_out);
  xor xor_1 (out_3[0], n16_buffer_1_out_3[0], in_2);
  xor xor_2 (out_3[1], n16_buffer_1_out_3[1], and_1_out);
  xor xor_3 (out_3[2], n16_buffer_1_out_3[2], and_2_out);
  xor xor_4 (out_3[3], n16_buffer_1_out_3[3], and_3_out);
  xor xor_5 (out_3[4], n16_buffer_1_out_3[4], and_4_out);
  xor xor_6 (out_3[5], n16_buffer_1_out_3[5], and_5_out);
  xor xor_7 (out_3[6], n16_buffer_1_out_3[6], and_6_out);
  xor xor_8 (out_3[7], n16_buffer_1_out_3[7], and_7_out);
  xor xor_9 (out_3[8], n16_buffer_1_out_3[8], and_8_out);
  xor xor_10 (out_3[9], n16_buffer_1_out_3[9], and_9_out);
  xor xor_11 (out_3[10], n16_buffer_1_out_3[10], and_10_out);
  xor xor_12 (out_3[11], n16_buffer_1_out_3[11], and_11_out);
  xor xor_13 (out_3[12], n16_buffer_1_out_3[12], and_12_out);
  xor xor_14 (out_3[13], n16_buffer_1_out_3[13], and_13_out);
  xor xor_15 (out_3[14], n16_buffer_1_out_3[14], and_14_out);
  xor xor_16 (out_3[15], n16_buffer_1_out_3[15], and_15_out);
endmodule

module _16_OR (
  input  [15:0] in_1,
  input  [15:0] in_2,
  input  in_3,
  output [15:0] out_4
);

  wire [15:0] n16_buffer_1_out_3, n16_buffer_2_out_3;

  _16_Buffer u_16_buffer_1 (.in_1(in_1), .in_2(in_3), .out_3(n16_buffer_1_out_3));
  _16_Buffer u_16_buffer_2 (.in_1(in_2), .in_2(in_3), .out_3(n16_buffer_2_out_3));
  or or_1 (out_4[0], n16_buffer_1_out_3[0], n16_buffer_2_out_3[0]);
  or or_2 (out_4[1], n16_buffer_1_out_3[1], n16_buffer_2_out_3[1]);
  or or_3 (out_4[2], n16_buffer_1_out_3[2], n16_buffer_2_out_3[2]);
  or or_4 (out_4[3], n16_buffer_1_out_3[3], n16_buffer_2_out_3[3]);
  or or_5 (out_4[4], n16_buffer_1_out_3[4], n16_buffer_2_out_3[4]);
  or or_6 (out_4[5], n16_buffer_1_out_3[5], n16_buffer_2_out_3[5]);
  or or_7 (out_4[6], n16_buffer_1_out_3[6], n16_buffer_2_out_3[6]);
  or or_8 (out_4[7], n16_buffer_1_out_3[7], n16_buffer_2_out_3[7]);
  or or_9 (out_4[8], n16_buffer_1_out_3[8], n16_buffer_2_out_3[8]);
  or or_10 (out_4[9], n16_buffer_1_out_3[9], n16_buffer_2_out_3[9]);
  or or_11 (out_4[10], n16_buffer_1_out_3[10], n16_buffer_2_out_3[10]);
  or or_12 (out_4[11], n16_buffer_1_out_3[11], n16_buffer_2_out_3[11]);
  or or_13 (out_4[12], n16_buffer_1_out_3[12], n16_buffer_2_out_3[12]);
  or or_14 (out_4[13], n16_buffer_1_out_3[13], n16_buffer_2_out_3[13]);
  or or_15 (out_4[14], n16_buffer_1_out_3[14], n16_buffer_2_out_3[14]);
  or or_16 (out_4[15], n16_buffer_1_out_3[15], n16_buffer_2_out_3[15]);
endmodule

module _16_AND (
  input  [15:0] in_1,
  input  [15:0] in_2,
  input  in_3,
  output [15:0] out_4
);

  wire [15:0] n16_buffer_1_out_3, n16_buffer_2_out_3;

  _16_Buffer u_16_buffer_1 (.in_1(in_1), .in_2(in_3), .out_3(n16_buffer_1_out_3));
  _16_Buffer u_16_buffer_2 (.in_1(in_2), .in_2(in_3), .out_3(n16_buffer_2_out_3));
  and and_1 (out_4[0], n16_buffer_1_out_3[0], n16_buffer_2_out_3[0]);
  and and_2 (out_4[1], n16_buffer_1_out_3[1], n16_buffer_2_out_3[1]);
  and and_3 (out_4[2], n16_buffer_1_out_3[2], n16_buffer_2_out_3[2]);
  and and_4 (out_4[3], n16_buffer_1_out_3[3], n16_buffer_2_out_3[3]);
  and and_5 (out_4[4], n16_buffer_1_out_3[4], n16_buffer_2_out_3[4]);
  and and_6 (out_4[5], n16_buffer_1_out_3[5], n16_buffer_2_out_3[5]);
  and and_7 (out_4[6], n16_buffer_1_out_3[6], n16_buffer_2_out_3[6]);
  and and_8 (out_4[7], n16_buffer_1_out_3[7], n16_buffer_2_out_3[7]);
  and and_9 (out_4[8], n16_buffer_1_out_3[8], n16_buffer_2_out_3[8]);
  and and_10 (out_4[9], n16_buffer_1_out_3[9], n16_buffer_2_out_3[9]);
  and and_11 (out_4[10], n16_buffer_1_out_3[10], n16_buffer_2_out_3[10]);
  and and_12 (out_4[11], n16_buffer_1_out_3[11], n16_buffer_2_out_3[11]);
  and and_13 (out_4[12], n16_buffer_1_out_3[12], n16_buffer_2_out_3[12]);
  and and_14 (out_4[13], n16_buffer_1_out_3[13], n16_buffer_2_out_3[13]);
  and and_15 (out_4[14], n16_buffer_1_out_3[14], n16_buffer_2_out_3[14]);
  and and_16 (out_4[15], n16_buffer_1_out_3[15], n16_buffer_2_out_3[15]);
endmodule

module _16_XOR (
  input  [15:0] in_1,
  input  [15:0] in_2,
  input  in_3,
  output [15:0] out_4
);

  wire [15:0] n16_buffer_1_out_3, n16_buffer_2_out_3;

  _16_Buffer u_16_buffer_1 (.in_1(in_1), .in_2(in_3), .out_3(n16_buffer_1_out_3));
  _16_Buffer u_16_buffer_2 (.in_1(in_2), .in_2(in_3), .out_3(n16_buffer_2_out_3));
  xor xor_1 (out_4[0], n16_buffer_1_out_3[0], n16_buffer_2_out_3[0]);
  xor xor_2 (out_4[1], n16_buffer_1_out_3[1], n16_buffer_2_out_3[1]);
  xor xor_3 (out_4[2], n16_buffer_1_out_3[2], n16_buffer_2_out_3[2]);
  xor xor_4 (out_4[3], n16_buffer_1_out_3[3], n16_buffer_2_out_3[3]);
  xor xor_5 (out_4[4], n16_buffer_1_out_3[4], n16_buffer_2_out_3[4]);
  xor xor_6 (out_4[5], n16_buffer_1_out_3[5], n16_buffer_2_out_3[5]);
  xor xor_7 (out_4[6], n16_buffer_1_out_3[6], n16_buffer_2_out_3[6]);
  xor xor_8 (out_4[7], n16_buffer_1_out_3[7], n16_buffer_2_out_3[7]);
  xor xor_9 (out_4[8], n16_buffer_1_out_3[8], n16_buffer_2_out_3[8]);
  xor xor_10 (out_4[9], n16_buffer_1_out_3[9], n16_buffer_2_out_3[9]);
  xor xor_11 (out_4[10], n16_buffer_1_out_3[10], n16_buffer_2_out_3[10]);
  xor xor_12 (out_4[11], n16_buffer_1_out_3[11], n16_buffer_2_out_3[11]);
  xor xor_13 (out_4[12], n16_buffer_1_out_3[12], n16_buffer_2_out_3[12]);
  xor xor_14 (out_4[13], n16_buffer_1_out_3[13], n16_buffer_2_out_3[13]);
  xor xor_15 (out_4[14], n16_buffer_1_out_3[14], n16_buffer_2_out_3[14]);
  xor xor_16 (out_4[15], n16_buffer_1_out_3[15], n16_buffer_2_out_3[15]);
endmodule

module _16_NOR (
  input  [15:0] in_1,
  input  [15:0] in_2,
  input  in_3,
  output [15:0] out_4
);

  wire [15:0] n16_buffer_1_out_3, n16_buffer_2_out_3, nor_1_out;

  _16_Buffer u_16_buffer_1 (.in_1(in_1), .in_2(in_3), .out_3(n16_buffer_1_out_3));
  _16_Buffer u_16_buffer_2 (.in_1(in_2), .in_2(in_3), .out_3(n16_buffer_2_out_3));
  nor nor_1 (nor_1_out[0], n16_buffer_1_out_3[0], n16_buffer_2_out_3[0]);
  nor nor_2 (nor_1_out[1], n16_buffer_1_out_3[1], n16_buffer_2_out_3[1]);
  nor nor_3 (nor_1_out[2], n16_buffer_1_out_3[2], n16_buffer_2_out_3[2]);
  nor nor_4 (nor_1_out[3], n16_buffer_1_out_3[3], n16_buffer_2_out_3[3]);
  nor nor_5 (nor_1_out[4], n16_buffer_1_out_3[4], n16_buffer_2_out_3[4]);
  nor nor_6 (nor_1_out[5], n16_buffer_1_out_3[5], n16_buffer_2_out_3[5]);
  nor nor_7 (nor_1_out[6], n16_buffer_1_out_3[6], n16_buffer_2_out_3[6]);
  nor nor_8 (nor_1_out[7], n16_buffer_1_out_3[7], n16_buffer_2_out_3[7]);
  nor nor_9 (nor_1_out[8], n16_buffer_1_out_3[8], n16_buffer_2_out_3[8]);
  nor nor_10 (nor_1_out[9], n16_buffer_1_out_3[9], n16_buffer_2_out_3[9]);
  nor nor_11 (nor_1_out[10], n16_buffer_1_out_3[10], n16_buffer_2_out_3[10]);
  nor nor_12 (nor_1_out[11], n16_buffer_1_out_3[11], n16_buffer_2_out_3[11]);
  nor nor_13 (nor_1_out[12], n16_buffer_1_out_3[12], n16_buffer_2_out_3[12]);
  nor nor_14 (nor_1_out[13], n16_buffer_1_out_3[13], n16_buffer_2_out_3[13]);
  nor nor_15 (nor_1_out[14], n16_buffer_1_out_3[14], n16_buffer_2_out_3[14]);
  nor nor_16 (nor_1_out[15], n16_buffer_1_out_3[15], n16_buffer_2_out_3[15]);
  _16_Buffer u_16_buffer_3 (.in_1(nor_1_out), .in_2(in_3), .out_3(out_4));
endmodule

module _16_NAND (
  input  [15:0] in_1,
  input  [15:0] in_2,
  input  in_3,
  output [15:0] out_4
);

  wire [15:0] n16_buffer_1_out_3, n16_buffer_2_out_3, nand_1_out;

  _16_Buffer u_16_buffer_1 (.in_1(in_1), .in_2(in_3), .out_3(n16_buffer_1_out_3));
  _16_Buffer u_16_buffer_2 (.in_1(in_2), .in_2(in_3), .out_3(n16_buffer_2_out_3));
  nand nand_1 (nand_1_out[0], n16_buffer_1_out_3[0], n16_buffer_2_out_3[0]);
  nand nand_2 (nand_1_out[1], n16_buffer_1_out_3[1], n16_buffer_2_out_3[1]);
  nand nand_3 (nand_1_out[2], n16_buffer_1_out_3[2], n16_buffer_2_out_3[2]);
  nand nand_4 (nand_1_out[3], n16_buffer_1_out_3[3], n16_buffer_2_out_3[3]);
  nand nand_5 (nand_1_out[4], n16_buffer_1_out_3[4], n16_buffer_2_out_3[4]);
  nand nand_6 (nand_1_out[5], n16_buffer_1_out_3[5], n16_buffer_2_out_3[5]);
  nand nand_7 (nand_1_out[6], n16_buffer_1_out_3[6], n16_buffer_2_out_3[6]);
  nand nand_8 (nand_1_out[7], n16_buffer_1_out_3[7], n16_buffer_2_out_3[7]);
  nand nand_9 (nand_1_out[8], n16_buffer_1_out_3[8], n16_buffer_2_out_3[8]);
  nand nand_10 (nand_1_out[9], n16_buffer_1_out_3[9], n16_buffer_2_out_3[9]);
  nand nand_11 (nand_1_out[10], n16_buffer_1_out_3[10], n16_buffer_2_out_3[10]);
  nand nand_12 (nand_1_out[11], n16_buffer_1_out_3[11], n16_buffer_2_out_3[11]);
  nand nand_13 (nand_1_out[12], n16_buffer_1_out_3[12], n16_buffer_2_out_3[12]);
  nand nand_14 (nand_1_out[13], n16_buffer_1_out_3[13], n16_buffer_2_out_3[13]);
  nand nand_15 (nand_1_out[14], n16_buffer_1_out_3[14], n16_buffer_2_out_3[14]);
  nand nand_16 (nand_1_out[15], n16_buffer_1_out_3[15], n16_buffer_2_out_3[15]);
  _16_Buffer u_16_buffer_3 (.in_1(nand_1_out), .in_2(in_3), .out_3(out_4));
endmodule

module _16_XNOR (
  input  [15:0] in_1,
  input  [15:0] in_2,
  input  in_3,
  output [15:0] out_4
);

  wire [15:0] n16_buffer_1_out_3, n16_buffer_2_out_3, xnor_1_out;

  _16_Buffer u_16_buffer_1 (.in_1(in_1), .in_2(in_3), .out_3(n16_buffer_1_out_3));
  _16_Buffer u_16_buffer_2 (.in_1(in_2), .in_2(in_3), .out_3(n16_buffer_2_out_3));
  xnor xnor_1 (xnor_1_out[0], n16_buffer_1_out_3[0], n16_buffer_2_out_3[0]);
  xnor xnor_2 (xnor_1_out[1], n16_buffer_1_out_3[1], n16_buffer_2_out_3[1]);
  xnor xnor_3 (xnor_1_out[2], n16_buffer_1_out_3[2], n16_buffer_2_out_3[2]);
  xnor xnor_4 (xnor_1_out[3], n16_buffer_1_out_3[3], n16_buffer_2_out_3[3]);
  xnor xnor_5 (xnor_1_out[4], n16_buffer_1_out_3[4], n16_buffer_2_out_3[4]);
  xnor xnor_6 (xnor_1_out[5], n16_buffer_1_out_3[5], n16_buffer_2_out_3[5]);
  xnor xnor_7 (xnor_1_out[6], n16_buffer_1_out_3[6], n16_buffer_2_out_3[6]);
  xnor xnor_8 (xnor_1_out[7], n16_buffer_1_out_3[7], n16_buffer_2_out_3[7]);
  xnor xnor_9 (xnor_1_out[8], n16_buffer_1_out_3[8], n16_buffer_2_out_3[8]);
  xnor xnor_10 (xnor_1_out[9], n16_buffer_1_out_3[9], n16_buffer_2_out_3[9]);
  xnor xnor_11 (xnor_1_out[10], n16_buffer_1_out_3[10], n16_buffer_2_out_3[10]);
  xnor xnor_12 (xnor_1_out[11], n16_buffer_1_out_3[11], n16_buffer_2_out_3[11]);
  xnor xnor_13 (xnor_1_out[12], n16_buffer_1_out_3[12], n16_buffer_2_out_3[12]);
  xnor xnor_14 (xnor_1_out[13], n16_buffer_1_out_3[13], n16_buffer_2_out_3[13]);
  xnor xnor_15 (xnor_1_out[14], n16_buffer_1_out_3[14], n16_buffer_2_out_3[14]);
  xnor xnor_16 (xnor_1_out[15], n16_buffer_1_out_3[15], n16_buffer_2_out_3[15]);
  _16_Buffer u_16_buffer_3 (.in_1(xnor_1_out), .in_2(in_3), .out_3(out_4));
endmodule

module _16_2CMP (
  input  [15:0] in_1,
  input  in_2,
  output [15:0] out_3
);

  wire [15:0] n16_not_1_out_3;

  _16_INC u_16_inc_1 (.in_1(n16_not_1_out_3), .in_2(in_2), .out_3(out_3));
  _16_NOT u_16_not_1 (.in_1(in_1), .out_3(n16_not_1_out_3), .in_2(in_2));
endmodule

module _16_SUB (
  input  [15:0] in_1,
  input  [15:0] in_2,
  input  in_3,
  output [15:0] out_4,
  output out_5
);

  wire n16_cla_adder_1_out_5, not_1_out;
  wire [15:0] n16_2cmp_1_out_3;

  _16_2CMP u_16_2cmp_1 (.in_1(in_2), .in_2(in_3), .out_3(n16_2cmp_1_out_3));
  _16_CLA_Adder u_16_cla_adder_1 (
    .in_1(in_1), .Input_A(n16_2cmp_1_out_3), .out_4(out_4), .out_5(n16_cla_adder_1_out_5), .in_3(in_3));
  not not_1 (not_1_out, n16_cla_adder_1_out_5);
  and and_1 (out_5, not_1_out, in_3);
endmodule

module _16_BCNT (
  input  [15:0] in_1,
  input  in_2,
  output [15:0] out_3
);

  wire half_adder_1_out_4, half_adder_2_out_4, half_adder_3_out_4, ripple_carry_adder_1_out_4,
       ripple_carry_adder_1_out_5, ripple_carry_adder_2_out_4, ripple_carry_adder_2_out_5,
       ripple_carry_adder_3_out_4, ripple_carry_adder_3_out_5, ripple_carry_adder_4_out_4,
       ripple_carry_adder_4_out_5, ripple_carry_adder_5_out_4, ripple_carry_adder_5_out_5,
       ripple_carry_adder_6_out_4, ripple_carry_adder_6_out_5, ripple_carry_adder_7_out_4,
       ripple_carry_adder_7_out_5, ripple_carry_adder_8_out_4, ripple_carry_adder_8_out_5,
       ripple_carry_adder_9_out_4, ripple_carry_adder_9_out_5, ripple_carry_adder_10_out_4,
       ripple_carry_adder_10_out_5, ripple_carry_adder_11_out_4, ripple_carry_adder_11_out_5;
  wire [4:0] half_adder_1_out_3;
  wire [15:0] n16_buffer_1_out_3;

  _16_Buffer u_16_buffer_1 (.in_1(in_1), .in_2(in_2), .out_3(n16_buffer_1_out_3));
  Ripple_Carry_Adder ripple_carry_adder_1 (
    .in_2(n16_buffer_1_out_3[14]), .in_3(n16_buffer_1_out_3[13]), .out_4(ripple_carry_adder_1_out_4),
    .in_1(n16_buffer_1_out_3[12]), .out_5(ripple_carry_adder_1_out_5));
  Ripple_Carry_Adder ripple_carry_adder_2 (
    .in_2(n16_buffer_1_out_3[11]), .in_3(n16_buffer_1_out_3[10]), .out_4(ripple_carry_adder_2_out_4),
    .in_1(n16_buffer_1_out_3[9]), .out_5(ripple_carry_adder_2_out_5));
  Ripple_Carry_Adder ripple_carry_adder_3 (
    .in_2(n16_buffer_1_out_3[7]), .in_3(n16_buffer_1_out_3[6]), .out_4(ripple_carry_adder_3_out_4),
    .in_1(n16_buffer_1_out_3[5]), .out_5(ripple_carry_adder_3_out_5));
  Ripple_Carry_Adder ripple_carry_adder_4 (
    .in_2(n16_buffer_1_out_3[4]), .in_3(n16_buffer_1_out_3[3]), .out_4(ripple_carry_adder_4_out_4),
    .in_1(n16_buffer_1_out_3[2]), .out_5(ripple_carry_adder_4_out_5));
  Ripple_Carry_Adder ripple_carry_adder_5 (
    .in_2(ripple_carry_adder_1_out_4), .in_3(ripple_carry_adder_2_out_4), .out_4(ripple_carry_adder_5_out_4),
    .in_1(n16_buffer_1_out_3[8]), .out_5(ripple_carry_adder_5_out_5));
  Ripple_Carry_Adder ripple_carry_adder_6 (
    .in_2(ripple_carry_adder_1_out_5), .in_3(ripple_carry_adder_2_out_5), .out_4(ripple_carry_adder_6_out_4),
    .in_1(ripple_carry_adder_5_out_5), .out_5(ripple_carry_adder_6_out_5));
  Ripple_Carry_Adder ripple_carry_adder_7 (
    .in_2(ripple_carry_adder_3_out_4), .in_3(ripple_carry_adder_4_out_4), .out_4(ripple_carry_adder_7_out_4),
    .in_1(n16_buffer_1_out_3[1]), .out_5(ripple_carry_adder_7_out_5));
  Ripple_Carry_Adder ripple_carry_adder_8 (
    .in_2(ripple_carry_adder_3_out_5), .in_3(ripple_carry_adder_4_out_5), .out_4(ripple_carry_adder_8_out_4),
    .in_1(ripple_carry_adder_7_out_5), .out_5(ripple_carry_adder_8_out_5));
  Ripple_Carry_Adder ripple_carry_adder_9 (
    .in_2(ripple_carry_adder_5_out_4), .in_3(ripple_carry_adder_7_out_4), .out_4(ripple_carry_adder_9_out_4),
    .in_1(n16_buffer_1_out_3[0]), .out_5(ripple_carry_adder_9_out_5));
  Ripple_Carry_Adder ripple_carry_adder_10 (
    .in_2(ripple_carry_adder_6_out_4), .in_3(ripple_carry_adder_8_out_4),
    .out_4(ripple_carry_adder_10_out_4), .in_1(ripple_carry_adder_9_out_5),
    .out_5(ripple_carry_adder_10_out_5));
  Ripple_Carry_Adder ripple_carry_adder_11 (
    .in_2(ripple_carry_adder_6_out_5), .in_3(ripple_carry_adder_8_out_5),
    .out_4(ripple_carry_adder_11_out_4), .in_1(ripple_carry_adder_10_out_5),
    .out_5(ripple_carry_adder_11_out_5));
  Half_Adder half_adder_1 (
    .in_1(n16_buffer_1_out_3[15]), .in_2(ripple_carry_adder_9_out_4), .out_3(half_adder_1_out_3[0]),
    .out_4(half_adder_1_out_4));
  Half_Adder half_adder_2 (
    .in_1(half_adder_1_out_4), .in_2(ripple_carry_adder_10_out_4), .out_3(half_adder_1_out_3[1]),
    .out_4(half_adder_2_out_4));
  Half_Adder half_adder_3 (
    .in_1(half_adder_2_out_4), .in_2(ripple_carry_adder_11_out_4), .out_3(half_adder_1_out_3[2]),
    .out_4(half_adder_3_out_4));
  Half_Adder half_adder_4 (
    .in_1(half_adder_3_out_4), .in_2(ripple_carry_adder_11_out_5), .out_3(half_adder_1_out_3[3]),
    .out_4(half_adder_1_out_3[4]));
  _16_Buffer u_16_buffer_2 (.in_1({{11{1'b0}}, half_adder_1_out_3}), .in_2(in_2), .out_3(out_3));
endmodule

module _16_SQUR (
  input  [15:0] in_1,
  input  in_2,
  output [15:0] out_3
);

  wire square_controlled_adder_1_b_2, square_controlled_adder_1_e_2, square_controlled_adder_1_s,
       square_controlled_adder_2_b_2, square_controlled_adder_2_e_2, square_controlled_adder_2_s,
       square_controlled_adder_3_b_2, square_controlled_adder_3_e_2, square_controlled_adder_3_s,
       square_controlled_adder_4_b_2, square_controlled_adder_4_e_2, square_controlled_adder_4_s,
       square_controlled_adder_5_b_2, square_controlled_adder_5_e_2, square_controlled_adder_5_s,
       square_controlled_adder_6_b_2, square_controlled_adder_6_e_2, square_controlled_adder_6_s,
       square_controlled_adder_7_b_2, square_controlled_adder_7_e_2, square_controlled_adder_7_s,
       square_controlled_adder_8_e_2, square_controlled_adder_9_b_2, square_controlled_adder_9_cout,
       square_controlled_adder_9_s, square_controlled_adder_10_b_2, square_controlled_adder_10_cout,
       square_controlled_adder_10_e_2, square_controlled_adder_10_s, square_controlled_adder_11_b_2,
       square_controlled_adder_11_cout, square_controlled_adder_11_e_2, square_controlled_adder_11_s,
       square_controlled_adder_12_b_2, square_controlled_adder_12_cout, square_controlled_adder_12_e_2,
       square_controlled_adder_12_s, square_controlled_adder_13_b_2, square_controlled_adder_13_cout,
       square_controlled_adder_13_e_2, square_controlled_adder_13_s, square_controlled_adder_14_b_2,
       square_controlled_adder_14_cout, square_controlled_adder_14_e_2, square_controlled_adder_14_s,
       square_controlled_adder_15_b_2, square_controlled_adder_15_cout, square_controlled_adder_15_e_2,
       square_controlled_adder_15_s, square_controlled_adder_16_cout, square_controlled_adder_16_e_2,
       square_controlled_adder_17_b_2, square_controlled_adder_17_cout, square_controlled_adder_17_e_2,
       square_controlled_adder_17_s, square_controlled_adder_18_b_2, square_controlled_adder_18_cout,
       square_controlled_adder_18_e_2, square_controlled_adder_18_s, square_controlled_adder_19_b_2,
       square_controlled_adder_19_cout, square_controlled_adder_19_e_2, square_controlled_adder_19_s,
       square_controlled_adder_20_b_2, square_controlled_adder_20_cout, square_controlled_adder_20_e_2,
       square_controlled_adder_20_s, square_controlled_adder_21_b_2, square_controlled_adder_21_cout,
       square_controlled_adder_21_e_2, square_controlled_adder_21_s, square_controlled_adder_22_b_2,
       square_controlled_adder_22_cout, square_controlled_adder_22_e_2, square_controlled_adder_22_s,
       square_controlled_adder_23_cout, square_controlled_adder_23_e_2, square_controlled_adder_24_b_2,
       square_controlled_adder_24_cout, square_controlled_adder_24_s, square_controlled_adder_25_b_2,
       square_controlled_adder_25_cout, square_controlled_adder_25_e_2, square_controlled_adder_25_s,
       square_controlled_adder_26_b_2, square_controlled_adder_26_cout, square_controlled_adder_26_e_2,
       square_controlled_adder_26_s, square_controlled_adder_27_b_2, square_controlled_adder_27_cout,
       square_controlled_adder_27_e_2, square_controlled_adder_27_s, square_controlled_adder_28_b_2,
       square_controlled_adder_28_cout, square_controlled_adder_28_e_2, square_controlled_adder_28_s,
       square_controlled_adder_29_b_2, square_controlled_adder_29_cout, square_controlled_adder_29_e_2,
       square_controlled_adder_29_s, square_controlled_adder_30_cout, square_controlled_adder_30_e_2,
       square_controlled_adder_31_b_2, square_controlled_adder_31_cout, square_controlled_adder_31_e_2,
       square_controlled_adder_31_s, square_controlled_adder_32_b_2, square_controlled_adder_32_cout,
       square_controlled_adder_32_e_2, square_controlled_adder_32_s, square_controlled_adder_33_b_2,
       square_controlled_adder_33_cout, square_controlled_adder_33_e_2, square_controlled_adder_33_s,
       square_controlled_adder_34_b_2, square_controlled_adder_34_cout, square_controlled_adder_34_e_2,
       square_controlled_adder_34_s, square_controlled_adder_35_b_2, square_controlled_adder_35_cout,
       square_controlled_adder_35_e_2, square_controlled_adder_35_s, square_controlled_adder_36_cout,
       square_controlled_adder_36_e_2, square_controlled_adder_37_b_2, square_controlled_adder_37_cout,
       square_controlled_adder_37_s, square_controlled_adder_38_b_2, square_controlled_adder_38_cout,
       square_controlled_adder_38_e_2, square_controlled_adder_38_s, square_controlled_adder_39_b_2,
       square_controlled_adder_39_cout, square_controlled_adder_39_e_2, square_controlled_adder_39_s,
       square_controlled_adder_40_b_2, square_controlled_adder_40_cout, square_controlled_adder_40_e_2,
       square_controlled_adder_40_s, square_controlled_adder_41_b_2, square_controlled_adder_41_cout,
       square_controlled_adder_41_e_2, square_controlled_adder_41_s, square_controlled_adder_42_cout,
       square_controlled_adder_42_e_2, square_controlled_adder_43_b_2, square_controlled_adder_43_cout,
       square_controlled_adder_43_e_2, square_controlled_adder_43_s, square_controlled_adder_44_b_2,
       square_controlled_adder_44_cout, square_controlled_adder_44_e_2, square_controlled_adder_44_s,
       square_controlled_adder_45_b_2, square_controlled_adder_45_cout, square_controlled_adder_45_e_2,
       square_controlled_adder_45_s, square_controlled_adder_46_b_2, square_controlled_adder_46_cout,
       square_controlled_adder_46_e_2, square_controlled_adder_46_s, square_controlled_adder_47_cout,
       square_controlled_adder_47_e_2, square_controlled_adder_48_b_2, square_controlled_adder_48_cout,
       square_controlled_adder_48_s, square_controlled_adder_49_b_2, square_controlled_adder_49_cout,
       square_controlled_adder_49_e_2, square_controlled_adder_49_s, square_controlled_adder_50_b_2,
       square_controlled_adder_50_cout, square_controlled_adder_50_e_2, square_controlled_adder_50_s,
       square_controlled_adder_51_b_2, square_controlled_adder_51_cout, square_controlled_adder_51_e_2,
       square_controlled_adder_51_s, square_controlled_adder_52_cout, square_controlled_adder_52_e_2,
       square_controlled_adder_53_b_2, square_controlled_adder_53_cout, square_controlled_adder_53_e_2,
       square_controlled_adder_53_s, square_controlled_adder_54_b_2, square_controlled_adder_54_cout,
       square_controlled_adder_54_e_2, square_controlled_adder_54_s, square_controlled_adder_55_b_2,
       square_controlled_adder_55_cout, square_controlled_adder_55_e_2, square_controlled_adder_55_s,
       square_controlled_adder_56_cout, square_controlled_adder_56_e_2, square_controlled_adder_57_b_2,
       square_controlled_adder_57_cout, square_controlled_adder_57_s, square_controlled_adder_58_b_2,
       square_controlled_adder_58_cout, square_controlled_adder_58_e_2, square_controlled_adder_58_s,
       square_controlled_adder_59_b_2, square_controlled_adder_59_cout, square_controlled_adder_59_e_2,
       square_controlled_adder_59_s, square_controlled_adder_60_cout, square_controlled_adder_60_e_2,
       square_controlled_adder_61_b_2, square_controlled_adder_61_cout, square_controlled_adder_61_e_2,
       square_controlled_adder_61_s, square_controlled_adder_62_b_2, square_controlled_adder_62_cout,
       square_controlled_adder_62_e_2, square_controlled_adder_62_s, square_controlled_adder_63_cout,
       square_controlled_adder_63_e_2, square_controlled_adder_64_b_2, square_controlled_adder_64_cout,
       square_controlled_adder_64_s, square_controlled_adder_65_b_2, square_controlled_adder_65_cout,
       square_controlled_adder_65_e_2, square_controlled_adder_65_s, square_controlled_adder_66_cout,
       square_controlled_adder_66_e_2, square_controlled_adder_67_b_2, square_controlled_adder_67_cout,
       square_controlled_adder_67_e_2, square_controlled_adder_67_s, square_controlled_adder_68_cout,
       square_controlled_adder_68_e_2, square_controlled_adder_69_b_2, square_controlled_adder_69_cout,
       square_controlled_adder_69_s, square_controlled_adder_70_cout, square_controlled_adder_70_e_2,
       square_controlled_adder_71_cout, square_controlled_adder_71_e_2, square_controlled_adder_72_cout;
  wire [15:0] n16_buffer_1_out_3, square_controlled_adder_72_s;

  _16_Buffer u_16_buffer_1 (.in_1(in_1), .in_2(in_2), .out_3(n16_buffer_1_out_3));
  Square_Controlled_Adder square_controlled_adder_1 (
    .B(1'b0), .Cin(square_controlled_adder_9_cout), .A(1'b0), .E(n16_buffer_1_out_3[7]),
    .B_2(square_controlled_adder_1_b_2), .S(square_controlled_adder_1_s), .E_2(square_controlled_adder_1_e_2));  // open: Cout
  Square_Controlled_Adder square_controlled_adder_2 (
    .B(square_controlled_adder_1_b_2), .Cin(square_controlled_adder_10_cout),
    .A(square_controlled_adder_1_s), .E(n16_buffer_1_out_3[6]), .B_2(square_controlled_adder_2_b_2),
    .S(square_controlled_adder_2_s), .E_2(square_controlled_adder_2_e_2));  // open: Cout
  Square_Controlled_Adder square_controlled_adder_3 (
    .B(square_controlled_adder_2_b_2), .Cin(square_controlled_adder_11_cout),
    .A(square_controlled_adder_2_s), .E(n16_buffer_1_out_3[5]), .B_2(square_controlled_adder_3_b_2),
    .S(square_controlled_adder_3_s), .E_2(square_controlled_adder_3_e_2));  // open: Cout
  Square_Controlled_Adder square_controlled_adder_4 (
    .B(square_controlled_adder_3_b_2), .Cin(square_controlled_adder_12_cout),
    .A(square_controlled_adder_3_s), .E(n16_buffer_1_out_3[4]), .B_2(square_controlled_adder_4_b_2),
    .S(square_controlled_adder_4_s), .E_2(square_controlled_adder_4_e_2));  // open: Cout
  Square_Controlled_Adder square_controlled_adder_5 (
    .B(square_controlled_adder_4_b_2), .Cin(square_controlled_adder_13_cout),
    .A(square_controlled_adder_4_s), .E(n16_buffer_1_out_3[3]), .B_2(square_controlled_adder_5_b_2),
    .S(square_controlled_adder_5_s), .E_2(square_controlled_adder_5_e_2));  // open: Cout
  Square_Controlled_Adder square_controlled_adder_6 (
    .B(square_controlled_adder_5_b_2), .Cin(square_controlled_adder_14_cout),
    .A(square_controlled_adder_5_s), .E(n16_buffer_1_out_3[2]), .B_2(square_controlled_adder_6_b_2),
    .S(square_controlled_adder_6_s), .E_2(square_controlled_adder_6_e_2));  // open: Cout
  Square_Controlled_Adder square_controlled_adder_7 (
    .B(square_controlled_adder_6_b_2), .Cin(square_controlled_adder_15_cout),
    .A(square_controlled_adder_6_s), .E(n16_buffer_1_out_3[1]), .B_2(square_controlled_adder_7_b_2),
    .S(square_controlled_adder_7_s), .E_2(square_controlled_adder_7_e_2));  // open: Cout
  Square_Controlled_Adder square_controlled_adder_8 (
    .B(square_controlled_adder_7_b_2), .Cin(square_controlled_adder_16_cout),
    .A(square_controlled_adder_7_s), .E(n16_buffer_1_out_3[0]), .S(square_controlled_adder_72_s[15]),
    .E_2(square_controlled_adder_8_e_2));  // open: B_2, Cout
  Square_Controlled_Adder square_controlled_adder_9 (
    .B(1'b1), .Cin(1'b0), .A(1'b0), .E(square_controlled_adder_1_e_2), .B_2(square_controlled_adder_9_b_2),
    .Cout(square_controlled_adder_9_cout), .S(square_controlled_adder_9_s));  // open: E_2
  Square_Controlled_Adder square_controlled_adder_10 (
    .B(square_controlled_adder_1_e_2), .Cin(square_controlled_adder_17_cout),
    .A(square_controlled_adder_9_s), .E(square_controlled_adder_2_e_2), .B_2(square_controlled_adder_10_b_2),
    .Cout(square_controlled_adder_10_cout), .S(square_controlled_adder_10_s),
    .E_2(square_controlled_adder_10_e_2));
  Square_Controlled_Adder square_controlled_adder_11 (
    .B(square_controlled_adder_2_b_2), .Cin(square_controlled_adder_18_cout),
    .A(square_controlled_adder_10_s), .E(square_controlled_adder_3_e_2),
    .B_2(square_controlled_adder_11_b_2), .Cout(square_controlled_adder_11_cout),
    .S(square_controlled_adder_11_s), .E_2(square_controlled_adder_11_e_2));
  Square_Controlled_Adder square_controlled_adder_12 (
    .B(square_controlled_adder_3_b_2), .Cin(square_controlled_adder_19_cout),
    .A(square_controlled_adder_11_s), .E(square_controlled_adder_4_e_2),
    .B_2(square_controlled_adder_12_b_2), .Cout(square_controlled_adder_12_cout),
    .S(square_controlled_adder_12_s), .E_2(square_controlled_adder_12_e_2));
  Square_Controlled_Adder square_controlled_adder_13 (
    .B(square_controlled_adder_4_b_2), .Cin(square_controlled_adder_20_cout),
    .A(square_controlled_adder_12_s), .E(square_controlled_adder_5_e_2),
    .B_2(square_controlled_adder_13_b_2), .Cout(square_controlled_adder_13_cout),
    .S(square_controlled_adder_13_s), .E_2(square_controlled_adder_13_e_2));
  Square_Controlled_Adder square_controlled_adder_14 (
    .B(square_controlled_adder_5_b_2), .Cin(square_controlled_adder_21_cout),
    .A(square_controlled_adder_13_s), .E(square_controlled_adder_6_e_2),
    .B_2(square_controlled_adder_14_b_2), .Cout(square_controlled_adder_14_cout),
    .S(square_controlled_adder_14_s), .E_2(square_controlled_adder_14_e_2));
  Square_Controlled_Adder square_controlled_adder_15 (
    .B(square_controlled_adder_6_b_2), .Cin(square_controlled_adder_22_cout),
    .A(square_controlled_adder_14_s), .E(square_controlled_adder_7_e_2),
    .B_2(square_controlled_adder_15_b_2), .Cout(square_controlled_adder_15_cout),
    .S(square_controlled_adder_15_s), .E_2(square_controlled_adder_15_e_2));
  Square_Controlled_Adder square_controlled_adder_16 (
    .B(square_controlled_adder_7_b_2), .Cin(square_controlled_adder_23_cout),
    .A(square_controlled_adder_15_s), .E(square_controlled_adder_8_e_2),
    .Cout(square_controlled_adder_16_cout), .S(square_controlled_adder_72_s[14]),
    .E_2(square_controlled_adder_16_e_2));  // open: B_2
  Square_Controlled_Adder square_controlled_adder_17 (
    .B(square_controlled_adder_1_b_2), .Cin(square_controlled_adder_24_cout), .A(1'b0),
    .E(square_controlled_adder_10_e_2), .B_2(square_controlled_adder_17_b_2),
    .Cout(square_controlled_adder_17_cout), .S(square_controlled_adder_17_s),
    .E_2(square_controlled_adder_17_e_2));
  Square_Controlled_Adder square_controlled_adder_18 (
    .B(square_controlled_adder_10_b_2), .Cin(square_controlled_adder_25_cout),
    .A(square_controlled_adder_17_s), .E(square_controlled_adder_11_e_2),
    .B_2(square_controlled_adder_18_b_2), .Cout(square_controlled_adder_18_cout),
    .S(square_controlled_adder_18_s), .E_2(square_controlled_adder_18_e_2));
  Square_Controlled_Adder square_controlled_adder_19 (
    .B(square_controlled_adder_11_b_2), .Cin(square_controlled_adder_26_cout),
    .A(square_controlled_adder_18_s), .E(square_controlled_adder_12_e_2),
    .B_2(square_controlled_adder_19_b_2), .Cout(square_controlled_adder_19_cout),
    .S(square_controlled_adder_19_s), .E_2(square_controlled_adder_19_e_2));
  Square_Controlled_Adder square_controlled_adder_20 (
    .B(square_controlled_adder_12_b_2), .Cin(square_controlled_adder_27_cout),
    .A(square_controlled_adder_19_s), .E(square_controlled_adder_13_e_2),
    .B_2(square_controlled_adder_20_b_2), .Cout(square_controlled_adder_20_cout),
    .S(square_controlled_adder_20_s), .E_2(square_controlled_adder_20_e_2));
  Square_Controlled_Adder square_controlled_adder_21 (
    .B(square_controlled_adder_13_b_2), .Cin(square_controlled_adder_28_cout),
    .A(square_controlled_adder_20_s), .E(square_controlled_adder_14_e_2),
    .B_2(square_controlled_adder_21_b_2), .Cout(square_controlled_adder_21_cout),
    .S(square_controlled_adder_21_s), .E_2(square_controlled_adder_21_e_2));
  Square_Controlled_Adder square_controlled_adder_22 (
    .B(square_controlled_adder_14_b_2), .Cin(square_controlled_adder_29_cout),
    .A(square_controlled_adder_21_s), .E(square_controlled_adder_15_e_2),
    .B_2(square_controlled_adder_22_b_2), .Cout(square_controlled_adder_22_cout),
    .S(square_controlled_adder_22_s), .E_2(square_controlled_adder_22_e_2));
  Square_Controlled_Adder square_controlled_adder_23 (
    .B(square_controlled_adder_15_b_2), .Cin(square_controlled_adder_30_cout),
    .A(square_controlled_adder_22_s), .E(square_controlled_adder_16_e_2),
    .Cout(square_controlled_adder_23_cout), .S(square_controlled_adder_72_s[13]),
    .E_2(square_controlled_adder_23_e_2));  // open: B_2
  Square_Controlled_Adder square_controlled_adder_24 (
    .B(square_controlled_adder_9_b_2), .Cin(1'b0), .A(1'b0), .E(square_controlled_adder_17_e_2),
    .B_2(square_controlled_adder_24_b_2), .Cout(square_controlled_adder_24_cout),
    .S(square_controlled_adder_24_s));  // open: E_2
  Square_Controlled_Adder square_controlled_adder_25 (
    .B(square_controlled_adder_17_e_2), .Cin(square_controlled_adder_31_cout),
    .A(square_controlled_adder_24_s), .E(square_controlled_adder_18_e_2),
    .B_2(square_controlled_adder_25_b_2), .Cout(square_controlled_adder_25_cout),
    .S(square_controlled_adder_25_s), .E_2(square_controlled_adder_25_e_2));
  Square_Controlled_Adder square_controlled_adder_26 (
    .B(square_controlled_adder_18_b_2), .Cin(square_controlled_adder_32_cout),
    .A(square_controlled_adder_25_s), .E(square_controlled_adder_19_e_2),
    .B_2(square_controlled_adder_26_b_2), .Cout(square_controlled_adder_26_cout),
    .S(square_controlled_adder_26_s), .E_2(square_controlled_adder_26_e_2));
  Square_Controlled_Adder square_controlled_adder_27 (
    .B(square_controlled_adder_19_b_2), .Cin(square_controlled_adder_33_cout),
    .A(square_controlled_adder_26_s), .E(square_controlled_adder_20_e_2),
    .B_2(square_controlled_adder_27_b_2), .Cout(square_controlled_adder_27_cout),
    .S(square_controlled_adder_27_s), .E_2(square_controlled_adder_27_e_2));
  Square_Controlled_Adder square_controlled_adder_28 (
    .B(square_controlled_adder_20_b_2), .Cin(square_controlled_adder_34_cout),
    .A(square_controlled_adder_27_s), .E(square_controlled_adder_21_e_2),
    .B_2(square_controlled_adder_28_b_2), .Cout(square_controlled_adder_28_cout),
    .S(square_controlled_adder_28_s), .E_2(square_controlled_adder_28_e_2));
  Square_Controlled_Adder square_controlled_adder_29 (
    .B(square_controlled_adder_21_b_2), .Cin(square_controlled_adder_35_cout),
    .A(square_controlled_adder_28_s), .E(square_controlled_adder_22_e_2),
    .B_2(square_controlled_adder_29_b_2), .Cout(square_controlled_adder_29_cout),
    .S(square_controlled_adder_29_s), .E_2(square_controlled_adder_29_e_2));
  Square_Controlled_Adder square_controlled_adder_30 (
    .B(square_controlled_adder_22_b_2), .Cin(square_controlled_adder_36_cout),
    .A(square_controlled_adder_29_s), .E(square_controlled_adder_23_e_2),
    .Cout(square_controlled_adder_30_cout), .S(square_controlled_adder_72_s[12]),
    .E_2(square_controlled_adder_30_e_2));  // open: B_2
  Square_Controlled_Adder square_controlled_adder_31 (
    .B(square_controlled_adder_17_b_2), .Cin(square_controlled_adder_37_cout), .A(1'b0),
    .E(square_controlled_adder_25_e_2), .B_2(square_controlled_adder_31_b_2),
    .Cout(square_controlled_adder_31_cout), .S(square_controlled_adder_31_s),
    .E_2(square_controlled_adder_31_e_2));
  Square_Controlled_Adder square_controlled_adder_32 (
    .B(square_controlled_adder_25_b_2), .Cin(square_controlled_adder_38_cout),
    .A(square_controlled_adder_31_s), .E(square_controlled_adder_26_e_2),
    .B_2(square_controlled_adder_32_b_2), .Cout(square_controlled_adder_32_cout),
    .S(square_controlled_adder_32_s), .E_2(square_controlled_adder_32_e_2));
  Square_Controlled_Adder square_controlled_adder_33 (
    .B(square_controlled_adder_26_b_2), .Cin(square_controlled_adder_39_cout),
    .A(square_controlled_adder_32_s), .E(square_controlled_adder_27_e_2),
    .B_2(square_controlled_adder_33_b_2), .Cout(square_controlled_adder_33_cout),
    .S(square_controlled_adder_33_s), .E_2(square_controlled_adder_33_e_2));
  Square_Controlled_Adder square_controlled_adder_34 (
    .B(square_controlled_adder_27_b_2), .Cin(square_controlled_adder_40_cout),
    .A(square_controlled_adder_33_s), .E(square_controlled_adder_28_e_2),
    .B_2(square_controlled_adder_34_b_2), .Cout(square_controlled_adder_34_cout),
    .S(square_controlled_adder_34_s), .E_2(square_controlled_adder_34_e_2));
  Square_Controlled_Adder square_controlled_adder_35 (
    .B(square_controlled_adder_28_b_2), .Cin(square_controlled_adder_41_cout),
    .A(square_controlled_adder_34_s), .E(square_controlled_adder_29_e_2),
    .B_2(square_controlled_adder_35_b_2), .Cout(square_controlled_adder_35_cout),
    .S(square_controlled_adder_35_s), .E_2(square_controlled_adder_35_e_2));
  Square_Controlled_Adder square_controlled_adder_36 (
    .B(square_controlled_adder_29_b_2), .Cin(square_controlled_adder_42_cout),
    .A(square_controlled_adder_35_s), .E(square_controlled_adder_30_e_2),
    .Cout(square_controlled_adder_36_cout), .S(square_controlled_adder_72_s[11]),
    .E_2(square_controlled_adder_36_e_2));  // open: B_2
  Square_Controlled_Adder square_controlled_adder_37 (
    .B(square_controlled_adder_24_b_2), .Cin(1'b0), .A(1'b0), .E(square_controlled_adder_31_e_2),
    .B_2(square_controlled_adder_37_b_2), .Cout(square_controlled_adder_37_cout),
    .S(square_controlled_adder_37_s));  // open: E_2
  Square_Controlled_Adder square_controlled_adder_38 (
    .B(square_controlled_adder_31_e_2), .Cin(square_controlled_adder_43_cout),
    .A(square_controlled_adder_37_s), .E(square_controlled_adder_32_e_2),
    .B_2(square_controlled_adder_38_b_2), .Cout(square_controlled_adder_38_cout),
    .S(square_controlled_adder_38_s), .E_2(square_controlled_adder_38_e_2));
  Square_Controlled_Adder square_controlled_adder_39 (
    .B(square_controlled_adder_32_b_2), .Cin(square_controlled_adder_44_cout),
    .A(square_controlled_adder_38_s), .E(square_controlled_adder_33_e_2),
    .B_2(square_controlled_adder_39_b_2), .Cout(square_controlled_adder_39_cout),
    .S(square_controlled_adder_39_s), .E_2(square_controlled_adder_39_e_2));
  Square_Controlled_Adder square_controlled_adder_40 (
    .B(square_controlled_adder_33_b_2), .Cin(square_controlled_adder_45_cout),
    .A(square_controlled_adder_39_s), .E(square_controlled_adder_34_e_2),
    .B_2(square_controlled_adder_40_b_2), .Cout(square_controlled_adder_40_cout),
    .S(square_controlled_adder_40_s), .E_2(square_controlled_adder_40_e_2));
  Square_Controlled_Adder square_controlled_adder_41 (
    .B(square_controlled_adder_34_b_2), .Cin(square_controlled_adder_46_cout),
    .A(square_controlled_adder_40_s), .E(square_controlled_adder_35_e_2),
    .B_2(square_controlled_adder_41_b_2), .Cout(square_controlled_adder_41_cout),
    .S(square_controlled_adder_41_s), .E_2(square_controlled_adder_41_e_2));
  Square_Controlled_Adder square_controlled_adder_42 (
    .B(square_controlled_adder_35_b_2), .Cin(square_controlled_adder_47_cout),
    .A(square_controlled_adder_41_s), .E(square_controlled_adder_36_e_2),
    .Cout(square_controlled_adder_42_cout), .S(square_controlled_adder_72_s[10]),
    .E_2(square_controlled_adder_42_e_2));  // open: B_2
  Square_Controlled_Adder square_controlled_adder_43 (
    .B(square_controlled_adder_31_b_2), .Cin(square_controlled_adder_48_cout), .A(1'b0),
    .E(square_controlled_adder_38_e_2), .B_2(square_controlled_adder_43_b_2),
    .Cout(square_controlled_adder_43_cout), .S(square_controlled_adder_43_s),
    .E_2(square_controlled_adder_43_e_2));
  Square_Controlled_Adder square_controlled_adder_44 (
    .B(square_controlled_adder_38_b_2), .Cin(square_controlled_adder_49_cout),
    .A(square_controlled_adder_43_s), .E(square_controlled_adder_39_e_2),
    .B_2(square_controlled_adder_44_b_2), .Cout(square_controlled_adder_44_cout),
    .S(square_controlled_adder_44_s), .E_2(square_controlled_adder_44_e_2));
  Square_Controlled_Adder square_controlled_adder_45 (
    .B(square_controlled_adder_39_b_2), .Cin(square_controlled_adder_50_cout),
    .A(square_controlled_adder_44_s), .E(square_controlled_adder_40_e_2),
    .B_2(square_controlled_adder_45_b_2), .Cout(square_controlled_adder_45_cout),
    .S(square_controlled_adder_45_s), .E_2(square_controlled_adder_45_e_2));
  Square_Controlled_Adder square_controlled_adder_46 (
    .B(square_controlled_adder_40_b_2), .Cin(square_controlled_adder_51_cout),
    .A(square_controlled_adder_45_s), .E(square_controlled_adder_41_e_2),
    .B_2(square_controlled_adder_46_b_2), .Cout(square_controlled_adder_46_cout),
    .S(square_controlled_adder_46_s), .E_2(square_controlled_adder_46_e_2));
  Square_Controlled_Adder square_controlled_adder_47 (
    .B(square_controlled_adder_41_b_2), .Cin(square_controlled_adder_52_cout),
    .A(square_controlled_adder_46_s), .E(square_controlled_adder_42_e_2),
    .Cout(square_controlled_adder_47_cout), .S(square_controlled_adder_72_s[9]),
    .E_2(square_controlled_adder_47_e_2));  // open: B_2
  Square_Controlled_Adder square_controlled_adder_48 (
    .B(square_controlled_adder_37_b_2), .Cin(1'b0), .A(1'b0), .E(square_controlled_adder_43_e_2),
    .B_2(square_controlled_adder_48_b_2), .Cout(square_controlled_adder_48_cout),
    .S(square_controlled_adder_48_s));  // open: E_2
  Square_Controlled_Adder square_controlled_adder_49 (
    .B(square_controlled_adder_43_e_2), .Cin(square_controlled_adder_53_cout),
    .A(square_controlled_adder_48_s), .E(square_controlled_adder_44_e_2),
    .B_2(square_controlled_adder_49_b_2), .Cout(square_controlled_adder_49_cout),
    .S(square_controlled_adder_49_s), .E_2(square_controlled_adder_49_e_2));
  Square_Controlled_Adder square_controlled_adder_50 (
    .B(square_controlled_adder_44_b_2), .Cin(square_controlled_adder_54_cout),
    .A(square_controlled_adder_49_s), .E(square_controlled_adder_45_e_2),
    .B_2(square_controlled_adder_50_b_2), .Cout(square_controlled_adder_50_cout),
    .S(square_controlled_adder_50_s), .E_2(square_controlled_adder_50_e_2));
  Square_Controlled_Adder square_controlled_adder_51 (
    .B(square_controlled_adder_45_b_2), .Cin(square_controlled_adder_55_cout),
    .A(square_controlled_adder_50_s), .E(square_controlled_adder_46_e_2),
    .B_2(square_controlled_adder_51_b_2), .Cout(square_controlled_adder_51_cout),
    .S(square_controlled_adder_51_s), .E_2(square_controlled_adder_51_e_2));
  Square_Controlled_Adder square_controlled_adder_52 (
    .B(square_controlled_adder_46_b_2), .Cin(square_controlled_adder_56_cout),
    .A(square_controlled_adder_51_s), .E(square_controlled_adder_47_e_2),
    .Cout(square_controlled_adder_52_cout), .S(square_controlled_adder_72_s[8]),
    .E_2(square_controlled_adder_52_e_2));  // open: B_2
  Square_Controlled_Adder square_controlled_adder_53 (
    .B(square_controlled_adder_43_b_2), .Cin(square_controlled_adder_57_cout), .A(1'b0),
    .E(square_controlled_adder_49_e_2), .B_2(square_controlled_adder_53_b_2),
    .Cout(square_controlled_adder_53_cout), .S(square_controlled_adder_53_s),
    .E_2(square_controlled_adder_53_e_2));
  Square_Controlled_Adder square_controlled_adder_54 (
    .B(square_controlled_adder_49_b_2), .Cin(square_controlled_adder_58_cout),
    .A(square_controlled_adder_53_s), .E(square_controlled_adder_50_e_2),
    .B_2(square_controlled_adder_54_b_2), .Cout(square_controlled_adder_54_cout),
    .S(square_controlled_adder_54_s), .E_2(square_controlled_adder_54_e_2));
  Square_Controlled_Adder square_controlled_adder_55 (
    .B(square_controlled_adder_50_b_2), .Cin(square_controlled_adder_59_cout),
    .A(square_controlled_adder_54_s), .E(square_controlled_adder_51_e_2),
    .B_2(square_controlled_adder_55_b_2), .Cout(square_controlled_adder_55_cout),
    .S(square_controlled_adder_55_s), .E_2(square_controlled_adder_55_e_2));
  Square_Controlled_Adder square_controlled_adder_56 (
    .B(square_controlled_adder_51_b_2), .Cin(square_controlled_adder_60_cout),
    .A(square_controlled_adder_55_s), .E(square_controlled_adder_52_e_2),
    .Cout(square_controlled_adder_56_cout), .S(square_controlled_adder_72_s[7]),
    .E_2(square_controlled_adder_56_e_2));  // open: B_2
  Square_Controlled_Adder square_controlled_adder_57 (
    .B(square_controlled_adder_48_b_2), .Cin(1'b0), .A(1'b0), .E(square_controlled_adder_53_e_2),
    .B_2(square_controlled_adder_57_b_2), .Cout(square_controlled_adder_57_cout),
    .S(square_controlled_adder_57_s));  // open: E_2
  Square_Controlled_Adder square_controlled_adder_58 (
    .B(square_controlled_adder_53_e_2), .Cin(square_controlled_adder_61_cout),
    .A(square_controlled_adder_57_s), .E(square_controlled_adder_54_e_2),
    .B_2(square_controlled_adder_58_b_2), .Cout(square_controlled_adder_58_cout),
    .S(square_controlled_adder_58_s), .E_2(square_controlled_adder_58_e_2));
  Square_Controlled_Adder square_controlled_adder_59 (
    .B(square_controlled_adder_54_b_2), .Cin(square_controlled_adder_62_cout),
    .A(square_controlled_adder_58_s), .E(square_controlled_adder_55_e_2),
    .B_2(square_controlled_adder_59_b_2), .Cout(square_controlled_adder_59_cout),
    .S(square_controlled_adder_59_s), .E_2(square_controlled_adder_59_e_2));
  Square_Controlled_Adder square_controlled_adder_60 (
    .B(square_controlled_adder_55_b_2), .Cin(square_controlled_adder_63_cout),
    .A(square_controlled_adder_59_s), .E(square_controlled_adder_56_e_2),
    .Cout(square_controlled_adder_60_cout), .S(square_controlled_adder_72_s[6]),
    .E_2(square_controlled_adder_60_e_2));  // open: B_2
  Square_Controlled_Adder square_controlled_adder_61 (
    .B(square_controlled_adder_53_b_2), .Cin(square_controlled_adder_64_cout), .A(1'b0),
    .E(square_controlled_adder_58_e_2), .B_2(square_controlled_adder_61_b_2),
    .Cout(square_controlled_adder_61_cout), .S(square_controlled_adder_61_s),
    .E_2(square_controlled_adder_61_e_2));
  Square_Controlled_Adder square_controlled_adder_62 (
    .B(square_controlled_adder_58_b_2), .Cin(square_controlled_adder_65_cout),
    .A(square_controlled_adder_61_s), .E(square_controlled_adder_59_e_2),
    .B_2(square_controlled_adder_62_b_2), .Cout(square_controlled_adder_62_cout),
    .S(square_controlled_adder_62_s), .E_2(square_controlled_adder_62_e_2));
  Square_Controlled_Adder square_controlled_adder_63 (
    .B(square_controlled_adder_59_b_2), .Cin(square_controlled_adder_66_cout),
    .A(square_controlled_adder_62_s), .E(square_controlled_adder_60_e_2),
    .Cout(square_controlled_adder_63_cout), .S(square_controlled_adder_72_s[5]),
    .E_2(square_controlled_adder_63_e_2));  // open: B_2
  Square_Controlled_Adder square_controlled_adder_64 (
    .B(square_controlled_adder_57_b_2), .Cin(1'b0), .A(1'b0), .E(square_controlled_adder_61_e_2),
    .B_2(square_controlled_adder_64_b_2), .Cout(square_controlled_adder_64_cout),
    .S(square_controlled_adder_64_s));  // open: E_2
  Square_Controlled_Adder square_controlled_adder_65 (
    .B(square_controlled_adder_61_e_2), .Cin(square_controlled_adder_67_cout),
    .A(square_controlled_adder_64_s), .E(square_controlled_adder_62_e_2),
    .B_2(square_controlled_adder_65_b_2), .Cout(square_controlled_adder_65_cout),
    .S(square_controlled_adder_65_s), .E_2(square_controlled_adder_65_e_2));
  Square_Controlled_Adder square_controlled_adder_66 (
    .B(square_controlled_adder_62_b_2), .Cin(square_controlled_adder_68_cout),
    .A(square_controlled_adder_65_s), .E(square_controlled_adder_63_e_2),
    .Cout(square_controlled_adder_66_cout), .S(square_controlled_adder_72_s[4]),
    .E_2(square_controlled_adder_66_e_2));  // open: B_2
  Square_Controlled_Adder square_controlled_adder_67 (
    .B(square_controlled_adder_61_b_2), .Cin(square_controlled_adder_69_cout), .A(1'b0),
    .E(square_controlled_adder_65_e_2), .B_2(square_controlled_adder_67_b_2),
    .Cout(square_controlled_adder_67_cout), .S(square_controlled_adder_67_s),
    .E_2(square_controlled_adder_67_e_2));
  Square_Controlled_Adder square_controlled_adder_68 (
    .B(square_controlled_adder_65_b_2), .Cin(square_controlled_adder_70_cout),
    .A(square_controlled_adder_67_s), .E(square_controlled_adder_66_e_2),
    .Cout(square_controlled_adder_68_cout), .S(square_controlled_adder_72_s[3]),
    .E_2(square_controlled_adder_68_e_2));  // open: B_2
  Square_Controlled_Adder square_controlled_adder_69 (
    .B(square_controlled_adder_64_b_2), .Cin(1'b0), .A(1'b0), .E(square_controlled_adder_67_e_2),
    .B_2(square_controlled_adder_69_b_2), .Cout(square_controlled_adder_69_cout),
    .S(square_controlled_adder_69_s));  // open: E_2
  Square_Controlled_Adder square_controlled_adder_70 (
    .B(square_controlled_adder_67_e_2), .Cin(square_controlled_adder_71_cout),
    .A(square_controlled_adder_69_s), .E(square_controlled_adder_68_e_2),
    .Cout(square_controlled_adder_70_cout), .S(square_controlled_adder_72_s[2]),
    .E_2(square_controlled_adder_70_e_2));  // open: B_2
  _16_Buffer u_16_buffer_2 (.in_1(square_controlled_adder_72_s), .in_2(in_2), .out_3(out_3));
  Square_Controlled_Adder square_controlled_adder_71 (
    .B(square_controlled_adder_67_b_2), .Cin(square_controlled_adder_72_cout), .A(1'b0),
    .E(square_controlled_adder_70_e_2), .Cout(square_controlled_adder_71_cout),
    .S(square_controlled_adder_72_s[1]), .E_2(square_controlled_adder_71_e_2));  // open: B_2
  Square_Controlled_Adder square_controlled_adder_72 (
    .B(square_controlled_adder_69_b_2), .Cin(1'b0), .A(1'b0), .E(square_controlled_adder_71_e_2),
    .Cout(square_controlled_adder_72_cout), .S(square_controlled_adder_72_s[0]));  // open: B_2, E_2
endmodule

module _16_SQRT (
  input  [15:0] in_1,
  input  in_2,
  output [15:0] out_3
);

  wire controlled_root_adder_1_s, controlled_root_adder_2_s, controlled_root_adder_3_s,
       controlled_root_adder_4_s, controlled_root_adder_5_s, controlled_root_adder_6_s,
       controlled_root_adder_7_s, controlled_root_adder_9_cout, controlled_root_adder_9_s,
       controlled_root_adder_10_cout, controlled_root_adder_10_s, controlled_root_adder_11_cout,
       controlled_root_adder_11_s, controlled_root_adder_12_cout, controlled_root_adder_12_s,
       controlled_root_adder_13_cout, controlled_root_adder_13_s, controlled_root_adder_14_cout,
       controlled_root_adder_14_s, controlled_root_adder_15_cout, controlled_root_adder_15_s,
       controlled_root_adder_16_cout, controlled_root_adder_17_cout, controlled_root_adder_17_s,
       controlled_root_adder_18_cout, controlled_root_adder_18_s, controlled_root_adder_19_cout,
       controlled_root_adder_19_s, controlled_root_adder_20_cout, controlled_root_adder_20_s,
       controlled_root_adder_21_cout, controlled_root_adder_21_s, controlled_root_adder_22_cout,
       controlled_root_adder_22_s, controlled_root_adder_23_cout, controlled_root_adder_24_cout,
       controlled_root_adder_24_s, controlled_root_adder_25_cout, controlled_root_adder_25_s,
       controlled_root_adder_26_cout, controlled_root_adder_26_s, controlled_root_adder_27_cout,
       controlled_root_adder_27_s, controlled_root_adder_28_cout, controlled_root_adder_28_s,
       controlled_root_adder_29_cout, controlled_root_adder_29_s, controlled_root_adder_30_cout,
       controlled_root_adder_31_cout, controlled_root_adder_31_s, controlled_root_adder_32_cout,
       controlled_root_adder_32_s, controlled_root_adder_33_cout, controlled_root_adder_33_s,
       controlled_root_adder_34_cout, controlled_root_adder_34_s, controlled_root_adder_35_cout,
       controlled_root_adder_35_s, controlled_root_adder_36_cout, controlled_root_adder_37_cout,
       controlled_root_adder_37_s, controlled_root_adder_38_cout, controlled_root_adder_38_s,
       controlled_root_adder_39_cout, controlled_root_adder_39_s, controlled_root_adder_40_cout,
       controlled_root_adder_40_s, controlled_root_adder_41_cout, controlled_root_adder_41_s,
       controlled_root_adder_42_cout, controlled_root_adder_43_cout, controlled_root_adder_43_s,
       controlled_root_adder_44_cout, controlled_root_adder_44_s, controlled_root_adder_45_cout,
       controlled_root_adder_45_s, controlled_root_adder_46_cout, controlled_root_adder_46_s,
       controlled_root_adder_47_cout, controlled_root_adder_48_cout, controlled_root_adder_48_s,
       controlled_root_adder_49_cout, controlled_root_adder_49_s, controlled_root_adder_50_cout,
       controlled_root_adder_50_s, controlled_root_adder_51_cout, controlled_root_adder_51_s,
       controlled_root_adder_52_cout, controlled_root_adder_53_cout, controlled_root_adder_53_s,
       controlled_root_adder_54_cout, controlled_root_adder_54_s, controlled_root_adder_55_cout,
       controlled_root_adder_55_s, controlled_root_adder_56_cout, controlled_root_adder_57_cout,
       controlled_root_adder_57_s, controlled_root_adder_58_cout, controlled_root_adder_58_s,
       controlled_root_adder_59_cout, controlled_root_adder_59_s, controlled_root_adder_60_cout,
       controlled_root_adder_61_cout, controlled_root_adder_61_s, controlled_root_adder_62_cout,
       controlled_root_adder_62_s, controlled_root_adder_63_cout, controlled_root_adder_64_cout,
       controlled_root_adder_64_s, controlled_root_adder_65_cout, controlled_root_adder_65_s,
       controlled_root_adder_66_cout, controlled_root_adder_67_cout, controlled_root_adder_67_s,
       controlled_root_adder_68_cout, controlled_root_adder_69_cout, controlled_root_adder_69_s,
       controlled_root_adder_70_cout, controlled_root_adder_71_cout, controlled_root_adder_72_cout,
       not_1_out, not_2_out, not_3_out, not_4_out, not_5_out, not_6_out, not_7_out;
  wire [7:0] controlled_root_adder_8_cout;
  wire [15:0] n16_buffer_1_out_3;

  _16_Buffer u_16_buffer_1 (.in_1(in_1), .in_2(in_2), .out_3(n16_buffer_1_out_3));
  Controlled_Root_Adder controlled_root_adder_1 (
    .A(n16_buffer_1_out_3[15]), .B(1'b0), .Pin(1'b1), .Cin(controlled_root_adder_9_cout),
    .S(controlled_root_adder_1_s), .Cout(controlled_root_adder_8_cout[7]));
  Controlled_Root_Adder controlled_root_adder_2 (
    .A(controlled_root_adder_1_s), .B(1'b0), .Pin(controlled_root_adder_8_cout[7]),
    .Cin(controlled_root_adder_10_cout), .S(controlled_root_adder_2_s), .Cout(controlled_root_adder_8_cout[6]));
  Controlled_Root_Adder controlled_root_adder_3 (
    .A(controlled_root_adder_2_s), .B(1'b0), .Pin(controlled_root_adder_8_cout[6]),
    .Cin(controlled_root_adder_11_cout), .S(controlled_root_adder_3_s), .Cout(controlled_root_adder_8_cout[5]));
  Controlled_Root_Adder controlled_root_adder_4 (
    .A(controlled_root_adder_3_s), .B(1'b0), .Pin(controlled_root_adder_8_cout[5]),
    .Cin(controlled_root_adder_12_cout), .S(controlled_root_adder_4_s), .Cout(controlled_root_adder_8_cout[4]));
  Controlled_Root_Adder controlled_root_adder_5 (
    .A(controlled_root_adder_4_s), .B(1'b0), .Pin(controlled_root_adder_8_cout[4]),
    .Cin(controlled_root_adder_13_cout), .S(controlled_root_adder_5_s), .Cout(controlled_root_adder_8_cout[3]));
  Controlled_Root_Adder controlled_root_adder_6 (
    .A(controlled_root_adder_5_s), .B(1'b0), .Pin(controlled_root_adder_8_cout[3]),
    .Cin(controlled_root_adder_14_cout), .S(controlled_root_adder_6_s), .Cout(controlled_root_adder_8_cout[2]));
  Controlled_Root_Adder controlled_root_adder_7 (
    .A(controlled_root_adder_6_s), .B(1'b0), .Pin(controlled_root_adder_8_cout[2]),
    .Cin(controlled_root_adder_15_cout), .S(controlled_root_adder_7_s), .Cout(controlled_root_adder_8_cout[1]));
  Controlled_Root_Adder controlled_root_adder_8 (
    .A(controlled_root_adder_7_s), .B(1'b0), .Pin(controlled_root_adder_8_cout[1]),
    .Cin(controlled_root_adder_16_cout), .Cout(controlled_root_adder_8_cout[0]));  // open: S
  Controlled_Root_Adder controlled_root_adder_9 (
    .A(n16_buffer_1_out_3[14]), .B(1'b1), .Pin(1'b1), .Cin(1'b1), .S(controlled_root_adder_9_s),
    .Cout(controlled_root_adder_9_cout));
  not not_1 (not_1_out, controlled_root_adder_8_cout[7]);
  Controlled_Root_Adder controlled_root_adder_10 (
    .A(controlled_root_adder_9_s), .B(controlled_root_adder_8_cout[7]),
    .Pin(controlled_root_adder_8_cout[7]), .Cin(controlled_root_adder_17_cout),
    .S(controlled_root_adder_10_s), .Cout(controlled_root_adder_10_cout));
  Controlled_Root_Adder controlled_root_adder_11 (
    .A(controlled_root_adder_10_s), .B(1'b0), .Pin(controlled_root_adder_8_cout[6]),
    .Cin(controlled_root_adder_18_cout), .S(controlled_root_adder_11_s), .Cout(controlled_root_adder_11_cout));
  Controlled_Root_Adder controlled_root_adder_12 (
    .A(controlled_root_adder_11_s), .B(1'b0), .Pin(controlled_root_adder_8_cout[5]),
    .Cin(controlled_root_adder_19_cout), .S(controlled_root_adder_12_s), .Cout(controlled_root_adder_12_cout));
  Controlled_Root_Adder controlled_root_adder_13 (
    .A(controlled_root_adder_12_s), .B(1'b0), .Pin(controlled_root_adder_8_cout[4]),
    .Cin(controlled_root_adder_20_cout), .S(controlled_root_adder_13_s), .Cout(controlled_root_adder_13_cout));
  Controlled_Root_Adder controlled_root_adder_14 (
    .A(controlled_root_adder_13_s), .B(1'b0), .Pin(controlled_root_adder_8_cout[3]),
    .Cin(controlled_root_adder_21_cout), .S(controlled_root_adder_14_s), .Cout(controlled_root_adder_14_cout));
  Controlled_Root_Adder controlled_root_adder_15 (
    .A(controlled_root_adder_14_s), .B(1'b0), .Pin(controlled_root_adder_8_cout[2]),
    .Cin(controlled_root_adder_22_cout), .S(controlled_root_adder_15_s), .Cout(controlled_root_adder_15_cout));
  Controlled_Root_Adder controlled_root_adder_16 (
    .A(controlled_root_adder_15_s), .B(1'b0), .Pin(controlled_root_adder_8_cout[1]),
    .Cin(controlled_root_adder_23_cout), .Cout(controlled_root_adder_16_cout));  // open: S
  _16_Buffer u_16_buffer_2 (.in_1({{8{1'b0}}, controlled_root_adder_8_cout}), .in_2(in_2), .out_3(out_3));
  Controlled_Root_Adder controlled_root_adder_17 (
    .A(n16_buffer_1_out_3[13]), .B(not_1_out), .Pin(controlled_root_adder_8_cout[7]),
    .Cin(controlled_root_adder_24_cout), .S(controlled_root_adder_17_s), .Cout(controlled_root_adder_17_cout));
  Controlled_Root_Adder controlled_root_adder_18 (
    .A(controlled_root_adder_17_s), .B(controlled_root_adder_8_cout[7]),
    .Pin(controlled_root_adder_8_cout[6]), .Cin(controlled_root_adder_25_cout),
    .S(controlled_root_adder_18_s), .Cout(controlled_root_adder_18_cout));
  Controlled_Root_Adder controlled_root_adder_19 (
    .A(controlled_root_adder_18_s), .B(1'b0), .Pin(controlled_root_adder_8_cout[5]),
    .Cin(controlled_root_adder_26_cout), .S(controlled_root_adder_19_s), .Cout(controlled_root_adder_19_cout));
  Controlled_Root_Adder controlled_root_adder_20 (
    .A(controlled_root_adder_19_s), .B(1'b0), .Pin(controlled_root_adder_8_cout[4]),
    .Cin(controlled_root_adder_27_cout), .S(controlled_root_adder_20_s), .Cout(controlled_root_adder_20_cout));
  Controlled_Root_Adder controlled_root_adder_21 (
    .A(controlled_root_adder_20_s), .B(1'b0), .Pin(controlled_root_adder_8_cout[3]),
    .Cin(controlled_root_adder_28_cout), .S(controlled_root_adder_21_s), .Cout(controlled_root_adder_21_cout));
  Controlled_Root_Adder controlled_root_adder_22 (
    .A(controlled_root_adder_21_s), .B(1'b0), .Pin(controlled_root_adder_8_cout[2]),
    .Cin(controlled_root_adder_29_cout), .S(controlled_root_adder_22_s), .Cout(controlled_root_adder_22_cout));
  Controlled_Root_Adder controlled_root_adder_23 (
    .A(controlled_root_adder_22_s), .B(1'b0), .Pin(controlled_root_adder_8_cout[1]),
    .Cin(controlled_root_adder_30_cout), .Cout(controlled_root_adder_23_cout));  // open: S
  Controlled_Root_Adder controlled_root_adder_24 (
    .A(n16_buffer_1_out_3[12]), .B(1'b1), .Pin(controlled_root_adder_8_cout[7]),
    .Cin(controlled_root_adder_8_cout[7]), .S(controlled_root_adder_24_s),
    .Cout(controlled_root_adder_24_cout));
  Controlled_Root_Adder controlled_root_adder_25 (
    .A(controlled_root_adder_24_s), .B(controlled_root_adder_8_cout[6]),
    .Pin(controlled_root_adder_8_cout[6]), .Cin(controlled_root_adder_31_cout),
    .S(controlled_root_adder_25_s), .Cout(controlled_root_adder_25_cout));
  Controlled_Root_Adder controlled_root_adder_26 (
    .A(controlled_root_adder_25_s), .B(controlled_root_adder_8_cout[7]),
    .Pin(controlled_root_adder_8_cout[5]), .Cin(controlled_root_adder_32_cout),
    .S(controlled_root_adder_26_s), .Cout(controlled_root_adder_26_cout));
  Controlled_Root_Adder controlled_root_adder_27 (
    .A(controlled_root_adder_26_s), .B(1'b0), .Pin(controlled_root_adder_8_cout[4]),
    .Cin(controlled_root_adder_33_cout), .S(controlled_root_adder_27_s), .Cout(controlled_root_adder_27_cout));
  Controlled_Root_Adder controlled_root_adder_28 (
    .A(controlled_root_adder_27_s), .B(1'b0), .Pin(controlled_root_adder_8_cout[3]),
    .Cin(controlled_root_adder_34_cout), .S(controlled_root_adder_28_s), .Cout(controlled_root_adder_28_cout));
  Controlled_Root_Adder controlled_root_adder_29 (
    .A(controlled_root_adder_28_s), .B(1'b0), .Pin(controlled_root_adder_8_cout[2]),
    .Cin(controlled_root_adder_35_cout), .S(controlled_root_adder_29_s), .Cout(controlled_root_adder_29_cout));
  Controlled_Root_Adder controlled_root_adder_30 (
    .A(controlled_root_adder_29_s), .B(1'b0), .Pin(controlled_root_adder_8_cout[1]),
    .Cin(controlled_root_adder_36_cout), .Cout(controlled_root_adder_30_cout));  // open: S
  not not_2 (not_2_out, controlled_root_adder_8_cout[6]);
  Controlled_Root_Adder controlled_root_adder_31 (
    .A(n16_buffer_1_out_3[11]), .B(not_2_out), .Pin(controlled_root_adder_8_cout[6]),
    .Cin(controlled_root_adder_37_cout), .S(controlled_root_adder_31_s), .Cout(controlled_root_adder_31_cout));
  Controlled_Root_Adder controlled_root_adder_32 (
    .A(controlled_root_adder_31_s), .B(controlled_root_adder_8_cout[6]),
    .Pin(controlled_root_adder_8_cout[5]), .Cin(controlled_root_adder_38_cout),
    .S(controlled_root_adder_32_s), .Cout(controlled_root_adder_32_cout));
  Controlled_Root_Adder controlled_root_adder_33 (
    .A(controlled_root_adder_32_s), .B(controlled_root_adder_8_cout[7]),
    .Pin(controlled_root_adder_8_cout[4]), .Cin(controlled_root_adder_39_cout),
    .S(controlled_root_adder_33_s), .Cout(controlled_root_adder_33_cout));
  Controlled_Root_Adder controlled_root_adder_34 (
    .A(controlled_root_adder_33_s), .B(1'b0), .Pin(controlled_root_adder_8_cout[3]),
    .Cin(controlled_root_adder_40_cout), .S(controlled_root_adder_34_s), .Cout(controlled_root_adder_34_cout));
  Controlled_Root_Adder controlled_root_adder_35 (
    .A(controlled_root_adder_34_s), .B(1'b0), .Pin(controlled_root_adder_8_cout[2]),
    .Cin(controlled_root_adder_41_cout), .S(controlled_root_adder_35_s), .Cout(controlled_root_adder_35_cout));
  Controlled_Root_Adder controlled_root_adder_36 (
    .A(controlled_root_adder_35_s), .B(1'b0), .Pin(controlled_root_adder_8_cout[1]),
    .Cin(controlled_root_adder_42_cout), .Cout(controlled_root_adder_36_cout));  // open: S
  Controlled_Root_Adder controlled_root_adder_37 (
    .A(n16_buffer_1_out_3[10]), .B(1'b1), .Pin(controlled_root_adder_8_cout[6]),
    .Cin(controlled_root_adder_8_cout[6]), .S(controlled_root_adder_37_s),
    .Cout(controlled_root_adder_37_cout));
  not not_3 (not_3_out, controlled_root_adder_8_cout[5]);
  Controlled_Root_Adder controlled_root_adder_38 (
    .A(controlled_root_adder_37_s), .B(controlled_root_adder_8_cout[5]),
    .Pin(controlled_root_adder_8_cout[5]), .Cin(controlled_root_adder_43_cout),
    .S(controlled_root_adder_38_s), .Cout(controlled_root_adder_38_cout));
  Controlled_Root_Adder controlled_root_adder_39 (
    .A(controlled_root_adder_38_s), .B(controlled_root_adder_8_cout[6]),
    .Pin(controlled_root_adder_8_cout[4]), .Cin(controlled_root_adder_44_cout),
    .S(controlled_root_adder_39_s), .Cout(controlled_root_adder_39_cout));
  Controlled_Root_Adder controlled_root_adder_40 (
    .A(controlled_root_adder_39_s), .B(controlled_root_adder_8_cout[7]),
    .Pin(controlled_root_adder_8_cout[3]), .Cin(controlled_root_adder_45_cout),
    .S(controlled_root_adder_40_s), .Cout(controlled_root_adder_40_cout));
  Controlled_Root_Adder controlled_root_adder_41 (
    .A(controlled_root_adder_40_s), .B(1'b0), .Pin(controlled_root_adder_8_cout[2]),
    .Cin(controlled_root_adder_46_cout), .S(controlled_root_adder_41_s), .Cout(controlled_root_adder_41_cout));
  Controlled_Root_Adder controlled_root_adder_42 (
    .A(controlled_root_adder_41_s), .B(1'b0), .Pin(controlled_root_adder_8_cout[1]),
    .Cin(controlled_root_adder_47_cout), .Cout(controlled_root_adder_42_cout));  // open: S
  Controlled_Root_Adder controlled_root_adder_43 (
    .A(n16_buffer_1_out_3[9]), .B(not_3_out), .Pin(controlled_root_adder_8_cout[5]),
    .Cin(controlled_root_adder_48_cout), .S(controlled_root_adder_43_s), .Cout(controlled_root_adder_43_cout));
  Controlled_Root_Adder controlled_root_adder_44 (
    .A(controlled_root_adder_43_s), .B(controlled_root_adder_8_cout[5]),
    .Pin(controlled_root_adder_8_cout[4]), .Cin(controlled_root_adder_49_cout),
    .S(controlled_root_adder_44_s), .Cout(controlled_root_adder_44_cout));
  Controlled_Root_Adder controlled_root_adder_45 (
    .A(controlled_root_adder_44_s), .B(controlled_root_adder_8_cout[6]),
    .Pin(controlled_root_adder_8_cout[3]), .Cin(controlled_root_adder_50_cout),
    .S(controlled_root_adder_45_s), .Cout(controlled_root_adder_45_cout));
  Controlled_Root_Adder controlled_root_adder_46 (
    .A(controlled_root_adder_45_s), .B(controlled_root_adder_8_cout[7]),
    .Pin(controlled_root_adder_8_cout[2]), .Cin(controlled_root_adder_51_cout),
    .S(controlled_root_adder_46_s), .Cout(controlled_root_adder_46_cout));
  Controlled_Root_Adder controlled_root_adder_47 (
    .A(controlled_root_adder_46_s), .B(1'b0), .Pin(controlled_root_adder_8_cout[1]),
    .Cin(controlled_root_adder_52_cout), .Cout(controlled_root_adder_47_cout));  // open: S
  Controlled_Root_Adder controlled_root_adder_48 (
    .A(n16_buffer_1_out_3[8]), .B(1'b1), .Pin(controlled_root_adder_8_cout[5]),
    .Cin(controlled_root_adder_8_cout[5]), .S(controlled_root_adder_48_s),
    .Cout(controlled_root_adder_48_cout));
  Controlled_Root_Adder controlled_root_adder_49 (
    .A(controlled_root_adder_48_s), .B(controlled_root_adder_8_cout[4]),
    .Pin(controlled_root_adder_8_cout[4]), .Cin(controlled_root_adder_53_cout),
    .S(controlled_root_adder_49_s), .Cout(controlled_root_adder_49_cout));
  Controlled_Root_Adder controlled_root_adder_50 (
    .A(controlled_root_adder_49_s), .B(controlled_root_adder_8_cout[5]),
    .Pin(controlled_root_adder_8_cout[3]), .Cin(controlled_root_adder_54_cout),
    .S(controlled_root_adder_50_s), .Cout(controlled_root_adder_50_cout));
  Controlled_Root_Adder controlled_root_adder_51 (
    .A(controlled_root_adder_50_s), .B(controlled_root_adder_8_cout[6]),
    .Pin(controlled_root_adder_8_cout[2]), .Cin(controlled_root_adder_55_cout),
    .S(controlled_root_adder_51_s), .Cout(controlled_root_adder_51_cout));
  Controlled_Root_Adder controlled_root_adder_52 (
    .A(controlled_root_adder_51_s), .B(controlled_root_adder_8_cout[7]),
    .Pin(controlled_root_adder_8_cout[1]), .Cin(controlled_root_adder_56_cout),
    .Cout(controlled_root_adder_52_cout));  // open: S
  not not_4 (not_4_out, controlled_root_adder_8_cout[4]);
  Controlled_Root_Adder controlled_root_adder_53 (
    .A(n16_buffer_1_out_3[7]), .B(not_4_out), .Pin(controlled_root_adder_8_cout[4]),
    .Cin(controlled_root_adder_57_cout), .S(controlled_root_adder_53_s), .Cout(controlled_root_adder_53_cout));
  Controlled_Root_Adder controlled_root_adder_54 (
    .A(controlled_root_adder_53_s), .B(controlled_root_adder_8_cout[4]),
    .Pin(controlled_root_adder_8_cout[3]), .Cin(controlled_root_adder_58_cout),
    .S(controlled_root_adder_54_s), .Cout(controlled_root_adder_54_cout));
  Controlled_Root_Adder controlled_root_adder_55 (
    .A(controlled_root_adder_54_s), .B(controlled_root_adder_8_cout[5]),
    .Pin(controlled_root_adder_8_cout[2]), .Cin(controlled_root_adder_59_cout),
    .S(controlled_root_adder_55_s), .Cout(controlled_root_adder_55_cout));
  Controlled_Root_Adder controlled_root_adder_56 (
    .A(controlled_root_adder_55_s), .B(controlled_root_adder_8_cout[6]),
    .Pin(controlled_root_adder_8_cout[1]), .Cin(controlled_root_adder_60_cout),
    .Cout(controlled_root_adder_56_cout));  // open: S
  Controlled_Root_Adder controlled_root_adder_57 (
    .A(n16_buffer_1_out_3[6]), .B(1'b1), .Pin(controlled_root_adder_8_cout[4]),
    .Cin(controlled_root_adder_8_cout[4]), .S(controlled_root_adder_57_s),
    .Cout(controlled_root_adder_57_cout));
  not not_5 (not_5_out, controlled_root_adder_8_cout[3]);
  Controlled_Root_Adder controlled_root_adder_58 (
    .A(controlled_root_adder_57_s), .B(controlled_root_adder_8_cout[3]),
    .Pin(controlled_root_adder_8_cout[3]), .Cin(controlled_root_adder_61_cout),
    .S(controlled_root_adder_58_s), .Cout(controlled_root_adder_58_cout));
  Controlled_Root_Adder controlled_root_adder_59 (
    .A(controlled_root_adder_58_s), .B(controlled_root_adder_8_cout[4]),
    .Pin(controlled_root_adder_8_cout[2]), .Cin(controlled_root_adder_62_cout),
    .S(controlled_root_adder_59_s), .Cout(controlled_root_adder_59_cout));
  Controlled_Root_Adder controlled_root_adder_60 (
    .A(controlled_root_adder_59_s), .B(controlled_root_adder_8_cout[5]),
    .Pin(controlled_root_adder_8_cout[1]), .Cin(controlled_root_adder_63_cout),
    .Cout(controlled_root_adder_60_cout));  // open: S
  Controlled_Root_Adder controlled_root_adder_61 (
    .A(n16_buffer_1_out_3[5]), .B(not_5_out), .Pin(controlled_root_adder_8_cout[3]),
    .Cin(controlled_root_adder_64_cout), .S(controlled_root_adder_61_s), .Cout(controlled_root_adder_61_cout));
  Controlled_Root_Adder controlled_root_adder_62 (
    .A(controlled_root_adder_61_s), .B(controlled_root_adder_8_cout[3]),
    .Pin(controlled_root_adder_8_cout[2]), .Cin(controlled_root_adder_65_cout),
    .S(controlled_root_adder_62_s), .Cout(controlled_root_adder_62_cout));
  Controlled_Root_Adder controlled_root_adder_63 (
    .A(controlled_root_adder_62_s), .B(controlled_root_adder_8_cout[4]),
    .Pin(controlled_root_adder_8_cout[1]), .Cin(controlled_root_adder_66_cout),
    .Cout(controlled_root_adder_63_cout));  // open: S
  Controlled_Root_Adder controlled_root_adder_64 (
    .A(n16_buffer_1_out_3[4]), .B(1'b1), .Pin(controlled_root_adder_8_cout[3]),
    .Cin(controlled_root_adder_8_cout[3]), .S(controlled_root_adder_64_s),
    .Cout(controlled_root_adder_64_cout));
  Controlled_Root_Adder controlled_root_adder_65 (
    .A(controlled_root_adder_64_s), .B(controlled_root_adder_8_cout[2]),
    .Pin(controlled_root_adder_8_cout[2]), .Cin(controlled_root_adder_67_cout),
    .S(controlled_root_adder_65_s), .Cout(controlled_root_adder_65_cout));
  Controlled_Root_Adder controlled_root_adder_66 (
    .A(controlled_root_adder_65_s), .B(controlled_root_adder_8_cout[3]),
    .Pin(controlled_root_adder_8_cout[1]), .Cin(controlled_root_adder_68_cout),
    .Cout(controlled_root_adder_66_cout));  // open: S
  not not_6 (not_6_out, controlled_root_adder_8_cout[2]);
  Controlled_Root_Adder controlled_root_adder_67 (
    .A(n16_buffer_1_out_3[3]), .B(not_6_out), .Pin(controlled_root_adder_8_cout[2]),
    .Cin(controlled_root_adder_69_cout), .S(controlled_root_adder_67_s), .Cout(controlled_root_adder_67_cout));
  Controlled_Root_Adder controlled_root_adder_68 (
    .A(controlled_root_adder_67_s), .B(controlled_root_adder_8_cout[2]),
    .Pin(controlled_root_adder_8_cout[1]), .Cin(controlled_root_adder_70_cout),
    .Cout(controlled_root_adder_68_cout));  // open: S
  Controlled_Root_Adder controlled_root_adder_69 (
    .A(n16_buffer_1_out_3[2]), .B(1'b1), .Pin(controlled_root_adder_8_cout[2]),
    .Cin(controlled_root_adder_8_cout[2]), .S(controlled_root_adder_69_s),
    .Cout(controlled_root_adder_69_cout));
  not not_7 (not_7_out, controlled_root_adder_8_cout[1]);
  Controlled_Root_Adder controlled_root_adder_70 (
    .A(controlled_root_adder_69_s), .B(controlled_root_adder_8_cout[1]),
    .Pin(controlled_root_adder_8_cout[1]), .Cin(controlled_root_adder_71_cout),
    .Cout(controlled_root_adder_70_cout));  // open: S
  Controlled_Root_Adder controlled_root_adder_71 (
    .A(n16_buffer_1_out_3[1]), .B(not_7_out), .Pin(controlled_root_adder_8_cout[1]),
    .Cin(controlled_root_adder_72_cout), .Cout(controlled_root_adder_71_cout));  // open: S
  Controlled_Root_Adder controlled_root_adder_72 (
    .A(n16_buffer_1_out_3[0]), .B(1'b1), .Pin(controlled_root_adder_8_cout[1]),
    .Cin(controlled_root_adder_8_cout[1]), .Cout(controlled_root_adder_72_cout));  // open: S
endmodule

module _16_Rand (
  input  in_1,
  output [15:0] out_2
);

  wire and_1_out, and_2_out, and_3_out, and_4_out, and_5_out, and_6_out, and_7_out, and_8_out, and_9_out,
       and_10_out, and_11_out, and_12_out, and_13_out, and_14_out, and_15_out, and_16_out, buffer_1_out,
       buffer_2_out, buffer_3_out, clock_1_out, clock_2_out, clock_3_out, clock_4_out, clock_5_out,
       clock_6_out, clock_7_out, clock_8_out, clock_9_out, clock_10_out, clock_11_out, clock_12_out,
       clock_13_out, clock_14_out, clock_15_out, clock_16_out, not_1_out, t_ff_1_q, t_ff_2_q, t_ff_3_q,
       t_ff_4_q, t_ff_5_q, t_ff_6_q, t_ff_7_q, t_ff_8_q, t_ff_9_q, t_ff_10_q, t_ff_11_q, t_ff_12_q,
       t_ff_13_q, t_ff_14_q, t_ff_15_q, t_ff_16_q, xor_1_out;

  buf buffer_1 (buffer_1_out, in_1);
  buf buffer_2 (buffer_2_out, buffer_3_out);
  buf buffer_3 (buffer_3_out, buffer_1_out);
  xor xor_1 (xor_1_out, buffer_2_out, in_1);
  Clock #(.lowDuration(17)) clock_1 (.out(clock_1_out));
  T_Flip_Flop t_ff_1 (.clk(clock_1_out), .T(clock_1_out), .Q(t_ff_1_q));  // open: Qn, preset, reset, en
  Clock #(.lowDuration(2)) clock_2 (.out(clock_2_out));
  T_Flip_Flop t_ff_2 (.clk(clock_2_out), .T(clock_2_out), .Q(t_ff_2_q));  // open: Qn, preset, reset, en
  T_Flip_Flop t_ff_3 (.clk(clock_3_out), .T(clock_3_out), .Q(t_ff_3_q));  // open: Qn, preset, reset, en
  Clock #(.lowDuration(16)) clock_3 (.out(clock_3_out));
  Clock #(.lowDuration(15)) clock_4 (.out(clock_4_out));
  T_Flip_Flop t_ff_4 (.clk(clock_4_out), .T(clock_4_out), .Q(t_ff_4_q));  // open: Qn, preset, reset, en
  T_Flip_Flop t_ff_5 (.clk(clock_5_out), .T(clock_5_out), .Q(t_ff_5_q));  // open: Qn, preset, reset, en
  Clock #(.lowDuration(14)) clock_5 (.out(clock_5_out));
  Clock #(.lowDuration(13)) clock_6 (.out(clock_6_out));
  T_Flip_Flop t_ff_6 (.clk(clock_6_out), .T(clock_6_out), .Q(t_ff_6_q));  // open: Qn, preset, reset, en
  T_Flip_Flop t_ff_7 (.clk(clock_7_out), .T(clock_7_out), .Q(t_ff_7_q));  // open: Qn, preset, reset, en
  Clock #(.lowDuration(12)) clock_7 (.out(clock_7_out));
  Clock #(.lowDuration(11)) clock_8 (.out(clock_8_out));
  T_Flip_Flop t_ff_8 (.clk(clock_8_out), .T(clock_8_out), .Q(t_ff_8_q));  // open: Qn, preset, reset, en
  T_Flip_Flop t_ff_9 (.clk(clock_9_out), .T(clock_9_out), .Q(t_ff_9_q));  // open: Qn, preset, reset, en
  Clock #(.lowDuration(10)) clock_9 (.out(clock_9_out));
  T_Flip_Flop t_ff_10 (.clk(clock_10_out), .T(clock_10_out), .Q(t_ff_10_q));  // open: Qn, preset, reset, en
  Clock #(.lowDuration(9)) clock_10 (.out(clock_10_out));
  T_Flip_Flop t_ff_11 (.clk(clock_11_out), .T(clock_11_out), .Q(t_ff_11_q));  // open: Qn, preset, reset, en
  Clock #(.lowDuration(8)) clock_11 (.out(clock_11_out));
  T_Flip_Flop t_ff_12 (.clk(clock_12_out), .T(clock_12_out), .Q(t_ff_12_q));  // open: Qn, preset, reset, en
  Clock #(.lowDuration(7)) clock_12 (.out(clock_12_out));
  Clock #(.lowDuration(6)) clock_13 (.out(clock_13_out));
  T_Flip_Flop t_ff_13 (.clk(clock_13_out), .T(clock_13_out), .Q(t_ff_13_q));  // open: Qn, preset, reset, en
  T_Flip_Flop t_ff_14 (.clk(clock_14_out), .T(clock_14_out), .Q(t_ff_14_q));  // open: Qn, preset, reset, en
  Clock #(.lowDuration(5)) clock_14 (.out(clock_14_out));
  Clock #(.lowDuration(4)) clock_15 (.out(clock_15_out));
  T_Flip_Flop t_ff_15 (.clk(clock_15_out), .T(clock_15_out), .Q(t_ff_15_q));  // open: Qn, preset, reset, en
  Clock #(.lowDuration(3)) clock_16 (.out(clock_16_out));
  T_Flip_Flop t_ff_16 (.clk(clock_16_out), .T(clock_16_out), .Q(t_ff_16_q));  // open: Qn, preset, reset, en
  and and_1 (and_1_out, xor_1_out, t_ff_1_q);
  and and_2 (and_2_out, xor_1_out, t_ff_2_q);
  and and_3 (and_3_out, xor_1_out, t_ff_3_q);
  and and_4 (and_4_out, xor_1_out, t_ff_4_q);
  and and_5 (and_5_out, xor_1_out, t_ff_5_q);
  and and_6 (and_6_out, xor_1_out, t_ff_6_q);
  and and_7 (and_7_out, xor_1_out, t_ff_7_q);
  and and_8 (and_8_out, xor_1_out, t_ff_8_q);
  and and_9 (and_9_out, xor_1_out, t_ff_9_q);
  and and_10 (and_10_out, xor_1_out, t_ff_10_q);
  and and_11 (and_11_out, xor_1_out, t_ff_11_q);
  and and_12 (and_12_out, xor_1_out, t_ff_12_q);
  and and_13 (and_13_out, xor_1_out, t_ff_13_q);
  and and_14 (and_14_out, xor_1_out, t_ff_14_q);
  and and_15 (and_15_out, xor_1_out, t_ff_15_q);
  and and_16 (and_16_out, xor_1_out, t_ff_16_q);
  not not_1 (not_1_out, in_1);
  RS_NOR rs_nor_1 (.in_1(and_1_out), .in_2(not_1_out), .out_3(out_2[0]));
  RS_NOR rs_nor_2 (.in_1(and_2_out), .in_2(not_1_out), .out_3(out_2[1]));
  RS_NOR rs_nor_3 (.in_1(and_3_out), .in_2(not_1_out), .out_3(out_2[2]));
  RS_NOR rs_nor_4 (.in_1(and_4_out), .in_2(not_1_out), .out_3(out_2[3]));
  RS_NOR rs_nor_5 (.in_1(and_5_out), .in_2(not_1_out), .out_3(out_2[4]));
  RS_NOR rs_nor_6 (.in_1(and_6_out), .in_2(not_1_out), .out_3(out_2[5]));
  RS_NOR rs_nor_7 (.in_1(and_7_out), .in_2(not_1_out), .out_3(out_2[6]));
  RS_NOR rs_nor_8 (.in_1(and_8_out), .in_2(not_1_out), .out_3(out_2[7]));
  RS_NOR rs_nor_9 (.in_1(and_9_out), .in_2(not_1_out), .out_3(out_2[8]));
  RS_NOR rs_nor_10 (.in_1(and_10_out), .in_2(not_1_out), .out_3(out_2[9]));
  RS_NOR rs_nor_11 (.in_1(and_11_out), .in_2(not_1_out), .out_3(out_2[10]));
  RS_NOR rs_nor_12 (.in_1(and_12_out), .in_2(not_1_out), .out_3(out_2[11]));
  RS_NOR rs_nor_13 (.in_1(and_13_out), .in_2(not_1_out), .out_3(out_2[12]));
  RS_NOR rs_nor_14 (.in_1(and_14_out), .in_2(not_1_out), .out_3(out_2[13]));
  RS_NOR rs_nor_15 (.in_1(and_15_out), .in_2(not_1_out), .out_3(out_2[14]));
  RS_NOR rs_nor_16 (.in_1(and_16_out), .in_2(not_1_out), .out_3(out_2[15]));
  // Probe on out_2
endmodule

module Ripple_Carry_Adder (
  input  in_1,
  input  in_2,
  input  in_3,
  output out_4,
  output out_5
);

  wire and_1_out, and_2_out, xor_1_out;

  and and_1 (and_1_out, in_2, in_3);
  or or_1 (out_5, and_1_out, and_2_out);
  xor xor_1 (xor_1_out, in_2, in_3);
  and and_2 (and_2_out, xor_1_out, in_1);
  xor xor_2 (out_4, xor_1_out, in_1);
endmodule

module Carry_Lookahead_Adder (
  input  in_1,
  input  in_2,
  input  in_3,
  output out_4,
  output out_5,
  output out_6
);

  wire xor_1_out;

  xor xor_1 (xor_1_out, in_1, in_2);
  xor xor_2 (out_4, xor_1_out, in_3);
  and and_1 (out_5, in_2, in_3);
  or or_1 (out_6, in_2, in_3);
endmodule

module Lookahead_Unit (
  input  in_1,
  input  in_2,
  input  in_3,
  input  in_4,
  input  in_5,
  output out_6,
  output out_7,
  output out_8,
  output out_9
);

  wire and_1_out, and_3_out, nor_1_out, nor_2_out;

  and and_1 (and_1_out, in_1, in_3);
  nor nor_1 (nor_1_out, and_1_out, in_2);
  and and_2 (out_8, in_1, in_4);
  and and_3 (and_3_out, in_4, in_2);
  not not_1 (out_6, nor_1_out);
  not not_2 (out_9, nor_2_out);
  nor nor_2 (nor_2_out, and_3_out, in_5);

  assign out_7 = in_3;
endmodule

module Square_Controlled_Adder (
  input  B,
  input  Cin,
  input  A,
  input  E,
  output B_2,
  output Cout,
  output S,
  output E_2
);

  wire and_1_out, and_2_out, nand_1_out, nand_2_out, nand_3_out, not_1_out, not_2_out, xor_1_out, xor_2_out;

  nand nand_1 (nand_1_out, B, Cin);
  nand nand_2 (nand_2_out, B, A);
  nand nand_3 (nand_3_out, A, Cin);
  xor xor_1 (xor_1_out, B, Cin);
  nand nand_4 (Cout, nand_1_out, nand_2_out, nand_3_out);
  not not_1 (not_1_out, E);
  xor xor_2 (xor_2_out, xor_1_out, A);
  not not_2 (not_2_out, not_1_out);
  and and_1 (and_1_out, not_2_out, xor_2_out);
  or or_1 (S, and_1_out, and_2_out);
  and and_2 (and_2_out, not_1_out, A);

  assign B_2 = B;
  assign E_2 = E;
endmodule

module Controlled_Root_Adder (
  input  A,
  input  B,
  input  Pin,
  input  Cin,
  output S,
  output Cout
);

  wire and_1_out, and_2_out, or_1_out, xor_1_out, xor_2_out;

  xor xor_1 (xor_1_out, A, Cin);
  xor xor_2 (xor_2_out, B, Pin);
  or or_1 (or_1_out, A, Cin);
  and and_1 (and_1_out, A, Cin);
  xor xor_3 (S, xor_1_out, xor_2_out);
  and and_2 (and_2_out, xor_2_out, or_1_out);
  or or_2 (Cout, and_2_out, and_1_out);
endmodule

module Half_Adder (
  input  in_1,
  input  in_2,
  output out_3,
  output out_4
);

  and and_1 (out_4, in_1, in_2);
  xor xor_1 (out_3, in_1, in_2);
endmodule
module _16_Buffer (
  input  [15:0] in_1,
  input  in_2,
  output [15:0] out_3
);

  and and_1 (out_3[0], in_1[0], in_2);
  and and_2 (out_3[1], in_1[1], in_2);
  and and_3 (out_3[2], in_1[2], in_2);
  and and_4 (out_3[3], in_1[3], in_2);
  and and_5 (out_3[4], in_1[4], in_2);
  and and_6 (out_3[5], in_1[5], in_2);
  and and_7 (out_3[6], in_1[6], in_2);
  and and_8 (out_3[7], in_1[7], in_2);
  and and_9 (out_3[8], in_1[8], in_2);
  and and_10 (out_3[9], in_1[9], in_2);
  and and_11 (out_3[10], in_1[10], in_2);
  and and_12 (out_3[11], in_1[11], in_2);
  and and_13 (out_3[12], in_1[12], in_2);
  and and_14 (out_3[13], in_1[13], in_2);
  and and_15 (out_3[14], in_1[14], in_2);
  and and_16 (out_3[15], in_1[15], in_2);
endmodule

module RS_NOR (
  input  in_1,
  input  in_2,
  output out_3
);

  wire nor_1_out;

  nor nor_1 (nor_1_out, in_1, out_3);
  nor nor_2 (out_3, nor_1_out, in_2);
endmodule

module _5T_Edge_Trigger (
  input  in_1,
  output out_2
);

  wire not_1_out, not_2_out, not_3_out, not_4_out, not_5_out;

  not not_1 (not_1_out, not_3_out);
  not not_2 (not_2_out, not_1_out);
  not not_3 (not_3_out, in_1);
  not not_4 (not_4_out, not_2_out);
  not not_5 (not_5_out, not_4_out);
  and and_1 (out_2, not_5_out, in_1);
endmodule

module _1Byte_RSNor (
  input  [7:0] in_1,
  input  in_2,
  input  in_3,
  output [7:0] out_4
);

  wire [7:0] n8_buf_1_out_3;

  _8_BUF u_8_buf_1 (.in_2(in_2), .in_1(in_1), .out_3(n8_buf_1_out_3));
  RS_NOR rs_nor_1 (.in_1(n8_buf_1_out_3[0]), .in_2(in_3), .out_3(out_4[0]));
  RS_NOR rs_nor_2 (.in_1(n8_buf_1_out_3[1]), .in_2(in_3), .out_3(out_4[1]));
  RS_NOR rs_nor_3 (.in_1(n8_buf_1_out_3[2]), .in_2(in_3), .out_3(out_4[2]));
  RS_NOR rs_nor_4 (.in_1(n8_buf_1_out_3[3]), .in_2(in_3), .out_3(out_4[3]));
  RS_NOR rs_nor_5 (.in_1(n8_buf_1_out_3[4]), .in_2(in_3), .out_3(out_4[4]));
  RS_NOR rs_nor_6 (.in_1(n8_buf_1_out_3[5]), .in_2(in_3), .out_3(out_4[5]));
  RS_NOR rs_nor_7 (.in_1(n8_buf_1_out_3[6]), .in_2(in_3), .out_3(out_4[6]));
  RS_NOR rs_nor_8 (.in_1(n8_buf_1_out_3[7]), .in_2(in_3), .out_3(out_4[7]));
endmodule

module _2B_Register (
  input  [15:0] in_1,
  input  in_2,
  input  in_3,
  input  in_4,
  input  in_5,
  output out_6,
  output [15:0] out_7
);

  wire or_1_out;
  wire [15:0] register_1_q;

  Register #(.width(16)) register_1 (.D(in_1), .Q(register_1_q), .clk(in_2), .clr(or_1_out));  // open: en
  or or_1 (or_1_out, in_5, in_3);
  _16_Buffer u_16_buffer_1 (.in_1(register_1_q), .in_2(in_4), .out_3(out_7));

  assign out_6 = in_5;
endmodule

module _4_Decoder_Delay (
  input  in_1,
  input  in_2,
  input  in_3,
  input  in_4,
  output out_5,
  output out_6,
  output out_7,
  output out_8,
  output out_9
);

  wire buffer_2_out, buffer_3_out, buffer_4_out, buffer_5_out, buffer_6_out, buffer_7_out, buffer_8_out,
       buffer_9_out, buffer_10_out, or_1_out;

  buf buffer_1 (out_5, buffer_2_out);
  buf buffer_2 (buffer_2_out, buffer_3_out);
  buf buffer_3 (buffer_3_out, buffer_4_out);
  buf buffer_4 (buffer_4_out, buffer_5_out);
  buf buffer_5 (buffer_5_out, buffer_6_out);
  buf buffer_6 (buffer_6_out, buffer_7_out);
  buf buffer_7 (buffer_7_out, buffer_8_out);
  buf buffer_8 (buffer_8_out, buffer_9_out);
  buf buffer_9 (buffer_9_out, buffer_10_out);
  buf buffer_10 (buffer_10_out, or_1_out);
  or or_1 (or_1_out, in_1, in_2, in_3, in_4);

  assign out_6 = in_1;
  assign out_7 = in_2;
  assign out_8 = in_3;
  assign out_9 = in_4;
endmodule

module _4_Bin_Hex2 (
  input  in_1,
  input  in_2,
  input  in_3,
  input  in_4,
  output out_5,
  output out_6,
  output out_7,
  output out_8,
  output out_9,
  output out_10,
  output out_11,
  output out_12,
  output out_13,
  output out_14,
  output out_15,
  output out_16,
  output out_17,
  output out_18,
  output out_19,
  output out_20
);

  wire and_1_out, and_2_out, and_5_out, and_8_out, and_9_out, and_11_out, and_12_out, and_15_out, and_17_out,
       and_18_out, and_21_out, and_24_out, and_25_out, and_27_out, and_28_out, and_31_out, buffer_1_out,
       buffer_2_out, buffer_3_out, buffer_4_out, buffer_5_out, buffer_6_out, buffer_7_out, buffer_8_out,
       buffer_9_out, buffer_10_out, buffer_11_out, buffer_12_out, buffer_13_out, buffer_14_out,
       buffer_15_out, buffer_16_out, buffer_17_out, buffer_18_out, buffer_19_out, buffer_20_out,
       buffer_21_out, buffer_22_out, buffer_23_out, buffer_24_out, buffer_25_out, buffer_26_out,
       buffer_27_out, buffer_28_out, buffer_29_out, buffer_30_out, buffer_31_out, buffer_32_out,
       buffer_33_out, buffer_34_out, buffer_35_out, buffer_36_out, buffer_37_out, buffer_38_out,
       buffer_39_out, buffer_40_out, buffer_41_out, buffer_42_out, buffer_43_out, buffer_44_out,
       buffer_45_out, buffer_46_out, buffer_47_out, buffer_48_out, buffer_49_out, buffer_50_out,
       buffer_51_out, buffer_52_out, buffer_53_out, buffer_54_out, buffer_55_out, buffer_56_out,
       buffer_57_out, buffer_58_out, buffer_59_out, buffer_60_out, buffer_61_out, buffer_62_out,
       buffer_63_out, buffer_64_out, buffer_65_out, buffer_66_out, buffer_67_out, buffer_68_out,
       buffer_69_out, buffer_70_out, buffer_71_out, buffer_72_out, not_1_out, not_2_out, not_3_out,
       not_4_out, not_5_out, not_6_out, not_7_out, not_8_out, not_9_out, not_10_out, not_11_out, not_12_out,
       not_13_out, not_14_out, not_15_out, not_16_out, not_17_out, not_18_out, not_19_out, not_20_out,
       not_21_out, not_22_out, not_23_out, not_24_out, not_25_out, not_26_out, not_27_out, not_28_out,
       not_29_out, not_30_out, not_31_out, not_32_out, or_1_out;

  buf buffer_1 (buffer_1_out, or_1_out);
  buf buffer_2 (buffer_2_out, buffer_1_out);
  buf buffer_3 (buffer_3_out, buffer_2_out);
  buf buffer_4 (buffer_4_out, buffer_3_out);
  buf buffer_5 (buffer_5_out, buffer_4_out);
  buf buffer_6 (buffer_6_out, buffer_5_out);
  buf buffer_7 (buffer_7_out, buffer_6_out);
  buf buffer_8 (buffer_8_out, buffer_7_out);
  or or_1 (or_1_out, in_1, in_2, in_3, in_4);
  buf buffer_9 (buffer_9_out, not_4_out);
  not not_1 (not_1_out, in_3);
  not not_2 (not_2_out, in_3);
  not not_3 (not_3_out, in_2);
  not not_4 (not_4_out, in_1);
  not not_5 (not_5_out, in_2);
  not not_6 (not_6_out, in_4);
  buf buffer_10 (buffer_10_out, not_2_out);
  buf buffer_11 (buffer_11_out, not_5_out);
  buf buffer_12 (buffer_12_out, not_1_out);
  buf buffer_13 (buffer_13_out, not_6_out);
  buf buffer_14 (buffer_14_out, not_3_out);
  buf buffer_15 (buffer_15_out, in_1);
  and and_1 (and_1_out, buffer_15_out, buffer_11_out, buffer_10_out, buffer_19_out);
  and and_2 (and_2_out, buffer_9_out, buffer_14_out, buffer_12_out, buffer_13_out);
  and and_3 (out_5, buffer_8_out, and_2_out);
  and and_4 (out_6, buffer_8_out, and_1_out);
  not not_7 (not_7_out, in_1);
  not not_8 (not_8_out, in_4);
  not not_9 (not_9_out, in_4);
  not not_10 (not_10_out, in_3);
  buf buffer_16 (buffer_16_out, in_2);
  buf buffer_17 (buffer_17_out, not_9_out);
  buf buffer_18 (buffer_18_out, in_2);
  buf buffer_19 (buffer_19_out, not_8_out);
  buf buffer_20 (buffer_20_out, in_1);
  buf buffer_21 (buffer_21_out, not_10_out);
  buf buffer_22 (buffer_22_out, not_7_out);
  and and_5 (and_5_out, buffer_22_out, buffer_18_out, buffer_21_out, buffer_17_out);
  and and_6 (out_8, buffer_8_out, and_8_out);
  and and_7 (out_7, buffer_8_out, and_5_out);
  not not_11 (not_11_out, in_4);
  not not_12 (not_12_out, in_3);
  not not_13 (not_13_out, in_2);
  not not_14 (not_14_out, in_1);
  not not_15 (not_15_out, in_4);
  buf buffer_23 (buffer_23_out, not_13_out);
  buf buffer_24 (buffer_24_out, in_3);
  buf buffer_25 (buffer_25_out, not_11_out);
  buf buffer_26 (buffer_26_out, not_15_out);
  buf buffer_27 (buffer_27_out, not_14_out);
  buf buffer_28 (buffer_28_out, not_12_out);
  and and_8 (and_8_out, buffer_20_out, buffer_16_out, buffer_28_out, buffer_25_out);
  and and_9 (and_9_out, buffer_27_out, buffer_23_out, buffer_24_out, buffer_26_out);
  and and_10 (out_9, buffer_8_out, and_9_out);
  not not_16 (not_16_out, in_2);
  not not_17 (not_17_out, in_1);
  not not_18 (not_18_out, in_4);
  buf buffer_29 (buffer_29_out, not_16_out);
  buf buffer_30 (buffer_30_out, in_3);
  buf buffer_31 (buffer_31_out, not_17_out);
  buf buffer_32 (buffer_32_out, not_18_out);
  buf buffer_33 (buffer_33_out, in_1);
  buf buffer_34 (buffer_34_out, in_2);
  and and_11 (and_11_out, buffer_31_out, buffer_34_out, buffer_35_out, buffer_37_out);
  and and_12 (and_12_out, buffer_33_out, buffer_29_out, buffer_30_out, buffer_32_out);
  and and_13 (out_11, buffer_8_out, and_11_out);
  and and_14 (out_10, buffer_8_out, and_12_out);
  not not_19 (not_19_out, in_4);
  not not_20 (not_20_out, in_4);
  buf buffer_35 (buffer_35_out, in_3);
  buf buffer_36 (buffer_36_out, in_1);
  buf buffer_37 (buffer_37_out, not_20_out);
  buf buffer_38 (buffer_38_out, not_23_out);
  buf buffer_39 (buffer_39_out, in_2);
  buf buffer_40 (buffer_40_out, not_19_out);
  buf buffer_41 (buffer_41_out, in_3);
  and and_15 (and_15_out, buffer_36_out, buffer_39_out, buffer_41_out, buffer_40_out);
  and and_16 (out_12, buffer_8_out, and_15_out);
  not not_21 (not_21_out, in_3);
  not not_22 (not_22_out, in_2);
  not not_23 (not_23_out, in_1);
  not not_24 (not_24_out, in_3);
  not not_25 (not_25_out, in_2);
  buf buffer_42 (buffer_42_out, in_1);
  buf buffer_43 (buffer_43_out, not_24_out);
  buf buffer_44 (buffer_44_out, in_4);
  buf buffer_45 (buffer_45_out, not_25_out);
  buf buffer_46 (buffer_46_out, not_22_out);
  buf buffer_47 (buffer_47_out, not_21_out);
  and and_17 (and_17_out, buffer_38_out, buffer_46_out, buffer_47_out, buffer_44_out);
  and and_18 (and_18_out, buffer_42_out, buffer_45_out, buffer_43_out, buffer_53_out);
  and and_19 (out_13, buffer_8_out, and_17_out);
  and and_20 (out_14, buffer_8_out, and_18_out);
  not not_26 (not_26_out, in_1);
  not not_27 (not_27_out, in_3);
  buf buffer_48 (buffer_48_out, not_26_out);
  buf buffer_49 (buffer_49_out, in_2);
  buf buffer_50 (buffer_50_out, in_2);
  buf buffer_51 (buffer_51_out, in_1);
  buf buffer_52 (buffer_52_out, not_27_out);
  buf buffer_53 (buffer_53_out, in_4);
  buf buffer_54 (buffer_54_out, in_4);
  and and_21 (and_21_out, buffer_48_out, buffer_49_out, buffer_52_out, buffer_54_out);
  and and_22 (out_15, buffer_8_out, and_21_out);
  and and_23 (out_16, buffer_8_out, and_25_out);
  not not_28 (not_28_out, in_2);
  not not_29 (not_29_out, in_3);
  not not_30 (not_30_out, in_1);
  buf buffer_55 (buffer_55_out, not_28_out);
  buf buffer_56 (buffer_56_out, not_30_out);
  buf buffer_57 (buffer_57_out, in_3);
  buf buffer_58 (buffer_58_out, in_4);
  buf buffer_59 (buffer_59_out, in_4);
  buf buffer_60 (buffer_60_out, not_29_out);
  and and_24 (and_24_out, buffer_56_out, buffer_55_out, buffer_57_out, buffer_59_out);
  and and_25 (and_25_out, buffer_51_out, buffer_50_out, buffer_60_out, buffer_58_out);
  and and_26 (out_17, buffer_8_out, and_24_out);
  not not_31 (not_31_out, in_2);
  not not_32 (not_32_out, in_1);
  buf buffer_61 (buffer_61_out, in_3);
  buf buffer_62 (buffer_62_out, in_4);
  buf buffer_63 (buffer_63_out, not_31_out);
  buf buffer_64 (buffer_64_out, in_1);
  buf buffer_65 (buffer_65_out, in_2);
  buf buffer_66 (buffer_66_out, not_32_out);
  and and_27 (and_27_out, buffer_64_out, buffer_63_out, buffer_61_out, buffer_62_out);
  and and_28 (and_28_out, buffer_66_out, buffer_65_out, buffer_71_out, buffer_67_out);
  and and_29 (out_19, buffer_8_out, and_28_out);
  and and_30 (out_18, buffer_8_out, and_27_out);
  buf buffer_67 (buffer_67_out, in_4);
  buf buffer_68 (buffer_68_out, in_1);
  buf buffer_69 (buffer_69_out, in_3);
  buf buffer_70 (buffer_70_out, in_4);
  buf buffer_71 (buffer_71_out, in_3);
  buf buffer_72 (buffer_72_out, in_2);
  and and_31 (and_31_out, buffer_68_out, buffer_72_out, buffer_69_out, buffer_70_out);
  and and_32 (out_20, buffer_8_out, and_31_out);
endmodule

module _16_Detector (
  input  [15:0] in_1,
  output out_2
);

  or or_1 (out_2, in_1[0], in_1[1], in_1[2], in_1[3], in_1[4], in_1[5], in_1[6], in_1[7], in_1[9], in_1[10], in_1[11], in_1[12], in_1[13], in_1[14], in_1[15], in_1[8]);
endmodule

module _2B_Async_Register (
  input  [15:0] in_1,
  input  in_2,
  input  in_3,
  output [15:0] out_4
);

  wire [15:0] n16_buffer_1_out_3;

  _16_Buffer u_16_buffer_1 (.in_1(in_1), .in_2(in_2), .out_3(n16_buffer_1_out_3));
  RS_NOR rs_nor_1 (.in_1(n16_buffer_1_out_3[0]), .in_2(in_3), .out_3(out_4[0]));
  RS_NOR rs_nor_2 (.in_1(n16_buffer_1_out_3[1]), .in_2(in_3), .out_3(out_4[1]));
  RS_NOR rs_nor_3 (.in_1(n16_buffer_1_out_3[2]), .in_2(in_3), .out_3(out_4[2]));
  RS_NOR rs_nor_4 (.in_1(n16_buffer_1_out_3[3]), .in_2(in_3), .out_3(out_4[3]));
  RS_NOR rs_nor_5 (.in_1(n16_buffer_1_out_3[4]), .in_2(in_3), .out_3(out_4[4]));
  RS_NOR rs_nor_6 (.in_1(n16_buffer_1_out_3[5]), .in_2(in_3), .out_3(out_4[5]));
  RS_NOR rs_nor_7 (.in_1(n16_buffer_1_out_3[6]), .in_2(in_3), .out_3(out_4[6]));
  RS_NOR rs_nor_8 (.in_1(n16_buffer_1_out_3[7]), .in_2(in_3), .out_3(out_4[7]));
  RS_NOR rs_nor_9 (.in_1(n16_buffer_1_out_3[8]), .in_2(in_3), .out_3(out_4[8]));
  RS_NOR rs_nor_10 (.in_1(n16_buffer_1_out_3[9]), .in_2(in_3), .out_3(out_4[9]));
  RS_NOR rs_nor_11 (.in_1(n16_buffer_1_out_3[10]), .in_2(in_3), .out_3(out_4[10]));
  RS_NOR rs_nor_12 (.in_1(n16_buffer_1_out_3[11]), .in_2(in_3), .out_3(out_4[11]));
  RS_NOR rs_nor_13 (.in_1(n16_buffer_1_out_3[12]), .in_2(in_3), .out_3(out_4[12]));
  RS_NOR rs_nor_14 (.in_1(n16_buffer_1_out_3[13]), .in_2(in_3), .out_3(out_4[13]));
  RS_NOR rs_nor_15 (.in_1(n16_buffer_1_out_3[14]), .in_2(in_3), .out_3(out_4[14]));
  RS_NOR rs_nor_16 (.in_1(n16_buffer_1_out_3[15]), .in_2(in_3), .out_3(out_4[15]));
endmodule

module _6_Up_Down_Counter (
  input  in_1,
  input  in_2,
  input  in_3,
  output [5:0] out_4
);

  wire and_1_out, and_2_out, and_3_out, and_4_out, and_5_out, and_6_out, and_7_out, and_8_out, and_9_out,
       and_10_out, and_11_out, and_12_out, buffer_1_out, buffer_2_out, buffer_3_out, buffer_4_out,
       buffer_5_out, buffer_6_out, buffer_7_out, buffer_8_out, buffer_9_out, buffer_10_out, buffer_11_out,
       buffer_12_out, j_k_ff_1_qn, j_k_ff_2_qn, j_k_ff_3_qn, j_k_ff_4_qn, j_k_ff_5_qn, not_1_out, not_2_out,
       or_1_out, or_2_out, or_3_out, or_4_out, or_5_out, or_6_out, or_7_out, or_8_out;

  or or_1 (or_1_out, in_1, in_2);
  buf buffer_1 (buffer_1_out, or_1_out);
  buf buffer_2 (buffer_2_out, buffer_1_out);
  buf buffer_3 (buffer_3_out, buffer_2_out);
  buf buffer_4 (buffer_4_out, buffer_3_out);
  buf buffer_5 (buffer_5_out, buffer_4_out);
  buf buffer_6 (buffer_6_out, buffer_5_out);
  buf buffer_7 (buffer_7_out, buffer_6_out);
  buf buffer_8 (buffer_8_out, buffer_7_out);
  buf buffer_9 (buffer_9_out, buffer_8_out);
  buf buffer_10 (buffer_10_out, buffer_9_out);
  buf buffer_11 (buffer_11_out, buffer_10_out);
  buf buffer_12 (buffer_12_out, buffer_11_out);
  not not_1 (not_1_out, in_1);
  or or_2 (or_2_out, in_1, in_2);
  not not_2 (not_2_out, not_1_out);
  and and_1 (and_1_out, not_1_out, or_2_out);
  and and_2 (and_2_out, or_2_out, not_2_out);
  J_K_Flip_Flop j_k_ff_1 (
    .J(or_3_out), .clk(buffer_12_out), .K(or_3_out), .Q(out_4[0]), .Qn(j_k_ff_1_qn), .reset(in_3));  // open: preset, en
  J_K_Flip_Flop j_k_ff_2 (
    .J(or_4_out), .clk(buffer_12_out), .K(or_4_out), .Q(out_4[1]), .Qn(j_k_ff_2_qn), .reset(in_3));  // open: preset, en
  J_K_Flip_Flop j_k_ff_3 (
    .J(or_5_out), .clk(buffer_12_out), .K(or_5_out), .Q(out_4[2]), .Qn(j_k_ff_3_qn), .reset(in_3));  // open: preset, en
  J_K_Flip_Flop j_k_ff_4 (
    .J(or_6_out), .clk(buffer_12_out), .K(or_6_out), .Q(out_4[3]), .Qn(j_k_ff_4_qn), .reset(in_3));  // open: preset, en
  J_K_Flip_Flop j_k_ff_5 (
    .J(or_7_out), .clk(buffer_12_out), .K(or_7_out), .Q(out_4[4]), .Qn(j_k_ff_5_qn), .reset(in_3));  // open: preset, en
  J_K_Flip_Flop j_k_ff_6 (
    .J(or_8_out), .clk(buffer_12_out), .K(or_8_out), .Q(out_4[5]), .reset(in_3));  // open: Qn, preset, en
  and and_3 (and_3_out, and_1_out, out_4[0]);
  and and_4 (and_4_out, j_k_ff_1_qn, and_2_out);
  and and_5 (and_5_out, and_1_out, out_4[0], out_4[1]);
  and and_6 (and_6_out, j_k_ff_2_qn, and_2_out, j_k_ff_1_qn);
  and and_7 (and_7_out, and_1_out, out_4[0], out_4[1], out_4[2]);
  and and_8 (and_8_out, j_k_ff_3_qn, and_2_out, j_k_ff_1_qn, j_k_ff_2_qn);
  and and_9 (and_9_out, and_1_out, out_4[0], out_4[1], out_4[2], out_4[3]);
  and and_10 (and_10_out, j_k_ff_4_qn, and_2_out, j_k_ff_1_qn, j_k_ff_2_qn, j_k_ff_3_qn);
  and and_11 (and_11_out, and_1_out, out_4[0], out_4[1], out_4[2], out_4[3], out_4[4]);
  and and_12 (and_12_out, j_k_ff_5_qn, and_2_out, j_k_ff_1_qn, j_k_ff_2_qn, j_k_ff_3_qn, j_k_ff_4_qn);
  or or_3 (or_3_out, and_1_out, and_2_out);
  or or_4 (or_4_out, and_3_out, and_4_out);
  or or_5 (or_5_out, and_5_out, and_6_out);
  or or_6 (or_6_out, and_7_out, and_8_out);
  or or_7 (or_7_out, and_9_out, and_10_out);
  or or_8 (or_8_out, and_11_out, and_12_out);
endmodule

module Falling_Trigger (
  input  in_1,
  output out_2
);

  wire not_1_out, not_2_out, not_3_out, not_4_out, not_5_out, not_6_out, not_7_out, not_8_out, not_9_out,
       not_10_out, not_11_out, not_12_out, not_13_out, not_14_out, not_15_out, not_16_out, not_17_out,
       not_18_out, not_19_out, not_20_out, not_21_out, not_22_out, not_23_out, not_24_out, not_25_out,
       not_26_out, not_27_out, not_28_out, not_29_out, not_30_out, not_31_out, not_32_out, not_33_out,
       not_34_out, not_35_out, not_36_out;

  not not_1 (not_1_out, in_1);
  not not_2 (not_2_out, not_4_out);
  not not_3 (not_3_out, not_1_out);
  not not_4 (not_4_out, not_3_out);
  not not_5 (not_5_out, not_8_out);
  not not_6 (not_6_out, not_2_out);
  not not_7 (not_7_out, not_5_out);
  not not_8 (not_8_out, not_6_out);
  not not_9 (not_9_out, not_11_out);
  not not_10 (not_10_out, not_7_out);
  not not_11 (not_11_out, not_12_out);
  not not_12 (not_12_out, not_10_out);
  not not_13 (not_13_out, not_16_out);
  not not_14 (not_14_out, not_15_out);
  not not_15 (not_15_out, not_13_out);
  not not_16 (not_16_out, not_9_out);
  not not_17 (not_17_out, not_19_out);
  not not_18 (not_18_out, not_14_out);
  not not_19 (not_19_out, not_18_out);
  not not_20 (not_20_out, not_17_out);
  not not_21 (not_21_out, not_20_out);
  not not_22 (not_22_out, not_21_out);
  not not_23 (not_23_out, not_24_out);
  not not_24 (not_24_out, not_22_out);
  not not_25 (not_25_out, not_27_out);
  not not_26 (not_26_out, not_25_out);
  not not_27 (not_27_out, not_28_out);
  not not_28 (not_28_out, not_23_out);
  not not_29 (not_29_out, not_32_out);
  not not_30 (not_30_out, not_31_out);
  not not_31 (not_31_out, not_29_out);
  not not_32 (not_32_out, not_26_out);
  not not_33 (not_33_out, not_35_out);
  not not_34 (not_34_out, not_30_out);
  not not_35 (not_35_out, not_34_out);
  not not_36 (not_36_out, not_33_out);
  and and_1 (out_2, not_36_out, not_1_out);
endmodule

module _6_BUF (
  input  [5:0] in_1,
  input  in_2,
  output [5:0] out_3
);

  and and_1 (out_3[4], in_1[4], in_2);
  and and_2 (out_3[5], in_1[5], in_2);
  and and_3 (out_3[3], in_2, in_1[3]);
  and and_4 (out_3[2], in_1[2], in_2);
  and and_5 (out_3[0], in_2, in_1[0]);
  and and_6 (out_3[1], in_2, in_1[1]);
endmodule

module _4_Detector (
  input  [3:0] in_1,
  output out_2
);

  or or_1 (out_2, in_1[3], in_1[2], in_1[1], in_1[0]);
endmodule

module _2_BUF (
  input  [1:0] in_1,
  input  in_2,
  output [1:0] out_3
);

  and and_1 (out_3[1], in_2, in_1[1]);
  and and_2 (out_3[0], in_1[0], in_2);
endmodule

module _16_BUF_4_way (
  input  [15:0] in_1,
  input  in_2,
  input  in_3,
  input  in_4,
  input  in_5,
  input  [15:0] in_6,
  input  [15:0] in_7,
  input  [15:0] in_8,
  output [15:0] out_9,
  output [15:0] out_10,
  output [15:0] out_11,
  output [15:0] out_12
);

  wire or_1_out;

  or or_1 (or_1_out, in_3, in_2, in_4, in_5);
  _16_Buffer u_16_buffer_1 (.in_1(in_6), .in_2(or_1_out), .out_3(out_10));
  _16_Buffer u_16_buffer_2 (.in_1(in_8), .in_2(or_1_out), .out_3(out_9));
  _16_Buffer u_16_buffer_3 (.in_1(in_1), .in_2(or_1_out), .out_3(out_12));
  _16_Buffer u_16_buffer_4 (.in_1(in_7), .in_2(or_1_out), .out_3(out_11));
endmodule

module _1_16T_Delay (
  input  in_1,
  output out_2
);

  wire buffer_1_out, buffer_2_out, buffer_3_out, buffer_4_out, buffer_5_out, buffer_6_out, buffer_7_out,
       buffer_8_out, buffer_9_out, buffer_10_out, buffer_11_out, buffer_12_out, buffer_13_out, buffer_14_out,
       buffer_15_out;

  buf buffer_1 (buffer_1_out, buffer_3_out);
  buf buffer_2 (buffer_2_out, buffer_1_out);
  buf buffer_3 (buffer_3_out, in_1);
  buf buffer_4 (buffer_4_out, buffer_2_out);
  buf buffer_5 (buffer_5_out, buffer_8_out);
  buf buffer_6 (buffer_6_out, buffer_4_out);
  buf buffer_7 (buffer_7_out, buffer_5_out);
  buf buffer_8 (buffer_8_out, buffer_6_out);
  buf buffer_9 (buffer_9_out, buffer_12_out);
  buf buffer_10 (buffer_10_out, buffer_9_out);
  buf buffer_11 (buffer_11_out, buffer_7_out);
  buf buffer_12 (buffer_12_out, buffer_11_out);
  buf buffer_13 (buffer_13_out, buffer_15_out);
  buf buffer_14 (buffer_14_out, buffer_10_out);
  buf buffer_15 (buffer_15_out, buffer_14_out);
  buf buffer_16 (out_2, buffer_13_out);
endmodule

module _5_BUF (
  input  [4:0] in_1,
  input  in_2,
  output [4:0] out_3
);

  and and_1 (out_3[4], in_1[4], in_2);
  and and_2 (out_3[3], in_2, in_1[3]);
  and and_3 (out_3[2], in_1[2], in_2);
  and and_4 (out_3[1], in_2, in_1[1]);
  and and_5 (out_3[0], in_2, in_1[0]);
endmodule

module _6_Detector (
  input  [5:0] in_1,
  output out_2,
  output [5:0] out_3
);

  or or_1 (out_2, in_1[5], in_1[4], in_1[3], in_1[2], in_1[1], in_1[0]);

  assign out_3 = in_1;
endmodule

module _16T_Delay_RE_Trig (
  input  in_1,
  output out_2
);

  wire buffer_1_out, not_1_out, not_2_out, not_3_out, not_4_out, not_5_out, not_6_out, not_7_out, not_8_out,
       not_9_out, not_10_out, not_11_out, not_12_out, not_13_out, not_14_out, not_15_out, not_16_out,
       not_17_out, not_18_out, not_19_out, not_20_out, not_21_out, not_22_out, not_23_out, not_24_out,
       not_25_out, not_26_out, not_27_out, not_28_out, not_29_out, not_30_out, not_31_out;

  not not_1 (not_1_out, buffer_1_out);
  buf buffer_1 (buffer_1_out, in_1);
  not not_2 (not_2_out, not_5_out);
  not not_3 (not_3_out, not_4_out);
  not not_4 (not_4_out, not_2_out);
  not not_5 (not_5_out, not_1_out);
  not not_6 (not_6_out, not_3_out);
  not not_7 (not_7_out, not_6_out);
  not not_8 (not_8_out, not_7_out);
  not not_9 (not_9_out, not_8_out);
  not not_10 (not_10_out, not_12_out);
  not not_11 (not_11_out, not_13_out);
  not not_12 (not_12_out, not_11_out);
  not not_13 (not_13_out, not_9_out);
  not not_14 (not_14_out, not_15_out);
  not not_15 (not_15_out, not_17_out);
  not not_16 (not_16_out, not_14_out);
  not not_17 (not_17_out, not_10_out);
  not not_18 (not_18_out, not_21_out);
  not not_19 (not_19_out, not_18_out);
  not not_20 (not_20_out, not_19_out);
  not not_21 (not_21_out, not_16_out);
  not not_22 (not_22_out, not_25_out);
  not not_23 (not_23_out, not_20_out);
  not not_24 (not_24_out, not_22_out);
  not not_25 (not_25_out, not_23_out);
  not not_26 (not_26_out, not_29_out);
  not not_27 (not_27_out, not_28_out);
  not not_28 (not_28_out, not_26_out);
  not not_29 (not_29_out, not_24_out);
  not not_30 (not_30_out, not_31_out);
  not not_31 (not_31_out, not_27_out);
  and and_1 (out_2, not_30_out, buffer_1_out);
endmodule

module _16_BUF_N_S (
  input  [15:0] in_1,
  input  in_2,
  output [15:0] out_3
);

  and and_1 (out_3[0], in_1[0], in_2);
  and and_2 (out_3[1], in_1[1], in_2);
  and and_3 (out_3[2], in_1[2], in_2);
  and and_4 (out_3[3], in_1[3], in_2);
  and and_5 (out_3[4], in_1[4], in_2);
  and and_6 (out_3[5], in_1[5], in_2);
  and and_7 (out_3[6], in_1[6], in_2);
  and and_8 (out_3[7], in_1[7], in_2);
  and and_9 (out_3[8], in_1[8], in_2);
  and and_10 (out_3[9], in_1[9], in_2);
  and and_11 (out_3[10], in_1[10], in_2);
  and and_12 (out_3[11], in_1[11], in_2);
  and and_13 (out_3[12], in_1[12], in_2);
  and and_14 (out_3[13], in_1[13], in_2);
  and and_15 (out_3[14], in_1[14], in_2);
  and and_16 (out_3[15], in_1[15], in_2);
endmodule

module _16_BUF_W_E (
  input  [15:0] in_1,
  input  in_2,
  output [15:0] out_3
);

  and and_1 (out_3[0], in_1[0], in_2);
  and and_2 (out_3[1], in_1[1], in_2);
  and and_3 (out_3[2], in_1[2], in_2);
  and and_4 (out_3[3], in_1[3], in_2);
  and and_5 (out_3[4], in_1[4], in_2);
  and and_6 (out_3[5], in_1[5], in_2);
  and and_7 (out_3[6], in_1[6], in_2);
  and and_8 (out_3[7], in_1[7], in_2);
  and and_9 (out_3[8], in_1[8], in_2);
  and and_10 (out_3[9], in_1[9], in_2);
  and and_11 (out_3[10], in_1[10], in_2);
  and and_12 (out_3[11], in_1[11], in_2);
  and and_13 (out_3[12], in_1[12], in_2);
  and and_14 (out_3[13], in_1[13], in_2);
  and and_15 (out_3[14], in_1[14], in_2);
  and and_16 (out_3[15], in_1[15], in_2);
endmodule

module _4_BUF_N_S (
  input  [3:0] in_1,
  input  in_2,
  output [3:0] out_3
);

  and and_1 (out_3[3], in_2, in_1[3]);
  and and_2 (out_3[2], in_2, in_1[2]);
  and and_3 (out_3[0], in_1[0], in_2);
  and and_4 (out_3[1], in_1[1], in_2);
endmodule

module _4_BUF_W_E (
  input  [3:0] in_1,
  input  in_2,
  output [3:0] out_3
);

  and and_1 (out_3[2], in_2, in_1[2]);
  and and_2 (out_3[3], in_2, in_1[3]);
  and and_3 (out_3[1], in_1[1], in_2);
  and and_4 (out_3[0], in_1[0], in_2);
endmodule

module _1_4T_Delay (
  input  in_1,
  output out_2
);

  wire buffer_1_out, buffer_2_out, buffer_3_out;

  buf buffer_1 (buffer_1_out, buffer_2_out);
  buf buffer_2 (buffer_2_out, in_1);
  buf buffer_3 (buffer_3_out, buffer_1_out);
  buf buffer_4 (out_2, buffer_3_out);
endmodule

module _1_4T_Extd (
  input  in_1,
  output out_2
);

  wire buffer_1_out, buffer_2_out, buffer_3_out, buffer_4_out, buffer_5_out, buffer_6_out;

  buf buffer_1 (buffer_1_out, in_1);
  buf buffer_2 (buffer_2_out, in_1);
  buf buffer_3 (buffer_3_out, in_1);
  buf buffer_4 (buffer_4_out, buffer_1_out);
  buf buffer_5 (buffer_5_out, buffer_2_out);
  buf buffer_6 (buffer_6_out, buffer_4_out);
  or or_1 (out_2, in_1, buffer_6_out, buffer_5_out, buffer_3_out);
endmodule

module _4_REG (
  input  in_1,
  input  in_2,
  input  [3:0] in_3,
  output [3:0] out_4
);

  D_Flip_Flop d_ff_1 (.clk(in_1), .D(in_3[0]), .Q(out_4[0]), .reset(in_2));  // open: Qn, preset, en
  D_Flip_Flop d_ff_2 (.clk(in_1), .D(in_3[1]), .Q(out_4[1]), .reset(in_2));  // open: Qn, preset, en
  D_Flip_Flop d_ff_3 (.clk(in_1), .D(in_3[2]), .Q(out_4[2]), .reset(in_2));  // open: Qn, preset, en
  D_Flip_Flop d_ff_4 (.clk(in_1), .D(in_3[3]), .Q(out_4[3]), .reset(in_2));  // open: Qn, preset, en
endmodule

module Double_Dabble (
  input  [15:0] in_1,
  output [3:0] out_2,
  output [3:0] out_3,
  output [3:0] out_4,
  output [3:0] out_5,
  output [3:0] out_6
);

  wire dd_adder_1_out_5, dd_adder_1_out_6, dd_adder_1_out_7, dd_adder_1_out_8, dd_adder_2_out_5,
       dd_adder_2_out_6, dd_adder_2_out_7, dd_adder_2_out_8, dd_adder_3_out_5, dd_adder_3_out_6,
       dd_adder_3_out_7, dd_adder_3_out_8, dd_adder_4_out_5, dd_adder_4_out_6, dd_adder_4_out_7,
       dd_adder_4_out_8, dd_adder_5_out_5, dd_adder_5_out_6, dd_adder_5_out_7, dd_adder_5_out_8,
       dd_adder_6_out_5, dd_adder_6_out_6, dd_adder_6_out_7, dd_adder_6_out_8, dd_adder_7_out_5,
       dd_adder_7_out_6, dd_adder_7_out_7, dd_adder_7_out_8, dd_adder_8_out_5, dd_adder_8_out_6,
       dd_adder_8_out_7, dd_adder_8_out_8, dd_adder_9_out_6, dd_adder_9_out_7, dd_adder_9_out_8,
       dd_adder_10_out_5, dd_adder_10_out_6, dd_adder_10_out_7, dd_adder_10_out_8, dd_adder_11_out_6,
       dd_adder_11_out_7, dd_adder_11_out_8, dd_adder_12_out_6, dd_adder_12_out_7, dd_adder_12_out_8,
       dd_adder_14_out_5, dd_adder_14_out_6, dd_adder_14_out_7, dd_adder_14_out_8, dd_adder_15_out_5,
       dd_adder_15_out_6, dd_adder_15_out_7, dd_adder_15_out_8, dd_adder_16_out_5, dd_adder_16_out_6,
       dd_adder_16_out_7, dd_adder_16_out_8, dd_adder_17_out_5, dd_adder_17_out_6, dd_adder_17_out_7,
       dd_adder_17_out_8, dd_adder_18_out_5, dd_adder_18_out_6, dd_adder_18_out_7, dd_adder_18_out_8,
       dd_adder_19_out_5, dd_adder_19_out_6, dd_adder_19_out_7, dd_adder_19_out_8, dd_adder_20_out_5,
       dd_adder_20_out_6, dd_adder_20_out_7, dd_adder_20_out_8, dd_adder_21_out_5, dd_adder_21_out_6,
       dd_adder_21_out_7, dd_adder_21_out_8, dd_adder_22_out_5, dd_adder_22_out_6, dd_adder_22_out_7,
       dd_adder_22_out_8, dd_adder_23_out_5, dd_adder_23_out_6, dd_adder_23_out_7, dd_adder_23_out_8,
       dd_adder_24_out_5, dd_adder_24_out_6, dd_adder_24_out_7, dd_adder_24_out_8, dd_adder_25_out_5,
       dd_adder_25_out_6, dd_adder_25_out_7, dd_adder_25_out_8, dd_adder_26_out_5, dd_adder_26_out_6,
       dd_adder_26_out_7, dd_adder_26_out_8, dd_adder_27_out_5, dd_adder_27_out_6, dd_adder_27_out_7,
       dd_adder_27_out_8, dd_adder_28_out_5, dd_adder_28_out_6, dd_adder_28_out_7, dd_adder_28_out_8,
       dd_adder_29_out_5, dd_adder_29_out_6, dd_adder_29_out_7, dd_adder_29_out_8, dd_adder_32_out_5,
       dd_adder_32_out_6, dd_adder_32_out_7, dd_adder_32_out_8, dd_adder_33_out_5, dd_adder_33_out_6,
       dd_adder_33_out_7, dd_adder_33_out_8;

  DD_Adder dd_adder_1 (
    .in_1(1'b0), .in_2(in_1[15]), .in_3(in_1[14]), .in_4(in_1[13]), .out_5(dd_adder_1_out_5),
    .out_6(dd_adder_1_out_6), .out_7(dd_adder_1_out_7), .out_8(dd_adder_1_out_8));
  DD_Adder dd_adder_2 (
    .in_1(dd_adder_1_out_6), .in_2(dd_adder_1_out_7), .in_3(dd_adder_1_out_8), .in_4(in_1[12]),
    .out_5(dd_adder_2_out_5), .out_6(dd_adder_2_out_6), .out_7(dd_adder_2_out_7), .out_8(dd_adder_2_out_8));
  DD_Adder dd_adder_3 (
    .in_1(1'b0), .in_2(dd_adder_1_out_5), .in_3(dd_adder_2_out_5), .in_4(dd_adder_14_out_5),
    .out_5(dd_adder_3_out_5), .out_6(dd_adder_3_out_6), .out_7(dd_adder_3_out_7), .out_8(dd_adder_3_out_8));
  DD_Adder dd_adder_4 (
    .in_1(dd_adder_3_out_6), .in_2(dd_adder_3_out_7), .in_3(dd_adder_3_out_8), .in_4(dd_adder_15_out_5),
    .out_5(dd_adder_4_out_5), .out_6(dd_adder_4_out_6), .out_7(dd_adder_4_out_7), .out_8(dd_adder_4_out_8));
  DD_Adder dd_adder_5 (
    .in_1(dd_adder_4_out_6), .in_2(dd_adder_4_out_7), .in_3(dd_adder_4_out_8), .in_4(dd_adder_16_out_5),
    .out_5(dd_adder_5_out_5), .out_6(dd_adder_5_out_6), .out_7(dd_adder_5_out_7), .out_8(dd_adder_5_out_8));
  DD_Adder dd_adder_6 (
    .in_1(1'b0), .in_2(dd_adder_3_out_5), .in_3(dd_adder_4_out_5), .in_4(dd_adder_5_out_5),
    .out_5(dd_adder_6_out_5), .out_6(dd_adder_6_out_6), .out_7(dd_adder_6_out_7), .out_8(dd_adder_6_out_8));
  DD_Adder dd_adder_7 (
    .in_1(dd_adder_6_out_6), .in_2(dd_adder_6_out_7), .in_3(dd_adder_6_out_8), .in_4(dd_adder_18_out_5),
    .out_5(dd_adder_7_out_5), .out_6(dd_adder_7_out_6), .out_7(dd_adder_7_out_7), .out_8(dd_adder_7_out_8));
  DD_Adder dd_adder_8 (
    .in_1(dd_adder_7_out_6), .in_2(dd_adder_7_out_7), .in_3(dd_adder_7_out_8), .in_4(dd_adder_21_out_5),
    .out_5(dd_adder_8_out_5), .out_6(dd_adder_8_out_6), .out_7(dd_adder_8_out_7), .out_8(dd_adder_8_out_8));
  DD_Adder dd_adder_9 (
    .in_1(1'b0), .in_2(dd_adder_6_out_5), .in_3(dd_adder_7_out_5), .in_4(dd_adder_8_out_5), .out_5(out_2[3]),
    .out_6(dd_adder_9_out_6), .out_7(dd_adder_9_out_7), .out_8(dd_adder_9_out_8));
  DD_Adder dd_adder_10 (
    .in_1(dd_adder_8_out_6), .in_2(dd_adder_8_out_7), .in_3(dd_adder_8_out_8), .in_4(dd_adder_22_out_5),
    .out_5(dd_adder_10_out_5), .out_6(dd_adder_10_out_6), .out_7(dd_adder_10_out_7), .out_8(dd_adder_10_out_8));
  DD_Adder dd_adder_11 (
    .in_1(dd_adder_9_out_6), .in_2(dd_adder_9_out_7), .in_3(dd_adder_9_out_8), .in_4(dd_adder_10_out_5),
    .out_5(out_2[2]), .out_6(dd_adder_11_out_6), .out_7(dd_adder_11_out_7), .out_8(dd_adder_11_out_8));
  DD_Adder dd_adder_12 (
    .in_1(dd_adder_11_out_6), .in_2(dd_adder_11_out_7), .in_3(dd_adder_11_out_8), .in_4(dd_adder_26_out_5),
    .out_5(out_2[1]), .out_6(dd_adder_12_out_6), .out_7(dd_adder_12_out_7), .out_8(dd_adder_12_out_8));
  DD_Adder dd_adder_13 (
    .in_1(dd_adder_12_out_6), .in_2(dd_adder_12_out_7), .in_3(dd_adder_12_out_8), .in_4(dd_adder_29_out_5),
    .out_5(out_2[0]), .out_6(out_3[3]), .out_7(out_3[2]), .out_8(out_3[1]));
  DD_Adder dd_adder_14 (
    .in_1(dd_adder_2_out_6), .in_2(dd_adder_2_out_7), .in_3(dd_adder_2_out_8), .in_4(in_1[11]),
    .out_5(dd_adder_14_out_5), .out_6(dd_adder_14_out_6), .out_7(dd_adder_14_out_7), .out_8(dd_adder_14_out_8));
  DD_Adder dd_adder_15 (
    .in_1(dd_adder_14_out_6), .in_2(dd_adder_14_out_7), .in_3(dd_adder_14_out_8), .in_4(in_1[10]),
    .out_5(dd_adder_15_out_5), .out_6(dd_adder_15_out_6), .out_7(dd_adder_15_out_7), .out_8(dd_adder_15_out_8));
  DD_Adder dd_adder_16 (
    .in_1(dd_adder_15_out_6), .in_2(dd_adder_15_out_7), .in_3(dd_adder_15_out_8), .in_4(in_1[9]),
    .out_5(dd_adder_16_out_5), .out_6(dd_adder_16_out_6), .out_7(dd_adder_16_out_7), .out_8(dd_adder_16_out_8));
  DD_Adder dd_adder_17 (
    .in_1(dd_adder_16_out_6), .in_2(dd_adder_16_out_7), .in_3(dd_adder_16_out_8), .in_4(in_1[8]),
    .out_5(dd_adder_17_out_5), .out_6(dd_adder_17_out_6), .out_7(dd_adder_17_out_7), .out_8(dd_adder_17_out_8));
  DD_Adder dd_adder_18 (
    .in_1(dd_adder_5_out_6), .in_2(dd_adder_5_out_7), .in_3(dd_adder_5_out_8), .in_4(dd_adder_17_out_5),
    .out_5(dd_adder_18_out_5), .out_6(dd_adder_18_out_6), .out_7(dd_adder_18_out_7), .out_8(dd_adder_18_out_8));
  DD_Adder dd_adder_19 (
    .in_1(dd_adder_17_out_6), .in_2(dd_adder_17_out_7), .in_3(dd_adder_17_out_8), .in_4(in_1[7]),
    .out_5(dd_adder_19_out_5), .out_6(dd_adder_19_out_6), .out_7(dd_adder_19_out_7), .out_8(dd_adder_19_out_8));
  DD_Adder dd_adder_20 (
    .in_1(dd_adder_19_out_6), .in_2(dd_adder_19_out_7), .in_3(dd_adder_19_out_8), .in_4(in_1[6]),
    .out_5(dd_adder_20_out_5), .out_6(dd_adder_20_out_6), .out_7(dd_adder_20_out_7), .out_8(dd_adder_20_out_8));
  DD_Adder dd_adder_21 (
    .in_1(dd_adder_18_out_6), .in_2(dd_adder_18_out_7), .in_3(dd_adder_18_out_8), .in_4(dd_adder_19_out_5),
    .out_5(dd_adder_21_out_5), .out_6(dd_adder_21_out_6), .out_7(dd_adder_21_out_7), .out_8(dd_adder_21_out_8));
  DD_Adder dd_adder_22 (
    .in_1(dd_adder_21_out_6), .in_2(dd_adder_21_out_7), .in_3(dd_adder_21_out_8), .in_4(dd_adder_20_out_5),
    .out_5(dd_adder_22_out_5), .out_6(dd_adder_22_out_6), .out_7(dd_adder_22_out_7), .out_8(dd_adder_22_out_8));
  DD_Adder dd_adder_23 (
    .in_1(dd_adder_20_out_6), .in_2(dd_adder_20_out_7), .in_3(dd_adder_20_out_8), .in_4(in_1[5]),
    .out_5(dd_adder_23_out_5), .out_6(dd_adder_23_out_6), .out_7(dd_adder_23_out_7), .out_8(dd_adder_23_out_8));
  DD_Adder dd_adder_24 (
    .in_1(dd_adder_23_out_6), .in_2(dd_adder_23_out_7), .in_3(dd_adder_23_out_8), .in_4(in_1[4]),
    .out_5(dd_adder_24_out_5), .out_6(dd_adder_24_out_6), .out_7(dd_adder_24_out_7), .out_8(dd_adder_24_out_8));
  DD_Adder dd_adder_25 (
    .in_1(dd_adder_22_out_6), .in_2(dd_adder_22_out_7), .in_3(dd_adder_22_out_8), .in_4(dd_adder_23_out_5),
    .out_5(dd_adder_25_out_5), .out_6(dd_adder_25_out_6), .out_7(dd_adder_25_out_7), .out_8(dd_adder_25_out_8));
  DD_Adder dd_adder_26 (
    .in_1(dd_adder_10_out_6), .in_2(dd_adder_10_out_7), .in_3(dd_adder_10_out_8), .in_4(dd_adder_25_out_5),
    .out_5(dd_adder_26_out_5), .out_6(dd_adder_26_out_6), .out_7(dd_adder_26_out_7), .out_8(dd_adder_26_out_8));
  DD_Adder dd_adder_27 (
    .in_1(dd_adder_25_out_6), .in_2(dd_adder_25_out_7), .in_3(dd_adder_25_out_8), .in_4(dd_adder_24_out_5),
    .out_5(dd_adder_27_out_5), .out_6(dd_adder_27_out_6), .out_7(dd_adder_27_out_7), .out_8(dd_adder_27_out_8));
  DD_Adder dd_adder_28 (
    .in_1(dd_adder_27_out_6), .in_2(dd_adder_27_out_7), .in_3(dd_adder_27_out_8), .in_4(dd_adder_32_out_5),
    .out_5(dd_adder_28_out_5), .out_6(dd_adder_28_out_6), .out_7(dd_adder_28_out_7), .out_8(dd_adder_28_out_8));
  DD_Adder dd_adder_29 (
    .in_1(dd_adder_26_out_6), .in_2(dd_adder_26_out_7), .in_3(dd_adder_26_out_8), .in_4(dd_adder_27_out_5),
    .out_5(dd_adder_29_out_5), .out_6(dd_adder_29_out_6), .out_7(dd_adder_29_out_7), .out_8(dd_adder_29_out_8));
  DD_Adder dd_adder_30 (
    .in_1(dd_adder_28_out_6), .in_2(dd_adder_28_out_7), .in_3(dd_adder_28_out_8), .in_4(dd_adder_33_out_5),
    .out_5(out_4[0]), .out_6(out_5[3]), .out_7(out_5[2]), .out_8(out_5[1]));
  DD_Adder dd_adder_31 (
    .in_1(dd_adder_29_out_6), .in_2(dd_adder_29_out_7), .in_3(dd_adder_29_out_8), .in_4(dd_adder_28_out_5),
    .out_5(out_3[0]), .out_6(out_4[3]), .out_7(out_4[2]), .out_8(out_4[1]));
  DD_Adder dd_adder_32 (
    .in_1(dd_adder_24_out_6), .in_2(dd_adder_24_out_7), .in_3(dd_adder_24_out_8), .in_4(in_1[3]),
    .out_5(dd_adder_32_out_5), .out_6(dd_adder_32_out_6), .out_7(dd_adder_32_out_7), .out_8(dd_adder_32_out_8));
  DD_Adder dd_adder_33 (
    .in_1(dd_adder_32_out_6), .in_2(dd_adder_32_out_7), .in_3(dd_adder_32_out_8), .in_4(in_1[2]),
    .out_5(dd_adder_33_out_5), .out_6(dd_adder_33_out_6), .out_7(dd_adder_33_out_7), .out_8(dd_adder_33_out_8));
  DD_Adder dd_adder_34 (
    .in_1(dd_adder_33_out_6), .in_2(dd_adder_33_out_7), .in_3(dd_adder_33_out_8), .in_4(in_1[1]),
    .out_5(out_5[0]), .out_6(out_6[3]), .out_7(out_6[2]), .out_8(out_6[1]));
  // Probe on in_1
  // Probe on out_2
  // Probe on out_3
  // Probe on out_4
  // Probe on out_5
  // Probe on {out_6[3:1], in_1[0]}

  assign out_6[0] = in_1[0];
endmodule

module DD_Adder (
  input  in_1,
  input  in_2,
  input  in_3,
  input  in_4,
  output out_5,
  output out_6,
  output out_7,
  output out_8
);

  wire and_1_out, and_2_out, and_3_out, and_4_out, and_5_out, and_6_out, and_7_out, and_8_out, and_9_out,
       or_1_out, or_2_out, or_3_out, or_4_out, or_5_out, xor_1_out, xor_2_out, xor_3_out, xor_4_out;
  wire [3:0] xor_5_out;

  Multiplexer #(.width(4), .enable("false")) multiplexer_1 (
    .in0({in_1, in_2, in_3, in_4}), .in1(xor_5_out), .out({out_5, out_6, out_7, out_8}), .sel(or_2_out));
  and and_1 (and_1_out, in_2, or_1_out);
  or or_1 (or_1_out, in_4, in_3);
  or or_2 (or_2_out, in_1, and_1_out);
  and and_2 (and_2_out, in_4, 1'b1);
  or or_3 (or_3_out, and_2_out, and_6_out);
  and and_3 (and_3_out, in_3, 1'b1);
  or or_4 (or_4_out, and_3_out, and_7_out);
  and and_4 (and_4_out, in_2, 1'b0);
  or or_5 (or_5_out, and_4_out, and_8_out);
  and and_5 (and_5_out, in_1, 1'b0);
  // OR_Gate or_6 has open pins: in0=and_5_out, in1=and_9_out, out=open
  xor xor_1 (xor_1_out, in_4, 1'b1);
  and and_6 (and_6_out, 1'b0, xor_1_out);
  xor xor_2 (xor_2_out, in_3, 1'b1);
  and and_7 (and_7_out, or_3_out, xor_2_out);
  xor xor_3 (xor_3_out, in_2, 1'b0);
  and and_8 (and_8_out, or_4_out, xor_3_out);
  xor xor_4 (xor_4_out, in_1, 1'b0);
  and and_9 (and_9_out, or_5_out, xor_4_out);
  xor xor_5 (xor_5_out[0], xor_1_out, 1'b0);
  xor xor_6 (xor_5_out[1], xor_2_out, or_3_out);
  xor xor_7 (xor_5_out[2], xor_3_out, or_4_out);
  xor xor_8 (xor_5_out[3], xor_4_out, or_5_out);
endmodule

module _2B_ALU_Reg (
  input  [15:0] in_1,
  input  in_2,
  input  in_3,
  input  in_4,
  output [15:0] out_5
);

  wire [15:0] n16_buf_n_s_1_out_3, rs_nor_1_out_3;

  _16_BUF_N_S u_16_buf_n_s_1 (.in_1(in_1), .in_2(in_2), .out_3(n16_buf_n_s_1_out_3));
  RS_NOR rs_nor_1 (.in_1(n16_buf_n_s_1_out_3[0]), .in_2(in_4), .out_3(rs_nor_1_out_3[0]));
  RS_NOR rs_nor_2 (.in_1(n16_buf_n_s_1_out_3[1]), .in_2(in_4), .out_3(rs_nor_1_out_3[1]));
  RS_NOR rs_nor_3 (.in_1(n16_buf_n_s_1_out_3[2]), .in_2(in_4), .out_3(rs_nor_1_out_3[2]));
  RS_NOR rs_nor_4 (.in_1(n16_buf_n_s_1_out_3[3]), .in_2(in_4), .out_3(rs_nor_1_out_3[3]));
  RS_NOR rs_nor_5 (.in_1(n16_buf_n_s_1_out_3[4]), .in_2(in_4), .out_3(rs_nor_1_out_3[4]));
  RS_NOR rs_nor_6 (.in_1(n16_buf_n_s_1_out_3[5]), .in_2(in_4), .out_3(rs_nor_1_out_3[5]));
  RS_NOR rs_nor_7 (.in_1(n16_buf_n_s_1_out_3[6]), .in_2(in_4), .out_3(rs_nor_1_out_3[6]));
  RS_NOR rs_nor_8 (.in_1(n16_buf_n_s_1_out_3[7]), .in_2(in_4), .out_3(rs_nor_1_out_3[7]));
  RS_NOR rs_nor_9 (.in_1(n16_buf_n_s_1_out_3[8]), .in_2(in_4), .out_3(rs_nor_1_out_3[8]));
  RS_NOR rs_nor_10 (.in_1(n16_buf_n_s_1_out_3[9]), .in_2(in_4), .out_3(rs_nor_1_out_3[9]));
  RS_NOR rs_nor_11 (.in_1(n16_buf_n_s_1_out_3[10]), .in_2(in_4), .out_3(rs_nor_1_out_3[10]));
  RS_NOR rs_nor_12 (.in_1(n16_buf_n_s_1_out_3[11]), .in_2(in_4), .out_3(rs_nor_1_out_3[11]));
  RS_NOR rs_nor_13 (.in_1(n16_buf_n_s_1_out_3[12]), .in_2(in_4), .out_3(rs_nor_1_out_3[12]));
  RS_NOR rs_nor_14 (.in_1(n16_buf_n_s_1_out_3[13]), .in_2(in_4), .out_3(rs_nor_1_out_3[13]));
  RS_NOR rs_nor_15 (.in_1(n16_buf_n_s_1_out_3[14]), .in_2(in_4), .out_3(rs_nor_1_out_3[14]));
  RS_NOR rs_nor_16 (.in_1(n16_buf_n_s_1_out_3[15]), .in_2(in_4), .out_3(rs_nor_1_out_3[15]));
  _16_BUF_N_S u_16_buf_n_s_2 (.in_1(rs_nor_1_out_3), .in_2(in_3), .out_3(out_5));
endmodule

module Program__Division (
  output out_1,
  output [3:0] out_2,
  output [3:0] out_3,
  output [3:0] out_4,
  output [3:0] out_5,
  output out_6
);
endmodule
