// Logisim project SyzygyA100.circ as structural Verilog
module Syzygy_A100 (
);

  ALU alu_1 ();  // open: in_9, in_11, in_10, in_12, in_7, in_5, in_8, in_6, Pre_Shift_Amt, Op, Post, Shft, out_14, Condition_Met
endmodule

module ALU (
  input  [3:0] Pre_Shift_Amt,
  input  [3:0] Op,
  input  [1:0] Post,
  input  Shft,
  input  in_5,
  input  in_6,
  input  [15:0] in_7,
  input  [15:0] in_8,
  input  in_9,
  input  in_10,
  input  in_11,
  input  in_12,
  output Condition_Met,
  output [15:0] out_14
);

  wire alu_op_decoder_1_comp, alu_op_decoder_1_count, alu_op_decoder_1_ext, alu_op_decoder_1_logic,
       alu_op_decoder_1_pass, alu_op_decoder_1_rand, alu_op_decoder_1_shift, alu_op_decoder_1_sum, and_1_out,
       demultiplexer_1_out1, demultiplexer_1_out2, demultiplexer_1_out3, demultiplexer_1_out4,
       demultiplexer_1_out5, demultiplexer_1_out6, demultiplexer_1_out7, demultiplexer_2_out0,
       demultiplexer_2_out1, demultiplexer_2_out2, demultiplexer_2_out3, not_1_out, not_2_out, not_3_out,
       or_1_out, or_3_out, or_4_out;
  wire [2:0] n4_buf_1_out_3_2;
  wire [3:0] n4_buf_2_out_3;
  wire [3:3] n4_buf_1_out_3;
  wire [15:0] alu_logic_unit_1_p3, barrel_shifter_1_out_4, bit_counter_1_out_3, multiplexer_1_out,
       multiplexer_2_out, multiplexer_3_out, n16_buf_ns_1_out_3, n16_buf_ns_2_out_3, n16_buf_ns_3_out_3,
       n16_buf_ns_4_out_3, n16_buf_ns_5_out_3, n16_buf_ns_6_out_3, n16_buf_ns_7_out_3, n16_buf_ns_8_out_3,
       n16_buf_ns_9_out_3, n16_buf_ns_10_out_3, n16_buf_ns_11_out_3, n16_fulladder_1_out_4,
       n16_fulladder_2_out_4, n16_fulladder_3_out_4, n16_fulladder_4_out_4, n16_negator_1_out_3,
       n16_negator_2_out_3, n16_negator_3_out_3, n16_ram_1_out_5, n16_ram_2_out_5, or_2_out,
       random_gen_1_out_2;

  // Probe on in_7
  // Probe on in_8
  _16_RAM u_16_ram_1 (.in_2(in_7), .out_5(n16_ram_1_out_5), .in_3(in_10), .in_1(in_5), .in_4(in_9));
  _16_Negator u_16_negator_1 (.in_2(demultiplexer_1_out1), .in_1(n16_ram_1_out_5), .out_3(n16_negator_1_out_3));
  _16_FullAdder u_16_fulladder_1 (
    .in_2(n16_negator_1_out_3), .in_3(multiplexer_2_out), .out_4(n16_fulladder_1_out_4),
    .in_1(demultiplexer_1_out3));  // open: out_5
  _16_BUF_NS u_16_buf_ns_1 (.in_2(alu_op_decoder_1_sum), .in_1(n16_fulladder_1_out_4), .out_3(n16_buf_ns_1_out_3));
  _16_BUF_NS u_16_buf_ns_2 (.in_2(alu_op_decoder_1_logic), .in_1(n16_fulladder_1_out_4), .out_3(n16_buf_ns_2_out_3));
  _16_BUF_NS u_16_buf_ns_3 (.in_2(alu_op_decoder_1_ext), .in_1(n16_fulladder_1_out_4), .out_3(n16_buf_ns_3_out_3));
  _16_BUF_NS u_16_buf_ns_4 (.in_2(alu_op_decoder_1_comp), .in_1(n16_fulladder_1_out_4), .out_3(n16_buf_ns_4_out_3));
  _16_BUF_NS u_16_buf_ns_5 (.in_2(alu_op_decoder_1_pass), .in_1(n16_fulladder_1_out_4), .out_3(n16_buf_ns_5_out_3));
  _16_BUF_NS u_16_buf_ns_6 (.in_2(alu_op_decoder_1_sum), .in_1(n16_fulladder_2_out_4), .out_3(n16_buf_ns_6_out_3));
  _16_BUF_NS u_16_buf_ns_7 (.in_2(alu_op_decoder_1_logic), .in_1(n16_fulladder_2_out_4), .out_3(n16_buf_ns_7_out_3));
  _16_BUF_NS u_16_buf_ns_8 (.in_2(alu_op_decoder_1_comp), .in_1(n16_fulladder_2_out_4), .out_3(n16_buf_ns_8_out_3));
  _16_BUF_NS u_16_buf_ns_9 (.in_2(demultiplexer_2_out0), .in_1(or_2_out), .out_3(n16_buf_ns_9_out_3));
  _16_RAM u_16_ram_2 (.in_2(in_8), .out_5(n16_ram_2_out_5), .in_3(in_12), .in_1(in_6), .in_4(in_11));
  _16_Negator u_16_negator_2 (.in_2(or_1_out), .in_1(n16_ram_2_out_5), .out_3(n16_negator_2_out_3));
  _16_FullAdder u_16_fulladder_2 (
    .in_2(n16_negator_2_out_3), .in_3(multiplexer_3_out), .out_4(n16_fulladder_2_out_4), .in_1(or_4_out));  // open: out_5
  _16_BUF_NS u_16_buf_ns_10 (.in_2(or_3_out), .in_1(or_2_out), .out_3(n16_buf_ns_10_out_3));
  _16_BUF_NS u_16_buf_ns_11 (.in_2(demultiplexer_2_out1), .in_1(or_2_out), .out_3(n16_buf_ns_11_out_3));
  _16_Negator u_16_negator_3 (.in_2(demultiplexer_2_out1), .in_1(n16_buf_ns_11_out_3), .out_3(n16_negator_3_out_3));
  _16_FullAdder u_16_fulladder_3 (
    .in_2(n16_buf_ns_10_out_3), .in_3(multiplexer_1_out), .out_4(n16_fulladder_3_out_4),
    .in_1(demultiplexer_2_out2));  // open: out_5
  Demultiplexer #(.select(3), .enable("false")) demultiplexer_1 (
    .out1(demultiplexer_1_out1), .out2(demultiplexer_1_out2), .out3(demultiplexer_1_out3),
    .out4(demultiplexer_1_out4), .out5(demultiplexer_1_out5), .out6(demultiplexer_1_out6),
    .out7(demultiplexer_1_out7), .in(1'b1), .sel(n4_buf_1_out_3_2));  // open: out0
  or or_1 (or_1_out, demultiplexer_1_out2, demultiplexer_1_out7);
  _16_FullAdder u_16_fulladder_4 (
    .in_2(n16_buf_ns_1_out_3), .in_3(n16_buf_ns_6_out_3), .out_4(n16_fulladder_4_out_4), .in_1(1'b0));  // open: out_5
  assign or_2_out = n16_buf_ns_5_out_3 | n16_fulladder_4_out_4 | alu_logic_unit_1_p3 | barrel_shifter_1_out_4 | bit_counter_1_out_3 | random_gen_1_out_2;  // OR_Gate or_2, 16 bits wide
  or or_3 (or_3_out, demultiplexer_2_out2, demultiplexer_2_out3);
  or or_4 (or_4_out, demultiplexer_1_out7, demultiplexer_1_out4);
  Multiplexer #(.width(16), .enable("false")) multiplexer_1 (
    .in0({16{1'b0}}), .in1({16{1'b1}}), .out(multiplexer_1_out), .sel(demultiplexer_2_out3));
  not not_1 (not_1_out, and_1_out);
  _4_BUF u_4_buf_1 (.in_2(Pre_Shift_Amt), .out_3({n4_buf_1_out_3[3], n4_buf_1_out_3_2}), .in_1(not_1_out));
  Multiplexer #(.width(16), .enable("false")) multiplexer_2 (
    .in0({16{1'b0}}), .in1({16{1'b1}}), .out(multiplexer_2_out), .sel(demultiplexer_1_out5));
  Multiplexer #(.width(16), .enable("false")) multiplexer_3 (
    .in0({16{1'b0}}), .in1({16{1'b1}}), .out(multiplexer_3_out), .sel(demultiplexer_1_out6));
  ALU_Op_Decoder alu_op_decoder_1 (
    .PASS(alu_op_decoder_1_pass), .SUM(alu_op_decoder_1_sum), .LOGIC(alu_op_decoder_1_logic),
    .EXT(alu_op_decoder_1_ext), .COMP(alu_op_decoder_1_comp), .in_1(Op[0]), .in_2(Op[1]), .in_3(Op[2]),
    .in_4(Op[3]), .Shift(alu_op_decoder_1_shift), .Count(alu_op_decoder_1_count), .Rand(alu_op_decoder_1_rand));
  // ALU_Logic_Unit alu_logic_unit_1: pin names not known; wires that end beside it: n16_buf_ns_2_out_3, n16_buf_ns_7_out_3, alu_logic_unit_1_p3, Op
  assign out_14 = n16_buf_ns_9_out_3 | n16_negator_3_out_3 | n16_fulladder_3_out_4;  // OR_Gate or_5, 16 bits wide
  and and_1 (and_1_out, Op[0], not_2_out, not_3_out, Op[2]);
  Barrel_Shifter barrel_shifter_1 (
    .in_1(Shft), .in_2(n4_buf_2_out_3), .in_3(n16_buf_ns_3_out_3), .out_4(barrel_shifter_1_out_4));
  not not_2 (not_2_out, Op[1]);
  not not_3 (not_3_out, Op[3]);
  _4_BUF u_4_buf_2 (.in_2(Pre_Shift_Amt), .out_3(n4_buf_2_out_3), .in_1(alu_op_decoder_1_shift));
  Bit_Counter bit_counter_1 (.in_1(n16_buf_ns_3_out_3), .in_2(alu_op_decoder_1_count), .out_3(bit_counter_1_out_3));
  Demultiplexer #(.select(2), .enable("false")) demultiplexer_2 (
    .out0(demultiplexer_2_out0), .out1(demultiplexer_2_out1), .out2(demultiplexer_2_out2),
    .out3(demultiplexer_2_out3), .in(1'b1), .sel(Post));
  Random_Gen random_gen_1 (.in_1(alu_op_decoder_1_rand), .out_2(random_gen_1_out_2));
  Comparator comparator_1 (.in_2(n16_buf_ns_4_out_3), .in_3(n16_buf_ns_8_out_3), .in_1(Op), .out_4(Condition_Met));

  // Notes on the sheet:
  //   Comparator
  //   50 Ticks seems to be safe for
  //   the accumulator's rising edge.
  //   Sum
  //   Logic
  //   External
  //   Pass
  //   8 -
  //   9 -
  //   OPCodes
  //   0 - PASS
  //   1 - SUM
  //   2 - OR
  //   3 - AND
  //   4 - XOR
  //   5 - Shift
  //   6 - Bit Count
  //   7 - Random
  //   10 - A  = B
  //   11 - A != B
  //   12 - A < B
  //   13 - A > B
  //   14 - A <= B
  //   15 - A >= B
  //   PreOp
  //   0 - PASS
  //   1 - !A
  //   2 - !B
  //   3 - INC A
  //   4 - INC B
  //   5 - DEC A
  //   6 - DEC B
  //   7 - 2COMP B
  //   Post OP
  //   0 - PASS
  //   1 - Negate
  //   2 - INC
  //   3 - DEC
  //   Shift Dir
  //   0 <, 1 >
  //   Comparator
endmodule

module ALU_Op_Decoder (
  input  in_1,
  input  in_2,
  input  in_3,
  input  in_4,
  output PASS,
  output SUM,
  output LOGIC,
  output EXT,
  output COMP,
  output Shift,
  output Count,
  output Rand
);

  wire and_2_out, and_3_out, and_7_out, and_9_out, and_10_out, not_1_out, not_2_out, not_3_out, not_4_out,
       not_5_out, not_6_out, not_7_out, not_8_out, not_9_out, not_10_out, not_11_out, not_12_out, not_13_out,
       not_14_out, not_15_out, not_16_out, not_17_out, not_18_out, or_2_out, or_3_out;

  and and_1 (COMP, in_4, not_1_out);
  or or_1 (EXT, and_3_out, Rand, and_2_out, Count, Shift);
  or or_2 (or_2_out, and_2_out, and_3_out);
  not not_1 (not_1_out, or_2_out);
  not not_2 (not_2_out, in_2);
  not not_3 (not_3_out, in_3);
  not not_4 (not_4_out, in_3);
  and and_2 (and_2_out, in_4, not_4_out, not_2_out, in_1);
  not not_5 (not_5_out, in_4);
  not not_6 (not_6_out, in_2);
  not not_7 (not_7_out, in_1);
  and and_3 (and_3_out, in_4, not_3_out, not_6_out, not_7_out);
  and and_4 (Rand, not_5_out, in_3, in_2, in_1);
  and and_5 (LOGIC, or_3_out, not_8_out);
  not not_8 (not_8_out, in_4);
  not not_9 (not_9_out, in_4);
  not not_10 (not_10_out, in_1);
  and and_6 (Count, not_9_out, in_3, in_2, not_10_out);
  or or_3 (or_3_out, and_10_out, and_9_out, and_7_out);
  and and_7 (and_7_out, in_3, not_11_out, not_12_out);
  not not_11 (not_11_out, in_2);
  not not_12 (not_12_out, in_1);
  not not_13 (not_13_out, in_4);
  not not_14 (not_14_out, in_2);
  and and_8 (Shift, not_13_out, in_3, not_14_out, in_1);
  and and_9 (and_9_out, not_15_out, in_2, in_1);
  and and_10 (and_10_out, not_17_out, in_2, not_16_out);
  not not_15 (not_15_out, in_3);
  not not_16 (not_16_out, in_1);
  not not_17 (not_17_out, in_3);
  nor nor_1 (SUM, in_4, in_3, in_2, not_18_out);
  not not_18 (not_18_out, in_1);
  nor nor_2 (PASS, in_4, in_3, in_2, in_1);
endmodule

module ALU_Logic_Unit (
  input  [3:0] in_1,
  input  [15:0] in_2,
  input  [15:0] in_3,
  output [15:0] out_4
);

  wire demultiplexer_1_out2, demultiplexer_1_out3, demultiplexer_1_out4;
  wire [15:0] and_1_out, n16_buf_ns_1_out_3, n16_buf_ns_2_out_3, n16_buf_ns_3_out_3, n16_buf_ns_4_out_3,
       n16_buf_ns_5_out_3, n16_buf_ns_6_out_3, or_1_out, xor_1_out;

  _16_BUF_NS u_16_buf_ns_1 (.in_2(demultiplexer_1_out2), .in_1(in_2), .out_3(n16_buf_ns_1_out_3));
  assign or_1_out = n16_buf_ns_1_out_3 | n16_buf_ns_4_out_3;  // OR_Gate or_1, 16 bits wide
  _16_BUF_NS u_16_buf_ns_2 (.in_2(demultiplexer_1_out4), .in_1(in_2), .out_3(n16_buf_ns_2_out_3));
  _16_BUF_NS u_16_buf_ns_3 (.in_2(demultiplexer_1_out3), .in_1(in_2), .out_3(n16_buf_ns_3_out_3));
  assign and_1_out = n16_buf_ns_3_out_3 & n16_buf_ns_5_out_3;  // AND_Gate and_1, 16 bits wide
  assign out_4 = or_1_out | and_1_out | xor_1_out;  // OR_Gate or_2, 16 bits wide
  assign xor_1_out = n16_buf_ns_2_out_3 ^ n16_buf_ns_6_out_3;  // XOR_Gate xor_1, 16 bits wide
  _16_BUF_NS u_16_buf_ns_4 (.in_2(demultiplexer_1_out2), .in_1(in_3), .out_3(n16_buf_ns_4_out_3));
  _16_BUF_NS u_16_buf_ns_5 (.in_2(demultiplexer_1_out3), .in_1(in_3), .out_3(n16_buf_ns_5_out_3));
  _16_BUF_NS u_16_buf_ns_6 (.in_2(demultiplexer_1_out4), .in_1(in_3), .out_3(n16_buf_ns_6_out_3));
  Demultiplexer #(.select(4), .enable("false")) demultiplexer_1 (
    .out2(demultiplexer_1_out2), .out3(demultiplexer_1_out3), .out4(demultiplexer_1_out4), .in(1'b1),
    .sel(in_1));  // open: out0, out1, out5, out6, out7, out8, out9, out10, out11, out12, out13, out14, out15
endmodule

module Bit_Counter (
  input  [15:0] in_1,
  input  in_2,
  output [15:0] out_3
);

  wire n16_fa_1_out_4, n16_fa_1_out_5, n16_fa_2_out_4, n16_fa_2_out_5, n16_fa_3_out_4, n16_fa_3_out_5,
       n16_fa_4_out_4, n16_fa_4_out_5, n16_fa_5_out_4, n16_fa_5_out_5, n16_fa_6_out_4, n16_fa_6_out_5,
       n16_fa_7_out_4, n16_fa_7_out_5, n16_fa_8_out_4, n16_fa_8_out_5, n16_fa_9_out_4, n16_fa_9_out_5,
       n16_fa_10_out_4, n16_fa_10_out_5, n16_fa_11_out_4, n16_fa_11_out_5, n16_ha_1_out_4, n16_ha_2_out_4,
       n16_ha_3_out_4;
  wire [15:0] n16_buf_1_out_3;

  _16_BUF u_16_buf_1 (.in_1(in_1), .in_2(in_2), .out_3(n16_buf_1_out_3));
  _16_FA u_16_fa_1 (
    .in_2(n16_buf_1_out_3[14]), .in_3(n16_buf_1_out_3[13]), .out_4(n16_fa_1_out_4),
    .in_1(n16_buf_1_out_3[12]), .out_5(n16_fa_1_out_5));
  _16_FA u_16_fa_2 (
    .in_2(n16_buf_1_out_3[11]), .in_3(n16_buf_1_out_3[10]), .out_4(n16_fa_2_out_4),
    .in_1(n16_buf_1_out_3[9]), .out_5(n16_fa_2_out_5));
  _16_FA u_16_fa_3 (
    .in_2(n16_buf_1_out_3[7]), .in_3(n16_buf_1_out_3[6]), .out_4(n16_fa_3_out_4), .in_1(n16_buf_1_out_3[5]),
    .out_5(n16_fa_3_out_5));
  _16_FA u_16_fa_4 (
    .in_2(n16_buf_1_out_3[4]), .in_3(n16_buf_1_out_3[3]), .out_4(n16_fa_4_out_4), .in_1(n16_buf_1_out_3[2]),
    .out_5(n16_fa_4_out_5));
  _16_FA u_16_fa_5 (
    .in_2(n16_fa_1_out_4), .in_3(n16_fa_2_out_4), .out_4(n16_fa_5_out_4), .in_1(n16_buf_1_out_3[8]),
    .out_5(n16_fa_5_out_5));
  _16_FA u_16_fa_6 (
    .in_2(n16_fa_1_out_5), .in_3(n16_fa_2_out_5), .out_4(n16_fa_6_out_4), .in_1(n16_fa_5_out_5),
    .out_5(n16_fa_6_out_5));
  _16_FA u_16_fa_7 (
    .in_2(n16_fa_3_out_4), .in_3(n16_fa_4_out_4), .out_4(n16_fa_7_out_4), .in_1(n16_buf_1_out_3[1]),
    .out_5(n16_fa_7_out_5));
  _16_FA u_16_fa_8 (
    .in_2(n16_fa_3_out_5), .in_3(n16_fa_4_out_5), .out_4(n16_fa_8_out_4), .in_1(n16_fa_7_out_5),
    .out_5(n16_fa_8_out_5));
  _16_FA u_16_fa_9 (
    .in_2(n16_fa_5_out_4), .in_3(n16_fa_7_out_4), .out_4(n16_fa_9_out_4), .in_1(n16_buf_1_out_3[0]),
    .out_5(n16_fa_9_out_5));
  _16_FA u_16_fa_10 (
    .in_2(n16_fa_6_out_4), .in_3(n16_fa_8_out_4), .out_4(n16_fa_10_out_4), .in_1(n16_fa_9_out_5),
    .out_5(n16_fa_10_out_5));
  _16_FA u_16_fa_11 (
    .in_2(n16_fa_6_out_5), .in_3(n16_fa_8_out_5), .out_4(n16_fa_11_out_4), .in_1(n16_fa_10_out_5),
    .out_5(n16_fa_11_out_5));
  _16_HA u_16_ha_1 (.in_2(n16_fa_9_out_4), .out_3(out_3[0]), .in_1(n16_buf_1_out_3[15]), .out_4(n16_ha_1_out_4));
  _16_HA u_16_ha_2 (.in_2(n16_fa_10_out_4), .out_3(out_3[1]), .in_1(n16_ha_1_out_4), .out_4(n16_ha_2_out_4));
  _16_HA u_16_ha_3 (.in_2(n16_fa_11_out_4), .out_3(out_3[2]), .in_1(n16_ha_2_out_4), .out_4(n16_ha_3_out_4));
  _16_HA u_16_ha_4 (.in_2(n16_fa_11_out_5), .out_3(out_3[3]), .in_1(n16_ha_3_out_4), .out_4(out_3[4]));

  assign out_3[15:5] = {11{1'b0}};
endmodule

module Random_Gen (
  input  in_1,
  output [15:0] out_2
);

  wire and_1_out, and_2_out, and_3_out, and_4_out, and_5_out, and_6_out, and_7_out, and_8_out, and_9_out,
       and_10_out, and_11_out, and_12_out, and_13_out, and_14_out, and_15_out, and_16_out, buffer_1_out,
       buffer_2_out, buffer_3_out, clock_1_out, clock_2_out, clock_3_out, clock_4_out, clock_5_out,
       clock_6_out, clock_7_out, clock_8_out, clock_9_out, clock_10_out, clock_11_out, clock_12_out,
       clock_13_out, clock_14_out, clock_15_out, clock_16_out, not_1_out, t_ff_1_q, t_ff_2_q, t_ff_3_q,
       t_ff_4_q, t_ff_5_q, t_ff_6_q, t_ff_7_q, t_ff_8_q, t_ff_9_q, t_ff_10_q, t_ff_11_q, t_ff_12_q,
       t_ff_13_q, t_ff_14_q, t_ff_15_q, t_ff_16_q, xor_1_out;

  buf buffer_1 (buffer_1_out, in_1);
  buf buffer_2 (buffer_2_out, buffer_1_out);
  buf buffer_3 (buffer_3_out, buffer_2_out);
  xor xor_1 (xor_1_out, buffer_3_out, in_1);
  T_Flip_Flop t_ff_1 (.clk(clock_1_out), .T(clock_1_out), .Q(t_ff_1_q));  // open: Qn, preset, reset, en
  Clock #(.highDuration(11), .lowDuration(7)) clock_1 (.out(clock_1_out));
  T_Flip_Flop t_ff_2 (.clk(clock_2_out), .T(clock_2_out), .Q(t_ff_2_q));  // open: Qn, preset, reset, en
  Clock #(.highDuration(7), .lowDuration(7)) clock_2 (.out(clock_2_out));
  Clock #(.highDuration(7), .lowDuration(5)) clock_3 (.out(clock_3_out));
  T_Flip_Flop t_ff_3 (.clk(clock_3_out), .T(clock_3_out), .Q(t_ff_3_q));  // open: Qn, preset, reset, en
  T_Flip_Flop t_ff_4 (.clk(clock_4_out), .T(clock_4_out), .Q(t_ff_4_q));  // open: Qn, preset, reset, en
  Clock #(.highDuration(7), .lowDuration(3)) clock_4 (.out(clock_4_out));
  T_Flip_Flop t_ff_5 (.clk(clock_5_out), .T(clock_5_out), .Q(t_ff_5_q));  // open: Qn, preset, reset, en
  Clock #(.highDuration(5), .lowDuration(7)) clock_5 (.out(clock_5_out));
  Clock #(.highDuration(5), .lowDuration(5)) clock_6 (.out(clock_6_out));
  T_Flip_Flop t_ff_6 (.clk(clock_6_out), .T(clock_6_out), .Q(t_ff_6_q));  // open: Qn, preset, reset, en
  T_Flip_Flop t_ff_7 (.clk(clock_7_out), .T(clock_7_out), .Q(t_ff_7_q));  // open: Qn, preset, reset, en
  Clock #(.highDuration(5), .lowDuration(3)) clock_7 (.out(clock_7_out));
  Clock #(.highDuration(3), .lowDuration(11)) clock_8 (.out(clock_8_out));
  T_Flip_Flop t_ff_8 (.clk(clock_8_out), .T(clock_8_out), .Q(t_ff_8_q));  // open: Qn, preset, reset, en
  T_Flip_Flop t_ff_9 (.clk(clock_9_out), .T(clock_9_out), .Q(t_ff_9_q));  // open: Qn, preset, reset, en
  Clock #(.highDuration(3), .lowDuration(7)) clock_9 (.out(clock_9_out));
  T_Flip_Flop t_ff_10 (.clk(clock_10_out), .T(clock_10_out), .Q(t_ff_10_q));  // open: Qn, preset, reset, en
  Clock #(.highDuration(3), .lowDuration(5)) clock_10 (.out(clock_10_out));
  Clock #(.highDuration(3)) clock_11 (.out(clock_11_out));
  T_Flip_Flop t_ff_11 (.clk(clock_11_out), .T(clock_11_out), .Q(t_ff_11_q));  // open: Qn, preset, reset, en
  T_Flip_Flop t_ff_12 (.clk(clock_12_out), .T(clock_12_out), .Q(t_ff_12_q));  // open: Qn, preset, reset, en
  Clock #(.lowDuration(7)) clock_12 (.out(clock_12_out));
  T_Flip_Flop t_ff_13 (.clk(clock_13_out), .T(clock_13_out), .Q(t_ff_13_q));  // open: Qn, preset, reset, en
  Clock #(.lowDuration(5)) clock_13 (.out(clock_13_out));
  Clock #(.lowDuration(13)) clock_14 (.out(clock_14_out));
  T_Flip_Flop t_ff_14 (.clk(clock_14_out), .T(clock_14_out), .Q(t_ff_14_q));  // open: Qn, preset, reset, en
  Clock #(.lowDuration(11)) clock_15 (.out(clock_15_out));
  T_Flip_Flop t_ff_15 (.clk(clock_15_out), .T(clock_15_out), .Q(t_ff_15_q));  // open: Qn, preset, reset, en
  Clock #(.lowDuration(3)) clock_16 (.out(clock_16_out));
  T_Flip_Flop t_ff_16 (.clk(clock_16_out), .T(clock_16_out), .Q(t_ff_16_q));  // open: Qn, preset, reset, en
  and and_1 (and_1_out, xor_1_out, t_ff_1_q);
  and and_2 (and_2_out, xor_1_out, t_ff_2_q);
  and and_3 (and_3_out, xor_1_out, t_ff_3_q);
  and and_4 (and_4_out, xor_1_out, t_ff_4_q);
  and and_5 (and_5_out, xor_1_out, t_ff_5_q);
  and and_6 (and_6_out, xor_1_out, t_ff_6_q);
  and and_7 (and_7_out, xor_1_out, t_ff_7_q);
  and and_8 (and_8_out, xor_1_out, t_ff_8_q);
  and and_9 (and_9_out, xor_1_out, t_ff_9_q);
  and and_10 (and_10_out, xor_1_out, t_ff_10_q);
  and and_11 (and_11_out, xor_1_out, t_ff_11_q);
  and and_12 (and_12_out, xor_1_out, t_ff_12_q);
  and and_13 (and_13_out, xor_1_out, t_ff_13_q);
  and and_14 (and_14_out, xor_1_out, t_ff_14_q);
  and and_15 (and_15_out, xor_1_out, t_ff_15_q);
  and and_16 (and_16_out, xor_1_out, t_ff_16_q);
  not not_1 (not_1_out, in_1);
  RS_NOR rs_nor_1 (.in_1(and_1_out), .in_2(not_1_out), .out_3(out_2[0]));
  RS_NOR rs_nor_2 (.in_1(and_2_out), .in_2(not_1_out), .out_3(out_2[1]));
  RS_NOR rs_nor_3 (.in_1(and_3_out), .in_2(not_1_out), .out_3(out_2[2]));
  RS_NOR rs_nor_4 (.in_1(and_4_out), .in_2(not_1_out), .out_3(out_2[3]));
  RS_NOR rs_nor_5 (.in_1(and_5_out), .in_2(not_1_out), .out_3(out_2[4]));
  RS_NOR rs_nor_6 (.in_1(and_6_out), .in_2(not_1_out), .out_3(out_2[5]));
  RS_NOR rs_nor_7 (.in_1(and_7_out), .in_2(not_1_out), .out_3(out_2[6]));
  RS_NOR rs_nor_8 (.in_1(and_8_out), .in_2(not_1_out), .out_3(out_2[7]));
  RS_NOR rs_nor_9 (.in_1(and_9_out), .in_2(not_1_out), .out_3(out_2[8]));
  RS_NOR rs_nor_10 (.in_1(and_10_out), .in_2(not_1_out), .out_3(out_2[9]));
  RS_NOR rs_nor_11 (.in_1(and_11_out), .in_2(not_1_out), .out_3(out_2[10]));
  RS_NOR rs_nor_12 (.in_1(and_12_out), .in_2(not_1_out), .out_3(out_2[11]));
  RS_NOR rs_nor_13 (.in_1(and_13_out), .in_2(not_1_out), .out_3(out_2[12]));
  RS_NOR rs_nor_14 (.in_1(and_14_out), .in_2(not_1_out), .out_3(out_2[13]));
  RS_NOR rs_nor_15 (.in_1(and_15_out), .in_2(not_1_out), .out_3(out_2[14]));
  RS_NOR rs_nor_16 (.in_1(and_16_out), .in_2(not_1_out), .out_3(out_2[15]));
  // Probe on out_2
endmodule

module Barrel_Shifter (
  input  in_1,
  input  [3:0] in_2,
  input  [15:0] in_3,
  output [15:0] out_4
);

  wire multiplexer_1_out, multiplexer_2_out, multiplexer_3_out, multiplexer_4_out, multiplexer_5_out,
       multiplexer_6_out, multiplexer_7_out, multiplexer_8_out, multiplexer_9_out, multiplexer_10_out,
       multiplexer_11_out, multiplexer_12_out, multiplexer_13_out, multiplexer_14_out, multiplexer_15_out,
       multiplexer_16_out, multiplexer_17_out, multiplexer_18_out, multiplexer_19_out, multiplexer_20_out,
       multiplexer_21_out, multiplexer_22_out, multiplexer_23_out, multiplexer_24_out, multiplexer_25_out,
       multiplexer_26_out, multiplexer_27_out, multiplexer_28_out, multiplexer_29_out, multiplexer_30_out,
       multiplexer_31_out, multiplexer_32_out, multiplexer_33_out, multiplexer_34_out, multiplexer_35_out,
       multiplexer_36_out, multiplexer_37_out, multiplexer_38_out, multiplexer_39_out, multiplexer_40_out,
       multiplexer_41_out, multiplexer_42_out, multiplexer_43_out, multiplexer_44_out, multiplexer_45_out,
       multiplexer_46_out, multiplexer_47_out, multiplexer_48_out, multiplexer_49_out, multiplexer_50_out,
       multiplexer_51_out, multiplexer_52_out, multiplexer_53_out, multiplexer_54_out, multiplexer_55_out,
       multiplexer_56_out, multiplexer_57_out, multiplexer_58_out, multiplexer_59_out, multiplexer_60_out,
       multiplexer_61_out, multiplexer_62_out, multiplexer_63_out, multiplexer_64_out, multiplexer_65_out,
       multiplexer_66_out, multiplexer_67_out, multiplexer_68_out, multiplexer_69_out, multiplexer_70_out,
       multiplexer_71_out, multiplexer_72_out, multiplexer_73_out, multiplexer_74_out, multiplexer_75_out,
       multiplexer_76_out, multiplexer_77_out, multiplexer_78_out, multiplexer_79_out, multiplexer_80_out,
       multiplexer_81_out, multiplexer_82_out, multiplexer_83_out, multiplexer_84_out, multiplexer_85_out,
       multiplexer_86_out, multiplexer_87_out, multiplexer_88_out, multiplexer_89_out, multiplexer_90_out,
       multiplexer_91_out, multiplexer_92_out, multiplexer_93_out, multiplexer_94_out, multiplexer_95_out,
       multiplexer_96_out, multiplexer_97_out, multiplexer_98_out, multiplexer_99_out, multiplexer_100_out,
       multiplexer_101_out, multiplexer_102_out, multiplexer_103_out, multiplexer_104_out,
       multiplexer_105_out, multiplexer_106_out, multiplexer_107_out, multiplexer_108_out,
       multiplexer_109_out, multiplexer_110_out, multiplexer_111_out, multiplexer_112_out;

  Multiplexer #(.enable("false")) multiplexer_1 (.in0(in_3[14]), .in1(1'b0), .out(multiplexer_1_out), .sel(in_1));
  Multiplexer #(.enable("false")) multiplexer_2 (.in0(in_3[13]), .in1(in_3[15]), .out(multiplexer_2_out), .sel(in_1));
  Multiplexer #(.enable("false")) multiplexer_3 (.in0(in_3[12]), .in1(in_3[14]), .out(multiplexer_3_out), .sel(in_1));
  Multiplexer #(.enable("false")) multiplexer_4 (.in0(in_3[11]), .in1(in_3[13]), .out(multiplexer_4_out), .sel(in_1));
  Multiplexer #(.enable("false")) multiplexer_5 (.in0(in_3[10]), .in1(in_3[12]), .out(multiplexer_5_out), .sel(in_1));
  Multiplexer #(.enable("false")) multiplexer_6 (.in0(in_3[9]), .in1(in_3[11]), .out(multiplexer_6_out), .sel(in_1));
  Multiplexer #(.enable("false")) multiplexer_7 (.in0(in_3[8]), .in1(in_3[10]), .out(multiplexer_7_out), .sel(in_1));
  Multiplexer #(.enable("false")) multiplexer_8 (.in0(in_3[7]), .in1(in_3[9]), .out(multiplexer_8_out), .sel(in_1));
  Multiplexer #(.enable("false")) multiplexer_9 (.in0(in_3[6]), .in1(in_3[8]), .out(multiplexer_9_out), .sel(in_1));
  Multiplexer #(.enable("false")) multiplexer_10 (.in0(in_3[5]), .in1(in_3[7]), .out(multiplexer_10_out), .sel(in_1));
  Multiplexer #(.enable("false")) multiplexer_11 (.in0(in_3[4]), .in1(in_3[6]), .out(multiplexer_11_out), .sel(in_1));
  Multiplexer #(.enable("false")) multiplexer_12 (.in0(in_3[3]), .in1(in_3[5]), .out(multiplexer_12_out), .sel(in_1));
  Multiplexer #(.enable("false")) multiplexer_13 (.in0(in_3[2]), .in1(in_3[4]), .out(multiplexer_13_out), .sel(in_1));
  Multiplexer #(.enable("false")) multiplexer_14 (.in0(in_3[1]), .in1(in_3[3]), .out(multiplexer_14_out), .sel(in_1));
  Multiplexer #(.enable("false")) multiplexer_15 (.in0(in_3[0]), .in1(in_3[2]), .out(multiplexer_15_out), .sel(in_1));
  Multiplexer #(.enable("false")) multiplexer_16 (.in0(1'b0), .in1(in_3[1]), .out(multiplexer_16_out), .sel(in_1));
  Multiplexer #(.enable("false")) multiplexer_17 (
    .in0(in_3[15]), .in1(multiplexer_1_out), .out(multiplexer_17_out), .sel(in_2[0]));
  Multiplexer #(.enable("false")) multiplexer_18 (
    .in0(in_3[14]), .in1(multiplexer_2_out), .out(multiplexer_18_out), .sel(in_2[0]));
  Multiplexer #(.enable("false")) multiplexer_19 (
    .in0(in_3[13]), .in1(multiplexer_3_out), .out(multiplexer_19_out), .sel(in_2[0]));
  Multiplexer #(.enable("false")) multiplexer_20 (
    .in0(in_3[12]), .in1(multiplexer_4_out), .out(multiplexer_20_out), .sel(in_2[0]));
  Multiplexer #(.enable("false")) multiplexer_21 (
    .in0(in_3[11]), .in1(multiplexer_5_out), .out(multiplexer_21_out), .sel(in_2[0]));
  Multiplexer #(.enable("false")) multiplexer_22 (
    .in0(in_3[10]), .in1(multiplexer_6_out), .out(multiplexer_22_out), .sel(in_2[0]));
  Multiplexer #(.enable("false")) multiplexer_23 (
    .in0(in_3[9]), .in1(multiplexer_7_out), .out(multiplexer_23_out), .sel(in_2[0]));
  Multiplexer #(.enable("false")) multiplexer_24 (
    .in0(in_3[8]), .in1(multiplexer_8_out), .out(multiplexer_24_out), .sel(in_2[0]));
  Multiplexer #(.enable("false")) multiplexer_25 (
    .in0(in_3[7]), .in1(multiplexer_9_out), .out(multiplexer_25_out), .sel(in_2[0]));
  Multiplexer #(.enable("false")) multiplexer_26 (
    .in0(in_3[6]), .in1(multiplexer_10_out), .out(multiplexer_26_out), .sel(in_2[0]));
  Multiplexer #(.enable("false")) multiplexer_27 (
    .in0(in_3[5]), .in1(multiplexer_11_out), .out(multiplexer_27_out), .sel(in_2[0]));
  Multiplexer #(.enable("false")) multiplexer_28 (
    .in0(in_3[4]), .in1(multiplexer_12_out), .out(multiplexer_28_out), .sel(in_2[0]));
  Multiplexer #(.enable("false")) multiplexer_29 (
    .in0(in_3[3]), .in1(multiplexer_13_out), .out(multiplexer_29_out), .sel(in_2[0]));
  Multiplexer #(.enable("false")) multiplexer_30 (
    .in0(in_3[2]), .in1(multiplexer_14_out), .out(multiplexer_30_out), .sel(in_2[0]));
  Multiplexer #(.enable("false")) multiplexer_31 (
    .in0(in_3[1]), .in1(multiplexer_15_out), .out(multiplexer_31_out), .sel(in_2[0]));
  Multiplexer #(.enable("false")) multiplexer_32 (
    .in0(in_3[0]), .in1(multiplexer_16_out), .out(multiplexer_32_out), .sel(in_2[0]));
  Multiplexer #(.enable("false")) multiplexer_33 (
    .in0(multiplexer_17_out), .in1(multiplexer_34_out), .out(multiplexer_33_out), .sel(in_2[1]));
  Multiplexer #(.enable("false")) multiplexer_34 (
    .in0(multiplexer_19_out), .in1(1'b0), .out(multiplexer_34_out), .sel(in_1));
  Multiplexer #(.enable("false")) multiplexer_35 (
    .in0(multiplexer_18_out), .in1(multiplexer_36_out), .out(multiplexer_35_out), .sel(in_2[1]));
  Multiplexer #(.enable("false")) multiplexer_36 (
    .in0(multiplexer_20_out), .in1(1'b0), .out(multiplexer_36_out), .sel(in_1));
  Multiplexer #(.enable("false")) multiplexer_37 (
    .in0(multiplexer_19_out), .in1(multiplexer_38_out), .out(multiplexer_37_out), .sel(in_2[1]));
  Multiplexer #(.enable("false")) multiplexer_38 (
    .in0(multiplexer_21_out), .in1(multiplexer_17_out), .out(multiplexer_38_out), .sel(in_1));
  Multiplexer #(.enable("false")) multiplexer_39 (
    .in0(multiplexer_20_out), .in1(multiplexer_40_out), .out(multiplexer_39_out), .sel(in_2[1]));
  Multiplexer #(.enable("false")) multiplexer_40 (
    .in0(multiplexer_22_out), .in1(multiplexer_18_out), .out(multiplexer_40_out), .sel(in_1));
  Multiplexer #(.enable("false")) multiplexer_41 (
    .in0(multiplexer_21_out), .in1(multiplexer_42_out), .out(multiplexer_41_out), .sel(in_2[1]));
  Multiplexer #(.enable("false")) multiplexer_42 (
    .in0(multiplexer_23_out), .in1(multiplexer_19_out), .out(multiplexer_42_out), .sel(in_1));
  Multiplexer #(.enable("false")) multiplexer_43 (
    .in0(multiplexer_22_out), .in1(multiplexer_44_out), .out(multiplexer_43_out), .sel(in_2[1]));
  Multiplexer #(.enable("false")) multiplexer_44 (
    .in0(multiplexer_24_out), .in1(multiplexer_20_out), .out(multiplexer_44_out), .sel(in_1));
  Multiplexer #(.enable("false")) multiplexer_45 (
    .in0(multiplexer_23_out), .in1(multiplexer_46_out), .out(multiplexer_45_out), .sel(in_2[1]));
  Multiplexer #(.enable("false")) multiplexer_46 (
    .in0(multiplexer_25_out), .in1(multiplexer_21_out), .out(multiplexer_46_out), .sel(in_1));
  Multiplexer #(.enable("false")) multiplexer_47 (
    .in0(multiplexer_24_out), .in1(multiplexer_48_out), .out(multiplexer_47_out), .sel(in_2[1]));
  Multiplexer #(.enable("false")) multiplexer_48 (
    .in0(multiplexer_26_out), .in1(multiplexer_22_out), .out(multiplexer_48_out), .sel(in_1));
  Multiplexer #(.enable("false")) multiplexer_49 (
    .in0(multiplexer_25_out), .in1(multiplexer_50_out), .out(multiplexer_49_out), .sel(in_2[1]));
  Multiplexer #(.enable("false")) multiplexer_50 (
    .in0(multiplexer_27_out), .in1(multiplexer_23_out), .out(multiplexer_50_out), .sel(in_1));
  Multiplexer #(.enable("false")) multiplexer_51 (
    .in0(multiplexer_26_out), .in1(multiplexer_52_out), .out(multiplexer_51_out), .sel(in_2[1]));
  Multiplexer #(.enable("false")) multiplexer_52 (
    .in0(multiplexer_28_out), .in1(multiplexer_24_out), .out(multiplexer_52_out), .sel(in_1));
  Multiplexer #(.enable("false")) multiplexer_53 (
    .in0(multiplexer_27_out), .in1(multiplexer_54_out), .out(multiplexer_53_out), .sel(in_2[1]));
  Multiplexer #(.enable("false")) multiplexer_54 (
    .in0(multiplexer_29_out), .in1(multiplexer_25_out), .out(multiplexer_54_out), .sel(in_1));
  Multiplexer #(.enable("false")) multiplexer_55 (
    .in0(multiplexer_28_out), .in1(multiplexer_56_out), .out(multiplexer_55_out), .sel(in_2[1]));
  Multiplexer #(.enable("false")) multiplexer_56 (
    .in0(multiplexer_30_out), .in1(multiplexer_26_out), .out(multiplexer_56_out), .sel(in_1));
  Multiplexer #(.enable("false")) multiplexer_57 (
    .in0(multiplexer_29_out), .in1(multiplexer_58_out), .out(multiplexer_57_out), .sel(in_2[1]));
  Multiplexer #(.enable("false")) multiplexer_58 (
    .in0(multiplexer_31_out), .in1(multiplexer_27_out), .out(multiplexer_58_out), .sel(in_1));
  Multiplexer #(.enable("false")) multiplexer_59 (
    .in0(multiplexer_30_out), .in1(multiplexer_60_out), .out(multiplexer_59_out), .sel(in_2[1]));
  Multiplexer #(.enable("false")) multiplexer_60 (
    .in0(multiplexer_32_out), .in1(multiplexer_28_out), .out(multiplexer_60_out), .sel(in_1));
  Multiplexer #(.enable("false")) multiplexer_61 (
    .in0(multiplexer_31_out), .in1(multiplexer_62_out), .out(multiplexer_61_out), .sel(in_2[1]));
  Multiplexer #(.enable("false")) multiplexer_62 (
    .in0(1'b0), .in1(multiplexer_29_out), .out(multiplexer_62_out), .sel(in_1));
  Multiplexer #(.enable("false")) multiplexer_63 (
    .in0(multiplexer_32_out), .in1(multiplexer_64_out), .out(multiplexer_63_out), .sel(in_2[1]));
  Multiplexer #(.enable("false")) multiplexer_64 (
    .in0(1'b0), .in1(multiplexer_30_out), .out(multiplexer_64_out), .sel(in_1));
  Multiplexer #(.enable("false")) multiplexer_65 (
    .in0(multiplexer_41_out), .in1(1'b0), .out(multiplexer_65_out), .sel(in_1));
  Multiplexer #(.enable("false")) multiplexer_66 (
    .in0(multiplexer_43_out), .in1(1'b0), .out(multiplexer_66_out), .sel(in_1));
  Multiplexer #(.enable("false")) multiplexer_67 (
    .in0(multiplexer_45_out), .in1(1'b0), .out(multiplexer_67_out), .sel(in_1));
  Multiplexer #(.enable("false")) multiplexer_68 (
    .in0(multiplexer_47_out), .in1(1'b0), .out(multiplexer_68_out), .sel(in_1));
  Multiplexer #(.enable("false")) multiplexer_69 (
    .in0(multiplexer_49_out), .in1(multiplexer_33_out), .out(multiplexer_69_out), .sel(in_1));
  Multiplexer #(.enable("false")) multiplexer_70 (
    .in0(multiplexer_51_out), .in1(multiplexer_35_out), .out(multiplexer_70_out), .sel(in_1));
  Multiplexer #(.enable("false")) multiplexer_71 (
    .in0(multiplexer_53_out), .in1(multiplexer_37_out), .out(multiplexer_71_out), .sel(in_1));
  Multiplexer #(.enable("false")) multiplexer_72 (
    .in0(multiplexer_55_out), .in1(multiplexer_39_out), .out(multiplexer_72_out), .sel(in_1));
  Multiplexer #(.enable("false")) multiplexer_73 (
    .in0(multiplexer_57_out), .in1(multiplexer_41_out), .out(multiplexer_73_out), .sel(in_1));
  Multiplexer #(.enable("false")) multiplexer_74 (
    .in0(multiplexer_59_out), .in1(multiplexer_43_out), .out(multiplexer_74_out), .sel(in_1));
  Multiplexer #(.enable("false")) multiplexer_75 (
    .in0(multiplexer_61_out), .in1(multiplexer_45_out), .out(multiplexer_75_out), .sel(in_1));
  Multiplexer #(.enable("false")) multiplexer_76 (
    .in0(multiplexer_63_out), .in1(multiplexer_47_out), .out(multiplexer_76_out), .sel(in_1));
  Multiplexer #(.enable("false")) multiplexer_77 (
    .in0(1'b0), .in1(multiplexer_49_out), .out(multiplexer_77_out), .sel(in_1));
  Multiplexer #(.enable("false")) multiplexer_78 (
    .in0(1'b0), .in1(multiplexer_51_out), .out(multiplexer_78_out), .sel(in_1));
  Multiplexer #(.enable("false")) multiplexer_79 (
    .in0(1'b0), .in1(multiplexer_53_out), .out(multiplexer_79_out), .sel(in_1));
  Multiplexer #(.enable("false")) multiplexer_80 (
    .in0(1'b0), .in1(multiplexer_55_out), .out(multiplexer_80_out), .sel(in_1));
  Multiplexer #(.enable("false")) multiplexer_81 (
    .in0(multiplexer_33_out), .in1(multiplexer_65_out), .out(multiplexer_81_out), .sel(in_2[2]));
  Multiplexer #(.enable("false")) multiplexer_82 (
    .in0(multiplexer_35_out), .in1(multiplexer_66_out), .out(multiplexer_82_out), .sel(in_2[2]));
  Multiplexer #(.enable("false")) multiplexer_83 (
    .in0(multiplexer_37_out), .in1(multiplexer_67_out), .out(multiplexer_83_out), .sel(in_2[2]));
  Multiplexer #(.enable("false")) multiplexer_84 (
    .in0(multiplexer_39_out), .in1(multiplexer_68_out), .out(multiplexer_84_out), .sel(in_2[2]));
  Multiplexer #(.enable("false")) multiplexer_85 (
    .in0(multiplexer_41_out), .in1(multiplexer_69_out), .out(multiplexer_85_out), .sel(in_2[2]));
  Multiplexer #(.enable("false")) multiplexer_86 (
    .in0(multiplexer_43_out), .in1(multiplexer_70_out), .out(multiplexer_86_out), .sel(in_2[2]));
  Multiplexer #(.enable("false")) multiplexer_87 (
    .in0(multiplexer_45_out), .in1(multiplexer_71_out), .out(multiplexer_87_out), .sel(in_2[2]));
  Multiplexer #(.enable("false")) multiplexer_88 (
    .in0(multiplexer_47_out), .in1(multiplexer_72_out), .out(multiplexer_88_out), .sel(in_2[2]));
  Multiplexer #(.enable("false")) multiplexer_89 (
    .in0(multiplexer_49_out), .in1(multiplexer_73_out), .out(multiplexer_89_out), .sel(in_2[2]));
  Multiplexer #(.enable("false")) multiplexer_90 (
    .in0(multiplexer_51_out), .in1(multiplexer_74_out), .out(multiplexer_90_out), .sel(in_2[2]));
  Multiplexer #(.enable("false")) multiplexer_91 (
    .in0(multiplexer_53_out), .in1(multiplexer_75_out), .out(multiplexer_91_out), .sel(in_2[2]));
  Multiplexer #(.enable("false")) multiplexer_92 (
    .in0(multiplexer_55_out), .in1(multiplexer_76_out), .out(multiplexer_92_out), .sel(in_2[2]));
  Multiplexer #(.enable("false")) multiplexer_93 (
    .in0(multiplexer_57_out), .in1(multiplexer_77_out), .out(multiplexer_93_out), .sel(in_2[2]));
  Multiplexer #(.enable("false")) multiplexer_94 (
    .in0(multiplexer_59_out), .in1(multiplexer_78_out), .out(multiplexer_94_out), .sel(in_2[2]));
  Multiplexer #(.enable("false")) multiplexer_95 (
    .in0(multiplexer_61_out), .in1(multiplexer_79_out), .out(multiplexer_95_out), .sel(in_2[2]));
  Multiplexer #(.enable("false")) multiplexer_96 (
    .in0(multiplexer_63_out), .in1(multiplexer_80_out), .out(multiplexer_96_out), .sel(in_2[2]));
  Multiplexer #(.enable("false")) multiplexer_97 (
    .in0(multiplexer_89_out), .in1(1'b0), .out(multiplexer_97_out), .sel(in_1));
  Multiplexer #(.enable("false")) multiplexer_98 (
    .in0(multiplexer_90_out), .in1(1'b0), .out(multiplexer_98_out), .sel(in_1));
  Multiplexer #(.enable("false")) multiplexer_99 (
    .in0(multiplexer_91_out), .in1(1'b0), .out(multiplexer_99_out), .sel(in_1));
  Multiplexer #(.enable("false")) multiplexer_100 (
    .in0(multiplexer_92_out), .in1(1'b0), .out(multiplexer_100_out), .sel(in_1));
  Multiplexer #(.enable("false")) multiplexer_101 (
    .in0(multiplexer_93_out), .in1(1'b0), .out(multiplexer_101_out), .sel(in_1));
  Multiplexer #(.enable("false")) multiplexer_102 (
    .in0(multiplexer_94_out), .in1(1'b0), .out(multiplexer_102_out), .sel(in_1));
  Multiplexer #(.enable("false")) multiplexer_103 (
    .in0(multiplexer_95_out), .in1(1'b0), .out(multiplexer_103_out), .sel(in_1));
  Multiplexer #(.enable("false")) multiplexer_104 (
    .in0(multiplexer_96_out), .in1(1'b0), .out(multiplexer_104_out), .sel(in_1));
  Multiplexer #(.enable("false")) multiplexer_105 (
    .in0(1'b0), .in1(multiplexer_81_out), .out(multiplexer_105_out), .sel(in_1));
  Multiplexer #(.enable("false")) multiplexer_106 (
    .in0(1'b0), .in1(multiplexer_82_out), .out(multiplexer_106_out), .sel(in_1));
  Multiplexer #(.enable("false")) multiplexer_107 (
    .in0(1'b0), .in1(multiplexer_83_out), .out(multiplexer_107_out), .sel(in_1));
  Multiplexer #(.enable("false")) multiplexer_108 (
    .in0(1'b0), .in1(multiplexer_84_out), .out(multiplexer_108_out), .sel(in_1));
  Multiplexer #(.enable("false")) multiplexer_109 (
    .in0(1'b0), .in1(multiplexer_85_out), .out(multiplexer_109_out), .sel(in_1));
  Multiplexer #(.enable("false")) multiplexer_110 (
    .in0(1'b0), .in1(multiplexer_86_out), .out(multiplexer_110_out), .sel(in_1));
  Multiplexer #(.enable("false")) multiplexer_111 (
    .in0(1'b0), .in1(multiplexer_87_out), .out(multiplexer_111_out), .sel(in_1));
  Multiplexer #(.enable("false")) multiplexer_112 (
    .in0(1'b0), .in1(multiplexer_88_out), .out(multiplexer_112_out), .sel(in_1));
  Multiplexer #(.enable("false")) multiplexer_113 (
    .in0(multiplexer_81_out), .in1(multiplexer_97_out), .out(out_4[15]), .sel(in_2[3]));
  Multiplexer #(.enable("false")) multiplexer_114 (
    .in0(multiplexer_82_out), .in1(multiplexer_98_out), .out(out_4[14]), .sel(in_2[3]));
  Multiplexer #(.enable("false")) multiplexer_115 (
    .in0(multiplexer_83_out), .in1(multiplexer_99_out), .out(out_4[13]), .sel(in_2[3]));
  Multiplexer #(.enable("false")) multiplexer_116 (
    .in0(multiplexer_84_out), .in1(multiplexer_100_out), .out(out_4[12]), .sel(in_2[3]));
  Multiplexer #(.enable("false")) multiplexer_117 (
    .in0(multiplexer_85_out), .in1(multiplexer_101_out), .out(out_4[11]), .sel(in_2[3]));
  Multiplexer #(.enable("false")) multiplexer_118 (
    .in0(multiplexer_86_out), .in1(multiplexer_102_out), .out(out_4[10]), .sel(in_2[3]));
  Multiplexer #(.enable("false")) multiplexer_119 (
    .in0(multiplexer_87_out), .in1(multiplexer_103_out), .out(out_4[9]), .sel(in_2[3]));
  Multiplexer #(.enable("false")) multiplexer_120 (
    .in0(multiplexer_88_out), .in1(multiplexer_104_out), .out(out_4[8]), .sel(in_2[3]));
  Multiplexer #(.enable("false")) multiplexer_121 (
    .in0(multiplexer_89_out), .in1(multiplexer_105_out), .out(out_4[7]), .sel(in_2[3]));
  Multiplexer #(.enable("false")) multiplexer_122 (
    .in0(multiplexer_90_out), .in1(multiplexer_106_out), .out(out_4[6]), .sel(in_2[3]));
  Multiplexer #(.enable("false")) multiplexer_123 (
    .in0(multiplexer_91_out), .in1(multiplexer_107_out), .out(out_4[5]), .sel(in_2[3]));
  Multiplexer #(.enable("false")) multiplexer_124 (
    .in0(multiplexer_92_out), .in1(multiplexer_108_out), .out(out_4[4]), .sel(in_2[3]));
  Multiplexer #(.enable("false")) multiplexer_125 (
    .in0(multiplexer_93_out), .in1(multiplexer_109_out), .out(out_4[3]), .sel(in_2[3]));
  Multiplexer #(.enable("false")) multiplexer_126 (
    .in0(multiplexer_94_out), .in1(multiplexer_110_out), .out(out_4[2]), .sel(in_2[3]));
  Multiplexer #(.enable("false")) multiplexer_127 (
    .in0(multiplexer_95_out), .in1(multiplexer_111_out), .out(out_4[1]), .sel(in_2[3]));
  Multiplexer #(.enable("false")) multiplexer_128 (
    .in0(multiplexer_96_out), .in1(multiplexer_112_out), .out(out_4[0]), .sel(in_2[3]));
endmodule

module Comparator (
  input  [3:0] in_1,
  input  [15:0] in_2,
  input  [15:0] in_3,
  output out_4
);

  wire and_2_out, and_3_out, and_4_out, and_5_out, and_6_out, and_out, demultiplexer_1_out10,
       demultiplexer_1_out11, demultiplexer_1_out12, demultiplexer_1_out13, demultiplexer_1_out14,
       demultiplexer_1_out15, n4_comparator_1_out_6, n4_comparator_1_out_7, n4_comparator_2_out_6,
       n4_comparator_2_out_7, n4_comparator_3_out_6, n4_comparator_3_out_7, n4_comparator_4_out_6,
       n4_comparator_4_out_7, n4_comparator_4_out_8, or_1_out, or_2_out, or_3_out;

  _4_Comparator u_4_comparator_1 (
    .in_1(in_2[3:0]), .in_2(in_3[3:0]), .in_3(1'b0), .in_4(1'b1), .in_5(1'b1), .out_6(n4_comparator_1_out_6),
    .out_7(n4_comparator_1_out_7));  // open: out_8
  _4_Comparator u_4_comparator_2 (
    .in_1(in_2[7:4]), .in_2(in_3[7:4]), .in_3(n4_comparator_1_out_6), .in_4(n4_comparator_1_out_7),
    .in_5(1'b1), .out_6(n4_comparator_2_out_6), .out_7(n4_comparator_2_out_7));  // open: out_8
  _4_Comparator u_4_comparator_3 (
    .in_1(in_2[11:8]), .in_2(in_3[11:8]), .in_3(n4_comparator_2_out_6), .in_4(n4_comparator_2_out_7),
    .in_5(1'b1), .out_6(n4_comparator_3_out_6), .out_7(n4_comparator_3_out_7));  // open: out_8
  _4_Comparator u_4_comparator_4 (
    .in_1(in_2[15:12]), .in_2(in_3[15:12]), .in_3(n4_comparator_3_out_6), .in_4(n4_comparator_3_out_7),
    .in_5(1'b1), .out_6(n4_comparator_4_out_6), .out_7(n4_comparator_4_out_7), .out_8(n4_comparator_4_out_8));
  Demultiplexer #(.select(4), .enable("false")) demultiplexer_1 (
    .out10(demultiplexer_1_out10), .out11(demultiplexer_1_out11), .out12(demultiplexer_1_out12),
    .out13(demultiplexer_1_out13), .out14(demultiplexer_1_out14), .out15(demultiplexer_1_out15), .in(1'b1),
    .sel(in_1));  // open: out0, out1, out2, out3, out4, out5, out6, out7, out8, out9
  or or_1 (or_1_out, n4_comparator_4_out_7, n4_comparator_4_out_6);
  or or_2 (or_2_out, n4_comparator_4_out_8, n4_comparator_4_out_7);
  or or_3 (or_3_out, n4_comparator_4_out_6, n4_comparator_4_out_8);
  and \and  (and_out, n4_comparator_4_out_7, demultiplexer_1_out10);
  and and_2 (and_2_out, or_3_out, demultiplexer_1_out11);
  and and_3 (and_3_out, n4_comparator_4_out_6, demultiplexer_1_out12);
  and and_4 (and_4_out, n4_comparator_4_out_8, demultiplexer_1_out13);
  and and_5 (and_5_out, or_1_out, demultiplexer_1_out14);
  and and_6 (and_6_out, or_2_out, demultiplexer_1_out15);
  or or_4 (out_4, and_out, and_2_out, and_3_out, and_4_out, and_5_out, and_6_out);

  // Notes on the sheet:
  //   10 - A  = B
  //   11 - A != B
  //   12 - A < B
  //   13 - A > B
  //   14 - A <= B
  //   15 - A >= B
endmodule

module _16_RAM (
  input  in_1,
  input  [15:0] in_2,
  input  in_3,
  input  in_4,
  output [15:0] out_5
);

  wire d_ff_1_q, d_ff_2_q, d_ff_3_q, d_ff_4_q, d_ff_5_q, d_ff_6_q, d_ff_7_q, d_ff_8_q, d_ff_9_q, d_ff_10_q,
       d_ff_11_q, d_ff_12_q, d_ff_13_q, d_ff_14_q, d_ff_15_q, d_ff_16_q;

  D_Flip_Flop d_ff_1 (.clk(in_1), .D(in_2[0]), .Q(d_ff_1_q), .reset(in_4));  // open: Qn, preset, en
  D_Flip_Flop d_ff_2 (.clk(in_1), .D(in_2[1]), .Q(d_ff_2_q), .reset(in_4));  // open: Qn, preset, en
  D_Flip_Flop d_ff_3 (.clk(in_1), .D(in_2[2]), .Q(d_ff_3_q), .reset(in_4));  // open: Qn, preset, en
  D_Flip_Flop d_ff_4 (.clk(in_1), .D(in_2[3]), .Q(d_ff_4_q), .reset(in_4));  // open: Qn, preset, en
  D_Flip_Flop d_ff_5 (.clk(in_1), .D(in_2[4]), .Q(d_ff_5_q), .reset(in_4));  // open: Qn, preset, en
  D_Flip_Flop d_ff_6 (.clk(in_1), .D(in_2[5]), .Q(d_ff_6_q), .reset(in_4));  // open: Qn, preset, en
  D_Flip_Flop d_ff_7 (.clk(in_1), .D(in_2[6]), .Q(d_ff_7_q), .reset(in_4));  // open: Qn, preset, en
  D_Flip_Flop d_ff_8 (.clk(in_1), .D(in_2[7]), .Q(d_ff_8_q), .reset(in_4));  // open: Qn, preset, en
  D_Flip_Flop d_ff_9 (.clk(in_1), .D(in_2[8]), .Q(d_ff_9_q), .reset(in_4));  // open: Qn, preset, en
  D_Flip_Flop d_ff_10 (.clk(in_1), .D(in_2[9]), .Q(d_ff_10_q), .reset(in_4));  // open: Qn, preset, en
  D_Flip_Flop d_ff_11 (.clk(in_1), .D(in_2[10]), .Q(d_ff_11_q), .reset(in_4));  // open: Qn, preset, en
  D_Flip_Flop d_ff_12 (.clk(in_1), .D(in_2[11]), .Q(d_ff_12_q), .reset(in_4));  // open: Qn, preset, en
  D_Flip_Flop d_ff_13 (.clk(in_1), .D(in_2[12]), .Q(d_ff_13_q), .reset(in_4));  // open: Qn, preset, en
  D_Flip_Flop d_ff_14 (.clk(in_1), .D(in_2[13]), .Q(d_ff_14_q), .reset(in_4));  // open: Qn, preset, en
  D_Flip_Flop d_ff_15 (.clk(in_1), .D(in_2[14]), .Q(d_ff_15_q), .reset(in_4));  // open: Qn, preset, en
  D_Flip_Flop d_ff_16 (.clk(in_1), .D(in_2[15]), .Q(d_ff_16_q), .reset(in_4));  // open: Qn, preset, en
  and and_1 (out_5[0], d_ff_1_q, in_3);
  and and_2 (out_5[1], d_ff_2_q, in_3);
  and and_3 (out_5[2], d_ff_3_q, in_3);
  and and_4 (out_5[3], d_ff_4_q, in_3);
  and and_5 (out_5[4], d_ff_5_q, in_3);
  and and_6 (out_5[5], d_ff_6_q, in_3);
  and and_7 (out_5[6], d_ff_7_q, in_3);
  and and_8 (out_5[7], d_ff_8_q, in_3);
  and and_9 (out_5[8], d_ff_9_q, in_3);
  and and_10 (out_5[9], d_ff_10_q, in_3);
  and and_11 (out_5[10], d_ff_11_q, in_3);
  and and_12 (out_5[11], d_ff_12_q, in_3);
  and and_13 (out_5[12], d_ff_13_q, in_3);
  and and_14 (out_5[13], d_ff_14_q, in_3);
  and and_15 (out_5[14], d_ff_15_q, in_3);
  and and_16 (out_5[15], d_ff_16_q, in_3);
endmodule

module _16_FullAdder (
  input  in_1,
  input  [15:0] in_2,
  input  [15:0] in_3,
  output [15:0] out_4,
  output out_5
);

  wire and_1_out, and_2_out, and_3_out, and_4_out, and_5_out, and_6_out, and_7_out, and_8_out, and_9_out,
       and_10_out, and_11_out, and_12_out, and_13_out, and_14_out, and_15_out, and_16_out, and_17_out,
       and_18_out, and_19_out, and_20_out, and_21_out, and_22_out, and_23_out, and_24_out, and_25_out,
       and_26_out, and_27_out, and_28_out, and_29_out, and_30_out, or_1_out, or_2_out, or_3_out, or_4_out,
       or_5_out, or_6_out, or_7_out, or_8_out, or_9_out, or_10_out, or_11_out, or_12_out, or_13_out,
       or_14_out, or_15_out, xor_1_out, xor_2_out, xor_3_out, xor_4_out, xor_5_out, xor_6_out, xor_7_out,
       xor_8_out, xor_9_out, xor_10_out, xor_11_out, xor_12_out, xor_13_out, xor_14_out, xor_15_out,
       xor_16_out;

  xor xor_1 (xor_1_out, in_2[0], in_3[0]);
  and and_1 (and_1_out, in_2[0], in_3[0]);
  or or_1 (or_1_out, and_1_out, and_16_out);
  xor xor_2 (xor_2_out, in_2[1], in_3[1]);
  and and_2 (and_2_out, in_2[1], in_3[1]);
  or or_2 (or_2_out, and_2_out, and_17_out);
  xor xor_3 (xor_3_out, in_2[2], in_3[2]);
  and and_3 (and_3_out, in_2[2], in_3[2]);
  or or_3 (or_3_out, and_3_out, and_18_out);
  xor xor_4 (xor_4_out, in_2[3], in_3[3]);
  and and_4 (and_4_out, in_2[3], in_3[3]);
  or or_4 (or_4_out, and_4_out, and_19_out);
  xor xor_5 (xor_5_out, in_2[4], in_3[4]);
  and and_5 (and_5_out, in_2[4], in_3[4]);
  or or_5 (or_5_out, and_5_out, and_20_out);
  xor xor_6 (xor_6_out, in_2[5], in_3[5]);
  and and_6 (and_6_out, in_2[5], in_3[5]);
  or or_6 (or_6_out, and_6_out, and_21_out);
  xor xor_7 (xor_7_out, in_2[6], in_3[6]);
  and and_7 (and_7_out, in_2[6], in_3[6]);
  or or_7 (or_7_out, and_7_out, and_22_out);
  xor xor_8 (xor_8_out, in_2[7], in_3[7]);
  and and_8 (and_8_out, in_2[7], in_3[7]);
  or or_8 (or_8_out, and_8_out, and_23_out);
  xor xor_9 (xor_9_out, in_2[8], in_3[8]);
  and and_9 (and_9_out, in_2[8], in_3[8]);
  or or_9 (or_9_out, and_9_out, and_24_out);
  xor xor_10 (xor_10_out, in_2[9], in_3[9]);
  and and_10 (and_10_out, in_2[9], in_3[9]);
  or or_10 (or_10_out, and_10_out, and_25_out);
  xor xor_11 (xor_11_out, in_2[10], in_3[10]);
  and and_11 (and_11_out, in_2[10], in_3[10]);
  or or_11 (or_11_out, and_11_out, and_26_out);
  xor xor_12 (xor_12_out, in_2[11], in_3[11]);
  and and_12 (and_12_out, in_2[11], in_3[11]);
  or or_12 (or_12_out, and_12_out, and_27_out);
  xor xor_13 (xor_13_out, in_2[12], in_3[12]);
  and and_13 (and_13_out, in_2[12], in_3[12]);
  or or_13 (or_13_out, and_13_out, and_28_out);
  xor xor_14 (xor_14_out, in_2[13], in_3[13]);
  and and_14 (and_14_out, in_2[13], in_3[13]);
  or or_14 (or_14_out, and_14_out, and_29_out);
  xor xor_15 (xor_15_out, in_2[14], in_3[14]);
  and and_15 (and_15_out, in_2[14], in_3[14]);
  or or_15 (or_15_out, and_15_out, and_30_out);
  xor xor_16 (xor_16_out, in_2[15], in_3[15]);
  xor xor_17 (out_4[0], xor_1_out, in_1);
  and and_16 (and_16_out, xor_1_out, in_1);
  xor xor_18 (out_4[1], xor_2_out, or_1_out);
  and and_17 (and_17_out, xor_2_out, or_1_out);
  xor xor_19 (out_4[2], xor_3_out, or_2_out);
  and and_18 (and_18_out, xor_3_out, or_2_out);
  xor xor_20 (out_4[3], xor_4_out, or_3_out);
  and and_19 (and_19_out, xor_4_out, or_3_out);
  xor xor_21 (out_4[4], xor_5_out, or_4_out);
  and and_20 (and_20_out, xor_5_out, or_4_out);
  xor xor_22 (out_4[5], xor_6_out, or_5_out);
  and and_21 (and_21_out, xor_6_out, or_5_out);
  xor xor_23 (out_4[6], xor_7_out, or_6_out);
  and and_22 (and_22_out, xor_7_out, or_6_out);
  xor xor_24 (out_4[7], xor_8_out, or_7_out);
  and and_23 (and_23_out, xor_8_out, or_7_out);
  xor xor_25 (out_4[8], xor_9_out, or_8_out);
  and and_24 (and_24_out, xor_9_out, or_8_out);
  xor xor_26 (out_4[9], xor_10_out, or_9_out);
  and and_25 (and_25_out, xor_10_out, or_9_out);
  xor xor_27 (out_4[10], xor_11_out, or_10_out);
  and and_26 (and_26_out, xor_11_out, or_10_out);
  xor xor_28 (out_4[11], xor_12_out, or_11_out);
  and and_27 (and_27_out, xor_12_out, or_11_out);
  xor xor_29 (out_4[12], xor_13_out, or_12_out);
  and and_28 (and_28_out, xor_13_out, or_12_out);
  xor xor_30 (out_4[13], xor_14_out, or_13_out);
  and and_29 (and_29_out, xor_14_out, or_13_out);
  xor xor_31 (out_4[14], xor_15_out, or_14_out);
  and and_30 (and_30_out, xor_15_out, or_14_out);
  xor xor_32 (out_4[15], xor_16_out, or_15_out);

  assign out_5 = out_4[15];
endmodule

module _16_Negator (
  input  [15:0] in_1,
  input  in_2,
  output [15:0] out_3
);

  xor xor_1 (out_3[15], in_1[15], in_2);
  xor xor_2 (out_3[14], in_1[14], in_2);
  xor xor_3 (out_3[13], in_1[13], in_2);
  xor xor_4 (out_3[12], in_1[12], in_2);
  xor xor_5 (out_3[9], in_1[9], in_2);
  xor xor_6 (out_3[10], in_1[10], in_2);
  xor xor_7 (out_3[11], in_1[11], in_2);
  xor xor_8 (out_3[6], in_1[6], in_2);
  xor xor_9 (out_3[8], in_1[8], in_2);
  xor xor_10 (out_3[7], in_1[7], in_2);
  xor xor_11 (out_3[5], in_1[5], in_2);
  xor xor_12 (out_3[4], in_1[4], in_2);
  xor xor_13 (out_3[2], in_1[2], in_2);
  xor xor_14 (out_3[1], in_1[1], in_2);
  xor xor_15 (out_3[3], in_1[3], in_2);
  xor xor_16 (out_3[0], in_1[0], in_2);
endmodule

module _16_BUF_NS (
  input  [15:0] in_1,
  input  in_2,
  output [15:0] out_3
);

  and and_1 (out_3[14], in_1[14], in_2);
  and and_2 (out_3[15], in_1[15], in_2);
  and and_3 (out_3[13], in_1[13], in_2);
  and and_4 (out_3[12], in_1[12], in_2);
  and and_5 (out_3[11], in_1[11], in_2);
  and and_6 (out_3[9], in_1[9], in_2);
  and and_7 (out_3[10], in_1[10], in_2);
  and and_8 (out_3[6], in_1[6], in_2);
  and and_9 (out_3[8], in_1[8], in_2);
  and and_10 (out_3[7], in_1[7], in_2);
  and and_11 (out_3[4], in_1[4], in_2);
  and and_12 (out_3[5], in_1[5], in_2);
  and and_13 (out_3[1], in_1[1], in_2);
  and and_14 (out_3[2], in_1[2], in_2);
  and and_15 (out_3[3], in_1[3], in_2);
  and and_16 (out_3[0], in_1[0], in_2);
endmodule

module _16_FA (
  input  in_1,
  input  in_2,
  input  in_3,
  output out_4,
  output out_5
);

  wire and_1_out, and_2_out, xor_1_out;

  and and_1 (and_1_out, in_2, in_3);
  or or_1 (out_5, and_1_out, and_2_out);
  xor xor_1 (xor_1_out, in_2, in_3);
  and and_2 (and_2_out, xor_1_out, in_1);
  xor xor_2 (out_4, xor_1_out, in_1);
endmodule

module _16_HA (
  input  in_1,
  input  in_2,
  output out_3,
  output out_4
);

  and and_1 (out_4, in_1, in_2);
  xor xor_1 (out_3, in_1, in_2);
endmodule

module _16_BUF (
  input  [15:0] in_1,
  input  in_2,
  output [15:0] out_3
);

  and and_1 (out_3[0], in_1[0], in_2);
  and and_2 (out_3[1], in_1[1], in_2);
  and and_3 (out_3[2], in_1[2], in_2);
  and and_4 (out_3[3], in_1[3], in_2);
  and and_5 (out_3[4], in_1[4], in_2);
  and and_6 (out_3[5], in_1[5], in_2);
  and and_7 (out_3[6], in_1[6], in_2);
  and and_8 (out_3[7], in_1[7], in_2);
  and and_9 (out_3[8], in_1[8], in_2);
  and and_10 (out_3[9], in_1[9], in_2);
  and and_11 (out_3[10], in_1[10], in_2);
  and and_12 (out_3[11], in_1[11], in_2);
  and and_13 (out_3[12], in_1[12], in_2);
  and and_14 (out_3[13], in_1[13], in_2);
  and and_15 (out_3[14], in_1[14], in_2);
  and and_16 (out_3[15], in_1[15], in_2);
endmodule

module RS_NOR (
  input  in_1,
  input  in_2,
  output out_3
);

  wire nor_1_out;

  nor nor_1 (nor_1_out, in_1, out_3);
  nor nor_2 (out_3, nor_1_out, in_2);
endmodule

module _4_BUF (
  input  in_1,
  input  [3:0] in_2,
  output [3:0] out_3
);

  and and_1 (out_3[0], in_2[0], in_1);
  and and_2 (out_3[1], in_2[1], in_1);
  and and_3 (out_3[2], in_2[2], in_1);
  and and_4 (out_3[3], in_2[3], in_1);
endmodule

module _4_Comparator (
  input  [3:0] in_1,
  input  [3:0] in_2,
  input  in_3,
  input  in_4,
  input  in_5,
  output out_6,
  output out_7,
  output out_8
);

  wire nand_1_out, nand_2_out, nand_3_out, nand_4_out, nand_5_out, nand_6_out, nand_7_out, nand_8_out,
       nand_9_out, nand_10_out, nand_11_out, nand_12_out, not_1_out, not_2_out, not_3_out, not_4_out,
       not_5_out, not_6_out, not_7_out, not_8_out, not_9_out, not_10_out, not_11_out, not_12_out, not_13_out,
       not_14_out, not_15_out, not_16_out, not_17_out, not_18_out, not_19_out, or_1_out, or_2_out, or_3_out,
       or_4_out;

  not not_1 (not_1_out, not_2_out);
  not not_2 (not_2_out, in_2[3]);
  not not_3 (not_3_out, in_1[3]);
  not not_4 (not_4_out, not_3_out);
  not not_5 (not_5_out, in_2[2]);
  not not_6 (not_6_out, not_5_out);
  not not_7 (not_7_out, not_8_out);
  not not_8 (not_8_out, in_1[2]);
  not not_9 (not_9_out, in_2[1]);
  not not_10 (not_10_out, not_9_out);
  not not_11 (not_11_out, not_12_out);
  not not_12 (not_12_out, in_1[1]);
  not not_13 (not_13_out, not_14_out);
  not not_14 (not_14_out, in_2[0]);
  not not_15 (not_15_out, in_1[0]);
  not not_16 (not_16_out, not_15_out);
  not not_17 (not_17_out, in_3);
  not not_18 (not_18_out, in_4);
  not not_19 (not_19_out, in_5);
  nand nand_1 (nand_1_out, not_1_out, not_3_out);
  nand nand_2 (nand_2_out, not_2_out, not_4_out);
  nand nand_3 (nand_3_out, not_6_out, not_8_out);
  nand nand_4 (nand_4_out, not_5_out, not_7_out);
  nand nand_5 (nand_5_out, not_10_out, not_12_out);
  nand nand_6 (nand_6_out, not_9_out, not_11_out);
  nand nand_7 (nand_7_out, not_13_out, not_15_out);
  nand nand_8 (nand_8_out, not_14_out, not_16_out);
  nand nand_9 (nand_9_out, nand_1_out, nand_2_out);
  nand nand_10 (nand_10_out, nand_3_out, nand_4_out);
  nand nand_11 (nand_11_out, nand_5_out, nand_6_out);
  nand nand_12 (nand_12_out, nand_7_out, nand_8_out);
  or or_1 (or_1_out, nand_9_out, nand_3_out);
  or or_2 (or_2_out, nand_9_out, nand_10_out, nand_5_out);
  or or_3 (or_3_out, nand_9_out, nand_10_out, nand_11_out, nand_7_out);
  or or_4 (or_4_out, nand_9_out, nand_10_out, nand_11_out, nand_12_out, not_17_out);
  nor nor_1 (out_7, nand_9_out, nand_10_out, nand_11_out, nand_12_out, not_18_out);
  nand nand_13 (out_6, nand_1_out, or_1_out, or_2_out, or_3_out, or_4_out);
  nor nor_2 (out_8, out_6, out_7, not_19_out);
endmodule
