// Logisim project SyzygyA100v2.circ as structural Verilog
module ALU (
  input  [3:0] Pre_Op,
  input  [1:0] Post_Op,
  input  [1:0] Shift_Type,
  input  Shift_Dir,
  input  [3:0] Operation,
  input  in_6,
  input  in_7,
  input  [15:0] in_8,
  input  [15:0] in_9,
  input  in_10,
  input  in_11,
  input  in_12,
  input  in_13,
  input  in_14,
  input  in_15,
  input  in_16,
  output out_17,
  output [15:0] out_18
);

  wire and_2_out, comparator_1_out_3, comparator_1_out_4, comparator_1_out_5, condition_decoder_1_out_5,
       decoder_1_out1, decoder_1_out2, decoder_1_out3, decoder_1_out4, decoder_1_out5, decoder_1_out6,
       decoder_1_out7, decoder_2_out0, decoder_2_out1, decoder_2_out2, decoder_2_out3, decoder_3_out0,
       decoder_3_out1, decoder_3_out2, decoder_3_out3, decoder_3_out4, decoder_3_out5, decoder_3_out6,
       decoder_3_out7, decoder_3_out8, decoder_3_out9, long_delay_1_out_2, long_delay_2_out_2,
       long_delay_3_out_2, long_delay_4_out_2, long_delay_5_out_2, not_1_out, not_2_out, or_2_out, or_3_out,
       or_4_out, or_7_out;
  wire [2:0] demultiplexer_1_out0;
  wire [3:0] demultiplexer_1_out1;
  wire [3:3] demultiplexer_1_out0_2;
  wire [5:0] decoder_3_out10;
  wire [15:0] and_1_out, bit_counter_1_out_2, multiplexer_1_out, multiplexer_2_out, multiplexer_3_out,
       n2b_mem_1_out_5, n2b_mem_2_out_5, n16_buffer_1_out_3, n16_buffer_2_out_3, n16_buffer_3_out_3,
       n16_buffer_4_out_3, n16_buffer_5_out_3, n16_buffer_6_out_3, n16_buffer_7_out_3, n16_buffer_8_out_3,
       n16_buffer_9_out_3, n16_buffer_10_out_3, n16_buffer_11_out_3, n16_buffer_12_out_3,
       n16_buffer_13_out_3, n16_buffer_14_out_3, n16_buffer_15_out_3, n16_buffer_16_out_3,
       n16_buffer_17_out_3, n16_buffer_18_out_3, n16_fa_1_out_4, n16_fa_2_out_4, n16_fa_3_out_4,
       n16_fa_4_out_4, n16_lr_barrel_shifter_1_out_5, n16_neg_1_out_3, n16_neg_2_out_3, n16_neg_3_out_3,
       or_1_out, or_5_out, or_6_out, rng_1_out_2, sqrt_calculator_1_out_2, square_calculator_1_out_2,
       xor_1_out;

  _2B_Mem u_2b_mem_1 (.in_3(in_10), .in_1(in_8), .in_2(in_6), .in_4(in_11), .out_5(n2b_mem_1_out_5));
  _16_NEG u_16_neg_1 (.in_2(n2b_mem_1_out_5), .in_1(decoder_1_out1), .out_3(n16_neg_1_out_3));
  _16_FA u_16_fa_1 (.out_4(n16_fa_1_out_4), .in_2(n16_neg_1_out_3), .in_1(decoder_1_out3), .in_3(multiplexer_1_out));
  _16_Buffer u_16_buffer_1 (.in_2(decoder_3_out0), .in_1(n16_fa_1_out_4), .out_3(n16_buffer_1_out_3));
  // Probe on n2b_mem_1_out_5
  // Probe on n16_fa_1_out_4
  _16_Buffer u_16_buffer_2 (.in_2(decoder_3_out1), .in_1(n16_fa_1_out_4), .out_3(n16_buffer_2_out_3));
  _16_FA u_16_fa_2 (.out_4(n16_fa_2_out_4), .in_2(n16_buffer_2_out_3), .in_1(1'b0), .in_3(n16_buffer_3_out_3));
  _16_Buffer u_16_buffer_3 (.in_2(decoder_3_out1), .in_1(n16_fa_3_out_4), .out_3(n16_buffer_3_out_3));
  // Probe on n2b_mem_2_out_5
  // Probe on n16_fa_3_out_4
  _16_Buffer u_16_buffer_4 (.in_2(decoder_3_out2), .in_1(n16_fa_1_out_4), .out_3(n16_buffer_4_out_3));
  _16_Buffer u_16_buffer_5 (.in_2(decoder_3_out2), .in_1(n16_fa_3_out_4), .out_3(n16_buffer_5_out_3));
  assign or_1_out = n16_buffer_4_out_3 | n16_buffer_5_out_3;  // OR_Gate or_1, 16 bits wide
  Long_Delay long_delay_1 (.in_1(or_2_out), .out_2(long_delay_1_out_2));
  Long_Delay long_delay_2 (.in_1(long_delay_1_out_2), .out_2(long_delay_2_out_2));
  Long_Delay long_delay_3 (.in_1(long_delay_2_out_2), .out_2(long_delay_3_out_2));
  Long_Delay long_delay_4 (.in_1(long_delay_3_out_2), .out_2(long_delay_4_out_2));
  Long_Delay long_delay_5 (.in_1(long_delay_4_out_2), .out_2(long_delay_5_out_2));
  _2B_Mem u_2b_mem_2 (.in_3(in_12), .in_1(in_9), .in_2(in_7), .in_4(in_13), .out_5(n2b_mem_2_out_5));
  or or_2 (or_2_out, in_13, in_11);
  _16_NEG u_16_neg_2 (.in_2(n2b_mem_2_out_5), .in_1(or_3_out), .out_3(n16_neg_2_out_3));
  or or_3 (or_3_out, decoder_1_out7, decoder_1_out2);
  _16_FA u_16_fa_3 (.out_4(n16_fa_3_out_4), .in_2(n16_neg_2_out_3), .in_1(or_4_out), .in_3(multiplexer_2_out));
  _16_Buffer u_16_buffer_6 (.in_2(decoder_3_out3), .in_1(n16_fa_1_out_4), .out_3(n16_buffer_6_out_3));
  _16_Buffer u_16_buffer_7 (.in_2(decoder_2_out0), .in_1(or_5_out), .out_3(n16_buffer_7_out_3));
  _16_Buffer u_16_buffer_8 (.in_2(decoder_2_out1), .in_1(or_5_out), .out_3(n16_buffer_8_out_3));
  _16_NEG u_16_neg_3 (.in_2(n16_buffer_8_out_3), .in_1(decoder_2_out1), .out_3(n16_neg_3_out_3));
  _2B_Mem u_2b_mem_3 (.in_3(in_15), .in_1(or_6_out), .in_2(long_delay_5_out_2), .in_4(in_16), .out_5(out_18));
  or or_4 (or_4_out, decoder_1_out4, decoder_1_out7);
  _16_Buffer u_16_buffer_9 (.in_2(decoder_3_out3), .in_1(n16_fa_3_out_4), .out_3(n16_buffer_9_out_3));
  assign and_1_out = n16_buffer_6_out_3 & n16_buffer_9_out_3;  // AND_Gate and_1, 16 bits wide
  assign or_5_out = n16_buffer_1_out_3 | n16_fa_2_out_4 | or_1_out | and_1_out | xor_1_out | n16_lr_barrel_shifter_1_out_5 | square_calculator_1_out_2 | sqrt_calculator_1_out_2 | bit_counter_1_out_2 | n16_buffer_18_out_3;  // OR_Gate or_5, 16 bits wide
  _16_Buffer u_16_buffer_10 (.in_2(or_7_out), .in_1(or_5_out), .out_3(n16_buffer_10_out_3));
  assign or_6_out = n16_buffer_7_out_3 | n16_neg_3_out_3 | n16_fa_4_out_4;  // OR_Gate or_6, 16 bits wide
  Multiplexer #(.width(16), .enable("false")) multiplexer_1 (
    .in0({16{1'b0}}), .in1({16{1'b1}}), .out(multiplexer_1_out), .sel(decoder_1_out5));
  Multiplexer #(.width(16), .enable("false")) multiplexer_2 (
    .in0({16{1'b0}}), .in1({16{1'b1}}), .out(multiplexer_2_out), .sel(decoder_1_out6));
  _16_Buffer u_16_buffer_11 (.in_2(decoder_3_out4), .in_1(n16_fa_1_out_4), .out_3(n16_buffer_11_out_3));
  _16_Buffer u_16_buffer_12 (.in_2(decoder_3_out4), .in_1(n16_fa_3_out_4), .out_3(n16_buffer_12_out_3));
  assign xor_1_out = n16_buffer_11_out_3 ^ n16_buffer_12_out_3;  // XOR_Gate xor_1, 16 bits wide
  _16_Buffer u_16_buffer_13 (.in_2(or_7_out), .in_1(multiplexer_3_out), .out_3(n16_buffer_13_out_3));
  _16_FA u_16_fa_4 (
    .out_4(n16_fa_4_out_4), .in_2(n16_buffer_10_out_3), .in_1(decoder_2_out2), .in_3(n16_buffer_13_out_3));
  Decoder #(.select(3), .enable("false")) decoder_1 (
    .out1(decoder_1_out1), .out2(decoder_1_out2), .out3(decoder_1_out3), .out4(decoder_1_out4),
    .out5(decoder_1_out5), .out6(decoder_1_out6), .out7(decoder_1_out7), .sel(demultiplexer_1_out0));  // open: out0
  _16_Buffer u_16_buffer_14 (.in_2(decoder_3_out5), .in_1(n16_fa_1_out_4), .out_3(n16_buffer_14_out_3));
  _16_LR_Barrel_Shifter u_16_lr_barrel_shifter_1 (
    .in_4(n16_buffer_14_out_3), .in_1(demultiplexer_1_out1), .L___R(Shift_Dir), .Log_Arith(Shift_Type),
    .out_5(n16_lr_barrel_shifter_1_out_5));
  or or_7 (or_7_out, decoder_2_out2, decoder_2_out3);
  Demultiplexer #(.width(4), .enable("false")) demultiplexer_1 (
    .out0({demultiplexer_1_out0_2[3], demultiplexer_1_out0}), .out1(demultiplexer_1_out1), .in(Pre_Op),
    .sel(and_2_out));
  _16_Buffer u_16_buffer_15 (.in_2(decoder_3_out6), .in_1(n16_fa_1_out_4), .out_3(n16_buffer_15_out_3));
  Square_Calculator square_calculator_1 (.in_1(n16_buffer_15_out_3), .out_2(square_calculator_1_out_2));
  Multiplexer #(.width(16), .enable("false")) multiplexer_3 (
    .in0({16{1'b0}}), .in1({16{1'b1}}), .out(multiplexer_3_out), .sel(decoder_2_out3));
  _16_Buffer u_16_buffer_16 (.in_2(decoder_3_out7), .in_1(n16_fa_1_out_4), .out_3(n16_buffer_16_out_3));
  Sqrt_Calculator sqrt_calculator_1 (.in_1(n16_buffer_16_out_3), .out_2(sqrt_calculator_1_out_2));
  Decoder #(.select(2), .enable("false")) decoder_2 (
    .out0(decoder_2_out0), .out1(decoder_2_out1), .out2(decoder_2_out2), .out3(decoder_2_out3), .sel(Post_Op));
  _16_Buffer u_16_buffer_17 (.in_2(decoder_3_out8), .in_1(n16_fa_1_out_4), .out_3(n16_buffer_17_out_3));
  RNG rng_1 (.in_1(decoder_3_out9), .out_2(rng_1_out_2));
  Bit_Counter bit_counter_1 (.in_1(n16_buffer_17_out_3), .out_2(bit_counter_1_out_2));
  _16_Buffer u_16_buffer_18 (.in_2(decoder_3_out9), .in_1(rng_1_out_2), .out_3(n16_buffer_18_out_3));
  and and_2 (and_2_out, not_1_out, Operation[0], Operation[2], not_2_out);
  not not_1 (not_1_out, Operation[1]);
  not not_2 (not_2_out, Operation[3]);
  Comparator comparator_1 (
    .in_1(n16_fa_1_out_4), .in_2(n16_fa_3_out_4), .out_3(comparator_1_out_3), .out_4(comparator_1_out_4),
    .out_5(comparator_1_out_5));
  Condition_Decoder condition_decoder_1 (
    .out_5(condition_decoder_1_out_5), .in_4(decoder_3_out10), .in_1(comparator_1_out_3),
    .in_2(comparator_1_out_4), .in_3(comparator_1_out_5));
  Decoder #(.select(4), .enable("false")) decoder_3 (
    .out0(decoder_3_out0), .out1(decoder_3_out1), .out2(decoder_3_out2), .out3(decoder_3_out3),
    .out4(decoder_3_out4), .out5(decoder_3_out5), .out6(decoder_3_out6), .out7(decoder_3_out7),
    .out8(decoder_3_out8), .out9(decoder_3_out9), .out10(decoder_3_out10[0]), .out11(decoder_3_out10[1]),
    .out12(decoder_3_out10[2]), .out13(decoder_3_out10[3]), .out14(decoder_3_out10[4]),
    .out15(decoder_3_out10[5]), .sel(Operation));
  D_Flip_Flop d_ff_1 (.Q(out_17), .preset(condition_decoder_1_out_5), .reset(in_14));  // open: clk, D, Qn, en
endmodule

module CPU_Memory (
  input  [3:0] in_1,
  input  Wr,
  input  Clr,
  input  in_4,
  input  [15:0] in_5,
  input  Rd,
  output [15:0] out_7
);

  wire bin_hex_1_out_4, bin_hex_1_out_5, bin_hex_1_out_6, bin_hex_1_out_7, bin_hex_1_out_8, bin_hex_1_out_9,
       bin_hex_1_out_10, bin_hex_1_out_11, bin_hex_1_out_12, bin_hex_1_out_13, bin_hex_1_out_14,
       bin_hex_1_out_15, bin_hex_1_out_16, bin_hex_1_out_17, bin_hex_1_out_18, bin_hex_1_out_19,
       bin_hex_2_out_4, bin_hex_2_out_5, bin_hex_2_out_6, bin_hex_2_out_7, bin_hex_2_out_8, bin_hex_2_out_9,
       bin_hex_2_out_10, bin_hex_2_out_11, bin_hex_2_out_12, bin_hex_2_out_13, bin_hex_2_out_14,
       bin_hex_2_out_15, bin_hex_2_out_16, bin_hex_2_out_17, bin_hex_2_out_18, bin_hex_2_out_19,
       bin_hex_3_out_4, bin_hex_3_out_5, bin_hex_3_out_6, bin_hex_3_out_7, bin_hex_3_out_8, bin_hex_3_out_9,
       bin_hex_3_out_10, bin_hex_3_out_11, bin_hex_3_out_12, bin_hex_3_out_13, bin_hex_3_out_14,
       bin_hex_3_out_15, bin_hex_3_out_16, bin_hex_3_out_17, bin_hex_3_out_18, bin_hex_3_out_19;
  wire [15:0] n2b_mem_1_out_5, n2b_mem_2_out_5, n2b_mem_3_out_5, n2b_mem_4_out_5, n2b_mem_5_out_5,
       n2b_mem_6_out_5, n2b_mem_7_out_5, n2b_mem_8_out_5, n2b_mem_9_out_5, n2b_mem_10_out_5,
       n2b_mem_11_out_5, n2b_mem_12_out_5, n2b_mem_13_out_5, n2b_mem_14_out_5, n2b_mem_15_out_5,
       n2b_mem_16_out_5;

  Bin_Hex bin_hex_1 (
    .in_2(in_1), .in_1(Rd), .out_4(bin_hex_1_out_4), .out_5(bin_hex_1_out_5), .out_6(bin_hex_1_out_6),
    .out_7(bin_hex_1_out_7), .out_8(bin_hex_1_out_8), .out_9(bin_hex_1_out_9), .out_10(bin_hex_1_out_10),
    .out_11(bin_hex_1_out_11), .out_12(bin_hex_1_out_12), .out_13(bin_hex_1_out_13),
    .out_14(bin_hex_1_out_14), .out_15(bin_hex_1_out_15), .out_16(bin_hex_1_out_16),
    .out_17(bin_hex_1_out_17), .out_18(bin_hex_1_out_18), .out_19(bin_hex_1_out_19), .in_3(1'b0));
  assign out_7 = n2b_mem_4_out_5 | n2b_mem_3_out_5 | n2b_mem_2_out_5 | n2b_mem_1_out_5 | n2b_mem_7_out_5 | n2b_mem_6_out_5 | n2b_mem_5_out_5 | n2b_mem_8_out_5 | n2b_mem_11_out_5 | n2b_mem_10_out_5 | n2b_mem_9_out_5 | n2b_mem_12_out_5 | n2b_mem_15_out_5 | n2b_mem_14_out_5 | n2b_mem_13_out_5 | n2b_mem_16_out_5;  // OR_Gate or_1, 16 bits wide
  Bin_Hex bin_hex_2 (
    .in_2(in_1), .in_1(Clr), .out_4(bin_hex_2_out_4), .out_5(bin_hex_2_out_5), .out_6(bin_hex_2_out_6),
    .out_7(bin_hex_2_out_7), .out_8(bin_hex_2_out_8), .out_9(bin_hex_2_out_9), .out_10(bin_hex_2_out_10),
    .out_11(bin_hex_2_out_11), .out_12(bin_hex_2_out_12), .out_13(bin_hex_2_out_13),
    .out_14(bin_hex_2_out_14), .out_15(bin_hex_2_out_15), .out_16(bin_hex_2_out_16),
    .out_17(bin_hex_2_out_17), .out_18(bin_hex_2_out_18), .out_19(bin_hex_2_out_19), .in_3(in_4));
  _2B_Mem u_2b_mem_1 (
    .in_3(bin_hex_2_out_12), .in_1(in_5), .in_2(bin_hex_3_out_12), .in_4(bin_hex_1_out_12),
    .out_5(n2b_mem_1_out_5));
  _2B_Mem u_2b_mem_2 (
    .in_3(bin_hex_2_out_13), .in_1(in_5), .in_2(bin_hex_3_out_13), .in_4(bin_hex_1_out_13),
    .out_5(n2b_mem_2_out_5));
  _2B_Mem u_2b_mem_3 (
    .in_3(bin_hex_2_out_14), .in_1(in_5), .in_2(bin_hex_3_out_14), .in_4(bin_hex_1_out_14),
    .out_5(n2b_mem_3_out_5));
  _2B_Mem u_2b_mem_4 (
    .in_3(bin_hex_2_out_15), .in_1(in_5), .in_2(bin_hex_3_out_15), .in_4(bin_hex_1_out_15),
    .out_5(n2b_mem_4_out_5));
  Bin_Hex bin_hex_3 (
    .in_2(in_1), .in_1(Wr), .out_4(bin_hex_3_out_4), .out_5(bin_hex_3_out_5), .out_6(bin_hex_3_out_6),
    .out_7(bin_hex_3_out_7), .out_8(bin_hex_3_out_8), .out_9(bin_hex_3_out_9), .out_10(bin_hex_3_out_10),
    .out_11(bin_hex_3_out_11), .out_12(bin_hex_3_out_12), .out_13(bin_hex_3_out_13),
    .out_14(bin_hex_3_out_14), .out_15(bin_hex_3_out_15), .out_16(bin_hex_3_out_16),
    .out_17(bin_hex_3_out_17), .out_18(bin_hex_3_out_18), .out_19(bin_hex_3_out_19), .in_3(1'b0));
  _2B_Mem u_2b_mem_5 (
    .in_3(bin_hex_2_out_16), .in_1(in_5), .in_2(bin_hex_3_out_16), .in_4(bin_hex_1_out_16),
    .out_5(n2b_mem_5_out_5));
  _2B_Mem u_2b_mem_6 (
    .in_3(bin_hex_2_out_17), .in_1(in_5), .in_2(bin_hex_3_out_17), .in_4(bin_hex_1_out_17),
    .out_5(n2b_mem_6_out_5));
  _2B_Mem u_2b_mem_7 (
    .in_3(bin_hex_2_out_18), .in_1(in_5), .in_2(bin_hex_3_out_18), .in_4(bin_hex_1_out_18),
    .out_5(n2b_mem_7_out_5));
  _2B_Mem u_2b_mem_8 (
    .in_3(bin_hex_2_out_19), .in_1(in_5), .in_2(bin_hex_3_out_19), .in_4(bin_hex_1_out_19),
    .out_5(n2b_mem_8_out_5));
  _2B_Mem u_2b_mem_9 (
    .in_3(bin_hex_2_out_4), .in_1(in_5), .in_2(bin_hex_3_out_4), .in_4(bin_hex_1_out_4),
    .out_5(n2b_mem_9_out_5));
  _2B_Mem u_2b_mem_10 (
    .in_3(bin_hex_2_out_5), .in_1(in_5), .in_2(bin_hex_3_out_5), .in_4(bin_hex_1_out_5),
    .out_5(n2b_mem_10_out_5));
  _2B_Mem u_2b_mem_11 (
    .in_3(bin_hex_2_out_6), .in_1(in_5), .in_2(bin_hex_3_out_6), .in_4(bin_hex_1_out_6),
    .out_5(n2b_mem_11_out_5));
  _2B_Mem u_2b_mem_12 (
    .in_3(bin_hex_2_out_7), .in_1(in_5), .in_2(bin_hex_3_out_7), .in_4(bin_hex_1_out_7),
    .out_5(n2b_mem_12_out_5));
  _2B_Mem u_2b_mem_13 (
    .in_3(bin_hex_2_out_8), .in_1(in_5), .in_2(bin_hex_3_out_8), .in_4(bin_hex_1_out_8),
    .out_5(n2b_mem_13_out_5));
  _2B_Mem u_2b_mem_14 (
    .in_3(bin_hex_2_out_9), .in_1(in_5), .in_2(bin_hex_3_out_9), .in_4(bin_hex_1_out_9),
    .out_5(n2b_mem_14_out_5));
  _2B_Mem u_2b_mem_15 (
    .in_3(bin_hex_2_out_10), .in_1(in_5), .in_2(bin_hex_3_out_10), .in_4(bin_hex_1_out_10),
    .out_5(n2b_mem_15_out_5));
  _2B_Mem u_2b_mem_16 (
    .in_3(bin_hex_2_out_11), .in_1(in_5), .in_2(bin_hex_3_out_11), .in_4(bin_hex_1_out_11),
    .out_5(n2b_mem_16_out_5));
endmodule

module Program_Memory (
  input  [3:0] in_1,
  input  Wr,
  input  Clr,
  input  in_4,
  input  [15:0] in_5,
  input  Rd,
  output [15:0] out_7
);

  wire bin_hex_1_out_4, bin_hex_1_out_5, bin_hex_1_out_6, bin_hex_1_out_7, bin_hex_1_out_8, bin_hex_1_out_9,
       bin_hex_1_out_10, bin_hex_1_out_11, bin_hex_1_out_12, bin_hex_1_out_13, bin_hex_1_out_14,
       bin_hex_1_out_15, bin_hex_1_out_16, bin_hex_1_out_17, bin_hex_1_out_18, bin_hex_1_out_19,
       bin_hex_2_out_4, bin_hex_2_out_5, bin_hex_2_out_6, bin_hex_2_out_7, bin_hex_2_out_8, bin_hex_2_out_9,
       bin_hex_2_out_10, bin_hex_2_out_11, bin_hex_2_out_12, bin_hex_2_out_13, bin_hex_2_out_14,
       bin_hex_2_out_15, bin_hex_2_out_16, bin_hex_2_out_17, bin_hex_2_out_18, bin_hex_2_out_19,
       bin_hex_3_out_4, bin_hex_3_out_5, bin_hex_3_out_6, bin_hex_3_out_7, bin_hex_3_out_8, bin_hex_3_out_9,
       bin_hex_3_out_10, bin_hex_3_out_11, bin_hex_3_out_12, bin_hex_3_out_13, bin_hex_3_out_14,
       bin_hex_3_out_15, bin_hex_3_out_16, bin_hex_3_out_17, bin_hex_3_out_18, bin_hex_3_out_19;
  wire [15:0] n2b_mem_1_out_5, n2b_mem_2_out_5, n2b_mem_3_out_5, n2b_mem_4_out_5, n2b_mem_5_out_5,
       n2b_mem_6_out_5, n2b_mem_7_out_5, n2b_mem_8_out_5, n2b_mem_9_out_5, n2b_mem_10_out_5,
       n2b_mem_11_out_5, n2b_mem_12_out_5, n2b_mem_13_out_5, n2b_mem_14_out_5, n2b_mem_15_out_5,
       n2b_mem_16_out_5;

  Bin_Hex bin_hex_1 (
    .in_2(in_1), .in_1(Rd), .out_4(bin_hex_1_out_4), .out_5(bin_hex_1_out_5), .out_6(bin_hex_1_out_6),
    .out_7(bin_hex_1_out_7), .out_8(bin_hex_1_out_8), .out_9(bin_hex_1_out_9), .out_10(bin_hex_1_out_10),
    .out_11(bin_hex_1_out_11), .out_12(bin_hex_1_out_12), .out_13(bin_hex_1_out_13),
    .out_14(bin_hex_1_out_14), .out_15(bin_hex_1_out_15), .out_16(bin_hex_1_out_16),
    .out_17(bin_hex_1_out_17), .out_18(bin_hex_1_out_18), .out_19(bin_hex_1_out_19), .in_3(1'b0));
  assign out_7 = n2b_mem_4_out_5 | n2b_mem_3_out_5 | n2b_mem_2_out_5 | n2b_mem_1_out_5 | n2b_mem_7_out_5 | n2b_mem_6_out_5 | n2b_mem_5_out_5 | n2b_mem_8_out_5 | n2b_mem_11_out_5 | n2b_mem_10_out_5 | n2b_mem_9_out_5 | n2b_mem_12_out_5 | n2b_mem_15_out_5 | n2b_mem_14_out_5 | n2b_mem_13_out_5 | n2b_mem_16_out_5;  // OR_Gate or_1, 16 bits wide
  Bin_Hex bin_hex_2 (
    .in_2(in_1), .in_1(Clr), .out_4(bin_hex_2_out_4), .out_5(bin_hex_2_out_5), .out_6(bin_hex_2_out_6),
    .out_7(bin_hex_2_out_7), .out_8(bin_hex_2_out_8), .out_9(bin_hex_2_out_9), .out_10(bin_hex_2_out_10),
    .out_11(bin_hex_2_out_11), .out_12(bin_hex_2_out_12), .out_13(bin_hex_2_out_13),
    .out_14(bin_hex_2_out_14), .out_15(bin_hex_2_out_15), .out_16(bin_hex_2_out_16),
    .out_17(bin_hex_2_out_17), .out_18(bin_hex_2_out_18), .out_19(bin_hex_2_out_19), .in_3(in_4));
  _2B_Mem u_2b_mem_1 (
    .in_3(bin_hex_2_out_12), .in_1(in_5), .in_2(bin_hex_3_out_12), .in_4(bin_hex_1_out_12),
    .out_5(n2b_mem_1_out_5));
  _2B_Mem u_2b_mem_2 (
    .in_3(bin_hex_2_out_13), .in_1(in_5), .in_2(bin_hex_3_out_13), .in_4(bin_hex_1_out_13),
    .out_5(n2b_mem_2_out_5));
  _2B_Mem u_2b_mem_3 (
    .in_3(bin_hex_2_out_14), .in_1(in_5), .in_2(bin_hex_3_out_14), .in_4(bin_hex_1_out_14),
    .out_5(n2b_mem_3_out_5));
  _2B_Mem u_2b_mem_4 (
    .in_3(bin_hex_2_out_15), .in_1(in_5), .in_2(bin_hex_3_out_15), .in_4(bin_hex_1_out_15),
    .out_5(n2b_mem_4_out_5));
  Bin_Hex bin_hex_3 (
    .in_2(in_1), .in_1(Wr), .out_4(bin_hex_3_out_4), .out_5(bin_hex_3_out_5), .out_6(bin_hex_3_out_6),
    .out_7(bin_hex_3_out_7), .out_8(bin_hex_3_out_8), .out_9(bin_hex_3_out_9), .out_10(bin_hex_3_out_10),
    .out_11(bin_hex_3_out_11), .out_12(bin_hex_3_out_12), .out_13(bin_hex_3_out_13),
    .out_14(bin_hex_3_out_14), .out_15(bin_hex_3_out_15), .out_16(bin_hex_3_out_16),
    .out_17(bin_hex_3_out_17), .out_18(bin_hex_3_out_18), .out_19(bin_hex_3_out_19), .in_3(1'b0));
  _2B_Mem u_2b_mem_5 (
    .in_3(bin_hex_2_out_16), .in_1(in_5), .in_2(bin_hex_3_out_16), .in_4(bin_hex_1_out_16),
    .out_5(n2b_mem_5_out_5));
  _2B_Mem u_2b_mem_6 (
    .in_3(bin_hex_2_out_17), .in_1(in_5), .in_2(bin_hex_3_out_17), .in_4(bin_hex_1_out_17),
    .out_5(n2b_mem_6_out_5));
  _2B_Mem u_2b_mem_7 (
    .in_3(bin_hex_2_out_18), .in_1(in_5), .in_2(bin_hex_3_out_18), .in_4(bin_hex_1_out_18),
    .out_5(n2b_mem_7_out_5));
  _2B_Mem u_2b_mem_8 (
    .in_3(bin_hex_2_out_19), .in_1(in_5), .in_2(bin_hex_3_out_19), .in_4(bin_hex_1_out_19),
    .out_5(n2b_mem_8_out_5));
  _2B_Mem u_2b_mem_9 (
    .in_3(bin_hex_2_out_4), .in_1(in_5), .in_2(bin_hex_3_out_4), .in_4(bin_hex_1_out_4),
    .out_5(n2b_mem_9_out_5));
  _2B_Mem u_2b_mem_10 (
    .in_3(bin_hex_2_out_5), .in_1(in_5), .in_2(bin_hex_3_out_5), .in_4(bin_hex_1_out_5),
    .out_5(n2b_mem_10_out_5));
  _2B_Mem u_2b_mem_11 (
    .in_3(bin_hex_2_out_6), .in_1(in_5), .in_2(bin_hex_3_out_6), .in_4(bin_hex_1_out_6),
    .out_5(n2b_mem_11_out_5));
  _2B_Mem u_2b_mem_12 (
    .in_3(bin_hex_2_out_7), .in_1(in_5), .in_2(bin_hex_3_out_7), .in_4(bin_hex_1_out_7),
    .out_5(n2b_mem_12_out_5));
  _2B_Mem u_2b_mem_13 (
    .in_3(bin_hex_2_out_8), .in_1(in_5), .in_2(bin_hex_3_out_8), .in_4(bin_hex_1_out_8),
    .out_5(n2b_mem_13_out_5));
  _2B_Mem u_2b_mem_14 (
    .in_3(bin_hex_2_out_9), .in_1(in_5), .in_2(bin_hex_3_out_9), .in_4(bin_hex_1_out_9),
    .out_5(n2b_mem_14_out_5));
  _2B_Mem u_2b_mem_15 (
    .in_3(bin_hex_2_out_10), .in_1(in_5), .in_2(bin_hex_3_out_10), .in_4(bin_hex_1_out_10),
    .out_5(n2b_mem_15_out_5));
  _2B_Mem u_2b_mem_16 (
    .in_3(bin_hex_2_out_11), .in_1(in_5), .in_2(bin_hex_3_out_11), .in_4(bin_hex_1_out_11),
    .out_5(n2b_mem_16_out_5));
endmodule

module _16_FA (
  input  in_1,
  input  [15:0] in_2,
  input  [15:0] in_3,
  output [15:0] out_4
);

  wire fa_1_out_5, fa_2_out_5, fa_3_out_5, fa_4_out_5, fa_5_out_5, fa_6_out_5, fa_7_out_5, fa_8_out_5,
       fa_9_out_5, fa_10_out_5, fa_11_out_5, fa_12_out_5, fa_13_out_5, fa_14_out_5, fa_15_out_5;

  FA fa_1 (.in_2(in_2[0]), .in_3(in_3[0]), .out_4(out_4[0]), .in_1(in_1), .out_5(fa_1_out_5));
  FA fa_2 (.in_2(in_2[1]), .in_3(in_3[1]), .out_4(out_4[1]), .in_1(fa_1_out_5), .out_5(fa_2_out_5));
  FA fa_3 (.in_2(in_2[2]), .in_3(in_3[2]), .out_4(out_4[2]), .in_1(fa_2_out_5), .out_5(fa_3_out_5));
  FA fa_4 (.in_2(in_2[3]), .in_3(in_3[3]), .out_4(out_4[3]), .in_1(fa_3_out_5), .out_5(fa_4_out_5));
  FA fa_5 (.in_2(in_2[4]), .in_3(in_3[4]), .out_4(out_4[4]), .in_1(fa_4_out_5), .out_5(fa_5_out_5));
  FA fa_6 (.in_2(in_2[5]), .in_3(in_3[5]), .out_4(out_4[5]), .in_1(fa_5_out_5), .out_5(fa_6_out_5));
  FA fa_7 (.in_2(in_2[6]), .in_3(in_3[6]), .out_4(out_4[6]), .in_1(fa_6_out_5), .out_5(fa_7_out_5));
  FA fa_8 (.in_2(in_2[7]), .in_3(in_3[7]), .out_4(out_4[7]), .in_1(fa_7_out_5), .out_5(fa_8_out_5));
  FA fa_9 (.in_2(in_2[8]), .in_3(in_3[8]), .out_4(out_4[8]), .in_1(fa_8_out_5), .out_5(fa_9_out_5));
  FA fa_10 (.in_2(in_2[9]), .in_3(in_3[9]), .out_4(out_4[9]), .in_1(fa_9_out_5), .out_5(fa_10_out_5));
  FA fa_11 (.in_2(in_2[10]), .in_3(in_3[10]), .out_4(out_4[10]), .in_1(fa_10_out_5), .out_5(fa_11_out_5));
  FA fa_12 (.in_2(in_2[11]), .in_3(in_3[11]), .out_4(out_4[11]), .in_1(fa_11_out_5), .out_5(fa_12_out_5));
  FA fa_13 (.in_2(in_2[12]), .in_3(in_3[12]), .out_4(out_4[12]), .in_1(fa_12_out_5), .out_5(fa_13_out_5));
  FA fa_14 (.in_2(in_2[13]), .in_3(in_3[13]), .out_4(out_4[13]), .in_1(fa_13_out_5), .out_5(fa_14_out_5));
  FA fa_15 (.in_2(in_2[14]), .in_3(in_3[14]), .out_4(out_4[14]), .in_1(fa_14_out_5), .out_5(fa_15_out_5));
  FA fa_16 (.in_2(in_2[15]), .in_3(in_3[15]), .out_4(out_4[15]), .in_1(fa_15_out_5));  // open: out_5
endmodule

module FA (
  input  in_1,
  input  in_2,
  input  in_3,
  output out_4,
  output out_5
);

  wire and_1_out, and_2_out, xor_1_out;

  and and_1 (and_1_out, in_2, in_3);
  or or_1 (out_5, and_1_out, and_2_out);
  xor xor_1 (xor_1_out, in_2, in_3);
  and and_2 (and_2_out, in_1, xor_1_out);
  xor xor_2 (out_4, xor_1_out, in_1);
endmodule

module Memory_Cell (
  input  in_1,
  input  in_2,
  input  in_3,
  output out_4,
  output out_5
);

  D_Flip_Flop d_ff_1 (.clk(in_1), .D(in_2), .Q(out_5), .en(1'b1), .reset(in_3));  // open: Qn, preset

  assign out_4 = in_3;
endmodule

module _2B_Mem (
  input  [15:0] in_1,
  input  in_2,
  input  in_3,
  input  in_4,
  output [15:0] out_5
);

  wire memory_cell_1_out_5, memory_cell_2_out_4, memory_cell_2_out_5, memory_cell_3_out_4,
       memory_cell_3_out_5, memory_cell_4_out_4, memory_cell_4_out_5, memory_cell_5_out_4,
       memory_cell_5_out_5, memory_cell_6_out_4, memory_cell_6_out_5, memory_cell_7_out_4,
       memory_cell_7_out_5, memory_cell_8_out_4, memory_cell_8_out_5, memory_cell_9_out_4,
       memory_cell_9_out_5, memory_cell_10_out_4, memory_cell_10_out_5, memory_cell_11_out_4,
       memory_cell_11_out_5, memory_cell_12_out_4, memory_cell_12_out_5, memory_cell_13_out_4,
       memory_cell_13_out_5, memory_cell_14_out_4, memory_cell_14_out_5, memory_cell_15_out_4,
       memory_cell_15_out_5, memory_cell_16_out_4, memory_cell_16_out_5;

  Memory_Cell memory_cell_1 (
    .in_1(in_2), .in_2(in_1[0]), .out_5(memory_cell_1_out_5), .in_3(memory_cell_2_out_4));  // open: out_4
  Memory_Cell memory_cell_2 (
    .in_1(in_2), .in_2(in_1[1]), .out_5(memory_cell_2_out_5), .out_4(memory_cell_2_out_4),
    .in_3(memory_cell_3_out_4));
  Memory_Cell memory_cell_3 (
    .in_1(in_2), .in_2(in_1[2]), .out_5(memory_cell_3_out_5), .out_4(memory_cell_3_out_4),
    .in_3(memory_cell_4_out_4));
  Memory_Cell memory_cell_4 (
    .in_1(in_2), .in_2(in_1[3]), .out_5(memory_cell_4_out_5), .out_4(memory_cell_4_out_4),
    .in_3(memory_cell_5_out_4));
  Memory_Cell memory_cell_5 (
    .in_1(in_2), .in_2(in_1[4]), .out_5(memory_cell_5_out_5), .out_4(memory_cell_5_out_4),
    .in_3(memory_cell_6_out_4));
  Memory_Cell memory_cell_6 (
    .in_1(in_2), .in_2(in_1[5]), .out_5(memory_cell_6_out_5), .out_4(memory_cell_6_out_4),
    .in_3(memory_cell_7_out_4));
  Memory_Cell memory_cell_7 (
    .in_1(in_2), .in_2(in_1[6]), .out_5(memory_cell_7_out_5), .out_4(memory_cell_7_out_4),
    .in_3(memory_cell_8_out_4));
  Memory_Cell memory_cell_8 (
    .in_1(in_2), .in_2(in_1[7]), .out_5(memory_cell_8_out_5), .out_4(memory_cell_8_out_4),
    .in_3(memory_cell_9_out_4));
  Memory_Cell memory_cell_9 (
    .in_1(in_2), .in_2(in_1[8]), .out_5(memory_cell_9_out_5), .out_4(memory_cell_9_out_4),
    .in_3(memory_cell_10_out_4));
  Memory_Cell memory_cell_10 (
    .in_1(in_2), .in_2(in_1[9]), .out_5(memory_cell_10_out_5), .out_4(memory_cell_10_out_4),
    .in_3(memory_cell_11_out_4));
  Memory_Cell memory_cell_11 (
    .in_1(in_2), .in_2(in_1[10]), .out_5(memory_cell_11_out_5), .out_4(memory_cell_11_out_4),
    .in_3(memory_cell_12_out_4));
  Memory_Cell memory_cell_12 (
    .in_1(in_2), .in_2(in_1[11]), .out_5(memory_cell_12_out_5), .out_4(memory_cell_12_out_4),
    .in_3(memory_cell_13_out_4));
  Memory_Cell memory_cell_13 (
    .in_1(in_2), .in_2(in_1[12]), .out_5(memory_cell_13_out_5), .out_4(memory_cell_13_out_4),
    .in_3(memory_cell_14_out_4));
  Memory_Cell memory_cell_14 (
    .in_1(in_2), .in_2(in_1[13]), .out_5(memory_cell_14_out_5), .out_4(memory_cell_14_out_4),
    .in_3(memory_cell_15_out_4));
  Memory_Cell memory_cell_15 (
    .in_1(in_2), .in_2(in_1[14]), .out_5(memory_cell_15_out_5), .out_4(memory_cell_15_out_4),
    .in_3(memory_cell_16_out_4));
  Memory_Cell memory_cell_16 (
    .in_1(in_2), .in_2(in_1[15]), .out_5(memory_cell_16_out_5), .out_4(memory_cell_16_out_4), .in_3(in_3));
  and and_1 (out_5[0], memory_cell_1_out_5, in_4);
  and and_2 (out_5[1], memory_cell_2_out_5, in_4);
  and and_3 (out_5[2], memory_cell_3_out_5, in_4);
  and and_4 (out_5[3], memory_cell_4_out_5, in_4);
  and and_5 (out_5[4], memory_cell_5_out_5, in_4);
  and and_6 (out_5[5], memory_cell_6_out_5, in_4);
  and and_7 (out_5[6], memory_cell_7_out_5, in_4);
  and and_8 (out_5[7], memory_cell_8_out_5, in_4);
  and and_9 (out_5[8], memory_cell_9_out_5, in_4);
  and and_10 (out_5[9], memory_cell_10_out_5, in_4);
  and and_11 (out_5[10], memory_cell_11_out_5, in_4);
  and and_12 (out_5[11], memory_cell_12_out_5, in_4);
  and and_13 (out_5[12], memory_cell_13_out_5, in_4);
  and and_14 (out_5[13], memory_cell_14_out_5, in_4);
  and and_15 (out_5[14], memory_cell_15_out_5, in_4);
  and and_16 (out_5[15], memory_cell_16_out_5, in_4);
endmodule

module _16_NEG (
  input  in_1,
  input  [15:0] in_2,
  output [15:0] out_3
);

  xor xor_1 (out_3[0], in_2[0], in_1);
  xor xor_2 (out_3[1], in_2[1], in_1);
  xor xor_3 (out_3[2], in_2[2], in_1);
  xor xor_4 (out_3[3], in_2[3], in_1);
  xor xor_5 (out_3[4], in_2[4], in_1);
  xor xor_6 (out_3[5], in_2[5], in_1);
  xor xor_7 (out_3[6], in_2[6], in_1);
  xor xor_8 (out_3[7], in_2[7], in_1);
  xor xor_9 (out_3[8], in_2[8], in_1);
  xor xor_10 (out_3[9], in_2[9], in_1);
  xor xor_11 (out_3[10], in_2[10], in_1);
  xor xor_12 (out_3[11], in_2[11], in_1);
  xor xor_13 (out_3[12], in_2[12], in_1);
  xor xor_14 (out_3[13], in_2[13], in_1);
  xor xor_15 (out_3[14], in_2[14], in_1);
  xor xor_16 (out_3[15], in_2[15], in_1);
endmodule

module _16_Buffer (
  input  [15:0] in_1,
  input  in_2,
  output [15:0] out_3
);

  wire [15:0] n1_16_1_out_2;

  assign out_3 = in_1 & n1_16_1_out_2;  // AND_Gate and_1, 16 bits wide
  _1_16 u_1_16_1 (.in_1(in_2), .out_2(n1_16_1_out_2));
endmodule

module _1_16 (
  input  in_1,
  output [15:0] out_2
);


  assign out_2 = {16{in_1}};
endmodule

module _16_LR_Barrel_Shifter (
  input  [3:0] in_1,
  input  L___R,
  input  [1:0] Log_Arith,
  input  [15:0] in_4,
  output [15:0] out_5
);

  wire multiplexer_1_out, multiplexer_2_out, multiplexer_3_out, multiplexer_4_out, multiplexer_5_out,
       multiplexer_6_out, multiplexer_7_out, multiplexer_8_out, multiplexer_9_out, multiplexer_10_out,
       multiplexer_11_out, multiplexer_12_out, multiplexer_13_out, multiplexer_14_out, multiplexer_15_out,
       multiplexer_16_out, multiplexer_17_out, multiplexer_18_out, multiplexer_19_out, multiplexer_20_out,
       multiplexer_21_out, multiplexer_22_out, multiplexer_23_out, multiplexer_24_out, multiplexer_25_out,
       multiplexer_26_out, multiplexer_27_out, multiplexer_28_out, multiplexer_29_out, multiplexer_30_out,
       multiplexer_31_out, multiplexer_32_out, multiplexer_33_out, multiplexer_34_out, multiplexer_35_out,
       multiplexer_36_out, multiplexer_37_out, multiplexer_38_out, multiplexer_39_out, multiplexer_40_out,
       multiplexer_41_out, multiplexer_42_out, multiplexer_43_out, multiplexer_44_out, multiplexer_45_out,
       multiplexer_46_out, multiplexer_47_out, multiplexer_48_out, multiplexer_49_out, multiplexer_50_out,
       multiplexer_51_out, multiplexer_52_out, multiplexer_53_out, multiplexer_54_out, multiplexer_55_out,
       multiplexer_56_out, multiplexer_57_out, multiplexer_58_out, multiplexer_59_out, multiplexer_60_out,
       multiplexer_61_out, multiplexer_62_out, multiplexer_63_out, multiplexer_64_out, multiplexer_65_out,
       multiplexer_66_out, multiplexer_67_out, multiplexer_68_out, multiplexer_69_out, multiplexer_70_out,
       multiplexer_71_out, multiplexer_72_out, multiplexer_73_out, multiplexer_74_out, multiplexer_75_out,
       multiplexer_76_out, multiplexer_77_out, multiplexer_78_out, multiplexer_79_out, multiplexer_80_out,
       multiplexer_81_out, multiplexer_82_out, multiplexer_83_out, multiplexer_84_out, multiplexer_85_out,
       multiplexer_86_out, multiplexer_87_out, multiplexer_88_out, multiplexer_89_out, multiplexer_90_out,
       multiplexer_91_out, multiplexer_92_out, multiplexer_93_out, multiplexer_94_out, multiplexer_95_out,
       multiplexer_96_out, multiplexer_97_out, multiplexer_98_out, multiplexer_99_out, multiplexer_100_out,
       multiplexer_101_out, multiplexer_102_out, multiplexer_103_out, multiplexer_104_out,
       multiplexer_105_out, multiplexer_106_out, multiplexer_107_out, multiplexer_108_out,
       multiplexer_109_out, multiplexer_110_out, multiplexer_111_out, multiplexer_112_out,
       multiplexer_128_out;

  Multiplexer #(.enable("false")) multiplexer_1 (
    .in0(in_4[0]), .in1(multiplexer_2_out), .out(multiplexer_1_out), .sel(in_1[0]));
  Multiplexer #(.enable("false")) multiplexer_2 (.in0(1'b0), .in1(in_4[1]), .out(multiplexer_2_out), .sel(L___R));
  Multiplexer #(.enable("false")) multiplexer_3 (
    .in0(in_4[1]), .in1(multiplexer_4_out), .out(multiplexer_3_out), .sel(in_1[0]));
  Multiplexer #(.enable("false")) multiplexer_4 (.in0(in_4[0]), .in1(in_4[2]), .out(multiplexer_4_out), .sel(L___R));
  Multiplexer #(.enable("false")) multiplexer_5 (
    .in0(in_4[2]), .in1(multiplexer_6_out), .out(multiplexer_5_out), .sel(in_1[0]));
  Multiplexer #(.enable("false")) multiplexer_6 (.in0(in_4[1]), .in1(in_4[3]), .out(multiplexer_6_out), .sel(L___R));
  Multiplexer #(.enable("false")) multiplexer_7 (
    .in0(in_4[3]), .in1(multiplexer_8_out), .out(multiplexer_7_out), .sel(in_1[0]));
  Multiplexer #(.enable("false")) multiplexer_8 (.in0(in_4[2]), .in1(in_4[4]), .out(multiplexer_8_out), .sel(L___R));
  Multiplexer #(.enable("false")) multiplexer_9 (
    .in0(in_4[4]), .in1(multiplexer_10_out), .out(multiplexer_9_out), .sel(in_1[0]));
  Multiplexer #(.enable("false")) multiplexer_10 (.in0(in_4[3]), .in1(in_4[5]), .out(multiplexer_10_out), .sel(L___R));
  Multiplexer #(.enable("false")) multiplexer_11 (
    .in0(in_4[5]), .in1(multiplexer_12_out), .out(multiplexer_11_out), .sel(in_1[0]));
  Multiplexer #(.enable("false")) multiplexer_12 (.in0(in_4[4]), .in1(in_4[6]), .out(multiplexer_12_out), .sel(L___R));
  Multiplexer #(.enable("false")) multiplexer_13 (
    .in0(in_4[6]), .in1(multiplexer_14_out), .out(multiplexer_13_out), .sel(in_1[0]));
  Multiplexer #(.enable("false")) multiplexer_14 (.in0(in_4[5]), .in1(in_4[7]), .out(multiplexer_14_out), .sel(L___R));
  Multiplexer #(.enable("false")) multiplexer_15 (
    .in0(in_4[7]), .in1(multiplexer_16_out), .out(multiplexer_15_out), .sel(in_1[0]));
  Multiplexer #(.enable("false")) multiplexer_16 (.in0(in_4[6]), .in1(in_4[8]), .out(multiplexer_16_out), .sel(L___R));
  Multiplexer #(.enable("false")) multiplexer_17 (
    .in0(in_4[8]), .in1(multiplexer_18_out), .out(multiplexer_17_out), .sel(in_1[0]));
  Multiplexer #(.enable("false")) multiplexer_18 (.in0(in_4[7]), .in1(in_4[9]), .out(multiplexer_18_out), .sel(L___R));
  Multiplexer #(.enable("false")) multiplexer_19 (
    .in0(in_4[9]), .in1(multiplexer_20_out), .out(multiplexer_19_out), .sel(in_1[0]));
  Multiplexer #(.enable("false")) multiplexer_20 (.in0(in_4[8]), .in1(in_4[10]), .out(multiplexer_20_out), .sel(L___R));
  Multiplexer #(.enable("false")) multiplexer_21 (
    .in0(in_4[10]), .in1(multiplexer_22_out), .out(multiplexer_21_out), .sel(in_1[0]));
  Multiplexer #(.enable("false")) multiplexer_22 (.in0(in_4[9]), .in1(in_4[11]), .out(multiplexer_22_out), .sel(L___R));
  Multiplexer #(.enable("false")) multiplexer_23 (
    .in0(in_4[11]), .in1(multiplexer_24_out), .out(multiplexer_23_out), .sel(in_1[0]));
  Multiplexer #(.enable("false")) multiplexer_24 (
    .in0(in_4[10]), .in1(in_4[12]), .out(multiplexer_24_out), .sel(L___R));
  Multiplexer #(.enable("false")) multiplexer_25 (
    .in0(in_4[12]), .in1(multiplexer_26_out), .out(multiplexer_25_out), .sel(in_1[0]));
  Multiplexer #(.enable("false")) multiplexer_26 (
    .in0(in_4[11]), .in1(in_4[13]), .out(multiplexer_26_out), .sel(L___R));
  Multiplexer #(.enable("false")) multiplexer_27 (
    .in0(in_4[13]), .in1(multiplexer_28_out), .out(multiplexer_27_out), .sel(in_1[0]));
  Multiplexer #(.enable("false")) multiplexer_28 (
    .in0(in_4[12]), .in1(in_4[14]), .out(multiplexer_28_out), .sel(L___R));
  Multiplexer #(.enable("false")) multiplexer_29 (
    .in0(in_4[14]), .in1(multiplexer_30_out), .out(multiplexer_29_out), .sel(in_1[0]));
  Multiplexer #(.enable("false")) multiplexer_30 (
    .in0(in_4[13]), .in1(in_4[15]), .out(multiplexer_30_out), .sel(L___R));
  Multiplexer #(.enable("false")) multiplexer_31 (
    .in0(in_4[15]), .in1(multiplexer_32_out), .out(multiplexer_31_out), .sel(in_1[0]));
  Multiplexer #(.enable("false")) multiplexer_32 (.in0(in_4[14]), .in1(1'b0), .out(multiplexer_32_out), .sel(L___R));
  Multiplexer #(.enable("false")) multiplexer_33 (
    .in0(1'b0), .in1(multiplexer_5_out), .out(multiplexer_33_out), .sel(L___R));
  Multiplexer #(.enable("false")) multiplexer_34 (
    .in0(1'b0), .in1(multiplexer_7_out), .out(multiplexer_34_out), .sel(L___R));
  Multiplexer #(.enable("false")) multiplexer_35 (
    .in0(multiplexer_1_out), .in1(multiplexer_9_out), .out(multiplexer_35_out), .sel(L___R));
  Multiplexer #(.enable("false")) multiplexer_36 (
    .in0(multiplexer_3_out), .in1(multiplexer_11_out), .out(multiplexer_36_out), .sel(L___R));
  Multiplexer #(.enable("false")) multiplexer_37 (
    .in0(multiplexer_5_out), .in1(multiplexer_13_out), .out(multiplexer_37_out), .sel(L___R));
  Multiplexer #(.enable("false")) multiplexer_38 (
    .in0(multiplexer_7_out), .in1(multiplexer_15_out), .out(multiplexer_38_out), .sel(L___R));
  Multiplexer #(.enable("false")) multiplexer_39 (
    .in0(multiplexer_9_out), .in1(multiplexer_17_out), .out(multiplexer_39_out), .sel(L___R));
  Multiplexer #(.enable("false")) multiplexer_40 (
    .in0(multiplexer_11_out), .in1(multiplexer_19_out), .out(multiplexer_40_out), .sel(L___R));
  Multiplexer #(.enable("false")) multiplexer_41 (
    .in0(multiplexer_13_out), .in1(multiplexer_21_out), .out(multiplexer_41_out), .sel(L___R));
  Multiplexer #(.enable("false")) multiplexer_42 (
    .in0(multiplexer_15_out), .in1(multiplexer_23_out), .out(multiplexer_42_out), .sel(L___R));
  Multiplexer #(.enable("false")) multiplexer_43 (
    .in0(multiplexer_17_out), .in1(multiplexer_25_out), .out(multiplexer_43_out), .sel(L___R));
  Multiplexer #(.enable("false")) multiplexer_44 (
    .in0(multiplexer_19_out), .in1(multiplexer_27_out), .out(multiplexer_44_out), .sel(L___R));
  Multiplexer #(.enable("false")) multiplexer_45 (
    .in0(multiplexer_21_out), .in1(multiplexer_29_out), .out(multiplexer_45_out), .sel(L___R));
  Multiplexer #(.enable("false")) multiplexer_46 (
    .in0(multiplexer_23_out), .in1(multiplexer_31_out), .out(multiplexer_46_out), .sel(L___R));
  Multiplexer #(.enable("false")) multiplexer_47 (
    .in0(multiplexer_25_out), .in1(1'b0), .out(multiplexer_47_out), .sel(L___R));
  Multiplexer #(.enable("false")) multiplexer_48 (
    .in0(multiplexer_27_out), .in1(1'b0), .out(multiplexer_48_out), .sel(L___R));
  Multiplexer #(.enable("false")) multiplexer_49 (
    .in0(multiplexer_1_out), .in1(multiplexer_33_out), .out(multiplexer_49_out), .sel(in_1[1]));
  Multiplexer #(.enable("false")) multiplexer_50 (
    .in0(multiplexer_3_out), .in1(multiplexer_34_out), .out(multiplexer_50_out), .sel(in_1[1]));
  Multiplexer #(.enable("false")) multiplexer_51 (
    .in0(multiplexer_5_out), .in1(multiplexer_35_out), .out(multiplexer_51_out), .sel(in_1[1]));
  Multiplexer #(.enable("false")) multiplexer_52 (
    .in0(multiplexer_7_out), .in1(multiplexer_36_out), .out(multiplexer_52_out), .sel(in_1[1]));
  Multiplexer #(.enable("false")) multiplexer_53 (
    .in0(multiplexer_9_out), .in1(multiplexer_37_out), .out(multiplexer_53_out), .sel(in_1[1]));
  Multiplexer #(.enable("false")) multiplexer_54 (
    .in0(multiplexer_11_out), .in1(multiplexer_38_out), .out(multiplexer_54_out), .sel(in_1[1]));
  Multiplexer #(.enable("false")) multiplexer_55 (
    .in0(multiplexer_13_out), .in1(multiplexer_39_out), .out(multiplexer_55_out), .sel(in_1[1]));
  Multiplexer #(.enable("false")) multiplexer_56 (
    .in0(multiplexer_15_out), .in1(multiplexer_40_out), .out(multiplexer_56_out), .sel(in_1[1]));
  Multiplexer #(.enable("false")) multiplexer_57 (
    .in0(multiplexer_17_out), .in1(multiplexer_41_out), .out(multiplexer_57_out), .sel(in_1[1]));
  Multiplexer #(.enable("false")) multiplexer_58 (
    .in0(multiplexer_19_out), .in1(multiplexer_42_out), .out(multiplexer_58_out), .sel(in_1[1]));
  Multiplexer #(.enable("false")) multiplexer_59 (
    .in0(multiplexer_21_out), .in1(multiplexer_43_out), .out(multiplexer_59_out), .sel(in_1[1]));
  Multiplexer #(.enable("false")) multiplexer_60 (
    .in0(multiplexer_23_out), .in1(multiplexer_44_out), .out(multiplexer_60_out), .sel(in_1[1]));
  Multiplexer #(.enable("false")) multiplexer_61 (
    .in0(multiplexer_25_out), .in1(multiplexer_45_out), .out(multiplexer_61_out), .sel(in_1[1]));
  Multiplexer #(.enable("false")) multiplexer_62 (
    .in0(multiplexer_27_out), .in1(multiplexer_46_out), .out(multiplexer_62_out), .sel(in_1[1]));
  Multiplexer #(.enable("false")) multiplexer_63 (
    .in0(multiplexer_29_out), .in1(multiplexer_47_out), .out(multiplexer_63_out), .sel(in_1[1]));
  Multiplexer #(.enable("false")) multiplexer_64 (
    .in0(multiplexer_31_out), .in1(multiplexer_48_out), .out(multiplexer_64_out), .sel(in_1[1]));
  Multiplexer #(.enable("false")) multiplexer_65 (
    .in0(multiplexer_49_out), .in1(multiplexer_66_out), .out(multiplexer_65_out), .sel(in_1[2]));
  Multiplexer #(.enable("false")) multiplexer_66 (
    .in0(1'b0), .in1(multiplexer_53_out), .out(multiplexer_66_out), .sel(L___R));
  Multiplexer #(.enable("false")) multiplexer_67 (
    .in0(multiplexer_50_out), .in1(multiplexer_68_out), .out(multiplexer_67_out), .sel(in_1[2]));
  Multiplexer #(.enable("false")) multiplexer_68 (
    .in0(1'b0), .in1(multiplexer_54_out), .out(multiplexer_68_out), .sel(L___R));
  Multiplexer #(.enable("false")) multiplexer_69 (
    .in0(multiplexer_51_out), .in1(multiplexer_70_out), .out(multiplexer_69_out), .sel(in_1[2]));
  Multiplexer #(.enable("false")) multiplexer_70 (
    .in0(1'b0), .in1(multiplexer_55_out), .out(multiplexer_70_out), .sel(L___R));
  Multiplexer #(.enable("false")) multiplexer_71 (
    .in0(multiplexer_52_out), .in1(multiplexer_72_out), .out(multiplexer_71_out), .sel(in_1[2]));
  Multiplexer #(.enable("false")) multiplexer_72 (
    .in0(1'b0), .in1(multiplexer_56_out), .out(multiplexer_72_out), .sel(L___R));
  Multiplexer #(.enable("false")) multiplexer_73 (
    .in0(multiplexer_53_out), .in1(multiplexer_74_out), .out(multiplexer_73_out), .sel(in_1[2]));
  Multiplexer #(.enable("false")) multiplexer_74 (
    .in0(multiplexer_49_out), .in1(multiplexer_57_out), .out(multiplexer_74_out), .sel(L___R));
  Multiplexer #(.enable("false")) multiplexer_75 (
    .in0(multiplexer_54_out), .in1(multiplexer_76_out), .out(multiplexer_75_out), .sel(in_1[2]));
  Multiplexer #(.enable("false")) multiplexer_76 (
    .in0(multiplexer_50_out), .in1(multiplexer_58_out), .out(multiplexer_76_out), .sel(L___R));
  Multiplexer #(.enable("false")) multiplexer_77 (
    .in0(multiplexer_55_out), .in1(multiplexer_78_out), .out(multiplexer_77_out), .sel(in_1[2]));
  Multiplexer #(.enable("false")) multiplexer_78 (
    .in0(multiplexer_51_out), .in1(multiplexer_59_out), .out(multiplexer_78_out), .sel(L___R));
  Multiplexer #(.enable("false")) multiplexer_79 (
    .in0(multiplexer_56_out), .in1(multiplexer_80_out), .out(multiplexer_79_out), .sel(in_1[2]));
  Multiplexer #(.enable("false")) multiplexer_80 (
    .in0(multiplexer_52_out), .in1(multiplexer_60_out), .out(multiplexer_80_out), .sel(L___R));
  Multiplexer #(.enable("false")) multiplexer_81 (
    .in0(multiplexer_57_out), .in1(multiplexer_82_out), .out(multiplexer_81_out), .sel(in_1[2]));
  Multiplexer #(.enable("false")) multiplexer_82 (
    .in0(multiplexer_53_out), .in1(multiplexer_61_out), .out(multiplexer_82_out), .sel(L___R));
  Multiplexer #(.enable("false")) multiplexer_83 (
    .in0(multiplexer_58_out), .in1(multiplexer_84_out), .out(multiplexer_83_out), .sel(in_1[2]));
  Multiplexer #(.enable("false")) multiplexer_84 (
    .in0(multiplexer_54_out), .in1(multiplexer_62_out), .out(multiplexer_84_out), .sel(L___R));
  Multiplexer #(.enable("false")) multiplexer_85 (
    .in0(multiplexer_59_out), .in1(multiplexer_86_out), .out(multiplexer_85_out), .sel(in_1[2]));
  Multiplexer #(.enable("false")) multiplexer_86 (
    .in0(multiplexer_55_out), .in1(multiplexer_63_out), .out(multiplexer_86_out), .sel(L___R));
  Multiplexer #(.enable("false")) multiplexer_87 (
    .in0(multiplexer_60_out), .in1(multiplexer_88_out), .out(multiplexer_87_out), .sel(in_1[2]));
  Multiplexer #(.enable("false")) multiplexer_88 (
    .in0(multiplexer_56_out), .in1(multiplexer_64_out), .out(multiplexer_88_out), .sel(L___R));
  Multiplexer #(.enable("false")) multiplexer_89 (
    .in0(multiplexer_61_out), .in1(multiplexer_90_out), .out(multiplexer_89_out), .sel(in_1[2]));
  Multiplexer #(.enable("false")) multiplexer_90 (
    .in0(multiplexer_57_out), .in1(1'b0), .out(multiplexer_90_out), .sel(L___R));
  Multiplexer #(.enable("false")) multiplexer_91 (
    .in0(multiplexer_62_out), .in1(multiplexer_92_out), .out(multiplexer_91_out), .sel(in_1[2]));
  Multiplexer #(.enable("false")) multiplexer_92 (
    .in0(multiplexer_58_out), .in1(1'b0), .out(multiplexer_92_out), .sel(L___R));
  Multiplexer #(.enable("false")) multiplexer_93 (
    .in0(multiplexer_63_out), .in1(multiplexer_94_out), .out(multiplexer_93_out), .sel(in_1[2]));
  Multiplexer #(.enable("false")) multiplexer_94 (
    .in0(multiplexer_59_out), .in1(1'b0), .out(multiplexer_94_out), .sel(L___R));
  Multiplexer #(.enable("false")) multiplexer_95 (
    .in0(multiplexer_64_out), .in1(multiplexer_96_out), .out(multiplexer_95_out), .sel(in_1[2]));
  Multiplexer #(.enable("false")) multiplexer_96 (
    .in0(multiplexer_60_out), .in1(1'b0), .out(multiplexer_96_out), .sel(L___R));
  Multiplexer #(.enable("false")) multiplexer_97 (
    .in0(1'b0), .in1(multiplexer_81_out), .out(multiplexer_97_out), .sel(L___R));
  Multiplexer #(.enable("false")) multiplexer_98 (
    .in0(1'b0), .in1(multiplexer_83_out), .out(multiplexer_98_out), .sel(L___R));
  Multiplexer #(.enable("false")) multiplexer_99 (
    .in0(1'b0), .in1(multiplexer_85_out), .out(multiplexer_99_out), .sel(L___R));
  Multiplexer #(.enable("false")) multiplexer_100 (
    .in0(1'b0), .in1(multiplexer_87_out), .out(multiplexer_100_out), .sel(L___R));
  Multiplexer #(.enable("false")) multiplexer_101 (
    .in0(1'b0), .in1(multiplexer_89_out), .out(multiplexer_101_out), .sel(L___R));
  Multiplexer #(.enable("false")) multiplexer_102 (
    .in0(1'b0), .in1(multiplexer_91_out), .out(multiplexer_102_out), .sel(L___R));
  Multiplexer #(.enable("false")) multiplexer_103 (
    .in0(1'b0), .in1(multiplexer_93_out), .out(multiplexer_103_out), .sel(L___R));
  Multiplexer #(.enable("false")) multiplexer_104 (
    .in0(1'b0), .in1(multiplexer_95_out), .out(multiplexer_104_out), .sel(L___R));
  Multiplexer #(.enable("false")) multiplexer_105 (
    .in0(multiplexer_65_out), .in1(1'b0), .out(multiplexer_105_out), .sel(L___R));
  Multiplexer #(.enable("false")) multiplexer_106 (
    .in0(multiplexer_67_out), .in1(1'b0), .out(multiplexer_106_out), .sel(L___R));
  Multiplexer #(.enable("false")) multiplexer_107 (
    .in0(multiplexer_69_out), .in1(1'b0), .out(multiplexer_107_out), .sel(L___R));
  Multiplexer #(.enable("false")) multiplexer_108 (
    .in0(multiplexer_71_out), .in1(1'b0), .out(multiplexer_108_out), .sel(L___R));
  Multiplexer #(.enable("false")) multiplexer_109 (
    .in0(multiplexer_73_out), .in1(1'b0), .out(multiplexer_109_out), .sel(L___R));
  Multiplexer #(.enable("false")) multiplexer_110 (
    .in0(multiplexer_75_out), .in1(1'b0), .out(multiplexer_110_out), .sel(L___R));
  Multiplexer #(.enable("false")) multiplexer_111 (
    .in0(multiplexer_77_out), .in1(1'b0), .out(multiplexer_111_out), .sel(L___R));
  Multiplexer #(.enable("false")) multiplexer_112 (
    .in0(multiplexer_79_out), .in1(1'b0), .out(multiplexer_112_out), .sel(L___R));
  Multiplexer #(.enable("false")) multiplexer_113 (
    .in0(multiplexer_65_out), .in1(multiplexer_97_out), .out(out_5[0]), .sel(in_1[3]));
  Multiplexer #(.enable("false")) multiplexer_114 (
    .in0(multiplexer_67_out), .in1(multiplexer_98_out), .out(out_5[1]), .sel(in_1[3]));
  Multiplexer #(.enable("false")) multiplexer_115 (
    .in0(multiplexer_69_out), .in1(multiplexer_99_out), .out(out_5[2]), .sel(in_1[3]));
  Multiplexer #(.enable("false")) multiplexer_116 (
    .in0(multiplexer_71_out), .in1(multiplexer_100_out), .out(out_5[3]), .sel(in_1[3]));
  Multiplexer #(.enable("false")) multiplexer_117 (
    .in0(multiplexer_73_out), .in1(multiplexer_101_out), .out(out_5[4]), .sel(in_1[3]));
  Multiplexer #(.enable("false")) multiplexer_118 (
    .in0(multiplexer_75_out), .in1(multiplexer_102_out), .out(out_5[5]), .sel(in_1[3]));
  Multiplexer #(.enable("false")) multiplexer_119 (
    .in0(multiplexer_77_out), .in1(multiplexer_103_out), .out(out_5[6]), .sel(in_1[3]));
  Multiplexer #(.enable("false")) multiplexer_120 (
    .in0(multiplexer_79_out), .in1(multiplexer_104_out), .out(out_5[7]), .sel(in_1[3]));
  Multiplexer #(.enable("false")) multiplexer_121 (
    .in0(multiplexer_81_out), .in1(multiplexer_105_out), .out(out_5[8]), .sel(in_1[3]));
  Multiplexer #(.enable("false")) multiplexer_122 (
    .in0(multiplexer_83_out), .in1(multiplexer_106_out), .out(out_5[9]), .sel(in_1[3]));
  Multiplexer #(.enable("false")) multiplexer_123 (
    .in0(multiplexer_85_out), .in1(multiplexer_107_out), .out(out_5[10]), .sel(in_1[3]));
  Multiplexer #(.enable("false")) multiplexer_124 (
    .in0(multiplexer_87_out), .in1(multiplexer_108_out), .out(out_5[11]), .sel(in_1[3]));
  Multiplexer #(.enable("false")) multiplexer_125 (
    .in0(multiplexer_89_out), .in1(multiplexer_109_out), .out(out_5[12]), .sel(in_1[3]));
  Multiplexer #(.enable("false")) multiplexer_126 (
    .in0(multiplexer_91_out), .in1(multiplexer_110_out), .out(out_5[13]), .sel(in_1[3]));
  Multiplexer #(.enable("false")) multiplexer_127 (
    .in0(multiplexer_93_out), .in1(multiplexer_111_out), .out(out_5[14]), .sel(in_1[3]));
  Multiplexer #(.enable("false")) multiplexer_128 (
    .in0(multiplexer_95_out), .in1(multiplexer_112_out), .out(multiplexer_128_out), .sel(in_1[3]));
  Multiplexer #(.enable("false")) multiplexer_129 (
    .in0(multiplexer_128_out), .in1(in_4[15]), .out(out_5[15]), .sel(Log_Arith[0]));
endmodule

module Square_Cell (
  input  B,
  input  Cin,
  input  A,
  input  E,
  output B_2,
  output Cout,
  output S,
  output E_2
);

  wire and_1_out, and_2_out, nand_1_out, nand_2_out, nand_3_out, not_1_out, not_2_out, xor_1_out, xor_2_out;

  nand nand_1 (nand_1_out, B, Cin);
  nand nand_2 (nand_2_out, B, A);
  nand nand_3 (nand_3_out, A, Cin);
  xor xor_1 (xor_1_out, B, Cin);
  nand nand_4 (Cout, nand_1_out, nand_2_out, nand_3_out);
  not not_1 (not_1_out, E);
  xor xor_2 (xor_2_out, xor_1_out, A);
  not not_2 (not_2_out, not_1_out);
  and and_1 (and_1_out, not_2_out, xor_2_out);
  or or_1 (S, and_1_out, and_2_out);
  and and_2 (and_2_out, not_1_out, A);

  assign B_2 = B;
  assign E_2 = E;
endmodule

module Square_Calculator (
  input  [15:0] in_1,
  output [15:0] out_2
);

  wire square_cell_1_b_2, square_cell_1_e_2, square_cell_1_s, square_cell_2_b_2, square_cell_2_e_2,
       square_cell_2_s, square_cell_3_b_2, square_cell_3_e_2, square_cell_3_s, square_cell_4_b_2,
       square_cell_4_e_2, square_cell_4_s, square_cell_5_b_2, square_cell_5_e_2, square_cell_5_s,
       square_cell_6_b_2, square_cell_6_e_2, square_cell_6_s, square_cell_7_b_2, square_cell_7_e_2,
       square_cell_7_s, square_cell_8_e_2, square_cell_9_b_2, square_cell_9_cout, square_cell_9_s,
       square_cell_10_b_2, square_cell_10_cout, square_cell_10_e_2, square_cell_10_s, square_cell_11_b_2,
       square_cell_11_cout, square_cell_11_e_2, square_cell_11_s, square_cell_12_b_2, square_cell_12_cout,
       square_cell_12_e_2, square_cell_12_s, square_cell_13_b_2, square_cell_13_cout, square_cell_13_e_2,
       square_cell_13_s, square_cell_14_b_2, square_cell_14_cout, square_cell_14_e_2, square_cell_14_s,
       square_cell_15_b_2, square_cell_15_cout, square_cell_15_e_2, square_cell_15_s, square_cell_16_cout,
       square_cell_16_e_2, square_cell_17_b_2, square_cell_17_cout, square_cell_17_e_2, square_cell_17_s,
       square_cell_18_b_2, square_cell_18_cout, square_cell_18_e_2, square_cell_18_s, square_cell_19_b_2,
       square_cell_19_cout, square_cell_19_e_2, square_cell_19_s, square_cell_20_b_2, square_cell_20_cout,
       square_cell_20_e_2, square_cell_20_s, square_cell_21_b_2, square_cell_21_cout, square_cell_21_e_2,
       square_cell_21_s, square_cell_22_b_2, square_cell_22_cout, square_cell_22_e_2, square_cell_22_s,
       square_cell_23_cout, square_cell_23_e_2, square_cell_24_b_2, square_cell_24_cout, square_cell_24_s,
       square_cell_25_b_2, square_cell_25_cout, square_cell_25_e_2, square_cell_25_s, square_cell_26_b_2,
       square_cell_26_cout, square_cell_26_e_2, square_cell_26_s, square_cell_27_b_2, square_cell_27_cout,
       square_cell_27_e_2, square_cell_27_s, square_cell_28_b_2, square_cell_28_cout, square_cell_28_e_2,
       square_cell_28_s, square_cell_29_b_2, square_cell_29_cout, square_cell_29_e_2, square_cell_29_s,
       square_cell_30_cout, square_cell_30_e_2, square_cell_31_b_2, square_cell_31_cout, square_cell_31_e_2,
       square_cell_31_s, square_cell_32_b_2, square_cell_32_cout, square_cell_32_e_2, square_cell_32_s,
       square_cell_33_b_2, square_cell_33_cout, square_cell_33_e_2, square_cell_33_s, square_cell_34_b_2,
       square_cell_34_cout, square_cell_34_e_2, square_cell_34_s, square_cell_35_b_2, square_cell_35_cout,
       square_cell_35_e_2, square_cell_35_s, square_cell_36_cout, square_cell_36_e_2, square_cell_37_b_2,
       square_cell_37_cout, square_cell_37_s, square_cell_38_b_2, square_cell_38_cout, square_cell_38_e_2,
       square_cell_38_s, square_cell_39_b_2, square_cell_39_cout, square_cell_39_e_2, square_cell_39_s,
       square_cell_40_b_2, square_cell_40_cout, square_cell_40_e_2, square_cell_40_s, square_cell_41_b_2,
       square_cell_41_cout, square_cell_41_e_2, square_cell_41_s, square_cell_42_cout, square_cell_42_e_2,
       square_cell_43_b_2, square_cell_43_cout, square_cell_43_e_2, square_cell_43_s, square_cell_44_b_2,
       square_cell_44_cout, square_cell_44_e_2, square_cell_44_s, square_cell_45_b_2, square_cell_45_cout,
       square_cell_45_e_2, square_cell_45_s, square_cell_46_b_2, square_cell_46_cout, square_cell_46_e_2,
       square_cell_46_s, square_cell_47_cout, square_cell_47_e_2, square_cell_48_b_2, square_cell_48_cout,
       square_cell_48_s, square_cell_49_b_2, square_cell_49_cout, square_cell_49_e_2, square_cell_49_s,
       square_cell_50_b_2, square_cell_50_cout, square_cell_50_e_2, square_cell_50_s, square_cell_51_b_2,
       square_cell_51_cout, square_cell_51_e_2, square_cell_51_s, square_cell_52_cout, square_cell_52_e_2,
       square_cell_53_b_2, square_cell_53_cout, square_cell_53_e_2, square_cell_53_s, square_cell_54_b_2,
       square_cell_54_cout, square_cell_54_e_2, square_cell_54_s, square_cell_55_b_2, square_cell_55_cout,
       square_cell_55_e_2, square_cell_55_s, square_cell_56_cout, square_cell_56_e_2, square_cell_57_b_2,
       square_cell_57_cout, square_cell_57_s, square_cell_58_b_2, square_cell_58_cout, square_cell_58_e_2,
       square_cell_58_s, square_cell_59_b_2, square_cell_59_cout, square_cell_59_e_2, square_cell_59_s,
       square_cell_60_cout, square_cell_60_e_2, square_cell_61_b_2, square_cell_61_cout, square_cell_61_e_2,
       square_cell_61_s, square_cell_62_b_2, square_cell_62_cout, square_cell_62_e_2, square_cell_62_s,
       square_cell_63_cout, square_cell_63_e_2, square_cell_64_b_2, square_cell_64_cout, square_cell_64_s,
       square_cell_65_b_2, square_cell_65_cout, square_cell_65_e_2, square_cell_65_s, square_cell_66_cout,
       square_cell_66_e_2, square_cell_67_b_2, square_cell_67_cout, square_cell_67_e_2, square_cell_67_s,
       square_cell_68_cout, square_cell_68_e_2, square_cell_69_b_2, square_cell_69_cout, square_cell_69_s,
       square_cell_70_cout, square_cell_70_e_2, square_cell_71_cout, square_cell_71_e_2, square_cell_72_cout;

  Square_Cell square_cell_1 (
    .B(1'b0), .Cin(square_cell_9_cout), .A(1'b0), .E(in_1[7]), .B_2(square_cell_1_b_2), .S(square_cell_1_s),
    .E_2(square_cell_1_e_2));  // open: Cout
  Square_Cell square_cell_2 (
    .B(square_cell_1_b_2), .Cin(square_cell_10_cout), .A(square_cell_1_s), .E(in_1[6]),
    .B_2(square_cell_2_b_2), .S(square_cell_2_s), .E_2(square_cell_2_e_2));  // open: Cout
  Square_Cell square_cell_3 (
    .B(square_cell_2_b_2), .Cin(square_cell_11_cout), .A(square_cell_2_s), .E(in_1[5]),
    .B_2(square_cell_3_b_2), .S(square_cell_3_s), .E_2(square_cell_3_e_2));  // open: Cout
  Square_Cell square_cell_4 (
    .B(square_cell_3_b_2), .Cin(square_cell_12_cout), .A(square_cell_3_s), .E(in_1[4]),
    .B_2(square_cell_4_b_2), .S(square_cell_4_s), .E_2(square_cell_4_e_2));  // open: Cout
  Square_Cell square_cell_5 (
    .B(square_cell_4_b_2), .Cin(square_cell_13_cout), .A(square_cell_4_s), .E(in_1[3]),
    .B_2(square_cell_5_b_2), .S(square_cell_5_s), .E_2(square_cell_5_e_2));  // open: Cout
  Square_Cell square_cell_6 (
    .B(square_cell_5_b_2), .Cin(square_cell_14_cout), .A(square_cell_5_s), .E(in_1[2]),
    .B_2(square_cell_6_b_2), .S(square_cell_6_s), .E_2(square_cell_6_e_2));  // open: Cout
  Square_Cell square_cell_7 (
    .B(square_cell_6_b_2), .Cin(square_cell_15_cout), .A(square_cell_6_s), .E(in_1[1]),
    .B_2(square_cell_7_b_2), .S(square_cell_7_s), .E_2(square_cell_7_e_2));  // open: Cout
  Square_Cell square_cell_8 (
    .B(square_cell_7_b_2), .Cin(square_cell_16_cout), .A(square_cell_7_s), .E(in_1[0]), .S(out_2[15]),
    .E_2(square_cell_8_e_2));  // open: B_2, Cout
  Square_Cell square_cell_9 (
    .B(1'b1), .Cin(1'b0), .A(1'b0), .E(square_cell_1_e_2), .B_2(square_cell_9_b_2),
    .Cout(square_cell_9_cout), .S(square_cell_9_s));  // open: E_2
  Square_Cell square_cell_10 (
    .B(square_cell_1_e_2), .Cin(square_cell_17_cout), .A(square_cell_9_s), .E(square_cell_2_e_2),
    .B_2(square_cell_10_b_2), .Cout(square_cell_10_cout), .S(square_cell_10_s), .E_2(square_cell_10_e_2));
  Square_Cell square_cell_11 (
    .B(square_cell_2_b_2), .Cin(square_cell_18_cout), .A(square_cell_10_s), .E(square_cell_3_e_2),
    .B_2(square_cell_11_b_2), .Cout(square_cell_11_cout), .S(square_cell_11_s), .E_2(square_cell_11_e_2));
  Square_Cell square_cell_12 (
    .B(square_cell_3_b_2), .Cin(square_cell_19_cout), .A(square_cell_11_s), .E(square_cell_4_e_2),
    .B_2(square_cell_12_b_2), .Cout(square_cell_12_cout), .S(square_cell_12_s), .E_2(square_cell_12_e_2));
  Square_Cell square_cell_13 (
    .B(square_cell_4_b_2), .Cin(square_cell_20_cout), .A(square_cell_12_s), .E(square_cell_5_e_2),
    .B_2(square_cell_13_b_2), .Cout(square_cell_13_cout), .S(square_cell_13_s), .E_2(square_cell_13_e_2));
  Square_Cell square_cell_14 (
    .B(square_cell_5_b_2), .Cin(square_cell_21_cout), .A(square_cell_13_s), .E(square_cell_6_e_2),
    .B_2(square_cell_14_b_2), .Cout(square_cell_14_cout), .S(square_cell_14_s), .E_2(square_cell_14_e_2));
  Square_Cell square_cell_15 (
    .B(square_cell_6_b_2), .Cin(square_cell_22_cout), .A(square_cell_14_s), .E(square_cell_7_e_2),
    .B_2(square_cell_15_b_2), .Cout(square_cell_15_cout), .S(square_cell_15_s), .E_2(square_cell_15_e_2));
  Square_Cell square_cell_16 (
    .B(square_cell_7_b_2), .Cin(square_cell_23_cout), .A(square_cell_15_s), .E(square_cell_8_e_2),
    .Cout(square_cell_16_cout), .S(out_2[14]), .E_2(square_cell_16_e_2));  // open: B_2
  Square_Cell square_cell_17 (
    .B(square_cell_1_b_2), .Cin(square_cell_24_cout), .A(1'b0), .E(square_cell_10_e_2),
    .B_2(square_cell_17_b_2), .Cout(square_cell_17_cout), .S(square_cell_17_s), .E_2(square_cell_17_e_2));
  Square_Cell square_cell_18 (
    .B(square_cell_10_b_2), .Cin(square_cell_25_cout), .A(square_cell_17_s), .E(square_cell_11_e_2),
    .B_2(square_cell_18_b_2), .Cout(square_cell_18_cout), .S(square_cell_18_s), .E_2(square_cell_18_e_2));
  Square_Cell square_cell_19 (
    .B(square_cell_11_b_2), .Cin(square_cell_26_cout), .A(square_cell_18_s), .E(square_cell_12_e_2),
    .B_2(square_cell_19_b_2), .Cout(square_cell_19_cout), .S(square_cell_19_s), .E_2(square_cell_19_e_2));
  Square_Cell square_cell_20 (
    .B(square_cell_12_b_2), .Cin(square_cell_27_cout), .A(square_cell_19_s), .E(square_cell_13_e_2),
    .B_2(square_cell_20_b_2), .Cout(square_cell_20_cout), .S(square_cell_20_s), .E_2(square_cell_20_e_2));
  Square_Cell square_cell_21 (
    .B(square_cell_13_b_2), .Cin(square_cell_28_cout), .A(square_cell_20_s), .E(square_cell_14_e_2),
    .B_2(square_cell_21_b_2), .Cout(square_cell_21_cout), .S(square_cell_21_s), .E_2(square_cell_21_e_2));
  Square_Cell square_cell_22 (
    .B(square_cell_14_b_2), .Cin(square_cell_29_cout), .A(square_cell_21_s), .E(square_cell_15_e_2),
    .B_2(square_cell_22_b_2), .Cout(square_cell_22_cout), .S(square_cell_22_s), .E_2(square_cell_22_e_2));
  Square_Cell square_cell_23 (
    .B(square_cell_15_b_2), .Cin(square_cell_30_cout), .A(square_cell_22_s), .E(square_cell_16_e_2),
    .Cout(square_cell_23_cout), .S(out_2[13]), .E_2(square_cell_23_e_2));  // open: B_2
  Square_Cell square_cell_24 (
    .B(square_cell_9_b_2), .Cin(1'b0), .A(1'b0), .E(square_cell_17_e_2), .B_2(square_cell_24_b_2),
    .Cout(square_cell_24_cout), .S(square_cell_24_s));  // open: E_2
  Square_Cell square_cell_25 (
    .B(square_cell_17_e_2), .Cin(square_cell_31_cout), .A(square_cell_24_s), .E(square_cell_18_e_2),
    .B_2(square_cell_25_b_2), .Cout(square_cell_25_cout), .S(square_cell_25_s), .E_2(square_cell_25_e_2));
  Square_Cell square_cell_26 (
    .B(square_cell_18_b_2), .Cin(square_cell_32_cout), .A(square_cell_25_s), .E(square_cell_19_e_2),
    .B_2(square_cell_26_b_2), .Cout(square_cell_26_cout), .S(square_cell_26_s), .E_2(square_cell_26_e_2));
  Square_Cell square_cell_27 (
    .B(square_cell_19_b_2), .Cin(square_cell_33_cout), .A(square_cell_26_s), .E(square_cell_20_e_2),
    .B_2(square_cell_27_b_2), .Cout(square_cell_27_cout), .S(square_cell_27_s), .E_2(square_cell_27_e_2));
  Square_Cell square_cell_28 (
    .B(square_cell_20_b_2), .Cin(square_cell_34_cout), .A(square_cell_27_s), .E(square_cell_21_e_2),
    .B_2(square_cell_28_b_2), .Cout(square_cell_28_cout), .S(square_cell_28_s), .E_2(square_cell_28_e_2));
  Square_Cell square_cell_29 (
    .B(square_cell_21_b_2), .Cin(square_cell_35_cout), .A(square_cell_28_s), .E(square_cell_22_e_2),
    .B_2(square_cell_29_b_2), .Cout(square_cell_29_cout), .S(square_cell_29_s), .E_2(square_cell_29_e_2));
  Square_Cell square_cell_30 (
    .B(square_cell_22_b_2), .Cin(square_cell_36_cout), .A(square_cell_29_s), .E(square_cell_23_e_2),
    .Cout(square_cell_30_cout), .S(out_2[12]), .E_2(square_cell_30_e_2));  // open: B_2
  Square_Cell square_cell_31 (
    .B(square_cell_17_b_2), .Cin(square_cell_37_cout), .A(1'b0), .E(square_cell_25_e_2),
    .B_2(square_cell_31_b_2), .Cout(square_cell_31_cout), .S(square_cell_31_s), .E_2(square_cell_31_e_2));
  Square_Cell square_cell_32 (
    .B(square_cell_25_b_2), .Cin(square_cell_38_cout), .A(square_cell_31_s), .E(square_cell_26_e_2),
    .B_2(square_cell_32_b_2), .Cout(square_cell_32_cout), .S(square_cell_32_s), .E_2(square_cell_32_e_2));
  Square_Cell square_cell_33 (
    .B(square_cell_26_b_2), .Cin(square_cell_39_cout), .A(square_cell_32_s), .E(square_cell_27_e_2),
    .B_2(square_cell_33_b_2), .Cout(square_cell_33_cout), .S(square_cell_33_s), .E_2(square_cell_33_e_2));
  Square_Cell square_cell_34 (
    .B(square_cell_27_b_2), .Cin(square_cell_40_cout), .A(square_cell_33_s), .E(square_cell_28_e_2),
    .B_2(square_cell_34_b_2), .Cout(square_cell_34_cout), .S(square_cell_34_s), .E_2(square_cell_34_e_2));
  Square_Cell square_cell_35 (
    .B(square_cell_28_b_2), .Cin(square_cell_41_cout), .A(square_cell_34_s), .E(square_cell_29_e_2),
    .B_2(square_cell_35_b_2), .Cout(square_cell_35_cout), .S(square_cell_35_s), .E_2(square_cell_35_e_2));
  Square_Cell square_cell_36 (
    .B(square_cell_29_b_2), .Cin(square_cell_42_cout), .A(square_cell_35_s), .E(square_cell_30_e_2),
    .Cout(square_cell_36_cout), .S(out_2[11]), .E_2(square_cell_36_e_2));  // open: B_2
  Square_Cell square_cell_37 (
    .B(square_cell_24_b_2), .Cin(1'b0), .A(1'b0), .E(square_cell_31_e_2), .B_2(square_cell_37_b_2),
    .Cout(square_cell_37_cout), .S(square_cell_37_s));  // open: E_2
  Square_Cell square_cell_38 (
    .B(square_cell_31_e_2), .Cin(square_cell_43_cout), .A(square_cell_37_s), .E(square_cell_32_e_2),
    .B_2(square_cell_38_b_2), .Cout(square_cell_38_cout), .S(square_cell_38_s), .E_2(square_cell_38_e_2));
  Square_Cell square_cell_39 (
    .B(square_cell_32_b_2), .Cin(square_cell_44_cout), .A(square_cell_38_s), .E(square_cell_33_e_2),
    .B_2(square_cell_39_b_2), .Cout(square_cell_39_cout), .S(square_cell_39_s), .E_2(square_cell_39_e_2));
  Square_Cell square_cell_40 (
    .B(square_cell_33_b_2), .Cin(square_cell_45_cout), .A(square_cell_39_s), .E(square_cell_34_e_2),
    .B_2(square_cell_40_b_2), .Cout(square_cell_40_cout), .S(square_cell_40_s), .E_2(square_cell_40_e_2));
  Square_Cell square_cell_41 (
    .B(square_cell_34_b_2), .Cin(square_cell_46_cout), .A(square_cell_40_s), .E(square_cell_35_e_2),
    .B_2(square_cell_41_b_2), .Cout(square_cell_41_cout), .S(square_cell_41_s), .E_2(square_cell_41_e_2));
  Square_Cell square_cell_42 (
    .B(square_cell_35_b_2), .Cin(square_cell_47_cout), .A(square_cell_41_s), .E(square_cell_36_e_2),
    .Cout(square_cell_42_cout), .S(out_2[10]), .E_2(square_cell_42_e_2));  // open: B_2
  Square_Cell square_cell_43 (
    .B(square_cell_31_b_2), .Cin(square_cell_48_cout), .A(1'b0), .E(square_cell_38_e_2),
    .B_2(square_cell_43_b_2), .Cout(square_cell_43_cout), .S(square_cell_43_s), .E_2(square_cell_43_e_2));
  Square_Cell square_cell_44 (
    .B(square_cell_38_b_2), .Cin(square_cell_49_cout), .A(square_cell_43_s), .E(square_cell_39_e_2),
    .B_2(square_cell_44_b_2), .Cout(square_cell_44_cout), .S(square_cell_44_s), .E_2(square_cell_44_e_2));
  Square_Cell square_cell_45 (
    .B(square_cell_39_b_2), .Cin(square_cell_50_cout), .A(square_cell_44_s), .E(square_cell_40_e_2),
    .B_2(square_cell_45_b_2), .Cout(square_cell_45_cout), .S(square_cell_45_s), .E_2(square_cell_45_e_2));
  Square_Cell square_cell_46 (
    .B(square_cell_40_b_2), .Cin(square_cell_51_cout), .A(square_cell_45_s), .E(square_cell_41_e_2),
    .B_2(square_cell_46_b_2), .Cout(square_cell_46_cout), .S(square_cell_46_s), .E_2(square_cell_46_e_2));
  Square_Cell square_cell_47 (
    .B(square_cell_41_b_2), .Cin(square_cell_52_cout), .A(square_cell_46_s), .E(square_cell_42_e_2),
    .Cout(square_cell_47_cout), .S(out_2[9]), .E_2(square_cell_47_e_2));  // open: B_2
  Square_Cell square_cell_48 (
    .B(square_cell_37_b_2), .Cin(1'b0), .A(1'b0), .E(square_cell_43_e_2), .B_2(square_cell_48_b_2),
    .Cout(square_cell_48_cout), .S(square_cell_48_s));  // open: E_2
  Square_Cell square_cell_49 (
    .B(square_cell_43_e_2), .Cin(square_cell_53_cout), .A(square_cell_48_s), .E(square_cell_44_e_2),
    .B_2(square_cell_49_b_2), .Cout(square_cell_49_cout), .S(square_cell_49_s), .E_2(square_cell_49_e_2));
  Square_Cell square_cell_50 (
    .B(square_cell_44_b_2), .Cin(square_cell_54_cout), .A(square_cell_49_s), .E(square_cell_45_e_2),
    .B_2(square_cell_50_b_2), .Cout(square_cell_50_cout), .S(square_cell_50_s), .E_2(square_cell_50_e_2));
  Square_Cell square_cell_51 (
    .B(square_cell_45_b_2), .Cin(square_cell_55_cout), .A(square_cell_50_s), .E(square_cell_46_e_2),
    .B_2(square_cell_51_b_2), .Cout(square_cell_51_cout), .S(square_cell_51_s), .E_2(square_cell_51_e_2));
  Square_Cell square_cell_52 (
    .B(square_cell_46_b_2), .Cin(square_cell_56_cout), .A(square_cell_51_s), .E(square_cell_47_e_2),
    .Cout(square_cell_52_cout), .S(out_2[8]), .E_2(square_cell_52_e_2));  // open: B_2
  Square_Cell square_cell_53 (
    .B(square_cell_43_b_2), .Cin(square_cell_57_cout), .A(1'b0), .E(square_cell_49_e_2),
    .B_2(square_cell_53_b_2), .Cout(square_cell_53_cout), .S(square_cell_53_s), .E_2(square_cell_53_e_2));
  Square_Cell square_cell_54 (
    .B(square_cell_49_b_2), .Cin(square_cell_58_cout), .A(square_cell_53_s), .E(square_cell_50_e_2),
    .B_2(square_cell_54_b_2), .Cout(square_cell_54_cout), .S(square_cell_54_s), .E_2(square_cell_54_e_2));
  Square_Cell square_cell_55 (
    .B(square_cell_50_b_2), .Cin(square_cell_59_cout), .A(square_cell_54_s), .E(square_cell_51_e_2),
    .B_2(square_cell_55_b_2), .Cout(square_cell_55_cout), .S(square_cell_55_s), .E_2(square_cell_55_e_2));
  Square_Cell square_cell_56 (
    .B(square_cell_51_b_2), .Cin(square_cell_60_cout), .A(square_cell_55_s), .E(square_cell_52_e_2),
    .Cout(square_cell_56_cout), .S(out_2[7]), .E_2(square_cell_56_e_2));  // open: B_2
  Square_Cell square_cell_57 (
    .B(square_cell_48_b_2), .Cin(1'b0), .A(1'b0), .E(square_cell_53_e_2), .B_2(square_cell_57_b_2),
    .Cout(square_cell_57_cout), .S(square_cell_57_s));  // open: E_2
  Square_Cell square_cell_58 (
    .B(square_cell_53_e_2), .Cin(square_cell_61_cout), .A(square_cell_57_s), .E(square_cell_54_e_2),
    .B_2(square_cell_58_b_2), .Cout(square_cell_58_cout), .S(square_cell_58_s), .E_2(square_cell_58_e_2));
  Square_Cell square_cell_59 (
    .B(square_cell_54_b_2), .Cin(square_cell_62_cout), .A(square_cell_58_s), .E(square_cell_55_e_2),
    .B_2(square_cell_59_b_2), .Cout(square_cell_59_cout), .S(square_cell_59_s), .E_2(square_cell_59_e_2));
  Square_Cell square_cell_60 (
    .B(square_cell_55_b_2), .Cin(square_cell_63_cout), .A(square_cell_59_s), .E(square_cell_56_e_2),
    .Cout(square_cell_60_cout), .S(out_2[6]), .E_2(square_cell_60_e_2));  // open: B_2
  Square_Cell square_cell_61 (
    .B(square_cell_53_b_2), .Cin(square_cell_64_cout), .A(1'b0), .E(square_cell_58_e_2),
    .B_2(square_cell_61_b_2), .Cout(square_cell_61_cout), .S(square_cell_61_s), .E_2(square_cell_61_e_2));
  Square_Cell square_cell_62 (
    .B(square_cell_58_b_2), .Cin(square_cell_65_cout), .A(square_cell_61_s), .E(square_cell_59_e_2),
    .B_2(square_cell_62_b_2), .Cout(square_cell_62_cout), .S(square_cell_62_s), .E_2(square_cell_62_e_2));
  Square_Cell square_cell_63 (
    .B(square_cell_59_b_2), .Cin(square_cell_66_cout), .A(square_cell_62_s), .E(square_cell_60_e_2),
    .Cout(square_cell_63_cout), .S(out_2[5]), .E_2(square_cell_63_e_2));  // open: B_2
  Square_Cell square_cell_64 (
    .B(square_cell_57_b_2), .Cin(1'b0), .A(1'b0), .E(square_cell_61_e_2), .B_2(square_cell_64_b_2),
    .Cout(square_cell_64_cout), .S(square_cell_64_s));  // open: E_2
  Square_Cell square_cell_65 (
    .B(square_cell_61_e_2), .Cin(square_cell_67_cout), .A(square_cell_64_s), .E(square_cell_62_e_2),
    .B_2(square_cell_65_b_2), .Cout(square_cell_65_cout), .S(square_cell_65_s), .E_2(square_cell_65_e_2));
  Square_Cell square_cell_66 (
    .B(square_cell_62_b_2), .Cin(square_cell_68_cout), .A(square_cell_65_s), .E(square_cell_63_e_2),
    .Cout(square_cell_66_cout), .S(out_2[4]), .E_2(square_cell_66_e_2));  // open: B_2
  Square_Cell square_cell_67 (
    .B(square_cell_61_b_2), .Cin(square_cell_69_cout), .A(1'b0), .E(square_cell_65_e_2),
    .B_2(square_cell_67_b_2), .Cout(square_cell_67_cout), .S(square_cell_67_s), .E_2(square_cell_67_e_2));
  Square_Cell square_cell_68 (
    .B(square_cell_65_b_2), .Cin(square_cell_70_cout), .A(square_cell_67_s), .E(square_cell_66_e_2),
    .Cout(square_cell_68_cout), .S(out_2[3]), .E_2(square_cell_68_e_2));  // open: B_2
  Square_Cell square_cell_69 (
    .B(square_cell_64_b_2), .Cin(1'b0), .A(1'b0), .E(square_cell_67_e_2), .B_2(square_cell_69_b_2),
    .Cout(square_cell_69_cout), .S(square_cell_69_s));  // open: E_2
  Square_Cell square_cell_70 (
    .B(square_cell_67_e_2), .Cin(square_cell_71_cout), .A(square_cell_69_s), .E(square_cell_68_e_2),
    .Cout(square_cell_70_cout), .S(out_2[2]), .E_2(square_cell_70_e_2));  // open: B_2
  Square_Cell square_cell_71 (
    .B(square_cell_67_b_2), .Cin(square_cell_72_cout), .A(1'b0), .E(square_cell_70_e_2),
    .Cout(square_cell_71_cout), .S(out_2[1]), .E_2(square_cell_71_e_2));  // open: B_2
  Square_Cell square_cell_72 (
    .B(square_cell_69_b_2), .Cin(1'b0), .A(1'b0), .E(square_cell_71_e_2), .Cout(square_cell_72_cout),
    .S(out_2[0]));  // open: B_2, E_2
endmodule

module Sqrt_Cell (
  input  A,
  input  B,
  input  Pin,
  input  Cin,
  output S,
  output Cout
);

  wire and_1_out, and_2_out, or_1_out, xor_1_out, xor_2_out;

  xor xor_1 (xor_1_out, A, Cin);
  xor xor_2 (xor_2_out, B, Pin);
  or or_1 (or_1_out, A, Cin);
  and and_1 (and_1_out, A, Cin);
  xor xor_3 (S, xor_1_out, xor_2_out);
  and and_2 (and_2_out, xor_2_out, or_1_out);
  or or_2 (Cout, and_2_out, and_1_out);
endmodule

module Sqrt_Calculator (
  input  [15:0] in_1,
  output [15:0] out_2
);

  wire not_1_out, not_2_out, not_3_out, not_4_out, not_5_out, not_6_out, not_7_out, sqrt_cell_1_s,
       sqrt_cell_2_s, sqrt_cell_3_s, sqrt_cell_4_s, sqrt_cell_5_s, sqrt_cell_6_s, sqrt_cell_7_s,
       sqrt_cell_9_cout, sqrt_cell_9_s, sqrt_cell_10_cout, sqrt_cell_10_s, sqrt_cell_11_cout, sqrt_cell_11_s,
       sqrt_cell_12_cout, sqrt_cell_12_s, sqrt_cell_13_cout, sqrt_cell_13_s, sqrt_cell_14_cout,
       sqrt_cell_14_s, sqrt_cell_15_cout, sqrt_cell_15_s, sqrt_cell_16_cout, sqrt_cell_17_cout,
       sqrt_cell_17_s, sqrt_cell_18_cout, sqrt_cell_18_s, sqrt_cell_19_cout, sqrt_cell_19_s,
       sqrt_cell_20_cout, sqrt_cell_20_s, sqrt_cell_21_cout, sqrt_cell_21_s, sqrt_cell_22_cout,
       sqrt_cell_22_s, sqrt_cell_23_cout, sqrt_cell_24_cout, sqrt_cell_24_s, sqrt_cell_25_cout,
       sqrt_cell_25_s, sqrt_cell_26_cout, sqrt_cell_26_s, sqrt_cell_27_cout, sqrt_cell_27_s,
       sqrt_cell_28_cout, sqrt_cell_28_s, sqrt_cell_29_cout, sqrt_cell_29_s, sqrt_cell_30_cout,
       sqrt_cell_31_cout, sqrt_cell_31_s, sqrt_cell_32_cout, sqrt_cell_32_s, sqrt_cell_33_cout,
       sqrt_cell_33_s, sqrt_cell_34_cout, sqrt_cell_34_s, sqrt_cell_35_cout, sqrt_cell_35_s,
       sqrt_cell_36_cout, sqrt_cell_37_cout, sqrt_cell_37_s, sqrt_cell_38_cout, sqrt_cell_38_s,
       sqrt_cell_39_cout, sqrt_cell_39_s, sqrt_cell_40_cout, sqrt_cell_40_s, sqrt_cell_41_cout,
       sqrt_cell_41_s, sqrt_cell_42_cout, sqrt_cell_43_cout, sqrt_cell_43_s, sqrt_cell_44_cout,
       sqrt_cell_44_s, sqrt_cell_45_cout, sqrt_cell_45_s, sqrt_cell_46_cout, sqrt_cell_46_s,
       sqrt_cell_47_cout, sqrt_cell_48_cout, sqrt_cell_48_s, sqrt_cell_49_cout, sqrt_cell_49_s,
       sqrt_cell_50_cout, sqrt_cell_50_s, sqrt_cell_51_cout, sqrt_cell_51_s, sqrt_cell_52_cout,
       sqrt_cell_53_cout, sqrt_cell_53_s, sqrt_cell_54_cout, sqrt_cell_54_s, sqrt_cell_55_cout,
       sqrt_cell_55_s, sqrt_cell_56_cout, sqrt_cell_57_cout, sqrt_cell_57_s, sqrt_cell_58_cout,
       sqrt_cell_58_s, sqrt_cell_59_cout, sqrt_cell_59_s, sqrt_cell_60_cout, sqrt_cell_61_cout,
       sqrt_cell_61_s, sqrt_cell_62_cout, sqrt_cell_62_s, sqrt_cell_63_cout, sqrt_cell_64_cout,
       sqrt_cell_64_s, sqrt_cell_65_cout, sqrt_cell_65_s, sqrt_cell_66_cout, sqrt_cell_67_cout,
       sqrt_cell_67_s, sqrt_cell_68_cout, sqrt_cell_69_cout, sqrt_cell_69_s, sqrt_cell_70_cout,
       sqrt_cell_71_cout, sqrt_cell_72_cout;

  Sqrt_Cell sqrt_cell_1 (
    .A(in_1[15]), .B(1'b0), .Pin(1'b1), .Cin(sqrt_cell_9_cout), .S(sqrt_cell_1_s), .Cout(out_2[7]));
  Sqrt_Cell sqrt_cell_2 (
    .A(sqrt_cell_1_s), .B(1'b0), .Pin(out_2[7]), .Cin(sqrt_cell_10_cout), .S(sqrt_cell_2_s), .Cout(out_2[6]));
  Sqrt_Cell sqrt_cell_3 (
    .A(sqrt_cell_2_s), .B(1'b0), .Pin(out_2[6]), .Cin(sqrt_cell_11_cout), .S(sqrt_cell_3_s), .Cout(out_2[5]));
  Sqrt_Cell sqrt_cell_4 (
    .A(sqrt_cell_3_s), .B(1'b0), .Pin(out_2[5]), .Cin(sqrt_cell_12_cout), .S(sqrt_cell_4_s), .Cout(out_2[4]));
  Sqrt_Cell sqrt_cell_5 (
    .A(sqrt_cell_4_s), .B(1'b0), .Pin(out_2[4]), .Cin(sqrt_cell_13_cout), .S(sqrt_cell_5_s), .Cout(out_2[3]));
  Sqrt_Cell sqrt_cell_6 (
    .A(sqrt_cell_5_s), .B(1'b0), .Pin(out_2[3]), .Cin(sqrt_cell_14_cout), .S(sqrt_cell_6_s), .Cout(out_2[2]));
  Sqrt_Cell sqrt_cell_7 (
    .A(sqrt_cell_6_s), .B(1'b0), .Pin(out_2[2]), .Cin(sqrt_cell_15_cout), .S(sqrt_cell_7_s), .Cout(out_2[1]));
  Sqrt_Cell sqrt_cell_8 (
    .A(sqrt_cell_7_s), .B(1'b0), .Pin(out_2[1]), .Cin(sqrt_cell_16_cout), .Cout(out_2[0]));  // open: S
  Sqrt_Cell sqrt_cell_9 (.A(in_1[14]), .B(1'b1), .Pin(1'b1), .Cin(1'b1), .S(sqrt_cell_9_s), .Cout(sqrt_cell_9_cout));
  Sqrt_Cell sqrt_cell_10 (
    .A(sqrt_cell_9_s), .B(out_2[7]), .Pin(out_2[7]), .Cin(sqrt_cell_17_cout), .S(sqrt_cell_10_s),
    .Cout(sqrt_cell_10_cout));
  Sqrt_Cell sqrt_cell_11 (
    .A(sqrt_cell_10_s), .B(1'b0), .Pin(out_2[6]), .Cin(sqrt_cell_18_cout), .S(sqrt_cell_11_s),
    .Cout(sqrt_cell_11_cout));
  Sqrt_Cell sqrt_cell_12 (
    .A(sqrt_cell_11_s), .B(1'b0), .Pin(out_2[5]), .Cin(sqrt_cell_19_cout), .S(sqrt_cell_12_s),
    .Cout(sqrt_cell_12_cout));
  Sqrt_Cell sqrt_cell_13 (
    .A(sqrt_cell_12_s), .B(1'b0), .Pin(out_2[4]), .Cin(sqrt_cell_20_cout), .S(sqrt_cell_13_s),
    .Cout(sqrt_cell_13_cout));
  Sqrt_Cell sqrt_cell_14 (
    .A(sqrt_cell_13_s), .B(1'b0), .Pin(out_2[3]), .Cin(sqrt_cell_21_cout), .S(sqrt_cell_14_s),
    .Cout(sqrt_cell_14_cout));
  Sqrt_Cell sqrt_cell_15 (
    .A(sqrt_cell_14_s), .B(1'b0), .Pin(out_2[2]), .Cin(sqrt_cell_22_cout), .S(sqrt_cell_15_s),
    .Cout(sqrt_cell_15_cout));
  Sqrt_Cell sqrt_cell_16 (
    .A(sqrt_cell_15_s), .B(1'b0), .Pin(out_2[1]), .Cin(sqrt_cell_23_cout), .Cout(sqrt_cell_16_cout));  // open: S
  not not_1 (not_1_out, out_2[7]);
  Sqrt_Cell sqrt_cell_17 (
    .A(in_1[13]), .B(not_1_out), .Pin(out_2[7]), .Cin(sqrt_cell_24_cout), .S(sqrt_cell_17_s),
    .Cout(sqrt_cell_17_cout));
  Sqrt_Cell sqrt_cell_18 (
    .A(sqrt_cell_17_s), .B(out_2[7]), .Pin(out_2[6]), .Cin(sqrt_cell_25_cout), .S(sqrt_cell_18_s),
    .Cout(sqrt_cell_18_cout));
  Sqrt_Cell sqrt_cell_19 (
    .A(sqrt_cell_18_s), .B(1'b0), .Pin(out_2[5]), .Cin(sqrt_cell_26_cout), .S(sqrt_cell_19_s),
    .Cout(sqrt_cell_19_cout));
  Sqrt_Cell sqrt_cell_20 (
    .A(sqrt_cell_19_s), .B(1'b0), .Pin(out_2[4]), .Cin(sqrt_cell_27_cout), .S(sqrt_cell_20_s),
    .Cout(sqrt_cell_20_cout));
  Sqrt_Cell sqrt_cell_21 (
    .A(sqrt_cell_20_s), .B(1'b0), .Pin(out_2[3]), .Cin(sqrt_cell_28_cout), .S(sqrt_cell_21_s),
    .Cout(sqrt_cell_21_cout));
  Sqrt_Cell sqrt_cell_22 (
    .A(sqrt_cell_21_s), .B(1'b0), .Pin(out_2[2]), .Cin(sqrt_cell_29_cout), .S(sqrt_cell_22_s),
    .Cout(sqrt_cell_22_cout));
  Sqrt_Cell sqrt_cell_23 (
    .A(sqrt_cell_22_s), .B(1'b0), .Pin(out_2[1]), .Cin(sqrt_cell_30_cout), .Cout(sqrt_cell_23_cout));  // open: S
  Sqrt_Cell sqrt_cell_24 (
    .A(in_1[12]), .B(1'b1), .Pin(out_2[7]), .Cin(out_2[7]), .S(sqrt_cell_24_s), .Cout(sqrt_cell_24_cout));
  Sqrt_Cell sqrt_cell_25 (
    .A(sqrt_cell_24_s), .B(out_2[6]), .Pin(out_2[6]), .Cin(sqrt_cell_31_cout), .S(sqrt_cell_25_s),
    .Cout(sqrt_cell_25_cout));
  Sqrt_Cell sqrt_cell_26 (
    .A(sqrt_cell_25_s), .B(out_2[7]), .Pin(out_2[5]), .Cin(sqrt_cell_32_cout), .S(sqrt_cell_26_s),
    .Cout(sqrt_cell_26_cout));
  Sqrt_Cell sqrt_cell_27 (
    .A(sqrt_cell_26_s), .B(1'b0), .Pin(out_2[4]), .Cin(sqrt_cell_33_cout), .S(sqrt_cell_27_s),
    .Cout(sqrt_cell_27_cout));
  Sqrt_Cell sqrt_cell_28 (
    .A(sqrt_cell_27_s), .B(1'b0), .Pin(out_2[3]), .Cin(sqrt_cell_34_cout), .S(sqrt_cell_28_s),
    .Cout(sqrt_cell_28_cout));
  Sqrt_Cell sqrt_cell_29 (
    .A(sqrt_cell_28_s), .B(1'b0), .Pin(out_2[2]), .Cin(sqrt_cell_35_cout), .S(sqrt_cell_29_s),
    .Cout(sqrt_cell_29_cout));
  Sqrt_Cell sqrt_cell_30 (
    .A(sqrt_cell_29_s), .B(1'b0), .Pin(out_2[1]), .Cin(sqrt_cell_36_cout), .Cout(sqrt_cell_30_cout));  // open: S
  not not_2 (not_2_out, out_2[6]);
  Sqrt_Cell sqrt_cell_31 (
    .A(in_1[11]), .B(not_2_out), .Pin(out_2[6]), .Cin(sqrt_cell_37_cout), .S(sqrt_cell_31_s),
    .Cout(sqrt_cell_31_cout));
  Sqrt_Cell sqrt_cell_32 (
    .A(sqrt_cell_31_s), .B(out_2[6]), .Pin(out_2[5]), .Cin(sqrt_cell_38_cout), .S(sqrt_cell_32_s),
    .Cout(sqrt_cell_32_cout));
  Sqrt_Cell sqrt_cell_33 (
    .A(sqrt_cell_32_s), .B(out_2[7]), .Pin(out_2[4]), .Cin(sqrt_cell_39_cout), .S(sqrt_cell_33_s),
    .Cout(sqrt_cell_33_cout));
  Sqrt_Cell sqrt_cell_34 (
    .A(sqrt_cell_33_s), .B(1'b0), .Pin(out_2[3]), .Cin(sqrt_cell_40_cout), .S(sqrt_cell_34_s),
    .Cout(sqrt_cell_34_cout));
  Sqrt_Cell sqrt_cell_35 (
    .A(sqrt_cell_34_s), .B(1'b0), .Pin(out_2[2]), .Cin(sqrt_cell_41_cout), .S(sqrt_cell_35_s),
    .Cout(sqrt_cell_35_cout));
  Sqrt_Cell sqrt_cell_36 (
    .A(sqrt_cell_35_s), .B(1'b0), .Pin(out_2[1]), .Cin(sqrt_cell_42_cout), .Cout(sqrt_cell_36_cout));  // open: S
  Sqrt_Cell sqrt_cell_37 (
    .A(in_1[10]), .B(1'b1), .Pin(out_2[6]), .Cin(out_2[6]), .S(sqrt_cell_37_s), .Cout(sqrt_cell_37_cout));
  not not_3 (not_3_out, out_2[5]);
  Sqrt_Cell sqrt_cell_38 (
    .A(sqrt_cell_37_s), .B(out_2[5]), .Pin(out_2[5]), .Cin(sqrt_cell_43_cout), .S(sqrt_cell_38_s),
    .Cout(sqrt_cell_38_cout));
  Sqrt_Cell sqrt_cell_39 (
    .A(sqrt_cell_38_s), .B(out_2[6]), .Pin(out_2[4]), .Cin(sqrt_cell_44_cout), .S(sqrt_cell_39_s),
    .Cout(sqrt_cell_39_cout));
  Sqrt_Cell sqrt_cell_40 (
    .A(sqrt_cell_39_s), .B(out_2[7]), .Pin(out_2[3]), .Cin(sqrt_cell_45_cout), .S(sqrt_cell_40_s),
    .Cout(sqrt_cell_40_cout));
  Sqrt_Cell sqrt_cell_41 (
    .A(sqrt_cell_40_s), .B(1'b0), .Pin(out_2[2]), .Cin(sqrt_cell_46_cout), .S(sqrt_cell_41_s),
    .Cout(sqrt_cell_41_cout));
  Sqrt_Cell sqrt_cell_42 (
    .A(sqrt_cell_41_s), .B(1'b0), .Pin(out_2[1]), .Cin(sqrt_cell_47_cout), .Cout(sqrt_cell_42_cout));  // open: S
  Sqrt_Cell sqrt_cell_43 (
    .A(in_1[9]), .B(not_3_out), .Pin(out_2[5]), .Cin(sqrt_cell_48_cout), .S(sqrt_cell_43_s),
    .Cout(sqrt_cell_43_cout));
  Sqrt_Cell sqrt_cell_44 (
    .A(sqrt_cell_43_s), .B(out_2[5]), .Pin(out_2[4]), .Cin(sqrt_cell_49_cout), .S(sqrt_cell_44_s),
    .Cout(sqrt_cell_44_cout));
  Sqrt_Cell sqrt_cell_45 (
    .A(sqrt_cell_44_s), .B(out_2[6]), .Pin(out_2[3]), .Cin(sqrt_cell_50_cout), .S(sqrt_cell_45_s),
    .Cout(sqrt_cell_45_cout));
  Sqrt_Cell sqrt_cell_46 (
    .A(sqrt_cell_45_s), .B(out_2[7]), .Pin(out_2[2]), .Cin(sqrt_cell_51_cout), .S(sqrt_cell_46_s),
    .Cout(sqrt_cell_46_cout));
  Sqrt_Cell sqrt_cell_47 (
    .A(sqrt_cell_46_s), .B(1'b0), .Pin(out_2[1]), .Cin(sqrt_cell_52_cout), .Cout(sqrt_cell_47_cout));  // open: S
  Sqrt_Cell sqrt_cell_48 (
    .A(in_1[8]), .B(1'b1), .Pin(out_2[5]), .Cin(out_2[5]), .S(sqrt_cell_48_s), .Cout(sqrt_cell_48_cout));
  not not_4 (not_4_out, out_2[4]);
  Sqrt_Cell sqrt_cell_49 (
    .A(sqrt_cell_48_s), .B(out_2[4]), .Pin(out_2[4]), .Cin(sqrt_cell_53_cout), .S(sqrt_cell_49_s),
    .Cout(sqrt_cell_49_cout));
  Sqrt_Cell sqrt_cell_50 (
    .A(sqrt_cell_49_s), .B(out_2[5]), .Pin(out_2[3]), .Cin(sqrt_cell_54_cout), .S(sqrt_cell_50_s),
    .Cout(sqrt_cell_50_cout));
  Sqrt_Cell sqrt_cell_51 (
    .A(sqrt_cell_50_s), .B(out_2[6]), .Pin(out_2[2]), .Cin(sqrt_cell_55_cout), .S(sqrt_cell_51_s),
    .Cout(sqrt_cell_51_cout));
  Sqrt_Cell sqrt_cell_52 (
    .A(sqrt_cell_51_s), .B(out_2[7]), .Pin(out_2[1]), .Cin(sqrt_cell_56_cout), .Cout(sqrt_cell_52_cout));  // open: S
  Sqrt_Cell sqrt_cell_53 (
    .A(in_1[7]), .B(not_4_out), .Pin(out_2[4]), .Cin(sqrt_cell_57_cout), .S(sqrt_cell_53_s),
    .Cout(sqrt_cell_53_cout));
  Sqrt_Cell sqrt_cell_54 (
    .A(sqrt_cell_53_s), .B(out_2[4]), .Pin(out_2[3]), .Cin(sqrt_cell_58_cout), .S(sqrt_cell_54_s),
    .Cout(sqrt_cell_54_cout));
  Sqrt_Cell sqrt_cell_55 (
    .A(sqrt_cell_54_s), .B(out_2[5]), .Pin(out_2[2]), .Cin(sqrt_cell_59_cout), .S(sqrt_cell_55_s),
    .Cout(sqrt_cell_55_cout));
  Sqrt_Cell sqrt_cell_56 (
    .A(sqrt_cell_55_s), .B(out_2[6]), .Pin(out_2[1]), .Cin(sqrt_cell_60_cout), .Cout(sqrt_cell_56_cout));  // open: S
  Sqrt_Cell sqrt_cell_57 (
    .A(in_1[6]), .B(1'b1), .Pin(out_2[4]), .Cin(out_2[4]), .S(sqrt_cell_57_s), .Cout(sqrt_cell_57_cout));
  Sqrt_Cell sqrt_cell_58 (
    .A(sqrt_cell_57_s), .B(out_2[3]), .Pin(out_2[3]), .Cin(sqrt_cell_61_cout), .S(sqrt_cell_58_s),
    .Cout(sqrt_cell_58_cout));
  Sqrt_Cell sqrt_cell_59 (
    .A(sqrt_cell_58_s), .B(out_2[4]), .Pin(out_2[2]), .Cin(sqrt_cell_62_cout), .S(sqrt_cell_59_s),
    .Cout(sqrt_cell_59_cout));
  Sqrt_Cell sqrt_cell_60 (
    .A(sqrt_cell_59_s), .B(out_2[5]), .Pin(out_2[1]), .Cin(sqrt_cell_63_cout), .Cout(sqrt_cell_60_cout));  // open: S
  not not_5 (not_5_out, out_2[3]);
  Sqrt_Cell sqrt_cell_61 (
    .A(in_1[5]), .B(not_5_out), .Pin(out_2[3]), .Cin(sqrt_cell_64_cout), .S(sqrt_cell_61_s),
    .Cout(sqrt_cell_61_cout));
  Sqrt_Cell sqrt_cell_62 (
    .A(sqrt_cell_61_s), .B(out_2[3]), .Pin(out_2[2]), .Cin(sqrt_cell_65_cout), .S(sqrt_cell_62_s),
    .Cout(sqrt_cell_62_cout));
  Sqrt_Cell sqrt_cell_63 (
    .A(sqrt_cell_62_s), .B(out_2[4]), .Pin(out_2[1]), .Cin(sqrt_cell_66_cout), .Cout(sqrt_cell_63_cout));  // open: S
  Sqrt_Cell sqrt_cell_64 (
    .A(in_1[4]), .B(1'b1), .Pin(out_2[3]), .Cin(out_2[3]), .S(sqrt_cell_64_s), .Cout(sqrt_cell_64_cout));
  Sqrt_Cell sqrt_cell_65 (
    .A(sqrt_cell_64_s), .B(out_2[2]), .Pin(out_2[2]), .Cin(sqrt_cell_67_cout), .S(sqrt_cell_65_s),
    .Cout(sqrt_cell_65_cout));
  Sqrt_Cell sqrt_cell_66 (
    .A(sqrt_cell_65_s), .B(out_2[3]), .Pin(out_2[1]), .Cin(sqrt_cell_68_cout), .Cout(sqrt_cell_66_cout));  // open: S
  not not_6 (not_6_out, out_2[2]);
  Sqrt_Cell sqrt_cell_67 (
    .A(in_1[3]), .B(not_6_out), .Pin(out_2[2]), .Cin(sqrt_cell_69_cout), .S(sqrt_cell_67_s),
    .Cout(sqrt_cell_67_cout));
  Sqrt_Cell sqrt_cell_68 (
    .A(sqrt_cell_67_s), .B(out_2[2]), .Pin(out_2[1]), .Cin(sqrt_cell_70_cout), .Cout(sqrt_cell_68_cout));  // open: S
  Sqrt_Cell sqrt_cell_69 (
    .A(in_1[2]), .B(1'b1), .Pin(out_2[2]), .Cin(out_2[2]), .S(sqrt_cell_69_s), .Cout(sqrt_cell_69_cout));
  not not_7 (not_7_out, out_2[1]);
  Sqrt_Cell sqrt_cell_70 (
    .A(sqrt_cell_69_s), .B(out_2[1]), .Pin(out_2[1]), .Cin(sqrt_cell_71_cout), .Cout(sqrt_cell_70_cout));  // open: S
  Sqrt_Cell sqrt_cell_71 (
    .A(in_1[1]), .B(not_7_out), .Pin(out_2[1]), .Cin(sqrt_cell_72_cout), .Cout(sqrt_cell_71_cout));  // open: S
  Sqrt_Cell sqrt_cell_72 (.A(in_1[0]), .B(1'b1), .Pin(out_2[1]), .Cin(out_2[1]), .Cout(sqrt_cell_72_cout));  // open: S

  assign out_2[15:8] = {8{1'b0}};
endmodule

module HA (
  input  in_1,
  input  in_2,
  output out_3,
  output out_4
);

  xor xor_1 (out_3, in_1, in_2);
  and and_1 (out_4, in_2, in_1);
endmodule

module Bit_Counter (
  input  [15:0] in_1,
  output [15:0] out_2
);

  wire fa_1_out_4, fa_1_out_5, fa_2_out_4, fa_2_out_5, fa_3_out_4, fa_3_out_5, fa_4_out_4, fa_4_out_5,
       fa_5_out_4, fa_5_out_5, fa_6_out_4, fa_6_out_5, fa_7_out_4, fa_7_out_5, fa_8_out_4, fa_8_out_5,
       fa_9_out_4, fa_9_out_5, fa_10_out_4, fa_10_out_5, fa_11_out_4, fa_11_out_5, ha_1_out_4, ha_2_out_4,
       ha_3_out_4;

  FA fa_1 (.in_2(in_1[13]), .in_3(in_1[14]), .out_4(fa_1_out_4), .in_1(in_1[12]), .out_5(fa_1_out_5));
  FA fa_2 (.in_2(in_1[10]), .in_3(in_1[11]), .out_4(fa_2_out_4), .in_1(in_1[9]), .out_5(fa_2_out_5));
  FA fa_3 (.in_2(in_1[6]), .in_3(in_1[5]), .out_4(fa_3_out_4), .in_1(in_1[7]), .out_5(fa_3_out_5));
  FA fa_4 (.in_2(in_1[3]), .in_3(in_1[4]), .out_4(fa_4_out_4), .in_1(in_1[2]), .out_5(fa_4_out_5));
  FA fa_5 (.in_2(fa_1_out_4), .in_3(fa_2_out_4), .out_4(fa_5_out_4), .in_1(in_1[8]), .out_5(fa_5_out_5));
  FA fa_6 (.in_2(fa_1_out_5), .in_3(fa_2_out_5), .out_4(fa_6_out_4), .in_1(fa_5_out_5), .out_5(fa_6_out_5));
  FA fa_7 (.in_2(fa_3_out_4), .in_3(fa_4_out_4), .out_4(fa_7_out_4), .in_1(in_1[1]), .out_5(fa_7_out_5));
  FA fa_8 (.in_2(fa_3_out_5), .in_3(fa_4_out_5), .out_4(fa_8_out_4), .in_1(fa_7_out_5), .out_5(fa_8_out_5));
  FA fa_9 (.in_2(fa_5_out_4), .in_3(fa_7_out_4), .out_4(fa_9_out_4), .in_1(in_1[0]), .out_5(fa_9_out_5));
  FA fa_10 (.in_2(fa_6_out_4), .in_3(fa_8_out_4), .out_4(fa_10_out_4), .in_1(fa_9_out_5), .out_5(fa_10_out_5));
  FA fa_11 (.in_2(fa_6_out_5), .in_3(fa_8_out_5), .out_4(fa_11_out_4), .in_1(fa_10_out_5), .out_5(fa_11_out_5));
  HA ha_1 (.in_1(fa_9_out_4), .in_2(in_1[15]), .out_3(out_2[0]), .out_4(ha_1_out_4));
  HA ha_2 (.in_1(fa_10_out_4), .in_2(ha_1_out_4), .out_3(out_2[1]), .out_4(ha_2_out_4));
  HA ha_3 (.in_1(fa_11_out_4), .in_2(ha_2_out_4), .out_3(out_2[2]), .out_4(ha_3_out_4));
  HA ha_4 (.in_1(fa_11_out_5), .in_2(ha_3_out_4), .out_3(out_2[3]), .out_4(out_2[4]));

  assign out_2[15:5] = {11{1'b0}};
endmodule

module RNG (
  input  in_1,
  output [15:0] out_2
);

  Random #(.width(16)) random_1 (.clk(in_1), .out(out_2));  // open: next, clr
endmodule

module Delay (
  input  in_1,
  output out_2
);

  wire buffer_1_out, buffer_2_out, buffer_3_out, buffer_4_out, buffer_5_out, buffer_6_out, buffer_7_out,
       buffer_8_out, buffer_9_out, buffer_10_out, buffer_11_out, buffer_12_out, buffer_13_out, buffer_14_out,
       buffer_15_out;

  buf buffer_1 (buffer_1_out, in_1);
  buf buffer_2 (buffer_2_out, buffer_1_out);
  buf buffer_3 (buffer_3_out, buffer_2_out);
  buf buffer_4 (buffer_4_out, buffer_3_out);
  buf buffer_5 (buffer_5_out, buffer_4_out);
  buf buffer_6 (buffer_6_out, buffer_5_out);
  buf buffer_7 (buffer_7_out, buffer_6_out);
  buf buffer_8 (buffer_8_out, buffer_7_out);
  buf buffer_9 (buffer_9_out, buffer_8_out);
  buf buffer_10 (buffer_10_out, buffer_9_out);
  buf buffer_11 (buffer_11_out, buffer_10_out);
  buf buffer_12 (buffer_12_out, buffer_11_out);
  buf buffer_13 (buffer_13_out, buffer_12_out);
  buf buffer_14 (buffer_14_out, buffer_13_out);
  buf buffer_15 (buffer_15_out, buffer_14_out);
  buf buffer_16 (out_2, buffer_15_out);
endmodule

module Comparator_Cell (
  input  [3:0] A,
  input  in_2,
  input  [3:0] B,
  input  in_4,
  input  in_5,
  output A___B,
  output A___B_2,
  output A___B_3
);

  wire nand_1_out, nand_2_out, nand_3_out, nand_4_out, nand_5_out, nand_6_out, nand_7_out, nand_8_out,
       nand_9_out, nand_10_out, nand_11_out, nand_12_out, not_1_out, not_2_out, not_3_out, not_4_out,
       not_5_out, not_6_out, not_7_out, not_8_out, not_9_out, not_10_out, not_11_out, not_12_out, not_13_out,
       not_14_out, not_15_out, not_16_out, not_17_out, not_18_out, not_19_out, or_1_out, or_2_out, or_3_out,
       or_4_out;

  not not_1 (not_1_out, B[3]);
  not not_2 (not_2_out, A[3]);
  not not_3 (not_3_out, B[2]);
  not not_4 (not_4_out, A[2]);
  not not_5 (not_5_out, B[1]);
  not not_6 (not_6_out, A[1]);
  not not_7 (not_7_out, B[0]);
  not not_8 (not_8_out, A[0]);
  not not_9 (not_9_out, not_1_out);
  not not_10 (not_10_out, not_2_out);
  not not_11 (not_11_out, not_3_out);
  not not_12 (not_12_out, not_4_out);
  not not_13 (not_13_out, not_5_out);
  not not_14 (not_14_out, not_6_out);
  not not_15 (not_15_out, not_7_out);
  not not_16 (not_16_out, not_8_out);
  nand nand_1 (nand_1_out, not_9_out, not_2_out);
  nand nand_2 (nand_2_out, not_1_out, not_10_out);
  nand nand_3 (nand_3_out, not_11_out, not_4_out);
  nand nand_4 (nand_4_out, not_3_out, not_12_out);
  nand nand_5 (nand_5_out, not_13_out, not_6_out);
  nand nand_6 (nand_6_out, not_5_out, not_14_out);
  nand nand_7 (nand_7_out, not_15_out, not_8_out);
  nand nand_8 (nand_8_out, not_7_out, not_16_out);
  not not_17 (not_17_out, in_2);
  not not_18 (not_18_out, in_4);
  not not_19 (not_19_out, in_5);
  nand nand_9 (nand_9_out, nand_1_out, nand_2_out);
  nand nand_10 (nand_10_out, nand_3_out, nand_4_out);
  nand nand_11 (nand_11_out, nand_5_out, nand_6_out);
  nand nand_12 (nand_12_out, nand_7_out, nand_8_out);
  or or_1 (or_1_out, nand_9_out, nand_3_out);
  or or_2 (or_2_out, nand_9_out, nand_10_out, nand_5_out);
  or or_3 (or_3_out, nand_9_out, nand_10_out, nand_11_out, nand_7_out);
  or or_4 (or_4_out, nand_9_out, nand_10_out, nand_11_out, nand_12_out, not_17_out);
  nor nor_1 (A___B_2, nand_9_out, nand_10_out, nand_11_out, nand_12_out, not_18_out);
  nand nand_13 (A___B, nand_1_out, or_1_out, or_2_out, or_3_out, or_4_out);
  nor nor_2 (A___B_3, A___B, A___B_2, not_19_out);
endmodule

module Comparator (
  input  [15:0] in_1,
  input  [15:0] in_2,
  output out_3,
  output out_4,
  output out_5
);

  wire comparator_cell_1_a___b, comparator_cell_1_a___b_2, comparator_cell_2_a___b,
       comparator_cell_2_a___b_2, comparator_cell_3_a___b, comparator_cell_3_a___b_2;

  Comparator_Cell comparator_cell_1 (
    .A(in_1[3:0]), .in_2(1'b0), .B(in_2[3:0]), .in_4(1'b1), .in_5(1'b1), .A___B(comparator_cell_1_a___b),
    .A___B_2(comparator_cell_1_a___b_2));  // open: A___B_3
  Comparator_Cell comparator_cell_2 (
    .A(in_1[7:4]), .in_2(comparator_cell_1_a___b), .B(in_2[7:4]), .in_4(comparator_cell_1_a___b_2),
    .in_5(1'b1), .A___B(comparator_cell_2_a___b), .A___B_2(comparator_cell_2_a___b_2));  // open: A___B_3
  Comparator_Cell comparator_cell_3 (
    .A(in_1[11:8]), .in_2(comparator_cell_2_a___b), .B(in_2[11:8]), .in_4(comparator_cell_2_a___b_2),
    .in_5(1'b1), .A___B(comparator_cell_3_a___b), .A___B_2(comparator_cell_3_a___b_2));  // open: A___B_3
  Comparator_Cell comparator_cell_4 (
    .A(in_1[15:12]), .in_2(comparator_cell_3_a___b), .B(in_2[15:12]), .in_4(comparator_cell_3_a___b_2),
    .in_5(1'b1), .A___B(out_3), .A___B_2(out_4), .A___B_3(out_5));
endmodule

module Condition_Decoder (
  input  in_1,
  input  in_2,
  input  in_3,
  input  [5:0] in_4,
  output out_5
);

  wire and_1_out, and_2_out, and_3_out, and_4_out, and_5_out, and_6_out, not_1_out, or_1_out, or_3_out;

  and and_1 (and_1_out, in_2, in_4[0]);
  not not_1 (not_1_out, in_2);
  and and_2 (and_2_out, in_1, in_4[2]);
  and and_3 (and_3_out, not_1_out, in_4[1]);
  or or_1 (or_1_out, in_2, in_1);
  and and_4 (and_4_out, in_4[3], in_3);
  or or_2 (out_5, and_1_out, and_3_out, and_2_out, and_4_out, and_5_out, and_6_out);
  or or_3 (or_3_out, in_3, in_2);
  and and_5 (and_5_out, or_1_out, in_4[4]);
  and and_6 (and_6_out, or_3_out, in_4[5]);
endmodule

module Long_Delay (
  input  in_1,
  output out_2
);

  wire buffer_1_out, buffer_2_out, buffer_3_out, buffer_4_out, buffer_5_out, buffer_6_out, buffer_7_out,
       buffer_8_out, buffer_9_out, buffer_10_out, buffer_11_out, buffer_12_out, buffer_13_out, buffer_14_out,
       buffer_15_out, buffer_16_out, buffer_17_out, buffer_18_out, buffer_19_out, buffer_20_out,
       buffer_21_out, buffer_22_out, buffer_23_out, buffer_24_out, buffer_25_out, buffer_26_out,
       buffer_27_out, buffer_28_out, buffer_29_out, buffer_30_out, buffer_31_out, buffer_32_out,
       buffer_33_out, buffer_34_out, buffer_35_out, buffer_36_out, buffer_37_out, buffer_38_out,
       buffer_39_out, buffer_40_out, buffer_41_out, buffer_42_out, buffer_43_out, buffer_44_out,
       buffer_45_out, buffer_46_out, buffer_47_out, buffer_48_out, buffer_50_out, buffer_51_out,
       buffer_52_out, buffer_53_out, buffer_54_out, buffer_55_out, buffer_56_out, buffer_57_out,
       buffer_58_out, buffer_59_out, buffer_60_out, buffer_61_out, buffer_62_out, buffer_63_out,
       buffer_64_out;

  buf buffer_1 (buffer_1_out, in_1);
  buf buffer_2 (buffer_2_out, buffer_1_out);
  buf buffer_3 (buffer_3_out, buffer_2_out);
  buf buffer_4 (buffer_4_out, buffer_3_out);
  buf buffer_5 (buffer_5_out, buffer_4_out);
  buf buffer_6 (buffer_6_out, buffer_5_out);
  buf buffer_7 (buffer_7_out, buffer_6_out);
  buf buffer_8 (buffer_8_out, buffer_7_out);
  buf buffer_9 (buffer_9_out, buffer_8_out);
  buf buffer_10 (buffer_10_out, buffer_9_out);
  buf buffer_11 (buffer_11_out, buffer_10_out);
  buf buffer_12 (buffer_12_out, buffer_11_out);
  buf buffer_13 (buffer_13_out, buffer_12_out);
  buf buffer_14 (buffer_14_out, buffer_13_out);
  buf buffer_15 (buffer_15_out, buffer_14_out);
  buf buffer_16 (buffer_16_out, buffer_15_out);
  buf buffer_17 (buffer_17_out, buffer_19_out);
  buf buffer_18 (buffer_18_out, buffer_17_out);
  buf buffer_19 (buffer_19_out, buffer_20_out);
  buf buffer_20 (buffer_20_out, buffer_22_out);
  buf buffer_21 (buffer_21_out, buffer_18_out);
  buf buffer_22 (buffer_22_out, buffer_24_out);
  buf buffer_23 (buffer_23_out, buffer_21_out);
  buf buffer_24 (buffer_24_out, buffer_27_out);
  buf buffer_25 (buffer_25_out, buffer_23_out);
  buf buffer_26 (buffer_26_out, buffer_25_out);
  buf buffer_27 (buffer_27_out, buffer_28_out);
  buf buffer_28 (buffer_28_out, buffer_31_out);
  buf buffer_29 (buffer_29_out, buffer_26_out);
  buf buffer_30 (buffer_30_out, buffer_29_out);
  buf buffer_31 (buffer_31_out, buffer_33_out);
  buf buffer_32 (buffer_32_out, buffer_30_out);
  buf buffer_33 (buffer_33_out, buffer_34_out);
  buf buffer_34 (buffer_34_out, buffer_37_out);
  buf buffer_35 (buffer_35_out, buffer_32_out);
  buf buffer_36 (buffer_36_out, buffer_35_out);
  buf buffer_37 (buffer_37_out, buffer_38_out);
  buf buffer_38 (buffer_38_out, buffer_40_out);
  buf buffer_39 (buffer_39_out, buffer_36_out);
  buf buffer_40 (buffer_40_out, buffer_43_out);
  buf buffer_41 (buffer_41_out, buffer_39_out);
  buf buffer_42 (buffer_42_out, buffer_41_out);
  buf buffer_43 (buffer_43_out, buffer_45_out);
  buf buffer_44 (buffer_44_out, buffer_42_out);
  buf buffer_45 (buffer_45_out, buffer_47_out);
  buf buffer_46 (buffer_46_out, buffer_44_out);
  buf buffer_47 (buffer_47_out, buffer_16_out);
  buf buffer_48 (buffer_48_out, buffer_46_out);
  buf buffer_49 (out_2, buffer_50_out);
  buf buffer_50 (buffer_50_out, buffer_51_out);
  buf buffer_51 (buffer_51_out, buffer_52_out);
  buf buffer_52 (buffer_52_out, buffer_53_out);
  buf buffer_53 (buffer_53_out, buffer_54_out);
  buf buffer_54 (buffer_54_out, buffer_55_out);
  buf buffer_55 (buffer_55_out, buffer_56_out);
  buf buffer_56 (buffer_56_out, buffer_57_out);
  buf buffer_57 (buffer_57_out, buffer_58_out);
  buf buffer_58 (buffer_58_out, buffer_59_out);
  buf buffer_59 (buffer_59_out, buffer_60_out);
  buf buffer_60 (buffer_60_out, buffer_61_out);
  buf buffer_61 (buffer_61_out, buffer_62_out);
  buf buffer_62 (buffer_62_out, buffer_63_out);
  buf buffer_63 (buffer_63_out, buffer_64_out);
  buf buffer_64 (buffer_64_out, buffer_48_out);
endmodule
module Bin_Hex (
  input  in_1,
  input  [3:0] in_2,
  input  in_3,
  output out_4,
  output out_5,
  output out_6,
  output out_7,
  output out_8,
  output out_9,
  output out_10,
  output out_11,
  output out_12,
  output out_13,
  output out_14,
  output out_15,
  output out_16,
  output out_17,
  output out_18,
  output out_19
);

  wire and_1_out, and_2_out, and_3_out, and_4_out, and_5_out, and_6_out, and_7_out, and_8_out, and_9_out,
       and_10_out, and_11_out, and_12_out, and_13_out, and_14_out, and_15_out, and_16_out, and_17_out,
       and_18_out, and_19_out, and_20_out, and_21_out, not_1_out, not_2_out, not_3_out, not_4_out, not_5_out,
       not_6_out, not_7_out, not_8_out, not_9_out, not_10_out, not_11_out, not_12_out, not_13_out,
       not_14_out, not_15_out, not_16_out, not_17_out, not_18_out, not_19_out, not_20_out, not_21_out,
       not_22_out, not_23_out, not_24_out, not_25_out, not_26_out, not_27_out, not_28_out, not_29_out,
       not_30_out, not_31_out, not_32_out;

  and and_1 (and_1_out, in_2[0], in_1);
  and and_2 (and_2_out, in_2[1], in_1);
  and and_3 (and_3_out, in_1, in_2[2]);
  and and_4 (and_4_out, in_1, in_2[3]);
  or or_1 (out_4, in_3, and_5_out);
  and and_5 (and_5_out, and_4_out, not_3_out, not_1_out, not_2_out);
  not not_1 (not_1_out, and_2_out);
  not not_2 (not_2_out, and_1_out);
  not not_3 (not_3_out, and_3_out);
  not not_4 (not_4_out, and_4_out);
  not not_5 (not_5_out, and_2_out);
  not not_6 (not_6_out, and_1_out);
  not not_7 (not_7_out, and_4_out);
  not not_8 (not_8_out, and_3_out);
  and and_6 (and_6_out, not_7_out, not_8_out, not_5_out, not_6_out);
  and and_7 (and_7_out, in_1, and_6_out);
  or or_2 (out_12, and_7_out, in_3);
  or or_3 (out_6, in_3, and_9_out);
  or or_4 (out_5, in_3, and_8_out);
  and and_8 (and_8_out, and_4_out, not_11_out, not_10_out, and_1_out);
  and and_9 (and_9_out, and_4_out, not_9_out, and_2_out, not_16_out);
  not not_9 (not_9_out, and_3_out);
  not not_10 (not_10_out, and_2_out);
  not not_11 (not_11_out, and_3_out);
  not not_12 (not_12_out, and_3_out);
  not not_13 (not_13_out, and_3_out);
  not not_14 (not_14_out, and_2_out);
  not not_15 (not_15_out, and_4_out);
  and and_10 (and_10_out, not_15_out, not_13_out, and_2_out, not_20_out);
  and and_11 (and_11_out, not_4_out, not_12_out, not_14_out, and_1_out);
  or or_5 (out_13, and_11_out, in_3);
  or or_6 (out_7, in_3, and_12_out);
  and and_12 (and_12_out, and_4_out, not_17_out, and_2_out, and_1_out);
  not not_16 (not_16_out, and_1_out);
  not not_17 (not_17_out, and_3_out);
  not not_18 (not_18_out, and_3_out);
  not not_19 (not_19_out, and_4_out);
  not not_20 (not_20_out, and_1_out);
  and and_13 (and_13_out, not_19_out, not_18_out, and_2_out, and_1_out);
  or or_7 (out_15, and_13_out, in_3);
  or or_8 (out_14, and_10_out, in_3);
  or or_9 (out_8, in_3, and_14_out);
  and and_14 (and_14_out, and_4_out, and_3_out, not_22_out, not_21_out);
  not not_21 (not_21_out, and_1_out);
  not not_22 (not_22_out, and_2_out);
  not not_23 (not_23_out, and_4_out);
  not not_24 (not_24_out, and_2_out);
  not not_25 (not_25_out, and_1_out);
  not not_26 (not_26_out, and_4_out);
  and and_15 (and_15_out, not_26_out, and_3_out, not_24_out, not_25_out);
  or or_10 (out_16, and_15_out, in_3);
  or or_11 (out_9, in_3, and_17_out);
  or or_12 (out_10, in_3, and_16_out);
  and and_16 (and_16_out, and_4_out, and_3_out, and_2_out, not_30_out);
  and and_17 (and_17_out, and_4_out, and_3_out, not_27_out, and_1_out);
  not not_27 (not_27_out, and_2_out);
  not not_28 (not_28_out, and_2_out);
  not not_29 (not_29_out, and_4_out);
  and and_18 (and_18_out, not_29_out, and_3_out, and_2_out, not_31_out);
  and and_19 (and_19_out, not_23_out, and_3_out, not_28_out, and_1_out);
  or or_13 (out_17, and_19_out, in_3);
  or or_14 (out_11, in_3, and_20_out);
  and and_20 (and_20_out, and_4_out, and_3_out, and_2_out, and_1_out);
  not not_30 (not_30_out, and_1_out);
  not not_31 (not_31_out, and_1_out);
  not not_32 (not_32_out, and_4_out);
  and and_21 (and_21_out, not_32_out, and_3_out, and_2_out, and_1_out);
  or or_15 (out_19, and_21_out, in_3);
  or or_16 (out_18, and_18_out, in_3);
endmodule
